// Logisim project 0_0_1.circ as structural Verilog: 27 circuits, main circuit main
module main (
);

  wire [63:0] mat_multipler_64bit_1_s0, mat_multipler_64bit_1_s1, mat_multipler_64bit_1_s2,
       mat_multipler_64bit_1_s3, mat_multipler_64bit_1_w0, mat_multipler_64bit_1_w1,
       mat_multipler_64bit_1_w2, mat_multipler_64bit_1_w3, test_coreadder_1_s0, test_coreadder_1_s1,
       test_coreadder_1_s2, test_coreadder_1_s3;

  MAT_Multipler_64Bit mat_multipler_64bit_1 (
    .B0(64'h5), .A0(64'h1), .B1(64'h6), .A1(64'h2), .B2(64'h7), .A2(64'h3), .B3(64'h8), .A3(64'h4),
    .S0(mat_multipler_64bit_1_s0), .S1(mat_multipler_64bit_1_s1), .S2(mat_multipler_64bit_1_s2),
    .S3(mat_multipler_64bit_1_s3), .W0(mat_multipler_64bit_1_w0), .W1(mat_multipler_64bit_1_w1),
    .W2(mat_multipler_64bit_1_w2), .W3(mat_multipler_64bit_1_w3));
  TEST_CoreAdder test_coreadder_1 (
    .B0(mat_multipler_64bit_1_s0), .A0(mat_multipler_64bit_1_w0), .B1(mat_multipler_64bit_1_s1),
    .A1(mat_multipler_64bit_1_w1), .B2(mat_multipler_64bit_1_s2), .A2(mat_multipler_64bit_1_w2),
    .B3(mat_multipler_64bit_1_s3), .A3(mat_multipler_64bit_1_w3), .S0(test_coreadder_1_s0),
    .S1(test_coreadder_1_s1), .S2(test_coreadder_1_s2), .S3(test_coreadder_1_s3));
  // Probe on test_coreadder_1_s0
  // Probe on test_coreadder_1_s2
  // Probe on test_coreadder_1_s1
  // Probe on test_coreadder_1_s3
endmodule

module ADD_HalfAdder (
  input  B,
  input  A,
  output S,
  output C_out
);

  xor xor_1 (S, B, A);
  and and_1 (C_out, B, A);
endmodule

module ADD_FullAdder (
  input  B,
  input  A,
  input  C_in,
  output S,
  output C_out
);

  wire add_halfadder_1_c_out, add_halfadder_1_s, add_halfadder_2_c_out;

  ADD_HalfAdder add_halfadder_1 (.B(B), .A(A), .S(add_halfadder_1_s), .C_out(add_halfadder_1_c_out));
  ADD_HalfAdder add_halfadder_2 (.B(add_halfadder_1_s), .A(C_in), .S(S), .C_out(add_halfadder_2_c_out));
  or or_1 (C_out, add_halfadder_1_c_out, add_halfadder_2_c_out);
endmodule

module ADD_Ripple_2Bit (
  input  [1:0] B,
  input  [1:0] A,
  input  C_in,
  output [1:0] S,
  output C_out
);

  wire add_fulladder_1_c_out;

  ADD_FullAdder add_fulladder_1 (.B(B[0]), .A(A[0]), .C_in(C_in), .S(S[0]), .C_out(add_fulladder_1_c_out));
  ADD_FullAdder add_fulladder_2 (.B(B[1]), .A(A[1]), .C_in(add_fulladder_1_c_out), .S(S[1]), .C_out(C_out));
endmodule

module ADD_Ripple_4Bit (
  input  [3:0] B,
  input  [3:0] A,
  input  C_in,
  output [3:0] S,
  output C_out
);

  wire add_ripple_2bit_1_c_out;

  ADD_Ripple_2Bit add_ripple_2bit_1 (.B(B[1:0]), .A(A[1:0]), .C_in(C_in), .S(S[1:0]), .C_out(add_ripple_2bit_1_c_out));
  ADD_Ripple_2Bit add_ripple_2bit_2 (.B(B[3:2]), .A(A[3:2]), .C_in(add_ripple_2bit_1_c_out), .S(S[3:2]), .C_out(C_out));
endmodule

module ADD_Ripple_8Bit (
  input  [7:0] B,
  input  [7:0] A,
  input  C_in,
  output [7:0] S,
  output C_out
);

  wire add_ripple_4bit_1_c_out;

  ADD_Ripple_4Bit add_ripple_4bit_1 (.B(B[3:0]), .A(A[3:0]), .C_in(C_in), .S(S[3:0]), .C_out(add_ripple_4bit_1_c_out));
  ADD_Ripple_4Bit add_ripple_4bit_2 (.B(B[7:4]), .A(A[7:4]), .C_in(add_ripple_4bit_1_c_out), .S(S[7:4]), .C_out(C_out));
endmodule

module ADD_Ripple_16Bit (
  input  [15:0] B,
  input  [15:0] A,
  input  C_in,
  output [15:0] S,
  output C_out
);

  wire add_ripple_8bit_1_c_out;

  ADD_Ripple_8Bit add_ripple_8bit_1 (.B(B[7:0]), .A(A[7:0]), .C_in(C_in), .S(S[7:0]), .C_out(add_ripple_8bit_1_c_out));
  ADD_Ripple_8Bit add_ripple_8bit_2 (
    .B(B[15:8]), .A(A[15:8]), .C_in(add_ripple_8bit_1_c_out), .S(S[15:8]), .C_out(C_out));
endmodule

module ADD_Ripple_32Bit (
  input  [31:0] B,
  input  [31:0] A,
  input  C_in,
  output [31:0] S,
  output C_out
);

  wire add_ripple_16bit_1_c_out;

  ADD_Ripple_16Bit add_ripple_16bit_1 (
    .B(B[15:0]), .A(A[15:0]), .C_in(C_in), .S(S[15:0]), .C_out(add_ripple_16bit_1_c_out));
  ADD_Ripple_16Bit add_ripple_16bit_2 (
    .B(B[31:16]), .A(A[31:16]), .C_in(add_ripple_16bit_1_c_out), .S(S[31:16]), .C_out(C_out));
endmodule

module ADD_Ripple_64Bit (
  input  [63:0] B,
  input  [63:0] A,
  input  C_in,
  output [63:0] S,
  output C_out
);

  wire add_ripple_32bit_1_c_out;

  ADD_Ripple_32Bit add_ripple_32bit_1 (
    .B(B[31:0]), .A(A[31:0]), .C_in(C_in), .S(S[31:0]), .C_out(add_ripple_32bit_1_c_out));
  ADD_Ripple_32Bit add_ripple_32bit_2 (
    .B(B[63:32]), .A(A[63:32]), .C_in(add_ripple_32bit_1_c_out), .S(S[63:32]), .C_out(C_out));
endmodule

module TEST_ADD_Ripple_64Bit (
  input  [63:0] in_1,
  input  [63:0] in_2,
  input  in_3,
  input  [63:0] in_4,
  input  [63:0] in_5,
  input  in_6
);

  wire add_ripple_64bit_1_p1, add_ripple_64bit_1_p2, add_ripple_64bit_2_p1, add_ripple_64bit_2_p2;

  // ADD_Ripple_64Bit add_ripple_64bit_1: pin names not known; wires that end beside it: add_ripple_64bit_1_p1, add_ripple_64bit_1_p2
  // ADD_Ripple_64Bit add_ripple_64bit_2: pin names not known; wires that end beside it: add_ripple_64bit_2_p1, add_ripple_64bit_2_p2
  // Probe on add_ripple_64bit_2_p2
  // Probe on add_ripple_64bit_2_p1
  // Probe on add_ripple_64bit_1_p2
  // Probe on add_ripple_64bit_1_p1
endmodule

module NODE_2x2_v1 (
  input  [31:0] B0,
  input  [31:0] A0,
  input  [31:0] B1,
  input  [31:0] A1,
  input  [31:0] B2,
  input  [31:0] A2,
  input  [31:0] B3,
  input  [31:0] A3,
  output [63:0] S0,
  output [63:0] S1,
  output [63:0] S2,
  output [63:0] S3
);

  // ADD_Ripple_64Bit add_ripple_64bit_1: pin names not known; wires that end beside it: B0, A0
endmodule

module MAT_Multipler_64Bit (
  input  [63:0] B0,
  input  [63:0] A0,
  input  [63:0] B1,
  input  [63:0] A1,
  input  [63:0] B2,
  input  [63:0] A2,
  input  [63:0] B3,
  input  [63:0] A3,
  output [63:0] S0,
  output [63:0] S1,
  output [63:0] S2,
  output [63:0] S3,
  output [63:0] W0,
  output [63:0] W1,
  output [63:0] W2,
  output [63:0] W3
);

  Multiplier #(.width(64)) multiplier_1 (.a(A0), .b(B0), .out(S0));  // open: cin, cout
  Multiplier #(.width(64)) multiplier_2 (.a(A0), .b(B1), .out(S1));  // open: cin, cout
  Multiplier #(.width(64)) multiplier_3 (.a(A2), .b(B0), .out(S2));  // open: cin, cout
  Multiplier #(.width(64)) multiplier_4 (.a(A2), .b(B1), .out(S3));  // open: cin, cout
  Multiplier #(.width(64)) multiplier_5 (.a(A1), .b(B2), .out(W0));  // open: cin, cout
  Multiplier #(.width(64)) multiplier_6 (.a(A1), .b(B3), .out(W1));  // open: cin, cout
  Multiplier #(.width(64)) multiplier_7 (.a(A3), .b(B2), .out(W2));  // open: cin, cout
  Multiplier #(.width(64)) multiplier_8 (.a(A3), .b(B3), .out(W3));  // open: cin, cout

  // Notes on the sheet:
  //   A0B0
  //   A0B1
  //   A2B0
  //   A2B1
  //   A1B2
  //   A1B3
  //   A3B2
  //   A3B3
  //   ABCD WXYZ
  //   AW AX; CW CX
  //   BY BZ; DY DZ
  //   AW
endmodule

module ASM (
);

  wire and_1_out, and_2_out, clock_1_out, not_1_out, undriven, undriven_2;
  wire [7:0] counter_1_q, ram_1_dout, ram_3_dout, ram_5_dout, ram_7_dout, ram_9_dout, ram_11_dout,
       ram_13_dout, ram_17_dout, ram_19_dout, ram_23_dout;
  wire [31:0] C1_dout, ram_2_dout, ram_6_dout, ram_8_dout, test_coreadder_1_p5, test_coreadder_1_p6,
       test_coreadder_1_p7, test_coreadder_1_p8;
  wire [63:0] S0, S1, S2, S3;

  Clock clock_1 (.out(clock_1_out));
  // Probe on counter_1_q
  RAM #(.dataWidth(32), .trigger("falling"), .\type ("nonvolatile")) C1 (
    .addr(counter_1_q), .oe(1'b1), .clk(clock_1_out), .dout(C1_dout));  // open: we, din
  RAM ram_1 (.addr(counter_1_q), .oe(1'b1), .clk(clock_1_out), .dout(ram_1_dout));  // open: we, din
  RAM #(.dataWidth(32), .trigger("falling"), .\type ("nonvolatile")) ram_2 (
    .addr(counter_1_q), .oe(1'b1), .clk(clock_1_out), .dout(ram_2_dout));  // open: we, din
  RAM ram_3 (.addr(counter_1_q), .we(undriven), .oe(1'b1), .clk(clock_1_out), .dout(ram_3_dout));  // open: din
  RAM #(.dataWidth(64), .\type ("nonvolatile")) ram_4 (
    .addr(counter_1_q), .we(1'b1), .oe(undriven_2), .clk(clock_1_out), .din(S0));  // open: dout
  RAM ram_5 (.addr(counter_1_q), .oe(1'b1), .clk(clock_1_out), .dout(ram_5_dout));  // open: we, din
  Counter counter_1 (
    .count(1'b1), .Q(counter_1_q), .up(1'b1), .clk(clock_1_out), .clr(and_2_out));  // open: load, D, carry
  // Probe on and_2_out
  and and_1 (and_1_out, counter_1_q[0], counter_1_q[1]);
  and and_2 (and_2_out, counter_1_q[2], not_1_out);
  not not_1 (not_1_out, and_1_out);
  RAM #(.dataWidth(32), .trigger("falling"), .\type ("nonvolatile")) ram_6 (
    .addr(counter_1_q), .oe(1'b1), .clk(clock_1_out), .dout(ram_6_dout));  // open: we, din
  RAM ram_7 (.addr(counter_1_q), .oe(1'b1), .clk(clock_1_out), .dout(ram_7_dout));  // open: we, din
  RAM #(.dataWidth(32), .trigger("falling"), .\type ("nonvolatile")) ram_8 (
    .addr(counter_1_q), .oe(1'b1), .clk(clock_1_out), .dout(ram_8_dout));  // open: we, din
  RAM ram_9 (.addr(counter_1_q), .oe(1'b1), .clk(clock_1_out), .dout(ram_9_dout));  // open: we, din
  RAM #(.dataWidth(64), .\type ("nonvolatile")) ram_10 (
    .addr(counter_1_q), .we(1'b1), .oe(undriven_2), .clk(clock_1_out), .din(S1));  // open: dout
  RAM ram_11 (.addr(counter_1_q), .oe(1'b1), .clk(clock_1_out), .dout(ram_11_dout));  // open: we, din
  // Probe on S3
  // Probe on S1
  // Probe on S0
  // Probe on S2
  // TEST_CoreAdder test_coreadder_1: pin names not known; wires that end beside it: ram_2_dout, C1_dout, ram_8_dout, ram_6_dout, test_coreadder_1_p5, test_coreadder_1_p6, test_coreadder_1_p7, test_coreadder_1_p8, S0, S1, S2, S3
  // Probe on S2
  // Probe on S0
  // Probe on ram_6_dout
  RAM #(.dataWidth(32), .trigger("falling"), .\type ("nonvolatile")) ram_12 (
    .addr(counter_1_q), .oe(1'b1), .clk(clock_1_out), .dout(test_coreadder_1_p6));  // open: we, din
  RAM ram_13 (.addr(counter_1_q), .oe(1'b1), .clk(clock_1_out), .dout(ram_13_dout));  // open: we, din
  RAM #(.dataWidth(32), .trigger("falling"), .\type ("nonvolatile")) ram_14 (
    .addr(counter_1_q), .oe(1'b1), .clk(clock_1_out), .dout(test_coreadder_1_p5));  // open: we, din
  RAM ram_15 (.addr(counter_1_q), .oe(1'b1), .clk(clock_1_out));  // open: we, din, dout
  RAM #(.dataWidth(64), .\type ("nonvolatile")) ram_16 (
    .addr(counter_1_q), .we(1'b1), .oe(undriven_2), .clk(clock_1_out), .din(S2));  // open: dout
  RAM ram_17 (.addr(counter_1_q), .oe(1'b1), .clk(clock_1_out), .dout(ram_17_dout));  // open: we, din
  // Probe on S1
  // Probe on S3
  // TEST_CoreAdder test_coreadder_2: pin names not known
  RAM #(.dataWidth(32), .trigger("falling"), .\type ("nonvolatile")) ram_18 (
    .addr(counter_1_q), .oe(1'b1), .clk(clock_1_out), .dout(test_coreadder_1_p8));  // open: we, din
  RAM ram_19 (.addr(counter_1_q), .oe(1'b1), .clk(clock_1_out), .dout(ram_19_dout));  // open: we, din
  RAM #(.dataWidth(32), .trigger("falling"), .\type ("nonvolatile")) ram_20 (
    .addr(counter_1_q), .oe(1'b1), .clk(clock_1_out), .dout(test_coreadder_1_p7));  // open: we, din
  RAM ram_21 (.addr(counter_1_q), .oe(1'b1), .clk(clock_1_out));  // open: we, din, dout
  RAM #(.dataWidth(64), .\type ("nonvolatile")) ram_22 (
    .addr(counter_1_q), .we(1'b1), .oe(undriven_2), .clk(clock_1_out), .din(S3));  // open: dout
  RAM ram_23 (.addr(counter_1_q), .oe(1'b1), .clk(clock_1_out), .dout(ram_23_dout));  // open: we, din

  // Notes on the sheet:
  //   2, 2; 1, 1
  //   C1
  //   W1
  //   S1
  //   Resets on 4
  //   C2
  //   W2
  //   S2
  //   C3
  //   W3
  //   S3
  //   C4
  //   W4
  //   S4
endmodule

module UTIL_BitExtender_32Bit (
  input  [31:0] A,
  output [63:0] S
);

  assign S = {{32{A[31]}}, A};  // Bit_Extender bit_extender_1
endmodule

module REG_RegisterFile_v1 (
  input  [2:0] Address,
  input  [31:0] in_2,
  input  [31:0] in_3,
  input  [31:0] in_4,
  input  [31:0] in_5,
  input  [31:0] D,
  input  Write_Enable,
  input  [31:0] A0_in,
  input  [31:0] A2_in,
  input  [31:0] A1_in,
  input  [31:0] A3_in,
  input  Clock,
  input  Reset,
  input  [31:0] in_14,
  input  [31:0] in_15,
  input  [31:0] in_16,
  input  [31:0] in_17,
  input  [31:0] in_18,
  input  [31:0] in_19,
  input  [31:0] in_20,
  input  [31:0] in_21,
  output [31:0] A1,
  output [31:0] A3,
  output [31:0] A2,
  output [31:0] A0,
  output [31:0] B1,
  output [31:0] B3,
  output [31:0] B2,
  output [31:0] B0,
  output [31:0] S1,
  output [31:0] S3,
  output [31:0] S2,
  output [31:0] S0
);

  wire undriven, undriven_2, undriven_3;

  Register #(.width(32)) register_1 (.D(A0_in), .en(Write_Enable), .clk(Clock), .Q(A0), .clr(Reset));
  Register #(.width(32)) register_2 (.D(A2_in), .en(Write_Enable), .clk(Clock), .Q(A2), .clr(Reset));
  Register #(.width(32)) register_3 (.D(in_14), .en(Write_Enable), .clk(Clock), .Q(B0), .clr(Reset));
  Register #(.width(32)) register_4 (.D(in_15), .en(Write_Enable), .clk(Clock), .Q(B2), .clr(Reset));
  Register #(.width(32)) register_5 (.D(in_18), .en(Write_Enable), .clk(Clock), .Q(S0), .clr(Reset));
  Register #(.width(32)) register_6 (.D(in_19), .en(Write_Enable), .clk(Clock), .Q(S2), .clr(Reset));
  Register #(.width(32)) register_7 (.D(A1_in), .en(Write_Enable), .clk(Clock), .Q(A1), .clr(undriven));
  Register #(.width(32)) register_8 (.D(A3_in), .en(Write_Enable), .clk(Clock), .Q(A3), .clr(Reset));
  Register #(.width(32)) register_9 (.D(in_16), .en(Write_Enable), .clk(Clock), .Q(B1), .clr(undriven_2));
  Register #(.width(32)) register_10 (.D(in_17), .en(Write_Enable), .clk(Clock), .Q(B3), .clr(Reset));
  Register #(.width(32)) register_11 (.D(in_20), .en(Write_Enable), .clk(Clock), .Q(S1), .clr(undriven_3));
  Register #(.width(32)) register_12 (.D(in_21), .en(Write_Enable), .clk(Clock), .Q(S3), .clr(Reset));
  RAM ram_1 ();  // open: addr, we, oe, clk, din, dout

  // Notes on the sheet:
  //   Clock
  //   Write Enable
  //   Reset (All)
  //   'A' Register Bank
  //   Weights Register Bank
  //   Output Register Bank
endmodule

module CORE_CoreAdder (
  input  [31:0] B0,
  input  [31:0] A0,
  input  [31:0] B1,
  input  [31:0] A1,
  input  [31:0] B2,
  input  [31:0] A2,
  input  [31:0] B3,
  input  [31:0] A3,
  output [63:0] S0,
  output [63:0] S1,
  output [63:0] S2,
  output [63:0] S3
);

  wire [31:0] adder_1_out, adder_2_out, adder_3_out, adder_4_out;

  Adder #(.width(32)) adder_1 (.a(B0), .b(A0), .out(adder_1_out));  // open: cin, cout
  Adder #(.width(32)) adder_2 (.a(B1), .b(A1), .out(adder_2_out));  // open: cin, cout
  Adder #(.width(32)) adder_3 (.a(B2), .b(A2), .out(adder_3_out));  // open: cin, cout
  Adder #(.width(32)) adder_4 (.a(B3), .b(A3), .out(adder_4_out));  // open: cin, cout
  assign S0 = {{32{adder_1_out[31]}}, adder_1_out};  // Bit_Extender bit_extender_1
  assign S1 = {{32{adder_2_out[31]}}, adder_2_out};  // Bit_Extender bit_extender_2
  assign S2 = {{32{adder_3_out[31]}}, adder_3_out};  // Bit_Extender bit_extender_3
  assign S3 = {{32{adder_4_out[31]}}, adder_4_out};  // Bit_Extender bit_extender_4
endmodule

module TEST_CoreAdder (
  input  [63:0] B0,
  input  [63:0] A0,
  input  [63:0] B1,
  input  [63:0] A1,
  input  [63:0] B2,
  input  [63:0] A2,
  input  [63:0] B3,
  input  [63:0] A3,
  output [63:0] S0,
  output [63:0] S1,
  output [63:0] S2,
  output [63:0] S3
);

  Adder #(.width(64)) adder_1 (.a(B0), .b(A0), .out(S0));  // open: cin, cout
  Adder #(.width(64)) adder_2 (.a(B1), .b(A1), .out(S1));  // open: cin, cout
  Adder #(.width(64)) adder_3 (.a(B2), .b(A2), .out(S2));  // open: cin, cout
  Adder #(.width(64)) adder_4 (.a(B3), .b(A3), .out(S3));  // open: cin, cout
endmodule

module TEST_asm_add_pair (
);

  wire and_1_out, and_2_out, clock_1_out, not_1_out;
  wire [7:0] counter_1_q;
  wire [31:0] C1_dout, ram_1_dout;
  wire [63:0] S0;

  Clock clock_1 (.out(clock_1_out));
  // Probe on counter_1_q
  RAM #(.dataWidth(32), .trigger("falling"), .\type ("nonvolatile")) C1 (
    .addr(counter_1_q), .oe(1'b1), .clk(clock_1_out), .dout(C1_dout));  // open: we, din
  RAM #(.dataWidth(32), .trigger("falling"), .\type ("nonvolatile")) ram_1 (
    .addr(counter_1_q), .oe(1'b1), .clk(clock_1_out), .dout(ram_1_dout));  // open: we, din
  RAM #(.dataWidth(64)) ram_2 (.addr(counter_1_q), .we(1'b1), .clk(clock_1_out), .din(S0));  // open: oe, dout
  Counter counter_1 (
    .count(1'b1), .Q(counter_1_q), .up(1'b1), .clk(clock_1_out), .clr(and_2_out));  // open: load, D, carry
  // Probe on and_2_out
  and and_1 (and_1_out, counter_1_q[0], counter_1_q[1]);
  and and_2 (and_2_out, counter_1_q[3], not_1_out);
  not not_1 (not_1_out, and_1_out);
  // Probe on S0
  // TEST_CoreAdder test_coreadder_1: pin names not known; wires that end beside it: ram_1_dout, C1_dout, S0
  // Probe on S0

  // Notes on the sheet:
  //   2, 2; 1, 1
  //   C1
  //   W1
  //   S1
  //   Resets on 8,12
endmodule

module TEST_ASM_Quiz (
);

  wire and_1_out, and_2_out, clock_1_out, clock_2_out, not_1_out;
  wire [7:0] counter_1_q;
  wire [63:0] C1_dout, ram_1_dout, ram_3_dout, ram_4_dout, ram_5_dout, ram_7_dout, ram_8_dout, ram_10_dout,
       ram_11_dout, S0, S1, S2, S3;

  Clock clock_1 (.out(clock_1_out));
  // Probe on counter_1_q
  Clock clock_2 (.out(clock_2_out));
  RAM #(.dataWidth(64), .\type ("nonvolatile")) C1 (
    .addr(counter_1_q), .oe(1'b1), .clk(clock_1_out), .dout(C1_dout));  // open: we, din
  RAM #(.dataWidth(64), .\type ("nonvolatile")) ram_1 (
    .addr(counter_1_q), .oe(1'b1), .clk(clock_1_out), .dout(ram_1_dout));  // open: we, din
  RAM #(.dataWidth(64)) ram_2 (.addr(counter_1_q), .we(1'b1), .clk(clock_1_out), .din(S0));  // open: oe, dout
  RAM #(.dataWidth(64), .\type ("nonvolatile")) ram_3 (
    .addr({8{1'b0}}), .we(1'b1), .clk(clock_2_out), .din(64'h2), .dout(ram_3_dout));  // open: oe
  Counter counter_1 (
    .count(1'b1), .Q(counter_1_q), .up(1'b1), .clk(clock_1_out), .clr(and_2_out));  // open: load, D, carry
  // Probe on and_2_out
  and and_1 (and_1_out, counter_1_q[0], counter_1_q[1]);
  and and_2 (and_2_out, counter_1_q[3], not_1_out);
  // Probe on C1_dout
  // Probe on ram_3_dout
  not not_1 (not_1_out, and_1_out);
  RAM #(.dataWidth(64), .\type ("nonvolatile")) ram_4 (
    .addr(counter_1_q), .oe(1'b1), .clk(clock_1_out), .dout(ram_4_dout));  // open: we, din
  RAM #(.dataWidth(64), .\type ("nonvolatile")) ram_5 (
    .addr(counter_1_q), .oe(1'b1), .clk(clock_1_out), .dout(ram_5_dout));  // open: we, din
  RAM #(.dataWidth(64)) ram_6 (.addr(counter_1_q), .we(1'b1), .clk(clock_1_out), .din(S1));  // open: oe, dout
  // Probe on S3
  // Probe on S1
  // Probe on S0
  // Probe on S2
  TEST_CoreAdder test_coreadder_1 (
    .B0(ram_1_dout), .A0(C1_dout), .B1(ram_5_dout), .A1(ram_4_dout), .B2(ram_8_dout), .A2(ram_7_dout),
    .B3(ram_11_dout), .A3(ram_10_dout), .S0(S0), .S1(S1), .S2(S2), .S3(S3));
  // Probe on S2
  // Probe on S0
  // Probe on ram_4_dout
  RAM #(.dataWidth(64), .\type ("nonvolatile")) ram_7 (
    .addr(counter_1_q), .oe(1'b1), .clk(clock_1_out), .dout(ram_7_dout));  // open: we, din
  RAM #(.dataWidth(64), .\type ("nonvolatile")) ram_8 (
    .addr(counter_1_q), .oe(1'b1), .clk(clock_1_out), .dout(ram_8_dout));  // open: we, din
  RAM #(.dataWidth(64)) ram_9 (.addr(counter_1_q), .we(1'b1), .clk(clock_1_out), .din(S2));  // open: oe, dout
  // Probe on S1
  // Probe on S3
  RAM #(.dataWidth(64), .\type ("nonvolatile")) ram_10 (
    .addr(counter_1_q), .oe(1'b1), .clk(clock_1_out), .dout(ram_10_dout));  // open: we, din
  RAM #(.dataWidth(64), .\type ("nonvolatile")) ram_11 (
    .addr(counter_1_q), .oe(1'b1), .clk(clock_1_out), .dout(ram_11_dout));  // open: we, din
  RAM #(.dataWidth(64)) ram_12 (.addr(counter_1_q), .we(1'b1), .clk(clock_1_out), .din(S3));  // open: oe, dout

  // Notes on the sheet:
  //   2, 2; 1, 1
  //   C1
  //   W1
  //   S1
  //   Resets on 8, 12
  //   C2
  //   W2
  //   S2
  //   C3
  //   W3
  //   S3
  //   C4
  //   W4
  //   S4
endmodule

module TEST_ASM_Quiz_v2 (
);

  wire and_1_out, and_2_out, clock_1_out, not_1_out;
  wire [7:0] counter_1_q, register_1_q, register_2_q;
  wire [63:0] C1_dout, ram_1_dout, ram_2_dout, ram_4_dout, ram_5_dout, ram_6_dout, ram_7_dout, ram_8_dout,
       ram_9_dout, ram_10_dout, ram_11_dout, ram_12_dout, S0, S1, S2, S3;

  Clock clock_1 (.out(clock_1_out));
  // Probe on counter_1_q
  Register register_1 (.D(counter_1_q), .en(1'b1), .clk(clock_1_out), .Q(register_1_q));  // open: clr
  Register register_2 (.D(register_1_q), .en(1'b1), .clk(clock_1_out), .Q(register_2_q));  // open: clr
  RAM #(.dataWidth(64), .\type ("nonvolatile")) C1 (
    .addr(counter_1_q), .oe(1'b1), .clk(clock_1_out), .dout(C1_dout));  // open: we, din
  RAM #(.dataWidth(64), .\type ("nonvolatile")) ram_1 (
    .addr(counter_1_q), .oe(1'b1), .clk(clock_1_out), .dout(ram_1_dout));  // open: we, din
  RAM #(.dataWidth(64)) ram_2 (
    .addr(register_1_q), .we(1'b1), .oe(1'b1), .clk(clock_1_out), .din(S0), .dout(ram_2_dout));
  Counter counter_1 (
    .count(1'b1), .Q(counter_1_q), .up(1'b1), .clk(clock_1_out), .clr(and_2_out));  // open: load, D, carry
  RAM #(.dataWidth(64)) ram_3 (.addr(register_2_q), .we(1'b1), .clk(clock_1_out), .din(ram_2_dout));  // open: oe, dout
  // Probe on and_2_out
  and and_1 (and_1_out, counter_1_q[0], counter_1_q[1]);
  and and_2 (and_2_out, counter_1_q[3], not_1_out);
  not not_1 (not_1_out, and_1_out);
  RAM #(.dataWidth(64), .\type ("nonvolatile")) ram_4 (
    .addr(counter_1_q), .oe(1'b1), .clk(clock_1_out), .dout(ram_4_dout));  // open: we, din
  RAM #(.dataWidth(64), .\type ("nonvolatile")) ram_5 (
    .addr(counter_1_q), .oe(1'b1), .clk(clock_1_out), .dout(ram_5_dout));  // open: we, din
  RAM #(.dataWidth(64)) ram_6 (
    .addr(register_1_q), .we(1'b1), .oe(1'b1), .clk(clock_1_out), .din(S1), .dout(ram_6_dout));
  // Probe on S3
  // Probe on S1
  // Probe on S0
  // Probe on S2
  TEST_CoreAdder test_coreadder_1 (
    .B0(ram_1_dout), .A0(C1_dout), .B1(ram_5_dout), .A1(ram_4_dout), .B2(ram_8_dout), .A2(ram_7_dout),
    .B3(ram_11_dout), .A3(ram_10_dout), .S0(S0), .S1(S1), .S2(S2), .S3(S3));
  // Probe on S2
  // Probe on S0
  // Probe on ram_4_dout
  RAM #(.dataWidth(64), .\type ("nonvolatile")) ram_7 (
    .addr(counter_1_q), .oe(1'b1), .clk(clock_1_out), .dout(ram_7_dout));  // open: we, din
  RAM #(.dataWidth(64), .\type ("nonvolatile")) ram_8 (
    .addr(counter_1_q), .oe(1'b1), .clk(clock_1_out), .dout(ram_8_dout));  // open: we, din
  RAM #(.dataWidth(64)) ram_9 (
    .addr(register_1_q), .we(1'b1), .oe(1'b1), .clk(clock_1_out), .din(S2), .dout(ram_9_dout));
  // Probe on S1
  // Probe on S3
  RAM #(.dataWidth(64), .\type ("nonvolatile")) ram_10 (
    .addr(counter_1_q), .oe(1'b1), .clk(clock_1_out), .dout(ram_10_dout));  // open: we, din
  RAM #(.dataWidth(64), .\type ("nonvolatile")) ram_11 (
    .addr(counter_1_q), .oe(1'b1), .clk(clock_1_out), .dout(ram_11_dout));  // open: we, din
  RAM #(.dataWidth(64)) ram_12 (
    .addr(register_1_q), .we(1'b1), .oe(1'b1), .clk(clock_1_out), .din(S3), .dout(ram_12_dout));

  // Notes on the sheet:
  //   C1
  //   W1
  //   S1
  //   Resets on 8, 12
  //   C2
  //   W2
  //   S2
  //   C3
  //   W3
  //   S3
  //   C4
  //   W4
  //   S4
endmodule

module ASM_WRITEBACK (
  input  in_1,
  input  in_2,
  input  in_3,
  input  in_4,
  input  in_5,
  input  in_6,
  input  in_7
);

  wire and_1_out, clock_1_out, clock_2_out, clock_3_out, clock_4_out, not_1_out, not_2_out, not_3_out;
  wire [7:0] counter_1_q, counter_2_q, counter_3_q, multiplexer_1_out, multiplexer_2_out, register_1_q,
       register_2_q, register_5_q;
  wire [63:0] adder_1_out, adder_3_out, C1_dout, ram_1_dout, ram_3_dout, ram_4_dout, reg_registerfile_v2_1_s,
       register_3_q, register_4_q, register_6_q, S0;

  // Probe on register_1_q
  // Probe on counter_2_q
  // Probe on counter_1_q
  Counter counter_1 (.count(1'b1), .Q(counter_1_q), .up(1'b1), .clk(clock_2_out), .clr(in_7));  // open: load, D, carry
  and and_1 (and_1_out, counter_3_q[0], clock_3_out);
  // Probe on register_2_q
  // Probe on register_6_q
  Clock clock_1 (.out(clock_1_out));
  // Probe on register_5_q
  Clock clock_2 (.out(clock_2_out));
  Clock clock_3 (.out(clock_3_out));
  Counter counter_2 (.count(1'b1), .Q(counter_2_q), .up(1'b1), .clk(clock_1_out));  // open: load, D, carry, clr
  Register register_1 (.D(counter_2_q), .en(1'b1), .clk(clock_1_out), .Q(register_1_q));  // open: clr
  Clock clock_4 (.out(clock_4_out));
  // Probe on register_4_q
  RAM #(.dataWidth(64), .\type ("nonvolatile")) C1 (
    .addr(multiplexer_1_out), .we(not_1_out), .oe(clock_3_out), .clk(clock_3_out), .din(register_6_q),
    .dout(C1_dout));
  Multiplexer #(.width(8)) multiplexer_1 (
    .in0(register_2_q), .in1(counter_3_q), .out(multiplexer_1_out), .sel(and_1_out));
  not not_1 (not_1_out, clock_3_out);
  RAM #(.dataWidth(64), .\type ("nonvolatile")) ram_1 (
    .addr(multiplexer_1_out), .we(not_2_out), .oe(clock_3_out), .clk(clock_3_out), .din(register_6_q),
    .dout(ram_1_dout));
  not not_2 (not_2_out, clock_3_out);
  // Probe on register_2_q
  RAM #(.dataWidth(64)) ram_2 (
    .addr(register_2_q), .we(clock_3_out), .oe(not_3_out), .clk(clock_3_out), .din(register_6_q));  // open: dout
  Register register_2 (.D(counter_3_q), .en(1'b1), .Q(register_2_q), .clk(clock_3_out));  // open: clr
  not not_3 (not_3_out, clock_3_out);
  // NOT_Gate not_4 is placed but not wired
  REG_RegisterFile_v2 reg_registerfile_v2_1 (
    .rs(counter_1_q), .rd(register_5_q), .D(register_4_q), .CLK(clock_2_out), .S(reg_registerfile_v2_1_s));
  RAM #(.asyncread("true"), .dataWidth(64), .trigger("falling"), .\type ("nonvolatile")) ram_3 (
    .addr(multiplexer_2_out), .we(in_2), .oe(in_3), .clk(clock_1_out), .din(register_3_q), .dout(ram_3_dout));
  Multiplexer #(.width(8)) multiplexer_2 (.in0(counter_2_q), .in1(register_1_q), .out(multiplexer_2_out), .sel(in_1));
  RAM #(.dataWidth(64), .trigger("falling"), .\type ("nonvolatile")) ram_4 (
    .addr(8'h1), .we(in_5), .oe(in_6), .clk(clock_4_out), .din(64'h2), .dout(ram_4_dout));
  Adder #(.width(64)) adder_1 (.a(reg_registerfile_v2_1_s), .b(64'h2), .out(adder_1_out));  // open: cin, cout
  // Probe on counter_3_q
  Counter counter_3 (.count(1'b1), .Q(counter_3_q), .up(1'b1), .clk(clock_3_out));  // open: load, D, carry, clr
  Register #(.width(64)) register_3 (.D(adder_3_out), .en(1'b1), .clk(clock_1_out), .Q(register_3_q), .clr(in_4));
  Register #(.width(64)) register_4 (.D(adder_1_out), .en(1'b1), .clk(clock_2_out), .Q(register_4_q));  // open: clr
  // Probe on register_4_q
  Register register_5 (.D(counter_1_q), .en(1'b1), .clk(clock_2_out), .Q(register_5_q));  // open: clr
  Register #(.width(64)) register_6 (.D(S0), .en(1'b1), .Q(register_6_q), .clk(clock_3_out));  // open: clr
  // Probe on C1_dout
  // Probe on ram_1_dout
  RAM #(.dataWidth(64), .trigger("falling"), .\type ("nonvolatile")) ram_5 ();  // open: addr, we, oe, clk, din, dout
  Adder #(.width(64)) adder_2 (.a(C1_dout), .b(ram_1_dout), .out(S0));  // open: cin, cout
  Adder #(.width(64)) adder_3 (.a(ram_3_dout), .b(64'h1), .out(adder_3_out));  // open: cin, cout
  // Probe on S0
  // Probe on ram_3_dout
  // Probe on ram_4_dout

  // Notes on the sheet:
  //   Register: 1-clock delay on address
  //   Writes in 1 Clock Cycle
  //   C1
  //   W1
  //   Checks if 2 * rd Clock Cycle
  //   Output comes in 1 Clock Cycle
endmodule

module REG_RegisterFile_v2 (
  input  [7:0] rs,
  input  [7:0] rd,
  input  [63:0] D,
  input  CLK,
  output [63:0] S
);

  wire d_ff_1_q, not_1_out;
  wire [7:0] multiplexer_1_out;

  D_Flip_Flop d_ff_1 (.clk(CLK), .D(1'b1), .Q(d_ff_1_q));  // open: Qn, preset, reset
  not not_1 (not_1_out, CLK);
  RAM #(.asyncread("true"), .dataWidth(64), .trigger("falling"), .\type ("nonvolatile")) ram_1 (
    .addr(multiplexer_1_out), .we(d_ff_1_q), .oe(not_1_out), .clk(CLK), .din(D), .dout(S));
  Multiplexer #(.width(8)) multiplexer_1 (.in0(rs), .in1(rd), .out(multiplexer_1_out), .sel(CLK));
  // Probe on S
endmodule

module ASM_MAT_ACCUM (
  input  in_1,
  input  in_2
);

  wire clock_1_out, ram_bank_2_p4, reg_registerfile_v3_1_oe, reg_registerfile_v3_1_we,
       reg_registerfile_v3_2_oe, reg_registerfile_v3_2_we;
  wire [7:0] adder_1_out, counter_1_q, counter_2_q, counter_3_q, ram_1_dout, reg_registerfile_v3_1_a,
       reg_registerfile_v3_2_a, register_1_q, register_2_q, register_3_q, register_4_q, undriven;
  wire [63:0] ram_bank_1_s0, ram_bank_1_s1, ram_bank_1_s2, ram_bank_1_s3, ram_bank_3_s0, ram_bank_3_s1,
       ram_bank_3_s2, ram_bank_3_s3, test_coreadder_v2_2_s0, test_coreadder_v2_2_s1, test_coreadder_v2_2_s2,
       test_coreadder_v2_2_s3;

  Counter counter_1 (.count(1'b1), .Q(counter_1_q), .up(1'b1), .clk(ram_bank_2_p4));  // open: load, D, carry, clr
  REG_RegisterFile_v3 reg_registerfile_v3_1 (
    .rs(counter_1_q), .rd(undriven), .CLK(ram_bank_2_p4), .A(reg_registerfile_v3_1_a),
    .WE(reg_registerfile_v3_1_we), .OE(reg_registerfile_v3_1_oe));
  Counter counter_2 (.count(1'b1), .Q(counter_2_q), .up(1'b1), .clk(clock_1_out));  // open: load, D, carry, clr
  Counter counter_3 (
    .load(in_1), .D(register_1_q), .count(counter_2_q[0]), .Q(counter_3_q), .up(1'b1), .clk(clock_1_out));  // open: carry, clr
  // Probe on test_coreadder_v2_2_s0
  // Probe on test_coreadder_v2_2_s2
  RAM #(.asyncread("true"), .trigger("falling")) ram_1 (
    .addr(reg_registerfile_v3_2_a), .we(reg_registerfile_v3_2_we), .oe(reg_registerfile_v3_2_oe),
    .clk(clock_1_out), .din(register_2_q), .dout(ram_1_dout));
  REG_RegisterFile_v3 reg_registerfile_v3_2 (
    .rs(counter_3_q), .rd(register_1_q), .CLK(clock_1_out), .A(reg_registerfile_v3_2_a),
    .WE(reg_registerfile_v3_2_we), .OE(reg_registerfile_v3_2_oe));
  Register register_1 (.D(counter_3_q), .Q(register_1_q), .clk(clock_1_out));  // open: en, clr
  RAM_BANK ram_bank_1 (
    .Address(reg_registerfile_v3_1_a), .WE(reg_registerfile_v3_1_we), .OE(reg_registerfile_v3_1_oe),
    .CLK(ram_bank_2_p4), .S3(ram_bank_1_s3), .S2(ram_bank_1_s2), .S1(ram_bank_1_s1), .S0(ram_bank_1_s0));  // open: D3, D2, D1, D0
  // RAM_BANK ram_bank_2: pin names not known; wires that end beside it: reg_registerfile_v3_1_a, reg_registerfile_v3_1_we, reg_registerfile_v3_1_oe, ram_bank_2_p4
  // Probe on ram_bank_1_s0
  TEST_CoreAdder_v2 test_coreadder_v2_1 ();  // open: B3, B2, B1, B0, A3, A2, A1, A0, S3, S2, S1, S0
  // Probe on register_1_q
  TEST_CoreAdder_v2 test_coreadder_v2_2 (
    .B3(ram_bank_3_s3), .B2(ram_bank_3_s2), .B1(ram_bank_3_s1), .B0(ram_bank_3_s0), .A3(ram_bank_1_s3),
    .A2(ram_bank_1_s2), .A1(ram_bank_1_s1), .A0(ram_bank_1_s0), .S3(test_coreadder_v2_2_s3),
    .S2(test_coreadder_v2_2_s2), .S1(test_coreadder_v2_2_s1), .S0(test_coreadder_v2_2_s0));
  Register register_2 (.D(adder_1_out), .en(in_2), .Q(register_2_q), .clk(clock_1_out));  // open: clr
  // Probe on test_coreadder_v2_2_s1
  // Probe on test_coreadder_v2_2_s3
  RAM_BANK ram_bank_3 (
    .Address(reg_registerfile_v3_1_a), .WE(reg_registerfile_v3_1_we), .OE(reg_registerfile_v3_1_oe),
    .CLK(ram_bank_2_p4), .S3(ram_bank_3_s3), .S2(ram_bank_3_s2), .S1(ram_bank_3_s1), .S0(ram_bank_3_s0));  // open: D3, D2, D1, D0
  // RAM_BANK ram_bank_4: pin names not known; wires that end beside it: reg_registerfile_v3_1_a, reg_registerfile_v3_1_we, reg_registerfile_v3_1_oe, ram_bank_2_p4
  // Probe on ram_1_dout
  Adder adder_1 (.a(ram_1_dout), .b(8'h1), .out(adder_1_out));  // open: cin, cout
  // Probe on register_2_q
  Clock clock_1 (.out(clock_1_out));
  Register register_3 (.D(reg_registerfile_v3_1_a), .en(1'b1), .Q(register_3_q), .clk(ram_bank_2_p4));  // open: clr
  Register register_4 (.D(reg_registerfile_v3_1_a), .en(1'b1), .Q(register_4_q), .clk(ram_bank_2_p4));  // open: clr
  Clock clock_2 (.out(ram_bank_2_p4));
  // RAM_BANK ram_bank_5: pin names not known; wires that end beside it: register_3_q, ram_bank_2_p4
  // RAM_BANK ram_bank_6: pin names not known; wires that end beside it: register_4_q, ram_bank_2_p4

  // Notes on the sheet:
  //   Pipelined
  //   Constant High Bit
  //   Pipelined
  //   A
  //   B
  //   O
endmodule

module RAM_BANK (
  input  [63:0] D3,
  input  [63:0] D2,
  input  [63:0] D1,
  input  [63:0] D0,
  input  [7:0] Address,
  input  WE,
  input  OE,
  input  CLK,
  output [63:0] S3,
  output [63:0] S2,
  output [63:0] S1,
  output [63:0] S0
);

  RAM #(.dataWidth(64), .trigger("falling"), .\type ("nonvolatile")) ram_1 ();  // open: addr, we, oe, clk, din, dout
  RAM #(.asyncread("true"), .dataWidth(64), .trigger("falling"), .\type ("nonvolatile")) C1 (
    .addr(Address), .we(WE), .oe(OE), .clk(CLK), .din(D0), .dout(S0));
  RAM #(.asyncread("true"), .dataWidth(64), .trigger("falling"), .\type ("nonvolatile")) ram_2 (
    .addr(Address), .we(WE), .oe(OE), .clk(CLK), .din(D1), .dout(S1));
  RAM #(.asyncread("true"), .dataWidth(64), .trigger("falling"), .\type ("nonvolatile")) ram_3 (
    .addr(Address), .we(WE), .oe(OE), .clk(CLK), .din(D2), .dout(S2));
  RAM #(.asyncread("true"), .dataWidth(64), .trigger("falling"), .\type ("nonvolatile")) ram_4 (
    .addr(Address), .we(WE), .oe(OE), .clk(CLK), .din(D3), .dout(S3));
endmodule

module REG_RegisterFile_v3 (
  input  [7:0] rs,
  input  [7:0] rd,
  input  CLK,
  output [7:0] A,
  output WE,
  output OE
);

  D_Flip_Flop d_ff_1 (.clk(CLK), .D(1'b1), .Q(WE));  // open: Qn, preset, reset
  not not_1 (OE, CLK);
  Multiplexer #(.width(8)) multiplexer_1 (.in0(rs), .in1(rd), .out(A), .sel(CLK));
endmodule

module TEST_CoreAdder_v2 (
  input  [63:0] B3,
  input  [63:0] B2,
  input  [63:0] B1,
  input  [63:0] B0,
  input  [63:0] A3,
  input  [63:0] A2,
  input  [63:0] A1,
  input  [63:0] A0,
  output [63:0] S3,
  output [63:0] S2,
  output [63:0] S1,
  output [63:0] S0
);

  Counter counter_1 ();  // open: load, D, count, Q, carry, up, clk, clr
  Adder #(.width(64)) adder_1 (.a(B0), .b(A0), .out(S0));  // open: cin, cout
  Adder #(.width(64)) adder_2 (.a(B1), .b(A1), .out(S1));  // open: cin, cout
  Adder #(.width(64)) adder_3 (.a(B2), .b(A2), .out(S2));  // open: cin, cout
  Adder #(.width(64)) adder_4 (.a(B3), .b(A3), .out(S3));  // open: cin, cout
endmodule

module TRASH_V1 (
);

  wire and_1_out, and_2_out, clock_1_out, not_1_out, undriven, undriven_2;
  wire [7:0] counter_1_q, ram_1_dout, ram_3_dout, ram_5_dout, ram_7_dout, ram_9_dout, ram_11_dout,
       ram_13_dout, ram_17_dout, ram_19_dout, ram_23_dout;
  wire [31:0] C1_dout, ram_2_dout, ram_6_dout, ram_8_dout, test_coreadder_1_p5, test_coreadder_1_p6,
       test_coreadder_1_p7, test_coreadder_1_p8;
  wire [63:0] S0, S1, S2, S3;

  Clock clock_1 (.out(clock_1_out));
  // Probe on counter_1_q
  RAM #(.dataWidth(32), .trigger("falling")) C1 (
    .addr(counter_1_q), .oe(1'b1), .clk(clock_1_out), .dout(C1_dout));  // open: we, din
  RAM ram_1 (.addr(counter_1_q), .oe(1'b1), .clk(clock_1_out), .dout(ram_1_dout));  // open: we, din
  RAM #(.dataWidth(32), .trigger("falling")) ram_2 (
    .addr(counter_1_q), .oe(1'b1), .clk(clock_1_out), .dout(ram_2_dout));  // open: we, din
  RAM ram_3 (.addr(counter_1_q), .we(undriven), .oe(1'b1), .clk(clock_1_out), .dout(ram_3_dout));  // open: din
  RAM #(.dataWidth(64)) ram_4 (
    .addr(counter_1_q), .we(1'b1), .oe(undriven_2), .clk(clock_1_out), .din(S0));  // open: dout
  RAM ram_5 (.addr(counter_1_q), .oe(1'b1), .clk(clock_1_out), .dout(ram_5_dout));  // open: we, din
  Counter counter_1 (
    .count(1'b1), .Q(counter_1_q), .up(1'b1), .clk(clock_1_out), .clr(and_2_out));  // open: load, D, carry
  // Probe on and_2_out
  and and_1 (and_1_out, counter_1_q[0], counter_1_q[1]);
  and and_2 (and_2_out, counter_1_q[2], not_1_out);
  not not_1 (not_1_out, and_1_out);
  RAM #(.dataWidth(32), .trigger("falling")) ram_6 (
    .addr(counter_1_q), .oe(1'b1), .clk(clock_1_out), .dout(ram_6_dout));  // open: we, din
  RAM ram_7 (.addr(counter_1_q), .oe(1'b1), .clk(clock_1_out), .dout(ram_7_dout));  // open: we, din
  RAM #(.dataWidth(32), .trigger("falling")) ram_8 (
    .addr(counter_1_q), .oe(1'b1), .clk(clock_1_out), .dout(ram_8_dout));  // open: we, din
  RAM ram_9 (.addr(counter_1_q), .oe(1'b1), .clk(clock_1_out), .dout(ram_9_dout));  // open: we, din
  RAM #(.dataWidth(64)) ram_10 (
    .addr(counter_1_q), .we(1'b1), .oe(undriven_2), .clk(clock_1_out), .din(S1));  // open: dout
  RAM ram_11 (.addr(counter_1_q), .oe(1'b1), .clk(clock_1_out), .dout(ram_11_dout));  // open: we, din
  // Probe on S3
  // Probe on S1
  // Probe on S0
  // Probe on S2
  // TEST_CoreAdder test_coreadder_1: pin names not known; wires that end beside it: ram_2_dout, C1_dout, ram_8_dout, ram_6_dout, test_coreadder_1_p5, test_coreadder_1_p6, test_coreadder_1_p7, test_coreadder_1_p8, S0, S1, S2, S3
  // Probe on S2
  // Probe on S0
  // Probe on ram_6_dout
  RAM #(.dataWidth(32), .trigger("falling")) ram_12 (
    .addr(counter_1_q), .oe(1'b1), .clk(clock_1_out), .dout(test_coreadder_1_p6));  // open: we, din
  RAM ram_13 (.addr(counter_1_q), .oe(1'b1), .clk(clock_1_out), .dout(ram_13_dout));  // open: we, din
  RAM #(.dataWidth(32), .trigger("falling")) ram_14 (
    .addr(counter_1_q), .oe(1'b1), .clk(clock_1_out), .dout(test_coreadder_1_p5));  // open: we, din
  RAM ram_15 (.addr(counter_1_q), .oe(1'b1), .clk(clock_1_out));  // open: we, din, dout
  RAM #(.dataWidth(64)) ram_16 (
    .addr(counter_1_q), .we(1'b1), .oe(undriven_2), .clk(clock_1_out), .din(S2));  // open: dout
  RAM ram_17 (.addr(counter_1_q), .oe(1'b1), .clk(clock_1_out), .dout(ram_17_dout));  // open: we, din
  // Probe on S1
  // Probe on S3
  // TEST_CoreAdder test_coreadder_2: pin names not known
  RAM #(.dataWidth(32), .trigger("falling")) ram_18 (
    .addr(counter_1_q), .oe(1'b1), .clk(clock_1_out), .dout(test_coreadder_1_p8));  // open: we, din
  RAM ram_19 (.addr(counter_1_q), .oe(1'b1), .clk(clock_1_out), .dout(ram_19_dout));  // open: we, din
  RAM #(.dataWidth(32), .trigger("falling")) ram_20 (
    .addr(counter_1_q), .oe(1'b1), .clk(clock_1_out), .dout(test_coreadder_1_p7));  // open: we, din
  RAM ram_21 (.addr(counter_1_q), .oe(1'b1), .clk(clock_1_out));  // open: we, din, dout
  RAM #(.dataWidth(64)) ram_22 (
    .addr(counter_1_q), .we(1'b1), .oe(undriven_2), .clk(clock_1_out), .din(S3));  // open: dout
  RAM ram_23 (.addr(counter_1_q), .oe(1'b1), .clk(clock_1_out), .dout(ram_23_dout));  // open: we, din

  // Notes on the sheet:
  //   2, 2; 1, 1
  //   C1
  //   W1
  //   S1
  //   Resets on 4
  //   C2
  //   W2
  //   S2
  //   C3
  //   W3
  //   S3
  //   C4
  //   W4
  //   S4
endmodule
