// Logisim project matrix_multipler.circ as structural Verilog
module adder_1_2 (
  input  B,
  input  A,
  input  Carry_in,
  output Carry_out,
  output O
);

  wire adder_1_2_half_1_carry_out, adder_1_2_half_1_o, adder_1_2_half_2_carry_out;

  adder_1_2_half adder_1_2_half_1 (.B(B), .A(A), .O(adder_1_2_half_1_o), .Carry_out(adder_1_2_half_1_carry_out));
  adder_1_2_half adder_1_2_half_2 (.B(adder_1_2_half_1_o), .A(Carry_in), .O(O), .Carry_out(adder_1_2_half_2_carry_out));
  or or_1 (Carry_out, adder_1_2_half_1_carry_out, adder_1_2_half_2_carry_out);
endmodule

module adder_1_2_half (
  input  B,
  input  A,
  output O,
  output Carry_out
);

  xor xor_1 (O, B, A);
  and and_1 (Carry_out, B, A);
endmodule
