// Logisim project release.circ as structural Verilog
module SUBCIRC_MatrixMultiplier (
  input  [63:0] B0,
  input  [63:0] A0,
  input  [63:0] B1,
  input  [63:0] A1,
  input  [63:0] B2,
  input  [63:0] A2,
  input  [63:0] B3,
  input  [63:0] A3,
  output [63:0] S0,
  output [63:0] S1,
  output [63:0] S2,
  output [63:0] S3,
  output [63:0] W0,
  output [63:0] W1,
  output [63:0] W2,
  output [63:0] W3
);

  Multiplier #(.width(64)) multiplier_1 (.a(A0), .b(B0), .out(S0));  // open: cin, cout
  Multiplier #(.width(64)) multiplier_2 (.a(A0), .b(B1), .out(S1));  // open: cin, cout
  Multiplier #(.width(64)) multiplier_3 (.a(A2), .b(B0), .out(S2));  // open: cin, cout
  Multiplier #(.width(64)) multiplier_4 (.a(A2), .b(B1), .out(S3));  // open: cin, cout
  Multiplier #(.width(64)) multiplier_5 (.a(A1), .b(B2), .out(W0));  // open: cin, cout
  Multiplier #(.width(64)) multiplier_6 (.a(A1), .b(B3), .out(W1));  // open: cin, cout
  Multiplier #(.width(64)) multiplier_7 (.a(A3), .b(B2), .out(W2));  // open: cin, cout
  Multiplier #(.width(64)) multiplier_8 (.a(A3), .b(B3), .out(W3));  // open: cin, cout

  // Notes on the sheet:
  //   Acts as a Partial Multiplication Node
  //   Supports Partial Matrix Multiplication where A*B = S1, S2 where S = S1+S2
  //   A0B0
  //   A0B1
  //   A2B0
  //   A2B1
  //   A1B2
  //   A1B3
  //   A3B2
  //   A3B3
endmodule

module RAMControllerRAW (
  input  [7:0] rs,
  input  [7:0] rd,
  input  CLK,
  output [7:0] A,
  output WE,
  output OE
);

  D_Flip_Flop d_ff_1 (.clk(CLK), .D(1'b1), .Q(WE));  // open: Qn, preset, reset
  not not_1 (OE, CLK);
  Multiplexer #(.width(8)) multiplexer_1 (.in0(rs), .in1(rd), .out(A), .sel(CLK));
endmodule

module SUBCIRC_RAMBank (
  input  [63:0] D3,
  input  [63:0] D2,
  input  [63:0] D1,
  input  [63:0] D0,
  input  [15:0] Address,
  input  WE,
  input  OE,
  input  CLK,
  output [63:0] S3,
  output [63:0] S2,
  output [63:0] S1,
  output [63:0] S0
);

  RAM #(.addrWidth(16), .dataWidth(64), .\type ("nonvolatile")) C1 (
    .addr(Address), .we(WE), .oe(OE), .clk(CLK), .din(D0), .dout(S0));
  RAM #(.addrWidth(16), .dataWidth(64), .\type ("nonvolatile")) ram_1 (
    .addr(Address), .we(WE), .oe(OE), .clk(CLK), .din(D1), .dout(S1));
  RAM #(.addrWidth(16), .dataWidth(64), .\type ("nonvolatile")) ram_2 (
    .addr(Address), .we(WE), .oe(OE), .clk(CLK), .din(D2), .dout(S2));
  RAM #(.addrWidth(16), .dataWidth(64), .\type ("nonvolatile")) ram_3 (
    .addr(Address), .we(WE), .oe(OE), .clk(CLK), .din(D3), .dout(S3));
endmodule

module Assembly (
);

  wire CLOCK_GLOBAL, comparator_2_eq, comparator_3_eq, undriven_2, undriven_3, undriven_4;
  wire [7:0] counter_4_q, counter_5_q, RAM_A_ADDRESS, RAM_B_ADDRESS;
  wire [15:0] bit_extender_1_out, bit_extender_2_out, COL_ITERCOUNT, RAM_S_ADDRESS, register_5_q,
       ROW_ITERCOUNT, undriven;
  wire [63:0] register_1_q, register_2_q, register_3_q, register_4_q, S0, S1, S2, S3,
       subcirc_matrixadder_1_s0, subcirc_matrixadder_1_s1, subcirc_matrixadder_1_s2,
       subcirc_matrixadder_1_s3, subcirc_matrixadder_2_s0, subcirc_matrixadder_2_s1,
       subcirc_matrixadder_2_s2, subcirc_matrixadder_2_s3, subcirc_matrixadder_3_s0,
       subcirc_matrixadder_3_s1, subcirc_matrixadder_3_s2, subcirc_matrixadder_3_s3, subcirc_rambank_1_p4,
       subcirc_rambank_1_p5, subcirc_rambank_1_p6, subcirc_rambank_1_p7, subcirc_rambank_2_p4,
       subcirc_rambank_2_p5, subcirc_rambank_2_p6, subcirc_rambank_2_p7, subcirc_rambank_3_p4,
       subcirc_rambank_3_p5, subcirc_rambank_3_p6, subcirc_rambank_3_p7, subcirc_rambank_4_p4,
       subcirc_rambank_4_p5, subcirc_rambank_4_p6, subcirc_rambank_4_p7, test_subcirc_matrixmultiplier_1_s0,
       test_subcirc_matrixmultiplier_1_s1, test_subcirc_matrixmultiplier_1_s2,
       test_subcirc_matrixmultiplier_1_s3, test_subcirc_matrixmultiplier_1_w0,
       test_subcirc_matrixmultiplier_1_w1, test_subcirc_matrixmultiplier_1_w2,
       test_subcirc_matrixmultiplier_1_w3, test_subcirc_matrixmultiplier_2_s0,
       test_subcirc_matrixmultiplier_2_s1, test_subcirc_matrixmultiplier_2_s2,
       test_subcirc_matrixmultiplier_2_s3, test_subcirc_matrixmultiplier_2_w0,
       test_subcirc_matrixmultiplier_2_w1, test_subcirc_matrixmultiplier_2_w2,
       test_subcirc_matrixmultiplier_2_w3, undriven_5, undriven_6, undriven_7, undriven_8;

  Counter #(.max('hffff), .width(16)) counter_1 (
    .count(1'b1), .Q(RAM_S_ADDRESS), .up(1'b1), .clk(CLOCK_GLOBAL));  // open: load, D, carry, clr
  Counter counter_2 (.count(1'b1), .Q(RAM_A_ADDRESS), .up(1'b1), .clk(CLOCK_GLOBAL));  // open: load, D, carry, clr
  Comparator #(.mode("unsigned"), .width(16)) comparator_1 (.a(undriven), .b(RAM_S_ADDRESS));  // open: gt, eq, lt
  Counter counter_3 (.count(1'b1), .Q(RAM_B_ADDRESS), .up(1'b1), .clk(CLOCK_GLOBAL));  // open: load, D, carry, clr
  // Probe on S0
  // Probe on S2
  // Probe on RAM_B_ADDRESS
  // Probe on RAM_A_ADDRESS
  // Probe on S1
  // Probe on S3
  // Probe on subcirc_rambank_1_p7
  // SUBCIRC_RAMBank subcirc_rambank_1: pin names not known; wires that end beside it: RAM_A_ADDRESS, 1'b1, CLOCK_GLOBAL, subcirc_rambank_1_p4, subcirc_rambank_1_p5, subcirc_rambank_1_p6, subcirc_rambank_1_p7
  // SUBCIRC_RAMBank subcirc_rambank_2: pin names not known; wires that end beside it: RAM_A_ADDRESS, 1'b1, CLOCK_GLOBAL, subcirc_rambank_2_p4, subcirc_rambank_2_p5, subcirc_rambank_2_p6, subcirc_rambank_2_p7
  // Probe on subcirc_rambank_1_p7
  // Probe on subcirc_matrixadder_2_s3
  // Probe on subcirc_matrixadder_2_s1
  SUBCIRC_MatrixAdder subcirc_matrixadder_1 (
    .B0(test_subcirc_matrixmultiplier_1_s0), .A0(test_subcirc_matrixmultiplier_1_w0),
    .B1(test_subcirc_matrixmultiplier_1_s1), .A1(test_subcirc_matrixmultiplier_1_w1),
    .B2(test_subcirc_matrixmultiplier_1_s2), .A2(test_subcirc_matrixmultiplier_1_w2),
    .B3(test_subcirc_matrixmultiplier_1_s3), .A3(test_subcirc_matrixmultiplier_1_w3),
    .S0(subcirc_matrixadder_1_s0), .S1(subcirc_matrixadder_1_s1), .S2(subcirc_matrixadder_1_s2),
    .S3(subcirc_matrixadder_1_s3));
  SUBCIRC_MatrixAdder subcirc_matrixadder_2 (
    .S0(subcirc_matrixadder_2_s0), .S1(subcirc_matrixadder_2_s1), .S2(subcirc_matrixadder_2_s2),
    .S3(subcirc_matrixadder_2_s3));  // open: B0, A0, B1, A1, B2, A2, B3, A3
  TEST_SUBCIRC_MatrixMultiplier test_subcirc_matrixmultiplier_1 (
    .B3(subcirc_rambank_4_p4), .B2(subcirc_rambank_4_p5), .B1(subcirc_rambank_4_p6),
    .B0(subcirc_rambank_4_p7), .A3(subcirc_rambank_2_p4), .A2(subcirc_rambank_2_p5),
    .A1(subcirc_rambank_2_p6), .A0(subcirc_rambank_2_p7), .S0(test_subcirc_matrixmultiplier_1_s0),
    .W0(test_subcirc_matrixmultiplier_1_w0), .S1(test_subcirc_matrixmultiplier_1_s1),
    .W1(test_subcirc_matrixmultiplier_1_w1), .S2(test_subcirc_matrixmultiplier_1_s2),
    .W2(test_subcirc_matrixmultiplier_1_w2), .S3(test_subcirc_matrixmultiplier_1_s3),
    .W3(test_subcirc_matrixmultiplier_1_w3));
  TEST_SUBCIRC_MatrixAdder test_subcirc_matrixadder_1 (
    .B0(subcirc_matrixadder_3_s0), .B1(subcirc_matrixadder_3_s1), .B2(subcirc_matrixadder_3_s2),
    .B3(subcirc_matrixadder_3_s3), .A0(subcirc_matrixadder_1_s0), .A1(subcirc_matrixadder_1_s1),
    .A2(subcirc_matrixadder_1_s2), .A3(subcirc_matrixadder_1_s3), .S0(S0), .S1(S1), .S2(S2), .S3(S3));
  // SUBCIRC_RAMBank subcirc_rambank_3: pin names not known; wires that end beside it: RAM_B_ADDRESS, 1'b1, CLOCK_GLOBAL, subcirc_rambank_3_p4, subcirc_rambank_3_p5, subcirc_rambank_3_p6, subcirc_rambank_3_p7
  // SUBCIRC_RAMBank subcirc_rambank_4: pin names not known; wires that end beside it: RAM_B_ADDRESS, 1'b1, CLOCK_GLOBAL, subcirc_rambank_4_p4, subcirc_rambank_4_p5, subcirc_rambank_4_p6, subcirc_rambank_4_p7
  TEST_SUBCIRC_MatrixMultiplier test_subcirc_matrixmultiplier_2 (
    .B3(subcirc_rambank_3_p4), .B2(subcirc_rambank_3_p5), .B1(subcirc_rambank_3_p6),
    .B0(subcirc_rambank_3_p7), .A3(subcirc_rambank_1_p4), .A2(subcirc_rambank_1_p5),
    .A1(subcirc_rambank_1_p6), .A0(subcirc_rambank_1_p7), .S0(test_subcirc_matrixmultiplier_2_s0),
    .W0(test_subcirc_matrixmultiplier_2_w0), .S1(test_subcirc_matrixmultiplier_2_s1),
    .W1(test_subcirc_matrixmultiplier_2_w1), .S2(test_subcirc_matrixmultiplier_2_s2),
    .W2(test_subcirc_matrixmultiplier_2_w2), .S3(test_subcirc_matrixmultiplier_2_s3),
    .W3(test_subcirc_matrixmultiplier_2_w3));
  SUBCIRC_MatrixAdder subcirc_matrixadder_3 (
    .B0(test_subcirc_matrixmultiplier_2_s0), .A0(test_subcirc_matrixmultiplier_2_w0),
    .B1(test_subcirc_matrixmultiplier_2_s1), .A1(test_subcirc_matrixmultiplier_2_w1),
    .B2(test_subcirc_matrixmultiplier_2_s2), .A2(test_subcirc_matrixmultiplier_2_w2),
    .B3(test_subcirc_matrixmultiplier_2_s3), .A3(test_subcirc_matrixmultiplier_2_w3),
    .S0(subcirc_matrixadder_3_s0), .S1(subcirc_matrixadder_3_s1), .S2(subcirc_matrixadder_3_s2),
    .S3(subcirc_matrixadder_3_s3));
  // Probe on subcirc_matrixadder_2_s2
  // Probe on subcirc_matrixadder_2_s0
  Register #(.width(64)) register_1 (.D(S0), .en(undriven_2), .Q(register_1_q), .clk(undriven_3), .clr(undriven_4));
  Register #(.width(64)) register_2 (.D(S1), .en(undriven_2), .Q(register_2_q), .clk(undriven_3), .clr(undriven_4));
  Register #(.width(64)) register_3 (.D(S2), .en(undriven_2), .Q(register_3_q), .clk(undriven_3), .clr(undriven_4));
  Register #(.width(64)) register_4 (.D(S3), .en(undriven_2), .Q(register_4_q), .clk(undriven_3), .clr(undriven_4));
  Register #(.width(16)) register_5 (.D(RAM_S_ADDRESS), .en(1'b1), .Q(register_5_q), .clk(CLOCK_GLOBAL));  // open: clr
  Clock clock_1 (.out(CLOCK_GLOBAL));
  SUBCIRC_RAMBankOutput subcirc_rambankoutput_1 (
    .D3(undriven_5), .D2(undriven_6), .D1(undriven_7), .D0(undriven_8), .Address(register_5_q),
    .CLK(CLOCK_GLOBAL));  // open: WE, OE, S3, S2, S1, S0
  assign bit_extender_1_out = {{8{counter_4_q[7]}}, counter_4_q};  // Bit_Extender bit_extender_1
  Counter counter_4 (.Q(counter_4_q));  // open: load, D, count, carry, up, clk, clr
  assign bit_extender_2_out = {{8{counter_5_q[7]}}, counter_5_q};  // Bit_Extender bit_extender_2
  Counter counter_5 (.Q(counter_5_q));  // open: load, D, count, carry, up, clk, clr
  Comparator #(.width(16)) comparator_2 (
    .a(bit_extender_1_out), .b(ROW_ITERCOUNT), .eq(comparator_2_eq));  // open: gt, lt
  Comparator #(.width(16)) comparator_3 (
    .a(bit_extender_2_out), .b(COL_ITERCOUNT), .eq(comparator_3_eq));  // open: gt, lt
  ROM #(.dataWidth(16)) rom_1 (.addr({8{1'b0}}), .data(ROW_ITERCOUNT));
  ROM #(.dataWidth(16)) rom_2 (.addr({8{1'b0}}), .data(COL_ITERCOUNT));

  // Notes on the sheet:
  //   Pipelined
  //   RAM A Addresses
  //   Constant High Bit
  //   RAM B Addresses
  //   Row[0]
  //   Row[1]
  //   A
  //   BY
  //   Col[0]
  //   Col[1]
  //   B
  //   AW
  //   S0
  //   S1
  //   S2
  //   S3
  //   O
  //   Control Unit
  //   contents of rom_1 (hex, n*v repeats v):
  //   1
  //   contents of rom_2 (hex, n*v repeats v):
  //   4
  //   Configuration RAM, Holds Matrix Size (N/4)[0], Data Type (0: int64, 1: float64)[1]
endmodule

module SUBCIRC_MatrixAdder (
  input  [63:0] B0,
  input  [63:0] A0,
  input  [63:0] B1,
  input  [63:0] A1,
  input  [63:0] B2,
  input  [63:0] A2,
  input  [63:0] B3,
  input  [63:0] A3,
  output [63:0] S0,
  output [63:0] S1,
  output [63:0] S2,
  output [63:0] S3
);

  Adder #(.width(64)) adder_1 (.a(B0), .b(A0), .out(S0));  // open: cin, cout
  Adder #(.width(64)) adder_2 (.a(B1), .b(A1), .out(S1));  // open: cin, cout
  Adder #(.width(64)) adder_3 (.a(B2), .b(A2), .out(S2));  // open: cin, cout
  Adder #(.width(64)) adder_4 (.a(B3), .b(A3), .out(S3));  // open: cin, cout

  // Notes on the sheet:
  //   Acts as a Addition Node
endmodule

module TEST_MatrixMultiplier (
);

  wire [63:0] subcirc_matrixadder_1_s0, subcirc_matrixadder_1_s1, subcirc_matrixadder_1_s2,
       subcirc_matrixadder_1_s3, subcirc_matrixmultiplier_1_s0, subcirc_matrixmultiplier_1_s1,
       subcirc_matrixmultiplier_1_s2, subcirc_matrixmultiplier_1_s3, subcirc_matrixmultiplier_1_w0,
       subcirc_matrixmultiplier_1_w1, subcirc_matrixmultiplier_1_w2, subcirc_matrixmultiplier_1_w3;

  SUBCIRC_MatrixMultiplier subcirc_matrixmultiplier_1 (
    .B0(64'h5), .A0(64'h1), .B1(64'h6), .A1(64'h2), .B2(64'h7), .A2(64'h3), .B3(64'h8), .A3(64'h4),
    .S0(subcirc_matrixmultiplier_1_s0), .S1(subcirc_matrixmultiplier_1_s1),
    .S2(subcirc_matrixmultiplier_1_s2), .S3(subcirc_matrixmultiplier_1_s3),
    .W0(subcirc_matrixmultiplier_1_w0), .W1(subcirc_matrixmultiplier_1_w1),
    .W2(subcirc_matrixmultiplier_1_w2), .W3(subcirc_matrixmultiplier_1_w3));
  SUBCIRC_MatrixAdder subcirc_matrixadder_1 (
    .B0(subcirc_matrixmultiplier_1_s0), .A0(subcirc_matrixmultiplier_1_w0),
    .B1(subcirc_matrixmultiplier_1_s1), .A1(subcirc_matrixmultiplier_1_w1),
    .B2(subcirc_matrixmultiplier_1_s2), .A2(subcirc_matrixmultiplier_1_w2),
    .B3(subcirc_matrixmultiplier_1_s3), .A3(subcirc_matrixmultiplier_1_w3), .S0(subcirc_matrixadder_1_s0),
    .S1(subcirc_matrixadder_1_s1), .S2(subcirc_matrixadder_1_s2), .S3(subcirc_matrixadder_1_s3));
  // Probe on subcirc_matrixadder_1_s0
  // Probe on subcirc_matrixadder_1_s2
  // Probe on subcirc_matrixadder_1_s1
  // Probe on subcirc_matrixadder_1_s3

  // Notes on the sheet:
  //   Subcircuit works perfectly for 2x2 Matrix Multiplicaton / Verified on multiple data with overflow
endmodule

module WorkBench (
);

  wire clock_1_out, clock_2_out;
  wire [7:0] counter_1_q, counter_2_q;
  wire [63:0] adder_1_out, adder_2_out, multiplier_1_out, multiplier_2_out, ram_1_dout, ram_2_dout,
       ram_3_dout, ram_4_dout, register_1_q, register_2_q;

  Clock clock_1 (.out(clock_1_out));
  RAM #(.dataWidth(64), .\type ("nonvolatile")) ram_1 (
    .addr(counter_1_q), .oe(1'b1), .clk(clock_1_out), .dout(ram_1_dout));  // open: we, din
  Counter counter_1 (.count(1'b1), .Q(counter_1_q), .up(1'b1), .clk(clock_1_out));  // open: load, D, carry, clr
  RAM #(.dataWidth(64), .\type ("nonvolatile")) ram_2 (
    .addr(counter_1_q), .oe(1'b1), .clk(clock_1_out), .dout(ram_2_dout));  // open: we, din
  Multiplier #(.width(64)) multiplier_1 (.a(ram_1_dout), .b(ram_2_dout), .out(multiplier_1_out));  // open: cin, cout
  Register #(.width(64)) register_1 (
    .D(multiplier_1_out), .en(1'b1), .Q(register_1_q), .clk(clock_1_out));  // open: clr
  Adder #(.width(64)) adder_1 (.a(register_1_q), .b(multiplier_1_out), .out(adder_1_out));  // open: cin, cout
  // Probe on adder_1_out
  Clock clock_2 (.out(clock_2_out));
  RAM #(.dataWidth(64), .\type ("nonvolatile")) ram_3 (
    .addr(counter_2_q), .oe(1'b1), .clk(clock_2_out), .dout(ram_3_dout));  // open: we, din
  Counter counter_2 (.count(1'b1), .Q(counter_2_q), .up(1'b1), .clk(clock_2_out));  // open: load, D, carry, clr
  RAM #(.dataWidth(64), .\type ("nonvolatile")) ram_4 (
    .addr(counter_2_q), .oe(1'b1), .clk(clock_2_out), .dout(ram_4_dout));  // open: we, din
  Multiplier #(.width(64)) multiplier_2 (.a(ram_3_dout), .b(ram_4_dout), .out(multiplier_2_out));  // open: cin, cout
  Register #(.width(64)) register_2 (
    .D(multiplier_2_out), .en(1'b1), .Q(register_2_q), .clk(clock_2_out));  // open: clr
  Adder #(.width(64)) adder_2 (.a(register_2_q), .b(multiplier_2_out), .out(adder_2_out));  // open: cin, cout
  // Probe on adder_2_out

  // Notes on the sheet:
  //   AB;CD
  //   A
  //   WX;YZ
  //   B
  //   AB;CD
  //   A
  //   WX;YZ
  //   B
endmodule

module DataRAMController (
  input  [15:0] SHIFT,
  input  CLK,
  output [15:0] A,
  output OE
);

  wire [15:0] adder_1_out, counter_1_q, multiplexer_1_out, multiplier_1_out;

  Counter #(.max('hffff), .trigger("falling"), .width(16)) counter_1 (
    .count(1'b1), .Q(counter_1_q), .up(1'b1), .clk(CLK));  // open: load, D, carry, clr
  Multiplier #(.width(16)) multiplier_1 (.a(counter_1_q), .b(16'h2), .out(multiplier_1_out));  // open: cin, cout
  Adder #(.width(16)) adder_1 (.a(multiplier_1_out), .b(16'h1), .out(adder_1_out));  // open: cin, cout
  Multiplexer #(.width(16)) multiplexer_1 (
    .in0(multiplier_1_out), .in1(adder_1_out), .out(multiplexer_1_out), .sel(CLK));
  Adder #(.width(16)) adder_2 (.a(SHIFT), .b(multiplexer_1_out), .out(A));  // open: cin, cout

  assign OE = 1'b1;

  // Notes on the sheet:
  //   Credits for doing with 1 counter goes to Ali
endmodule

module SUBCIRC_RAMBankOutput (
  input  [63:0] D3,
  input  [63:0] D2,
  input  [63:0] D1,
  input  [63:0] D0,
  input  [15:0] Address,
  input  WE,
  input  OE,
  input  CLK,
  output [63:0] S3,
  output [63:0] S2,
  output [63:0] S1,
  output [63:0] S0
);

  RAM #(.addrWidth(16), .dataWidth(64)) C1 (.addr(Address), .we(WE), .oe(OE), .clk(CLK), .din(D0), .dout(S0));
  RAM #(.addrWidth(16), .dataWidth(64)) ram_1 (.addr(Address), .we(WE), .oe(OE), .clk(CLK), .din(D1), .dout(S1));
  RAM #(.addrWidth(16), .dataWidth(64)) ram_2 (.addr(Address), .we(WE), .oe(OE), .clk(CLK), .din(D2), .dout(S2));
  RAM #(.addrWidth(16), .dataWidth(64)) ram_3 (.addr(Address), .we(WE), .oe(OE), .clk(CLK), .din(D3), .dout(S3));
endmodule

module TEST_Assebmly_ByDoc (
);

  wire CLOCK_GLOBAL;
  wire [7:0] RAM_A_ADDRESS, RAM_B_ADDRESS;
  wire [15:0] ITERCOUNT, RAM_S_ADDRESS, register_1_q, undriven;
  wire [63:0] subcirc_matrixadder_1_s0, subcirc_matrixadder_1_s1, subcirc_matrixadder_1_s2,
       subcirc_matrixadder_1_s3, subcirc_rambank_1_p4, subcirc_rambank_1_p5, subcirc_rambank_1_p6,
       subcirc_rambank_1_p7, subcirc_rambank_2_p4, subcirc_rambank_2_p5, subcirc_rambank_2_p6,
       subcirc_rambank_2_p7, subcirc_rambank_3_p4, subcirc_rambank_3_p5, subcirc_rambank_3_p6,
       subcirc_rambank_3_p7, subcirc_rambank_4_p4, subcirc_rambank_4_p5, subcirc_rambank_4_p6,
       subcirc_rambank_4_p7, test_core_1_s0, test_core_1_s1, test_core_1_s2, test_core_1_s3, undriven_2,
       undriven_3, undriven_4, undriven_5;

  Counter #(.max('hffff), .width(16)) counter_1 (
    .count(1'b1), .Q(RAM_S_ADDRESS), .up(1'b1), .clk(CLOCK_GLOBAL));  // open: load, D, carry, clr
  Counter counter_2 (.count(1'b1), .Q(RAM_A_ADDRESS), .up(1'b1), .clk(CLOCK_GLOBAL));  // open: load, D, carry, clr
  Comparator #(.mode("unsigned"), .width(16)) comparator_1 (.a(undriven), .b(RAM_S_ADDRESS));  // open: gt, eq, lt
  Counter counter_3 (.count(1'b1), .Q(RAM_B_ADDRESS), .up(1'b1), .clk(CLOCK_GLOBAL));  // open: load, D, carry, clr
  // Probe on RAM_B_ADDRESS
  // Probe on RAM_A_ADDRESS
  // SUBCIRC_RAMBank subcirc_rambank_1: pin names not known; wires that end beside it: RAM_A_ADDRESS, 1'b1, CLOCK_GLOBAL, subcirc_rambank_1_p4, subcirc_rambank_1_p5, subcirc_rambank_1_p6, subcirc_rambank_1_p7
  // SUBCIRC_RAMBank subcirc_rambank_2: pin names not known; wires that end beside it: RAM_A_ADDRESS, 1'b1, CLOCK_GLOBAL, subcirc_rambank_2_p4, subcirc_rambank_2_p5, subcirc_rambank_2_p6, subcirc_rambank_2_p7
  // Probe on subcirc_matrixadder_1_s3
  // Probe on subcirc_matrixadder_1_s1
  // Probe on test_core_1_s0
  // Probe on test_core_1_s2
  SUBCIRC_MatrixAdder subcirc_matrixadder_1 (
    .S0(subcirc_matrixadder_1_s0), .S1(subcirc_matrixadder_1_s1), .S2(subcirc_matrixadder_1_s2),
    .S3(subcirc_matrixadder_1_s3));  // open: B0, A0, B1, A1, B2, A2, B3, A3
  // SUBCIRC_RAMBank subcirc_rambank_3: pin names not known; wires that end beside it: RAM_B_ADDRESS, 1'b1, CLOCK_GLOBAL, subcirc_rambank_3_p4, subcirc_rambank_3_p5, subcirc_rambank_3_p6, subcirc_rambank_3_p7
  // SUBCIRC_RAMBank subcirc_rambank_4: pin names not known; wires that end beside it: RAM_B_ADDRESS, 1'b1, CLOCK_GLOBAL, subcirc_rambank_4_p4, subcirc_rambank_4_p5, subcirc_rambank_4_p6, subcirc_rambank_4_p7
  TEST_CORE test_core_1 (
    .B03(subcirc_rambank_3_p4), .B02(subcirc_rambank_3_p5), .B01(subcirc_rambank_3_p6),
    .B00(subcirc_rambank_3_p7), .B13(subcirc_rambank_4_p4), .B12(subcirc_rambank_4_p5),
    .B11(subcirc_rambank_4_p6), .B10(subcirc_rambank_4_p7), .A13(subcirc_rambank_2_p4),
    .A12(subcirc_rambank_2_p5), .A11(subcirc_rambank_2_p6), .A10(subcirc_rambank_2_p7),
    .A03(subcirc_rambank_1_p4), .A02(subcirc_rambank_1_p5), .A01(subcirc_rambank_1_p6),
    .A00(subcirc_rambank_1_p7), .S3(test_core_1_s3), .S2(test_core_1_s2), .S1(test_core_1_s1),
    .S0(test_core_1_s0));
  // Probe on subcirc_matrixadder_1_s2
  // Probe on subcirc_matrixadder_1_s0
  // Probe on test_core_1_s1
  // Probe on test_core_1_s3
  Register #(.width(16)) register_1 (.D(RAM_S_ADDRESS), .en(1'b1), .Q(register_1_q), .clk(CLOCK_GLOBAL));  // open: clr
  Clock clock_1 (.out(CLOCK_GLOBAL));
  SUBCIRC_RAMBankOutput subcirc_rambankoutput_1 (
    .D3(undriven_2), .D2(undriven_3), .D1(undriven_4), .D0(undriven_5), .Address(register_1_q),
    .CLK(CLOCK_GLOBAL));  // open: WE, OE, S3, S2, S1, S0
  ROM #(.dataWidth(16)) rom_1 (.addr({8{1'b0}}), .data(ITERCOUNT));

  // Notes on the sheet:
  //   Pipelined
  //   RAM A Addresses
  //   Constant High Bit
  //   RAM B Addresses
  //   Row[0]
  //   Row[1]
  //   A
  //   Col[0]
  //   Col[1]
  //   B
  //   O
  //   Configuration RAM, Holds Matrix Size (N/4)[0], Data Type (0: int64, 1: float64)[1]
endmodule

module TEST_SUBCIRC_MatrixMultiplier (
  input  [63:0] B3,
  input  [63:0] B2,
  input  [63:0] B1,
  input  [63:0] B0,
  input  [63:0] A3,
  input  [63:0] A2,
  input  [63:0] A1,
  input  [63:0] A0,
  output [63:0] S0,
  output [63:0] W0,
  output [63:0] S1,
  output [63:0] W1,
  output [63:0] S2,
  output [63:0] W2,
  output [63:0] S3,
  output [63:0] W3
);

  Multiplier #(.width(64)) multiplier_1 (.a(A0), .b(B0), .out(S0));  // open: cin, cout
  Multiplier #(.width(64)) multiplier_2 (.a(A0), .b(B1), .out(S1));  // open: cin, cout
  Multiplier #(.width(64)) multiplier_3 (.a(A2), .b(B0), .out(S2));  // open: cin, cout
  Multiplier #(.width(64)) multiplier_4 (.a(A2), .b(B1), .out(S3));  // open: cin, cout
  Multiplier #(.width(64)) multiplier_5 (.a(A1), .b(B2), .out(W0));  // open: cin, cout
  Multiplier #(.width(64)) multiplier_6 (.a(A1), .b(B3), .out(W1));  // open: cin, cout
  Multiplier #(.width(64)) multiplier_7 (.a(A3), .b(B2), .out(W2));  // open: cin, cout
  Multiplier #(.width(64)) multiplier_8 (.a(A3), .b(B3), .out(W3));  // open: cin, cout

  // Notes on the sheet:
  //   Acts as a Partial Multiplication Node
  //   Supports Partial Matrix Multiplication where A*B = S1, S2 where S = S1+S2
  //   A0B0
  //   A0B1
  //   A2B0
  //   A2B1
  //   A1B2
  //   A1B3
  //   A3B2
  //   A3B3
endmodule

module TEST_CORE (
  input  [63:0] B03,
  input  [63:0] B02,
  input  [63:0] B01,
  input  [63:0] B00,
  input  [63:0] B13,
  input  [63:0] B12,
  input  [63:0] B11,
  input  [63:0] B10,
  input  [63:0] A13,
  input  [63:0] A12,
  input  [63:0] A11,
  input  [63:0] A10,
  input  [63:0] A03,
  input  [63:0] A02,
  input  [63:0] A01,
  input  [63:0] A00,
  output [63:0] S3,
  output [63:0] S2,
  output [63:0] S1,
  output [63:0] S0
);

  wire [63:0] subcirc_matrixadder_1_s0, subcirc_matrixadder_1_s1, subcirc_matrixadder_1_s2,
       subcirc_matrixadder_1_s3, subcirc_matrixadder_2_s0, subcirc_matrixadder_2_s1,
       subcirc_matrixadder_2_s2, subcirc_matrixadder_2_s3, test_subcirc_matrixmultiplier_1_s0,
       test_subcirc_matrixmultiplier_1_s1, test_subcirc_matrixmultiplier_1_s2,
       test_subcirc_matrixmultiplier_1_s3, test_subcirc_matrixmultiplier_1_w0,
       test_subcirc_matrixmultiplier_1_w1, test_subcirc_matrixmultiplier_1_w2,
       test_subcirc_matrixmultiplier_1_w3, test_subcirc_matrixmultiplier_2_s0,
       test_subcirc_matrixmultiplier_2_s1, test_subcirc_matrixmultiplier_2_s2,
       test_subcirc_matrixmultiplier_2_s3, test_subcirc_matrixmultiplier_2_w0,
       test_subcirc_matrixmultiplier_2_w1, test_subcirc_matrixmultiplier_2_w2,
       test_subcirc_matrixmultiplier_2_w3;

  TEST_SUBCIRC_MatrixMultiplier test_subcirc_matrixmultiplier_1 (
    .B3(B13), .B2(B12), .B1(B11), .B0(B10), .A3(A13), .A2(A12), .A1(A11), .A0(A10),
    .S0(test_subcirc_matrixmultiplier_1_s0), .W0(test_subcirc_matrixmultiplier_1_w0),
    .S1(test_subcirc_matrixmultiplier_1_s1), .W1(test_subcirc_matrixmultiplier_1_w1),
    .S2(test_subcirc_matrixmultiplier_1_s2), .W2(test_subcirc_matrixmultiplier_1_w2),
    .S3(test_subcirc_matrixmultiplier_1_s3), .W3(test_subcirc_matrixmultiplier_1_w3));
  SUBCIRC_MatrixAdder subcirc_matrixadder_1 (
    .B0(test_subcirc_matrixmultiplier_1_s0), .A0(test_subcirc_matrixmultiplier_1_w0),
    .B1(test_subcirc_matrixmultiplier_1_s1), .A1(test_subcirc_matrixmultiplier_1_w1),
    .B2(test_subcirc_matrixmultiplier_1_s2), .A2(test_subcirc_matrixmultiplier_1_w2),
    .B3(test_subcirc_matrixmultiplier_1_s3), .A3(test_subcirc_matrixmultiplier_1_w3),
    .S0(subcirc_matrixadder_1_s0), .S1(subcirc_matrixadder_1_s1), .S2(subcirc_matrixadder_1_s2),
    .S3(subcirc_matrixadder_1_s3));
  TEST_SUBCIRC_MatrixMultiplier test_subcirc_matrixmultiplier_2 (
    .B3(B03), .B2(B02), .B1(B01), .B0(B00), .A3(A03), .A2(A02), .A1(A01), .A0(A00),
    .S0(test_subcirc_matrixmultiplier_2_s0), .W0(test_subcirc_matrixmultiplier_2_w0),
    .S1(test_subcirc_matrixmultiplier_2_s1), .W1(test_subcirc_matrixmultiplier_2_w1),
    .S2(test_subcirc_matrixmultiplier_2_s2), .W2(test_subcirc_matrixmultiplier_2_w2),
    .S3(test_subcirc_matrixmultiplier_2_s3), .W3(test_subcirc_matrixmultiplier_2_w3));
  SUBCIRC_MatrixAdder subcirc_matrixadder_2 (
    .B0(test_subcirc_matrixmultiplier_2_s0), .A0(test_subcirc_matrixmultiplier_2_w0),
    .B1(test_subcirc_matrixmultiplier_2_s1), .A1(test_subcirc_matrixmultiplier_2_w1),
    .B2(test_subcirc_matrixmultiplier_2_s2), .A2(test_subcirc_matrixmultiplier_2_w2),
    .B3(test_subcirc_matrixmultiplier_2_s3), .A3(test_subcirc_matrixmultiplier_2_w3),
    .S0(subcirc_matrixadder_2_s0), .S1(subcirc_matrixadder_2_s1), .S2(subcirc_matrixadder_2_s2),
    .S3(subcirc_matrixadder_2_s3));
  SUBCIRC_MatrixAdder subcirc_matrixadder_3 (
    .B0(subcirc_matrixadder_2_s0), .A0(subcirc_matrixadder_1_s0), .B1(subcirc_matrixadder_2_s1),
    .A1(subcirc_matrixadder_1_s1), .B2(subcirc_matrixadder_2_s2), .A2(subcirc_matrixadder_1_s2),
    .B3(subcirc_matrixadder_2_s3), .A3(subcirc_matrixadder_1_s3), .S0(S3), .S1(S2), .S2(S1), .S3(S0));

  // Notes on the sheet:
  //   by
  //   aw
endmodule

module TEST_SUBCIRC_MatrixAdder (
  input  [63:0] B0,
  input  [63:0] B1,
  input  [63:0] B2,
  input  [63:0] B3,
  input  [63:0] A0,
  input  [63:0] A1,
  input  [63:0] A2,
  input  [63:0] A3,
  output [63:0] S0,
  output [63:0] S1,
  output [63:0] S2,
  output [63:0] S3
);

  Adder #(.width(64)) adder_1 (.a(B0), .b(A0), .out(S0));  // open: cin, cout
  Adder #(.width(64)) adder_2 (.a(B1), .b(A1), .out(S1));  // open: cin, cout
  Adder #(.width(64)) adder_3 (.a(B2), .b(A2), .out(S2));  // open: cin, cout
  Adder #(.width(64)) adder_4 (.a(B3), .b(A3), .out(S3));  // open: cin, cout

  // Notes on the sheet:
  //   Acts as a Addition Node
endmodule

module Quiz (
);

  wire CLOCK_GLOBAL, comparator_1_eq, comparator_2_eq;
  wire [7:0] counter_4_q, counter_5_q, RAM_A_ADDRESS, RAM_B_ADDRESS;
  wire [15:0] bit_extender_1_out, bit_extender_2_out, COL_ITERCOUNT, RAM_S_ADDRESS, register_1_q,
       ROW_ITERCOUNT;
  wire [63:0] S0, S1, S2, S3, subcirc_matrixadder_1_s0, subcirc_matrixadder_1_s1, subcirc_matrixadder_1_s2,
       subcirc_matrixadder_1_s3, subcirc_matrixadder_2_s0, subcirc_matrixadder_2_s1,
       subcirc_matrixadder_2_s2, subcirc_matrixadder_2_s3, subcirc_matrixadder_3_s0,
       subcirc_matrixadder_3_s1, subcirc_matrixadder_3_s2, subcirc_matrixadder_3_s3,
       subcirc_matrixadder_4_s0, subcirc_matrixadder_4_s1, subcirc_matrixadder_4_s2,
       subcirc_matrixadder_4_s3, subcirc_matrixadder_5_s0, subcirc_matrixadder_5_s1,
       subcirc_matrixadder_5_s2, subcirc_matrixadder_5_s3, subcirc_rambank_1_p4, subcirc_rambank_1_p5,
       subcirc_rambank_1_p6, subcirc_rambank_1_p7, subcirc_rambank_2_p4, subcirc_rambank_2_p5,
       subcirc_rambank_2_p6, subcirc_rambank_2_p7, subcirc_rambank_3_p4, subcirc_rambank_3_p5,
       subcirc_rambank_3_p6, subcirc_rambank_3_p7, subcirc_rambank_4_p4, subcirc_rambank_4_p5,
       subcirc_rambank_4_p6, subcirc_rambank_4_p7, subcirc_rambank_5_p4, subcirc_rambank_5_p5,
       subcirc_rambank_5_p6, subcirc_rambank_5_p7, subcirc_rambank_6_p4, subcirc_rambank_6_p5,
       subcirc_rambank_6_p6, subcirc_rambank_6_p7, subcirc_rambank_7_p4, subcirc_rambank_7_p5,
       subcirc_rambank_7_p6, subcirc_rambank_7_p7, subcirc_rambank_8_p4, subcirc_rambank_8_p5,
       subcirc_rambank_8_p6, subcirc_rambank_8_p7, subcirc_rambankoutput_1_s0, subcirc_rambankoutput_1_s1,
       subcirc_rambankoutput_1_s2, subcirc_rambankoutput_1_s3, test_subcirc_matrixadder_1_s0,
       test_subcirc_matrixadder_1_s1, test_subcirc_matrixadder_1_s2, test_subcirc_matrixadder_1_s3,
       test_subcirc_matrixadder_2_s0, test_subcirc_matrixadder_2_s1, test_subcirc_matrixadder_2_s2,
       test_subcirc_matrixadder_2_s3, test_subcirc_matrixmultiplier_1_s0, test_subcirc_matrixmultiplier_1_s1,
       test_subcirc_matrixmultiplier_1_s2, test_subcirc_matrixmultiplier_1_s3,
       test_subcirc_matrixmultiplier_1_w0, test_subcirc_matrixmultiplier_1_w1,
       test_subcirc_matrixmultiplier_1_w2, test_subcirc_matrixmultiplier_1_w3,
       test_subcirc_matrixmultiplier_2_s0, test_subcirc_matrixmultiplier_2_s1,
       test_subcirc_matrixmultiplier_2_s2, test_subcirc_matrixmultiplier_2_s3,
       test_subcirc_matrixmultiplier_2_w0, test_subcirc_matrixmultiplier_2_w1,
       test_subcirc_matrixmultiplier_2_w2, test_subcirc_matrixmultiplier_2_w3,
       test_subcirc_matrixmultiplier_3_s0, test_subcirc_matrixmultiplier_3_s1,
       test_subcirc_matrixmultiplier_3_s2, test_subcirc_matrixmultiplier_3_s3,
       test_subcirc_matrixmultiplier_3_w0, test_subcirc_matrixmultiplier_3_w1,
       test_subcirc_matrixmultiplier_3_w2, test_subcirc_matrixmultiplier_3_w3,
       test_subcirc_matrixmultiplier_4_s0, test_subcirc_matrixmultiplier_4_s1,
       test_subcirc_matrixmultiplier_4_s2, test_subcirc_matrixmultiplier_4_s3,
       test_subcirc_matrixmultiplier_4_w0, test_subcirc_matrixmultiplier_4_w1,
       test_subcirc_matrixmultiplier_4_w2, test_subcirc_matrixmultiplier_4_w3;

  Counter #(.max('hffff), .width(16)) counter_1 (
    .count(1'b1), .Q(RAM_S_ADDRESS), .up(1'b1), .clk(CLOCK_GLOBAL));  // open: load, D, carry, clr
  Counter counter_2 (.count(1'b1), .Q(RAM_A_ADDRESS), .up(1'b1), .clk(CLOCK_GLOBAL));  // open: load, D, carry, clr
  Counter counter_3 (.count(1'b1), .Q(RAM_B_ADDRESS), .up(1'b1), .clk(CLOCK_GLOBAL));  // open: load, D, carry, clr
  // Probe on RAM_B_ADDRESS
  // Probe on RAM_A_ADDRESS
  // SUBCIRC_RAMBank subcirc_rambank_1: pin names not known; wires that end beside it: RAM_A_ADDRESS, 1'b1, CLOCK_GLOBAL, subcirc_rambank_1_p4, subcirc_rambank_1_p5, subcirc_rambank_1_p6, subcirc_rambank_1_p7
  // SUBCIRC_RAMBank subcirc_rambank_2: pin names not known; wires that end beside it: RAM_A_ADDRESS, 1'b1, CLOCK_GLOBAL, subcirc_rambank_2_p4, subcirc_rambank_2_p5, subcirc_rambank_2_p6, subcirc_rambank_2_p7
  // SUBCIRC_RAMBank subcirc_rambank_3: pin names not known; wires that end beside it: RAM_A_ADDRESS, 1'b1, CLOCK_GLOBAL, subcirc_rambank_3_p4, subcirc_rambank_3_p5, subcirc_rambank_3_p6, subcirc_rambank_3_p7
  // SUBCIRC_RAMBank subcirc_rambank_4: pin names not known; wires that end beside it: RAM_A_ADDRESS, 1'b1, CLOCK_GLOBAL, subcirc_rambank_4_p4, subcirc_rambank_4_p5, subcirc_rambank_4_p6, subcirc_rambank_4_p7
  // Probe on subcirc_matrixadder_1_s3
  // Probe on subcirc_matrixadder_1_s1
  SUBCIRC_MatrixAdder subcirc_matrixadder_1 (
    .S0(subcirc_matrixadder_1_s0), .S1(subcirc_matrixadder_1_s1), .S2(subcirc_matrixadder_1_s2),
    .S3(subcirc_matrixadder_1_s3));  // open: B0, A0, B1, A1, B2, A2, B3, A3
  // SUBCIRC_RAMBank subcirc_rambank_5: pin names not known; wires that end beside it: RAM_B_ADDRESS, 1'b1, CLOCK_GLOBAL, subcirc_rambank_5_p4, subcirc_rambank_5_p5, subcirc_rambank_5_p6, subcirc_rambank_5_p7
  // SUBCIRC_RAMBank subcirc_rambank_6: pin names not known; wires that end beside it: RAM_B_ADDRESS, 1'b1, CLOCK_GLOBAL, subcirc_rambank_6_p4, subcirc_rambank_6_p5, subcirc_rambank_6_p6, subcirc_rambank_6_p7
  // SUBCIRC_RAMBank subcirc_rambank_7: pin names not known; wires that end beside it: RAM_B_ADDRESS, 1'b1, CLOCK_GLOBAL, subcirc_rambank_7_p4, subcirc_rambank_7_p5, subcirc_rambank_7_p6, subcirc_rambank_7_p7
  // SUBCIRC_RAMBank subcirc_rambank_8: pin names not known; wires that end beside it: RAM_B_ADDRESS, 1'b1, CLOCK_GLOBAL, subcirc_rambank_8_p4, subcirc_rambank_8_p5, subcirc_rambank_8_p6, subcirc_rambank_8_p7
  // Probe on subcirc_matrixadder_1_s2
  // Probe on subcirc_matrixadder_1_s0
  Register #(.width(16)) register_1 (.D(RAM_S_ADDRESS), .en(1'b1), .Q(register_1_q), .clk(CLOCK_GLOBAL));  // open: clr
  TEST_SUBCIRC_MatrixMultiplier test_subcirc_matrixmultiplier_1 (
    .B3(subcirc_rambank_5_p4), .B2(subcirc_rambank_5_p5), .B1(subcirc_rambank_5_p6),
    .B0(subcirc_rambank_5_p7), .A3(subcirc_rambank_1_p4), .A2(subcirc_rambank_1_p5),
    .A1(subcirc_rambank_1_p6), .A0(subcirc_rambank_1_p7), .S0(test_subcirc_matrixmultiplier_1_s0),
    .W0(test_subcirc_matrixmultiplier_1_w0), .S1(test_subcirc_matrixmultiplier_1_s1),
    .W1(test_subcirc_matrixmultiplier_1_w1), .S2(test_subcirc_matrixmultiplier_1_s2),
    .W2(test_subcirc_matrixmultiplier_1_w2), .S3(test_subcirc_matrixmultiplier_1_s3),
    .W3(test_subcirc_matrixmultiplier_1_w3));
  SUBCIRC_MatrixAdder subcirc_matrixadder_2 (
    .B0(test_subcirc_matrixmultiplier_1_s0), .A0(test_subcirc_matrixmultiplier_1_w0),
    .B1(test_subcirc_matrixmultiplier_1_s1), .A1(test_subcirc_matrixmultiplier_1_w1),
    .B2(test_subcirc_matrixmultiplier_1_s2), .A2(test_subcirc_matrixmultiplier_1_w2),
    .B3(test_subcirc_matrixmultiplier_1_s3), .A3(test_subcirc_matrixmultiplier_1_w3),
    .S0(subcirc_matrixadder_2_s0), .S1(subcirc_matrixadder_2_s1), .S2(subcirc_matrixadder_2_s2),
    .S3(subcirc_matrixadder_2_s3));
  TEST_SUBCIRC_MatrixMultiplier test_subcirc_matrixmultiplier_2 (
    .B3(subcirc_rambank_6_p4), .B2(subcirc_rambank_6_p5), .B1(subcirc_rambank_6_p6),
    .B0(subcirc_rambank_6_p7), .A3(subcirc_rambank_2_p4), .A2(subcirc_rambank_2_p5),
    .A1(subcirc_rambank_2_p6), .A0(subcirc_rambank_2_p7), .S0(test_subcirc_matrixmultiplier_2_s0),
    .W0(test_subcirc_matrixmultiplier_2_w0), .S1(test_subcirc_matrixmultiplier_2_s1),
    .W1(test_subcirc_matrixmultiplier_2_w1), .S2(test_subcirc_matrixmultiplier_2_s2),
    .W2(test_subcirc_matrixmultiplier_2_w2), .S3(test_subcirc_matrixmultiplier_2_s3),
    .W3(test_subcirc_matrixmultiplier_2_w3));
  SUBCIRC_MatrixAdder subcirc_matrixadder_3 (
    .B0(test_subcirc_matrixmultiplier_2_s0), .A0(test_subcirc_matrixmultiplier_2_w0),
    .B1(test_subcirc_matrixmultiplier_2_s1), .A1(test_subcirc_matrixmultiplier_2_w1),
    .B2(test_subcirc_matrixmultiplier_2_s2), .A2(test_subcirc_matrixmultiplier_2_w2),
    .B3(test_subcirc_matrixmultiplier_2_s3), .A3(test_subcirc_matrixmultiplier_2_w3),
    .S0(subcirc_matrixadder_3_s0), .S1(subcirc_matrixadder_3_s1), .S2(subcirc_matrixadder_3_s2),
    .S3(subcirc_matrixadder_3_s3));
  TEST_SUBCIRC_MatrixMultiplier test_subcirc_matrixmultiplier_3 (
    .B3(subcirc_rambank_7_p4), .B2(subcirc_rambank_7_p5), .B1(subcirc_rambank_7_p6),
    .B0(subcirc_rambank_7_p7), .A3(subcirc_rambank_3_p4), .A2(subcirc_rambank_3_p5),
    .A1(subcirc_rambank_3_p6), .A0(subcirc_rambank_3_p7), .S0(test_subcirc_matrixmultiplier_3_s0),
    .W0(test_subcirc_matrixmultiplier_3_w0), .S1(test_subcirc_matrixmultiplier_3_s1),
    .W1(test_subcirc_matrixmultiplier_3_w1), .S2(test_subcirc_matrixmultiplier_3_s2),
    .W2(test_subcirc_matrixmultiplier_3_w2), .S3(test_subcirc_matrixmultiplier_3_s3),
    .W3(test_subcirc_matrixmultiplier_3_w3));
  SUBCIRC_MatrixAdder subcirc_matrixadder_4 (
    .B0(test_subcirc_matrixmultiplier_3_s0), .A0(test_subcirc_matrixmultiplier_3_w0),
    .B1(test_subcirc_matrixmultiplier_3_s1), .A1(test_subcirc_matrixmultiplier_3_w1),
    .B2(test_subcirc_matrixmultiplier_3_s2), .A2(test_subcirc_matrixmultiplier_3_w2),
    .B3(test_subcirc_matrixmultiplier_3_s3), .A3(test_subcirc_matrixmultiplier_3_w3),
    .S0(subcirc_matrixadder_4_s0), .S1(subcirc_matrixadder_4_s1), .S2(subcirc_matrixadder_4_s2),
    .S3(subcirc_matrixadder_4_s3));
  TEST_SUBCIRC_MatrixMultiplier test_subcirc_matrixmultiplier_4 (
    .B3(subcirc_rambank_8_p4), .B2(subcirc_rambank_8_p5), .B1(subcirc_rambank_8_p6),
    .B0(subcirc_rambank_8_p7), .A3(subcirc_rambank_4_p4), .A2(subcirc_rambank_4_p5),
    .A1(subcirc_rambank_4_p6), .A0(subcirc_rambank_4_p7), .S0(test_subcirc_matrixmultiplier_4_s0),
    .W0(test_subcirc_matrixmultiplier_4_w0), .S1(test_subcirc_matrixmultiplier_4_s1),
    .W1(test_subcirc_matrixmultiplier_4_w1), .S2(test_subcirc_matrixmultiplier_4_s2),
    .W2(test_subcirc_matrixmultiplier_4_w2), .S3(test_subcirc_matrixmultiplier_4_s3),
    .W3(test_subcirc_matrixmultiplier_4_w3));
  SUBCIRC_MatrixAdder subcirc_matrixadder_5 (
    .B0(test_subcirc_matrixmultiplier_4_s0), .A0(test_subcirc_matrixmultiplier_4_w0),
    .B1(test_subcirc_matrixmultiplier_4_s1), .A1(test_subcirc_matrixmultiplier_4_w1),
    .B2(test_subcirc_matrixmultiplier_4_s2), .A2(test_subcirc_matrixmultiplier_4_w2),
    .B3(test_subcirc_matrixmultiplier_4_s3), .A3(test_subcirc_matrixmultiplier_4_w3),
    .S0(subcirc_matrixadder_5_s0), .S1(subcirc_matrixadder_5_s1), .S2(subcirc_matrixadder_5_s2),
    .S3(subcirc_matrixadder_5_s3));
  Clock clock_1 (.out(CLOCK_GLOBAL));
  TEST_SUBCIRC_MatrixAdder test_subcirc_matrixadder_1 (
    .B0(subcirc_matrixadder_2_s0), .B1(subcirc_matrixadder_2_s1), .B2(subcirc_matrixadder_2_s2),
    .B3(subcirc_matrixadder_2_s3), .A0(subcirc_matrixadder_3_s0), .A1(subcirc_matrixadder_3_s1),
    .A2(subcirc_matrixadder_3_s2), .A3(subcirc_matrixadder_3_s3), .S0(test_subcirc_matrixadder_1_s0),
    .S1(test_subcirc_matrixadder_1_s1), .S2(test_subcirc_matrixadder_1_s2), .S3(test_subcirc_matrixadder_1_s3));
  TEST_SUBCIRC_MatrixAdder test_subcirc_matrixadder_2 (
    .B0(subcirc_matrixadder_4_s0), .B1(subcirc_matrixadder_4_s1), .B2(subcirc_matrixadder_4_s2),
    .B3(subcirc_matrixadder_4_s3), .A0(subcirc_matrixadder_5_s0), .A1(subcirc_matrixadder_5_s1),
    .A2(subcirc_matrixadder_5_s2), .A3(subcirc_matrixadder_5_s3), .S0(test_subcirc_matrixadder_2_s0),
    .S1(test_subcirc_matrixadder_2_s1), .S2(test_subcirc_matrixadder_2_s2), .S3(test_subcirc_matrixadder_2_s3));
  // Probe on subcirc_matrixadder_2_s0
  TEST_SUBCIRC_MatrixAdder test_subcirc_matrixadder_3 (
    .B0(test_subcirc_matrixadder_1_s0), .B1(test_subcirc_matrixadder_1_s1),
    .B2(test_subcirc_matrixadder_1_s2), .B3(test_subcirc_matrixadder_1_s3),
    .A0(test_subcirc_matrixadder_2_s0), .A1(test_subcirc_matrixadder_2_s1),
    .A2(test_subcirc_matrixadder_2_s2), .A3(test_subcirc_matrixadder_2_s3), .S0(S0), .S1(S1), .S2(S2), .S3(S3));
  SUBCIRC_RAMBankOutput subcirc_rambankoutput_1 (
    .D3(S3), .D2(S2), .D1(S1), .D0(S0), .Address(register_1_q), .WE(1'b1), .CLK(CLOCK_GLOBAL),
    .S3(subcirc_rambankoutput_1_s3), .S2(subcirc_rambankoutput_1_s2), .S1(subcirc_rambankoutput_1_s1),
    .S0(subcirc_rambankoutput_1_s0));  // open: OE
  // Probe on S0
  // Probe on S2
  // Probe on S1
  // Probe on S3
  assign bit_extender_1_out = {{8{counter_4_q[7]}}, counter_4_q};  // Bit_Extender bit_extender_1
  Counter counter_4 (.Q(counter_4_q));  // open: load, D, count, carry, up, clk, clr
  assign bit_extender_2_out = {{8{counter_5_q[7]}}, counter_5_q};  // Bit_Extender bit_extender_2
  Counter counter_5 (.Q(counter_5_q));  // open: load, D, count, carry, up, clk, clr
  Comparator #(.width(16)) comparator_1 (
    .a(bit_extender_1_out), .b(ROW_ITERCOUNT), .eq(comparator_1_eq));  // open: gt, lt
  Comparator #(.width(16)) comparator_2 (
    .a(bit_extender_2_out), .b(COL_ITERCOUNT), .eq(comparator_2_eq));  // open: gt, lt
  ROM #(.dataWidth(16)) rom_1 (.addr({8{1'b0}}), .data(ROW_ITERCOUNT));
  ROM #(.dataWidth(16)) rom_2 (.addr({8{1'b0}}), .data(COL_ITERCOUNT));

  // Notes on the sheet:
  //   Pipelined
  //   RAM A Addresses
  //   Constant High Bit
  //   RAM B Addresses
  //   Row[0][0]
  //   Row[0][1]
  //   Row[0][2]
  //   Row[0][3]
  //   A
  //   A
  //   Col[0][0]
  //   Col[0][1]
  //   Col[0][2]
  //   Col[0][3]
  //   B
  //   B
  //   AW
  //   BY
  //   O
  //   Control Unit
  //   contents of rom_1 (hex, n*v repeats v):
  //   1
  //   contents of rom_2 (hex, n*v repeats v):
  //   4
  //   Configuration RAM, Holds Matrix Size (N/4)[0], Data Type (0: int64, 1: float64)[1]
endmodule

module QuizV2 (
);

  wire CLOCK_GLOBAL, comparator_1_eq, comparator_2_eq, counter_3_carry;
  wire [7:0] counter_2_q, counter_3_q, counter_4_q, counter_5_q, multiplexer_1_out, multiplexer_2_out,
       RAM_A_ADDRESS, RAM_B_ADDRESS;
  wire [15:0] bit_extender_1_out, bit_extender_2_out, COL_ITERCOUNT, RAM_S_ADDRESS, register_1_q,
       ROW_ITERCOUNT;
  wire [63:0] S0, S1, S2, S3, subcirc_matrixadder_1_s0, subcirc_matrixadder_1_s1, subcirc_matrixadder_1_s2,
       subcirc_matrixadder_1_s3, subcirc_matrixadder_2_s0, subcirc_matrixadder_2_s1,
       subcirc_matrixadder_2_s2, subcirc_matrixadder_2_s3, subcirc_matrixadder_3_s0,
       subcirc_matrixadder_3_s1, subcirc_matrixadder_3_s2, subcirc_matrixadder_3_s3,
       subcirc_matrixadder_4_s0, subcirc_matrixadder_4_s1, subcirc_matrixadder_4_s2,
       subcirc_matrixadder_4_s3, subcirc_matrixadder_5_s0, subcirc_matrixadder_5_s1,
       subcirc_matrixadder_5_s2, subcirc_matrixadder_5_s3, subcirc_rambank_1_p4, subcirc_rambank_1_p5,
       subcirc_rambank_1_p6, subcirc_rambank_1_p7, subcirc_rambank_2_p4, subcirc_rambank_2_p5,
       subcirc_rambank_2_p6, subcirc_rambank_2_p7, subcirc_rambank_3_p4, subcirc_rambank_3_p5,
       subcirc_rambank_3_p6, subcirc_rambank_3_p7, subcirc_rambank_4_p4, subcirc_rambank_4_p5,
       subcirc_rambank_4_p6, subcirc_rambank_4_p7, subcirc_rambank_5_p4, subcirc_rambank_5_p5,
       subcirc_rambank_5_p6, subcirc_rambank_5_p7, subcirc_rambank_6_p4, subcirc_rambank_6_p5,
       subcirc_rambank_6_p6, subcirc_rambank_6_p7, subcirc_rambank_7_p4, subcirc_rambank_7_p5,
       subcirc_rambank_7_p6, subcirc_rambank_7_p7, subcirc_rambank_8_p4, subcirc_rambank_8_p5,
       subcirc_rambank_8_p6, subcirc_rambank_8_p7, subcirc_rambankoutput_1_s0, subcirc_rambankoutput_1_s1,
       subcirc_rambankoutput_1_s2, subcirc_rambankoutput_1_s3, test_subcirc_matrixadder_2_s0,
       test_subcirc_matrixadder_2_s1, test_subcirc_matrixadder_2_s2, test_subcirc_matrixadder_2_s3,
       test_subcirc_matrixmultiplier_1_s0, test_subcirc_matrixmultiplier_1_s1,
       test_subcirc_matrixmultiplier_1_s2, test_subcirc_matrixmultiplier_1_s3,
       test_subcirc_matrixmultiplier_1_w0, test_subcirc_matrixmultiplier_1_w1,
       test_subcirc_matrixmultiplier_1_w2, test_subcirc_matrixmultiplier_1_w3,
       test_subcirc_matrixmultiplier_2_s0, test_subcirc_matrixmultiplier_2_s1,
       test_subcirc_matrixmultiplier_2_s2, test_subcirc_matrixmultiplier_2_s3,
       test_subcirc_matrixmultiplier_2_w0, test_subcirc_matrixmultiplier_2_w1,
       test_subcirc_matrixmultiplier_2_w2, test_subcirc_matrixmultiplier_2_w3,
       test_subcirc_matrixmultiplier_3_s0, test_subcirc_matrixmultiplier_3_s1,
       test_subcirc_matrixmultiplier_3_s2, test_subcirc_matrixmultiplier_3_s3,
       test_subcirc_matrixmultiplier_3_w0, test_subcirc_matrixmultiplier_3_w1,
       test_subcirc_matrixmultiplier_3_w2, test_subcirc_matrixmultiplier_3_w3,
       test_subcirc_matrixmultiplier_4_s0, test_subcirc_matrixmultiplier_4_s1,
       test_subcirc_matrixmultiplier_4_s2, test_subcirc_matrixmultiplier_4_s3,
       test_subcirc_matrixmultiplier_4_w0, test_subcirc_matrixmultiplier_4_w1,
       test_subcirc_matrixmultiplier_4_w2, test_subcirc_matrixmultiplier_4_w3;

  Counter #(.max('hffff), .width(16)) counter_1 (
    .count(1'b1), .Q(RAM_S_ADDRESS), .up(1'b1), .clk(CLOCK_GLOBAL));  // open: load, D, carry, clr
  Counter #(.max('h1)) counter_2 (
    .count(counter_3_carry), .Q(counter_2_q), .up(1'b1), .clk(CLOCK_GLOBAL));  // open: load, D, carry, clr
  Multiplexer #(.width(8)) multiplexer_1 (.in0(8'h4), .in1({8{1'b0}}), .out(multiplexer_1_out));  // open: sel
  Multiplexer #(.width(8)) multiplexer_2 (.in0(8'h4), .in1({8{1'b0}}), .out(multiplexer_2_out));  // open: sel
  Counter #(.max('h1)) counter_3 (
    .count(1'b1), .Q(counter_3_q), .carry(counter_3_carry), .up(1'b1), .clk(CLOCK_GLOBAL));  // open: load, D, clr
  Adder adder_1 (.a(multiplexer_1_out), .b(counter_2_q), .out(RAM_A_ADDRESS));  // open: cin, cout
  Adder adder_2 (.a(multiplexer_2_out), .b(counter_3_q), .out(RAM_B_ADDRESS));  // open: cin, cout
  // Probe on counter_3_q
  // Probe on counter_2_q
  // SUBCIRC_RAMBank subcirc_rambank_1: pin names not known; wires that end beside it: RAM_A_ADDRESS, 1'b1, CLOCK_GLOBAL, subcirc_rambank_1_p4, subcirc_rambank_1_p5, subcirc_rambank_1_p6, subcirc_rambank_1_p7
  // SUBCIRC_RAMBank subcirc_rambank_2: pin names not known; wires that end beside it: RAM_A_ADDRESS, 1'b1, CLOCK_GLOBAL, subcirc_rambank_2_p4, subcirc_rambank_2_p5, subcirc_rambank_2_p6, subcirc_rambank_2_p7
  // SUBCIRC_RAMBank subcirc_rambank_3: pin names not known; wires that end beside it: RAM_A_ADDRESS, 1'b1, CLOCK_GLOBAL, subcirc_rambank_3_p4, subcirc_rambank_3_p5, subcirc_rambank_3_p6, subcirc_rambank_3_p7
  // SUBCIRC_RAMBank subcirc_rambank_4: pin names not known; wires that end beside it: RAM_A_ADDRESS, 1'b1, CLOCK_GLOBAL, subcirc_rambank_4_p4, subcirc_rambank_4_p5, subcirc_rambank_4_p6, subcirc_rambank_4_p7
  // Probe on subcirc_matrixadder_1_s3
  // Probe on subcirc_matrixadder_1_s1
  // Probe on subcirc_rambank_2_p7
  SUBCIRC_MatrixAdder subcirc_matrixadder_1 (
    .S0(subcirc_matrixadder_1_s0), .S1(subcirc_matrixadder_1_s1), .S2(subcirc_matrixadder_1_s2),
    .S3(subcirc_matrixadder_1_s3));  // open: B0, A0, B1, A1, B2, A2, B3, A3
  // SUBCIRC_RAMBank subcirc_rambank_5: pin names not known; wires that end beside it: RAM_B_ADDRESS, 1'b1, CLOCK_GLOBAL, subcirc_rambank_5_p4, subcirc_rambank_5_p5, subcirc_rambank_5_p6, subcirc_rambank_5_p7
  // SUBCIRC_RAMBank subcirc_rambank_6: pin names not known; wires that end beside it: RAM_B_ADDRESS, 1'b1, CLOCK_GLOBAL, subcirc_rambank_6_p4, subcirc_rambank_6_p5, subcirc_rambank_6_p6, subcirc_rambank_6_p7
  // SUBCIRC_RAMBank subcirc_rambank_7: pin names not known; wires that end beside it: RAM_B_ADDRESS, 1'b1, CLOCK_GLOBAL, subcirc_rambank_7_p4, subcirc_rambank_7_p5, subcirc_rambank_7_p6, subcirc_rambank_7_p7
  // SUBCIRC_RAMBank subcirc_rambank_8: pin names not known; wires that end beside it: RAM_B_ADDRESS, 1'b1, CLOCK_GLOBAL, subcirc_rambank_8_p4, subcirc_rambank_8_p5, subcirc_rambank_8_p6, subcirc_rambank_8_p7
  // Probe on subcirc_matrixadder_1_s2
  // Probe on subcirc_matrixadder_1_s0
  Register #(.width(16)) register_1 (.D(RAM_S_ADDRESS), .en(1'b1), .Q(register_1_q), .clk(CLOCK_GLOBAL));  // open: clr
  // Probe on subcirc_rambank_5_p7
  TEST_SUBCIRC_MatrixMultiplier test_subcirc_matrixmultiplier_1 (
    .B3(subcirc_rambank_5_p4), .B2(subcirc_rambank_5_p5), .B1(subcirc_rambank_5_p6),
    .B0(subcirc_rambank_5_p7), .A3(subcirc_rambank_1_p4), .A2(subcirc_rambank_1_p5),
    .A1(subcirc_rambank_1_p6), .A0(subcirc_rambank_1_p7), .S0(test_subcirc_matrixmultiplier_1_s0),
    .W0(test_subcirc_matrixmultiplier_1_w0), .S1(test_subcirc_matrixmultiplier_1_s1),
    .W1(test_subcirc_matrixmultiplier_1_w1), .S2(test_subcirc_matrixmultiplier_1_s2),
    .W2(test_subcirc_matrixmultiplier_1_w2), .S3(test_subcirc_matrixmultiplier_1_s3),
    .W3(test_subcirc_matrixmultiplier_1_w3));
  SUBCIRC_MatrixAdder subcirc_matrixadder_2 (
    .B0(test_subcirc_matrixmultiplier_1_s0), .A0(test_subcirc_matrixmultiplier_1_w0),
    .B1(test_subcirc_matrixmultiplier_1_s1), .A1(test_subcirc_matrixmultiplier_1_w1),
    .B2(test_subcirc_matrixmultiplier_1_s2), .A2(test_subcirc_matrixmultiplier_1_w2),
    .B3(test_subcirc_matrixmultiplier_1_s3), .A3(test_subcirc_matrixmultiplier_1_w3),
    .S0(subcirc_matrixadder_2_s0), .S1(subcirc_matrixadder_2_s1), .S2(subcirc_matrixadder_2_s2),
    .S3(subcirc_matrixadder_2_s3));
  TEST_SUBCIRC_MatrixMultiplier test_subcirc_matrixmultiplier_2 (
    .B3(subcirc_rambank_6_p4), .B2(subcirc_rambank_6_p5), .B1(subcirc_rambank_6_p6),
    .B0(subcirc_rambank_6_p7), .A3(subcirc_rambank_2_p4), .A2(subcirc_rambank_2_p5),
    .A1(subcirc_rambank_2_p6), .A0(subcirc_rambank_2_p7), .S0(test_subcirc_matrixmultiplier_2_s0),
    .W0(test_subcirc_matrixmultiplier_2_w0), .S1(test_subcirc_matrixmultiplier_2_s1),
    .W1(test_subcirc_matrixmultiplier_2_w1), .S2(test_subcirc_matrixmultiplier_2_s2),
    .W2(test_subcirc_matrixmultiplier_2_w2), .S3(test_subcirc_matrixmultiplier_2_s3),
    .W3(test_subcirc_matrixmultiplier_2_w3));
  SUBCIRC_MatrixAdder subcirc_matrixadder_3 (
    .B0(test_subcirc_matrixmultiplier_2_s0), .A0(test_subcirc_matrixmultiplier_2_w0),
    .B1(test_subcirc_matrixmultiplier_2_s1), .A1(test_subcirc_matrixmultiplier_2_w1),
    .B2(test_subcirc_matrixmultiplier_2_s2), .A2(test_subcirc_matrixmultiplier_2_w2),
    .B3(test_subcirc_matrixmultiplier_2_s3), .A3(test_subcirc_matrixmultiplier_2_w3),
    .S0(subcirc_matrixadder_3_s0), .S1(subcirc_matrixadder_3_s1), .S2(subcirc_matrixadder_3_s2),
    .S3(subcirc_matrixadder_3_s3));
  TEST_SUBCIRC_MatrixMultiplier test_subcirc_matrixmultiplier_3 (
    .B3(subcirc_rambank_7_p4), .B2(subcirc_rambank_7_p5), .B1(subcirc_rambank_7_p6),
    .B0(subcirc_rambank_7_p7), .A3(subcirc_rambank_3_p4), .A2(subcirc_rambank_3_p5),
    .A1(subcirc_rambank_3_p6), .A0(subcirc_rambank_3_p7), .S0(test_subcirc_matrixmultiplier_3_s0),
    .W0(test_subcirc_matrixmultiplier_3_w0), .S1(test_subcirc_matrixmultiplier_3_s1),
    .W1(test_subcirc_matrixmultiplier_3_w1), .S2(test_subcirc_matrixmultiplier_3_s2),
    .W2(test_subcirc_matrixmultiplier_3_w2), .S3(test_subcirc_matrixmultiplier_3_s3),
    .W3(test_subcirc_matrixmultiplier_3_w3));
  SUBCIRC_MatrixAdder subcirc_matrixadder_4 (
    .B0(test_subcirc_matrixmultiplier_3_s0), .A0(test_subcirc_matrixmultiplier_3_w0),
    .B1(test_subcirc_matrixmultiplier_3_s1), .A1(test_subcirc_matrixmultiplier_3_w1),
    .B2(test_subcirc_matrixmultiplier_3_s2), .A2(test_subcirc_matrixmultiplier_3_w2),
    .B3(test_subcirc_matrixmultiplier_3_s3), .A3(test_subcirc_matrixmultiplier_3_w3),
    .S0(subcirc_matrixadder_4_s0), .S1(subcirc_matrixadder_4_s1), .S2(subcirc_matrixadder_4_s2),
    .S3(subcirc_matrixadder_4_s3));
  TEST_SUBCIRC_MatrixMultiplier test_subcirc_matrixmultiplier_4 (
    .B3(subcirc_rambank_8_p4), .B2(subcirc_rambank_8_p5), .B1(subcirc_rambank_8_p6),
    .B0(subcirc_rambank_8_p7), .A3(subcirc_rambank_4_p4), .A2(subcirc_rambank_4_p5),
    .A1(subcirc_rambank_4_p6), .A0(subcirc_rambank_4_p7), .S0(test_subcirc_matrixmultiplier_4_s0),
    .W0(test_subcirc_matrixmultiplier_4_w0), .S1(test_subcirc_matrixmultiplier_4_s1),
    .W1(test_subcirc_matrixmultiplier_4_w1), .S2(test_subcirc_matrixmultiplier_4_s2),
    .W2(test_subcirc_matrixmultiplier_4_w2), .S3(test_subcirc_matrixmultiplier_4_s3),
    .W3(test_subcirc_matrixmultiplier_4_w3));
  SUBCIRC_MatrixAdder subcirc_matrixadder_5 (
    .B0(test_subcirc_matrixmultiplier_4_s0), .A0(test_subcirc_matrixmultiplier_4_w0),
    .B1(test_subcirc_matrixmultiplier_4_s1), .A1(test_subcirc_matrixmultiplier_4_w1),
    .B2(test_subcirc_matrixmultiplier_4_s2), .A2(test_subcirc_matrixmultiplier_4_w2),
    .B3(test_subcirc_matrixmultiplier_4_s3), .A3(test_subcirc_matrixmultiplier_4_w3),
    .S0(subcirc_matrixadder_5_s0), .S1(subcirc_matrixadder_5_s1), .S2(subcirc_matrixadder_5_s2),
    .S3(subcirc_matrixadder_5_s3));
  Clock clock_1 (.out(CLOCK_GLOBAL));
  TEST_SUBCIRC_MatrixAdder test_subcirc_matrixadder_1 (
    .B0(subcirc_matrixadder_2_s0), .B1(subcirc_matrixadder_2_s1), .B2(subcirc_matrixadder_2_s2),
    .B3(subcirc_matrixadder_2_s3), .A0(subcirc_matrixadder_3_s0), .A1(subcirc_matrixadder_3_s1),
    .A2(subcirc_matrixadder_3_s2), .A3(subcirc_matrixadder_3_s3), .S0(S0), .S1(S1), .S2(S2), .S3(S3));
  TEST_SUBCIRC_MatrixAdder test_subcirc_matrixadder_2 (
    .B0(subcirc_matrixadder_4_s0), .B1(subcirc_matrixadder_4_s1), .B2(subcirc_matrixadder_4_s2),
    .B3(subcirc_matrixadder_4_s3), .A0(subcirc_matrixadder_5_s0), .A1(subcirc_matrixadder_5_s1),
    .A2(subcirc_matrixadder_5_s2), .A3(subcirc_matrixadder_5_s3), .S0(test_subcirc_matrixadder_2_s0),
    .S1(test_subcirc_matrixadder_2_s1), .S2(test_subcirc_matrixadder_2_s2), .S3(test_subcirc_matrixadder_2_s3));
  SUBCIRC_RAMBankOutput subcirc_rambankoutput_1 (
    .D3(S3), .D2(S2), .D1(S1), .D0(S0), .Address(register_1_q), .WE(1'b1), .CLK(CLOCK_GLOBAL),
    .S3(subcirc_rambankoutput_1_s3), .S2(subcirc_rambankoutput_1_s2), .S1(subcirc_rambankoutput_1_s1),
    .S0(subcirc_rambankoutput_1_s0));  // open: OE
  // Probe on S0
  // Probe on S2
  // Probe on S1
  // Probe on S3
  assign bit_extender_1_out = {{8{counter_4_q[7]}}, counter_4_q};  // Bit_Extender bit_extender_1
  Counter counter_4 (.Q(counter_4_q));  // open: load, D, count, carry, up, clk, clr
  assign bit_extender_2_out = {{8{counter_5_q[7]}}, counter_5_q};  // Bit_Extender bit_extender_2
  Counter counter_5 (.Q(counter_5_q));  // open: load, D, count, carry, up, clk, clr
  Comparator #(.width(16)) comparator_1 (
    .a(bit_extender_1_out), .b(ROW_ITERCOUNT), .eq(comparator_1_eq));  // open: gt, lt
  Comparator #(.width(16)) comparator_2 (
    .a(bit_extender_2_out), .b(COL_ITERCOUNT), .eq(comparator_2_eq));  // open: gt, lt
  ROM #(.dataWidth(16)) rom_1 (.addr({8{1'b0}}), .data(ROW_ITERCOUNT));
  ROM #(.dataWidth(16)) rom_2 (.addr({8{1'b0}}), .data(COL_ITERCOUNT));

  // Notes on the sheet:
  //   Pipelined
  //   RAM A Addresses
  //   Constant High Bit
  //   RAM B Addresses
  //   Row[0][0]
  //   Row[0][1]
  //   Row[0][2]
  //   Row[0][3]
  //   A
  //   A
  //   Col[0][0]
  //   Col[0][1]
  //   Col[0][2]
  //   Col[0][3]
  //   B
  //   B
  //   AW
  //   BY
  //   O
  //   Control Unit
  //   contents of rom_1 (hex, n*v repeats v):
  //   1
  //   contents of rom_2 (hex, n*v repeats v):
  //   4
  //   Configuration RAM, Holds Matrix Size (N/4)[0], Data Type (0: int64, 1: float64)[1]
endmodule

module DisplayController (
  input  in_1
);
endmodule

module CHECKIN (
);

  wire CLOCK_GLOBAL, counter_3_carry;
  wire [7:0] counter_2_q, counter_3_q, multiplexer_1_out, multiplexer_2_out, RAM_A_ADDRESS, RAM_B_ADDRESS;
  wire [15:0] COL_ITERCOUNT, RAM_S_ADDRESS, register_1_q, ROW_ITERCOUNT;
  wire [63:0] S0, S1, S2, S3, S4, S5, S6, S7, subcirc_matrixadder_1_s0, subcirc_matrixadder_1_s1,
       subcirc_matrixadder_1_s2, subcirc_matrixadder_1_s3, subcirc_matrixadder_2_s0,
       subcirc_matrixadder_2_s1, subcirc_matrixadder_2_s2, subcirc_matrixadder_2_s3,
       subcirc_matrixadder_3_s0, subcirc_matrixadder_3_s1, subcirc_matrixadder_3_s2,
       subcirc_matrixadder_3_s3, subcirc_matrixadder_4_s0, subcirc_matrixadder_4_s1,
       subcirc_matrixadder_4_s2, subcirc_matrixadder_4_s3, subcirc_matrixadder_5_s0,
       subcirc_matrixadder_5_s1, subcirc_matrixadder_5_s2, subcirc_matrixadder_5_s3, subcirc_rambank_1_p4,
       subcirc_rambank_1_p5, subcirc_rambank_1_p6, subcirc_rambank_1_p7, subcirc_rambank_2_p4,
       subcirc_rambank_2_p5, subcirc_rambank_2_p6, subcirc_rambank_2_p7, subcirc_rambank_3_p4,
       subcirc_rambank_3_p5, subcirc_rambank_3_p6, subcirc_rambank_3_p7, subcirc_rambank_4_p4,
       subcirc_rambank_4_p5, subcirc_rambank_4_p6, subcirc_rambank_4_p7, subcirc_rambank_5_p4,
       subcirc_rambank_5_p5, subcirc_rambank_5_p6, subcirc_rambank_5_p7, subcirc_rambank_6_p4,
       subcirc_rambank_6_p5, subcirc_rambank_6_p6, subcirc_rambank_6_p7, subcirc_rambank_7_p4,
       subcirc_rambank_7_p5, subcirc_rambank_7_p6, subcirc_rambank_7_p7, subcirc_rambank_8_p4,
       subcirc_rambank_8_p5, subcirc_rambank_8_p6, subcirc_rambank_8_p7, subcirc_rambankoutput_1_s0,
       subcirc_rambankoutput_1_s1, subcirc_rambankoutput_1_s2, subcirc_rambankoutput_1_s3,
       test_subcirc_matrixmultiplier_1_s0, test_subcirc_matrixmultiplier_1_s1,
       test_subcirc_matrixmultiplier_1_s2, test_subcirc_matrixmultiplier_1_s3,
       test_subcirc_matrixmultiplier_1_w0, test_subcirc_matrixmultiplier_1_w1,
       test_subcirc_matrixmultiplier_1_w2, test_subcirc_matrixmultiplier_1_w3,
       test_subcirc_matrixmultiplier_2_s0, test_subcirc_matrixmultiplier_2_s1,
       test_subcirc_matrixmultiplier_2_s2, test_subcirc_matrixmultiplier_2_s3,
       test_subcirc_matrixmultiplier_2_w0, test_subcirc_matrixmultiplier_2_w1,
       test_subcirc_matrixmultiplier_2_w2, test_subcirc_matrixmultiplier_2_w3,
       test_subcirc_matrixmultiplier_3_s0, test_subcirc_matrixmultiplier_3_s1,
       test_subcirc_matrixmultiplier_3_s2, test_subcirc_matrixmultiplier_3_s3,
       test_subcirc_matrixmultiplier_3_w0, test_subcirc_matrixmultiplier_3_w1,
       test_subcirc_matrixmultiplier_3_w2, test_subcirc_matrixmultiplier_3_w3,
       test_subcirc_matrixmultiplier_4_s0, test_subcirc_matrixmultiplier_4_s1,
       test_subcirc_matrixmultiplier_4_s2, test_subcirc_matrixmultiplier_4_s3,
       test_subcirc_matrixmultiplier_4_w0, test_subcirc_matrixmultiplier_4_w1,
       test_subcirc_matrixmultiplier_4_w2, test_subcirc_matrixmultiplier_4_w3;

  Counter #(.max('hffff), .width(16)) counter_1 (
    .count(1'b1), .Q(RAM_S_ADDRESS), .up(1'b1), .clk(CLOCK_GLOBAL));  // open: load, D, carry, clr
  Counter #(.max('h1)) counter_2 (
    .count(counter_3_carry), .Q(counter_2_q), .up(1'b1), .clk(CLOCK_GLOBAL));  // open: load, D, carry, clr
  Multiplexer #(.width(8)) multiplexer_1 (.in0(8'h4), .in1({8{1'b0}}), .out(multiplexer_1_out));  // open: sel
  Multiplexer #(.width(8)) multiplexer_2 (.in0(8'h4), .in1({8{1'b0}}), .out(multiplexer_2_out));  // open: sel
  Counter #(.max('h1)) counter_3 (
    .count(1'b1), .Q(counter_3_q), .carry(counter_3_carry), .up(1'b1), .clk(CLOCK_GLOBAL));  // open: load, D, clr
  Adder adder_1 (.a(multiplexer_1_out), .b(counter_2_q), .out(RAM_A_ADDRESS));  // open: cin, cout
  Adder adder_2 (.a(multiplexer_2_out), .b(counter_3_q), .out(RAM_B_ADDRESS));  // open: cin, cout
  // Probe on counter_3_q
  // Probe on counter_2_q
  // SUBCIRC_RAMBank subcirc_rambank_1: pin names not known; wires that end beside it: RAM_A_ADDRESS, 1'b1, CLOCK_GLOBAL, subcirc_rambank_1_p4, subcirc_rambank_1_p5, subcirc_rambank_1_p6, subcirc_rambank_1_p7
  // SUBCIRC_RAMBank subcirc_rambank_2: pin names not known; wires that end beside it: RAM_A_ADDRESS, 1'b1, CLOCK_GLOBAL, subcirc_rambank_2_p4, subcirc_rambank_2_p5, subcirc_rambank_2_p6, subcirc_rambank_2_p7
  // SUBCIRC_RAMBank subcirc_rambank_3: pin names not known; wires that end beside it: RAM_A_ADDRESS, 1'b1, CLOCK_GLOBAL, subcirc_rambank_3_p4, subcirc_rambank_3_p5, subcirc_rambank_3_p6, subcirc_rambank_3_p7
  // SUBCIRC_RAMBank subcirc_rambank_4: pin names not known; wires that end beside it: RAM_A_ADDRESS, 1'b1, CLOCK_GLOBAL, subcirc_rambank_4_p4, subcirc_rambank_4_p5, subcirc_rambank_4_p6, subcirc_rambank_4_p7
  // Probe on subcirc_matrixadder_1_s3
  // Probe on subcirc_matrixadder_1_s1
  // Probe on subcirc_rambank_2_p7
  SUBCIRC_MatrixAdder subcirc_matrixadder_1 (
    .S0(subcirc_matrixadder_1_s0), .S1(subcirc_matrixadder_1_s1), .S2(subcirc_matrixadder_1_s2),
    .S3(subcirc_matrixadder_1_s3));  // open: B0, A0, B1, A1, B2, A2, B3, A3
  // SUBCIRC_RAMBank subcirc_rambank_5: pin names not known; wires that end beside it: RAM_B_ADDRESS, 1'b1, CLOCK_GLOBAL, subcirc_rambank_5_p4, subcirc_rambank_5_p5, subcirc_rambank_5_p6, subcirc_rambank_5_p7
  // SUBCIRC_RAMBank subcirc_rambank_6: pin names not known; wires that end beside it: RAM_B_ADDRESS, 1'b1, CLOCK_GLOBAL, subcirc_rambank_6_p4, subcirc_rambank_6_p5, subcirc_rambank_6_p6, subcirc_rambank_6_p7
  // SUBCIRC_RAMBank subcirc_rambank_7: pin names not known; wires that end beside it: RAM_B_ADDRESS, 1'b1, CLOCK_GLOBAL, subcirc_rambank_7_p4, subcirc_rambank_7_p5, subcirc_rambank_7_p6, subcirc_rambank_7_p7
  // SUBCIRC_RAMBank subcirc_rambank_8: pin names not known; wires that end beside it: RAM_B_ADDRESS, 1'b1, CLOCK_GLOBAL, subcirc_rambank_8_p4, subcirc_rambank_8_p5, subcirc_rambank_8_p6, subcirc_rambank_8_p7
  // Probe on subcirc_matrixadder_1_s2
  // Probe on subcirc_matrixadder_1_s0
  Register #(.width(16)) register_1 (.D(RAM_S_ADDRESS), .en(1'b1), .Q(register_1_q), .clk(CLOCK_GLOBAL));  // open: clr
  // Probe on subcirc_rambank_5_p7
  TEST_SUBCIRC_MatrixMultiplier test_subcirc_matrixmultiplier_1 (
    .B3(subcirc_rambank_5_p4), .B2(subcirc_rambank_5_p5), .B1(subcirc_rambank_5_p6),
    .B0(subcirc_rambank_5_p7), .A3(subcirc_rambank_1_p4), .A2(subcirc_rambank_1_p5),
    .A1(subcirc_rambank_1_p6), .A0(subcirc_rambank_1_p7), .S0(test_subcirc_matrixmultiplier_1_s0),
    .W0(test_subcirc_matrixmultiplier_1_w0), .S1(test_subcirc_matrixmultiplier_1_s1),
    .W1(test_subcirc_matrixmultiplier_1_w1), .S2(test_subcirc_matrixmultiplier_1_s2),
    .W2(test_subcirc_matrixmultiplier_1_w2), .S3(test_subcirc_matrixmultiplier_1_s3),
    .W3(test_subcirc_matrixmultiplier_1_w3));
  SUBCIRC_MatrixAdder subcirc_matrixadder_2 (
    .B0(test_subcirc_matrixmultiplier_1_s0), .A0(test_subcirc_matrixmultiplier_1_w0),
    .B1(test_subcirc_matrixmultiplier_1_s1), .A1(test_subcirc_matrixmultiplier_1_w1),
    .B2(test_subcirc_matrixmultiplier_1_s2), .A2(test_subcirc_matrixmultiplier_1_w2),
    .B3(test_subcirc_matrixmultiplier_1_s3), .A3(test_subcirc_matrixmultiplier_1_w3),
    .S0(subcirc_matrixadder_2_s0), .S1(subcirc_matrixadder_2_s1), .S2(subcirc_matrixadder_2_s2),
    .S3(subcirc_matrixadder_2_s3));
  TEST_SUBCIRC_MatrixMultiplier test_subcirc_matrixmultiplier_2 (
    .B3(subcirc_rambank_6_p4), .B2(subcirc_rambank_6_p5), .B1(subcirc_rambank_6_p6),
    .B0(subcirc_rambank_6_p7), .A3(subcirc_rambank_2_p4), .A2(subcirc_rambank_2_p5),
    .A1(subcirc_rambank_2_p6), .A0(subcirc_rambank_2_p7), .S0(test_subcirc_matrixmultiplier_2_s0),
    .W0(test_subcirc_matrixmultiplier_2_w0), .S1(test_subcirc_matrixmultiplier_2_s1),
    .W1(test_subcirc_matrixmultiplier_2_w1), .S2(test_subcirc_matrixmultiplier_2_s2),
    .W2(test_subcirc_matrixmultiplier_2_w2), .S3(test_subcirc_matrixmultiplier_2_s3),
    .W3(test_subcirc_matrixmultiplier_2_w3));
  SUBCIRC_MatrixAdder subcirc_matrixadder_3 (
    .B0(test_subcirc_matrixmultiplier_2_s0), .A0(test_subcirc_matrixmultiplier_2_w0),
    .B1(test_subcirc_matrixmultiplier_2_s1), .A1(test_subcirc_matrixmultiplier_2_w1),
    .B2(test_subcirc_matrixmultiplier_2_s2), .A2(test_subcirc_matrixmultiplier_2_w2),
    .B3(test_subcirc_matrixmultiplier_2_s3), .A3(test_subcirc_matrixmultiplier_2_w3),
    .S0(subcirc_matrixadder_3_s0), .S1(subcirc_matrixadder_3_s1), .S2(subcirc_matrixadder_3_s2),
    .S3(subcirc_matrixadder_3_s3));
  TEST_SUBCIRC_MatrixMultiplier test_subcirc_matrixmultiplier_3 (
    .B3(subcirc_rambank_7_p4), .B2(subcirc_rambank_7_p5), .B1(subcirc_rambank_7_p6),
    .B0(subcirc_rambank_7_p7), .A3(subcirc_rambank_3_p4), .A2(subcirc_rambank_3_p5),
    .A1(subcirc_rambank_3_p6), .A0(subcirc_rambank_3_p7), .S0(test_subcirc_matrixmultiplier_3_s0),
    .W0(test_subcirc_matrixmultiplier_3_w0), .S1(test_subcirc_matrixmultiplier_3_s1),
    .W1(test_subcirc_matrixmultiplier_3_w1), .S2(test_subcirc_matrixmultiplier_3_s2),
    .W2(test_subcirc_matrixmultiplier_3_w2), .S3(test_subcirc_matrixmultiplier_3_s3),
    .W3(test_subcirc_matrixmultiplier_3_w3));
  SUBCIRC_MatrixAdder subcirc_matrixadder_4 (
    .B0(test_subcirc_matrixmultiplier_3_s0), .A0(test_subcirc_matrixmultiplier_3_w0),
    .B1(test_subcirc_matrixmultiplier_3_s1), .A1(test_subcirc_matrixmultiplier_3_w1),
    .B2(test_subcirc_matrixmultiplier_3_s2), .A2(test_subcirc_matrixmultiplier_3_w2),
    .B3(test_subcirc_matrixmultiplier_3_s3), .A3(test_subcirc_matrixmultiplier_3_w3),
    .S0(subcirc_matrixadder_4_s0), .S1(subcirc_matrixadder_4_s1), .S2(subcirc_matrixadder_4_s2),
    .S3(subcirc_matrixadder_4_s3));
  TEST_SUBCIRC_MatrixMultiplier test_subcirc_matrixmultiplier_4 (
    .B3(subcirc_rambank_8_p4), .B2(subcirc_rambank_8_p5), .B1(subcirc_rambank_8_p6),
    .B0(subcirc_rambank_8_p7), .A3(subcirc_rambank_4_p4), .A2(subcirc_rambank_4_p5),
    .A1(subcirc_rambank_4_p6), .A0(subcirc_rambank_4_p7), .S0(test_subcirc_matrixmultiplier_4_s0),
    .W0(test_subcirc_matrixmultiplier_4_w0), .S1(test_subcirc_matrixmultiplier_4_s1),
    .W1(test_subcirc_matrixmultiplier_4_w1), .S2(test_subcirc_matrixmultiplier_4_s2),
    .W2(test_subcirc_matrixmultiplier_4_w2), .S3(test_subcirc_matrixmultiplier_4_s3),
    .W3(test_subcirc_matrixmultiplier_4_w3));
  SUBCIRC_MatrixAdder subcirc_matrixadder_5 (
    .B0(test_subcirc_matrixmultiplier_4_s0), .A0(test_subcirc_matrixmultiplier_4_w0),
    .B1(test_subcirc_matrixmultiplier_4_s1), .A1(test_subcirc_matrixmultiplier_4_w1),
    .B2(test_subcirc_matrixmultiplier_4_s2), .A2(test_subcirc_matrixmultiplier_4_w2),
    .B3(test_subcirc_matrixmultiplier_4_s3), .A3(test_subcirc_matrixmultiplier_4_w3),
    .S0(subcirc_matrixadder_5_s0), .S1(subcirc_matrixadder_5_s1), .S2(subcirc_matrixadder_5_s2),
    .S3(subcirc_matrixadder_5_s3));
  Clock clock_1 (.out(CLOCK_GLOBAL));
  TEST_SUBCIRC_MatrixAdder test_subcirc_matrixadder_1 (
    .B0(subcirc_matrixadder_2_s0), .B1(subcirc_matrixadder_2_s1), .B2(subcirc_matrixadder_2_s2),
    .B3(subcirc_matrixadder_2_s3), .A0(subcirc_matrixadder_3_s0), .A1(subcirc_matrixadder_3_s1),
    .A2(subcirc_matrixadder_3_s2), .A3(subcirc_matrixadder_3_s3), .S0(S0), .S1(S1), .S2(S2), .S3(S3));
  TEST_SUBCIRC_MatrixAdder test_subcirc_matrixadder_2 (
    .B0(subcirc_matrixadder_4_s0), .B1(subcirc_matrixadder_4_s1), .B2(subcirc_matrixadder_4_s2),
    .B3(subcirc_matrixadder_4_s3), .A0(subcirc_matrixadder_5_s0), .A1(subcirc_matrixadder_5_s1),
    .A2(subcirc_matrixadder_5_s2), .A3(subcirc_matrixadder_5_s3), .S0(S4), .S1(S5), .S2(S6), .S3(S7));
  SUBCIRC_RAMBankOutput subcirc_rambankoutput_1 (
    .D3(S3), .D2(S2), .D1(S1), .D0(S0), .Address(register_1_q), .WE(1'b1), .CLK(CLOCK_GLOBAL),
    .S3(subcirc_rambankoutput_1_s3), .S2(subcirc_rambankoutput_1_s2), .S1(subcirc_rambankoutput_1_s1),
    .S0(subcirc_rambankoutput_1_s0));  // open: OE
  Hex_Digit_Display #(.decimalPoint("false")) hex_digit_display_1 (.value(S0[63:60]));
  Hex_Digit_Display #(.decimalPoint("false")) hex_digit_display_2 (.value(S0[59:56]));
  Hex_Digit_Display #(.decimalPoint("false")) hex_digit_display_3 (.value(S2[63:60]));
  Hex_Digit_Display #(.decimalPoint("false")) hex_digit_display_4 (.value(S2[59:56]));
  Hex_Digit_Display #(.decimalPoint("false")) hex_digit_display_5 (.value(S0[55:52]));
  Hex_Digit_Display #(.decimalPoint("false")) hex_digit_display_6 (.value(S0[51:48]));
  Hex_Digit_Display #(.decimalPoint("false")) hex_digit_display_7 (.value(S2[55:52]));
  Hex_Digit_Display #(.decimalPoint("false")) hex_digit_display_8 (.value(S2[51:48]));
  // Probe on S0
  // Probe on S2
  Hex_Digit_Display #(.decimalPoint("false")) hex_digit_display_9 (.value(S0[47:44]));
  Hex_Digit_Display #(.decimalPoint("false")) hex_digit_display_10 (.value(S0[43:40]));
  Hex_Digit_Display #(.decimalPoint("false")) hex_digit_display_11 (.value(S2[47:44]));
  Hex_Digit_Display #(.decimalPoint("false")) hex_digit_display_12 (.value(S2[43:40]));
  // Probe on S1
  // Probe on S3
  Hex_Digit_Display #(.decimalPoint("false")) hex_digit_display_13 (.value(S0[39:36]));
  Hex_Digit_Display #(.decimalPoint("false")) hex_digit_display_14 (.value(S0[35:32]));
  Hex_Digit_Display #(.decimalPoint("false")) hex_digit_display_15 (.value(S2[39:36]));
  Hex_Digit_Display #(.decimalPoint("false")) hex_digit_display_16 (.value(S2[35:32]));
  Hex_Digit_Display #(.decimalPoint("false")) hex_digit_display_17 (.value(S0[31:28]));
  Hex_Digit_Display #(.decimalPoint("false")) hex_digit_display_18 (.value(S0[27:24]));
  Hex_Digit_Display #(.decimalPoint("false")) hex_digit_display_19 (.value(S2[31:28]));
  Hex_Digit_Display #(.decimalPoint("false")) hex_digit_display_20 (.value(S2[27:24]));
  Hex_Digit_Display #(.decimalPoint("false")) hex_digit_display_21 (.value(S0[23:20]));
  Hex_Digit_Display #(.decimalPoint("false")) hex_digit_display_22 (.value(S0[19:16]));
  Hex_Digit_Display #(.decimalPoint("false")) hex_digit_display_23 (.value(S2[23:20]));
  Hex_Digit_Display #(.decimalPoint("false")) hex_digit_display_24 (.value(S2[19:16]));
  Hex_Digit_Display #(.decimalPoint("false")) hex_digit_display_25 (.value(S0[15:12]));
  Hex_Digit_Display #(.decimalPoint("false")) hex_digit_display_26 (.value(S0[11:8]));
  Hex_Digit_Display #(.decimalPoint("false")) hex_digit_display_27 (.value(S2[15:12]));
  Hex_Digit_Display #(.decimalPoint("false")) hex_digit_display_28 (.value(S2[11:8]));
  Hex_Digit_Display #(.decimalPoint("false")) hex_digit_display_29 (.value(S0[7:4]));
  Hex_Digit_Display #(.decimalPoint("false")) hex_digit_display_30 (.value(S0[3:0]));
  Hex_Digit_Display #(.decimalPoint("false")) hex_digit_display_31 (.value(S2[7:4]));
  Hex_Digit_Display #(.decimalPoint("false")) hex_digit_display_32 (.value(S2[3:0]));
  Hex_Digit_Display #(.decimalPoint("false")) hex_digit_display_33 (.value(S1[63:60]));
  Hex_Digit_Display #(.decimalPoint("false")) hex_digit_display_34 (.value(S3[63:60]));
  Hex_Digit_Display #(.decimalPoint("false")) hex_digit_display_35 (.value(S1[59:56]));
  Hex_Digit_Display #(.decimalPoint("false")) hex_digit_display_36 (.value(S1[55:52]));
  Hex_Digit_Display #(.decimalPoint("false")) hex_digit_display_37 (.value(S3[59:56]));
  Hex_Digit_Display #(.decimalPoint("false")) hex_digit_display_38 (.value(S3[55:52]));
  Hex_Digit_Display #(.decimalPoint("false")) hex_digit_display_39 (.value(S1[51:48]));
  Hex_Digit_Display #(.decimalPoint("false")) hex_digit_display_40 (.value(S1[47:44]));
  Hex_Digit_Display #(.decimalPoint("false")) hex_digit_display_41 (.value(S3[51:48]));
  Hex_Digit_Display #(.decimalPoint("false")) hex_digit_display_42 (.value(S3[47:44]));
  Hex_Digit_Display #(.decimalPoint("false")) hex_digit_display_43 (.value(S1[43:40]));
  Hex_Digit_Display #(.decimalPoint("false")) hex_digit_display_44 (.value(S1[39:36]));
  Hex_Digit_Display #(.decimalPoint("false")) hex_digit_display_45 (.value(S3[43:40]));
  Hex_Digit_Display #(.decimalPoint("false")) hex_digit_display_46 (.value(S3[39:36]));
  ROM #(.dataWidth(16)) rom_1 (.addr({8{1'b0}}), .data(ROW_ITERCOUNT));
  ROM #(.dataWidth(16)) rom_2 (.addr({8{1'b0}}), .data(COL_ITERCOUNT));
  Hex_Digit_Display #(.decimalPoint("false")) hex_digit_display_47 (.value(S1[35:32]));
  Hex_Digit_Display #(.decimalPoint("false")) hex_digit_display_48 (.value(S1[31:28]));
  Hex_Digit_Display #(.decimalPoint("false")) hex_digit_display_49 (.value(S3[35:32]));
  Hex_Digit_Display #(.decimalPoint("false")) hex_digit_display_50 (.value(S3[31:28]));
  Hex_Digit_Display #(.decimalPoint("false")) hex_digit_display_51 (.value(S1[27:24]));
  Hex_Digit_Display #(.decimalPoint("false")) hex_digit_display_52 (.value(S1[23:20]));
  Hex_Digit_Display #(.decimalPoint("false")) hex_digit_display_53 (.value(S3[27:24]));
  Hex_Digit_Display #(.decimalPoint("false")) hex_digit_display_54 (.value(S3[23:20]));
  Hex_Digit_Display #(.decimalPoint("false")) hex_digit_display_55 (.value(S1[19:16]));
  Hex_Digit_Display #(.decimalPoint("false")) hex_digit_display_56 (.value(S1[15:12]));
  Hex_Digit_Display #(.decimalPoint("false")) hex_digit_display_57 (.value(S3[19:16]));
  Hex_Digit_Display #(.decimalPoint("false")) hex_digit_display_58 (.value(S3[15:12]));
  Hex_Digit_Display #(.decimalPoint("false")) hex_digit_display_59 (.value(S1[11:8]));
  Hex_Digit_Display #(.decimalPoint("false")) hex_digit_display_60 (.value(S1[7:4]));
  Hex_Digit_Display #(.decimalPoint("false")) hex_digit_display_61 (.value(S3[11:8]));
  Hex_Digit_Display #(.decimalPoint("false")) hex_digit_display_62 (.value(S3[7:4]));
  Hex_Digit_Display #(.decimalPoint("false")) hex_digit_display_63 (.value(S1[3:0]));
  Hex_Digit_Display #(.decimalPoint("false")) hex_digit_display_64 (.value(S3[3:0]));

  // Notes on the sheet:
  //   Pipelined
  //   RAM A Addresses
  //   Constant High Bit
  //   RAM B Addresses
  //   Row[0][0]
  //   Row[0][1]
  //   Row[0][2]
  //   Row[0][3]
  //   A
  //   A
  //   Col[0][0]
  //   Col[0][1]
  //   Col[0][2]
  //   Col[0][3]
  //   B
  //   B
  //   AW
  //   BY
  //   O
  //   Control Unit
  //   contents of rom_1 (hex, n*v repeats v):
  //   1
  //   contents of rom_2 (hex, n*v repeats v):
  //   4
  //   Configuration RAM, Holds Matrix Size (N/4)[0], Data Type (0: int64, 1: float64)[1]
endmodule
module MainAssemblyBouned8x8 (
);

  wire ACCUMULATOR_CLEAR, CLOCK_GLOBAL, comparator_1_gt, comparator_1_lt, comparator_2_gt, comparator_3_gt,
       comparator_3_lt, comparator_4_gt, DISPLAY_1, DISPLAY_2, DISPLAY_3, DISPLAY_4, DISPLAY_5, DISPLAY_6,
       DISPLAY_7, DISPLAY_8, DISPLAY_9, DISPLAY_10, DISPLAY_11, DISPLAY_12, DISPLAY_13, DISPLAY_14,
       DISPLAY_15, DISPLAY_16, not_1_out, not_2_out, undriven, undriven_2, undriven_3, undriven_4,
       undriven_5, undriven_6, undriven_7, undriven_8, undriven_9, undriven_10, undriven_11, undriven_12,
       undriven_13, undriven_14, undriven_15, undriven_16, undriven_17, undriven_18, undriven_19,
       undriven_20, undriven_21, undriven_22, undriven_23, undriven_24, undriven_25, undriven_26,
       undriven_27, undriven_28, undriven_29, undriven_30, undriven_31, undriven_32, undriven_33,
       undriven_34, undriven_35, undriven_36, undriven_37, undriven_38, undriven_39, undriven_40,
       undriven_41, undriven_42, undriven_43, undriven_44, undriven_45, undriven_46, undriven_47,
       undriven_48, undriven_49, undriven_50, undriven_51, undriven_52, undriven_53, undriven_54, undriven_55;
  wire [0:0] counter_9_carry;
  wire [15:0] ACCUMULATOR_ITERCOUNT, adder_3_out, adder_4_out, CLOCK_VALUE, COL_ITERCOUNT, counter_4_q,
       counter_5_q, counter_6_q, counter_7_q, multiplier_1_out, RAM_A_ADDRESS, RAM_B_ADDRESS, RAM_S_ADDRESS,
       register_1_q, register_2_q, register_3_q, register_4_q;
  wire [63:0] accumulator_1_s0, accumulator_1_s1, accumulator_1_s2, accumulator_1_s3, register_5_q,
       register_6_q, register_7_q, register_8_q, register_9_q, register_10_q, register_11_q, register_12_q,
       register_13_q, register_14_q, register_15_q, register_16_q, register_17_q, register_18_q,
       register_19_q, register_20_q, register_21_q, register_22_q, register_23_q, register_24_q,
       register_25_q, register_26_q, register_27_q, register_28_q, register_29_q, register_30_q,
       register_31_q, register_32_q, register_33_q, register_34_q, register_35_q, register_36_q,
       register_37_q, register_38_q, register_39_q, register_40_q, register_41_q, register_42_q,
       register_43_q, register_44_q, register_45_q, register_46_q, register_47_q, register_48_q,
       register_49_q, register_50_q, register_51_q, register_52_q, register_53_q, register_54_q,
       register_55_q, register_56_q, register_57_q, register_58_q, register_59_q, register_60_q,
       register_61_q, register_62_q, register_63_q, register_64_q, register_65_q, register_66_q,
       register_67_q, register_68_q, register_69_q, register_70_q, register_71_q, register_72_q,
       register_73_q, register_74_q, register_75_q, register_76_q, register_77_q, register_78_q,
       register_79_q, register_80_q, register_81_q, register_82_q, register_83_q, register_84_q,
       register_85_q, register_86_q, register_87_q, register_88_q, register_89_q, register_90_q,
       register_91_q, register_92_q, register_93_q, register_94_q, register_95_q, register_96_q,
       register_97_q, register_98_q, register_99_q, register_100_q, register_101_q, register_102_q,
       register_103_q, register_104_q, register_105_q, register_106_q, register_107_q, register_108_q,
       register_109_q, register_110_q, register_111_q, register_112_q, register_113_q, register_114_q,
       register_115_q, register_116_q, register_117_q, register_118_q, register_119_q, register_120_q,
       register_121_q, register_122_q, register_123_q, register_124_q, register_125_q, register_126_q,
       register_127_q, register_128_q, register_129_q, register_130_q, register_131_q, register_132_q, S0,
       S1, S2, S3, subcirc_matrixadder_1_s0, subcirc_matrixadder_1_s1, subcirc_matrixadder_1_s2,
       subcirc_matrixadder_1_s3, subcirc_matrixadder_2_s0, subcirc_matrixadder_2_s1,
       subcirc_matrixadder_2_s2, subcirc_matrixadder_2_s3, subcirc_matrixadder_3_s0,
       subcirc_matrixadder_3_s1, subcirc_matrixadder_3_s2, subcirc_matrixadder_3_s3,
       subcirc_matrixadder_4_s0, subcirc_matrixadder_4_s1, subcirc_matrixadder_4_s2,
       subcirc_matrixadder_4_s3, subcirc_rambank_1_s0, subcirc_rambank_1_s1, subcirc_rambank_1_s2,
       subcirc_rambank_1_s3, subcirc_rambank_2_s0, subcirc_rambank_2_s1, subcirc_rambank_2_s2,
       subcirc_rambank_2_s3, subcirc_rambank_3_s0, subcirc_rambank_3_s1, subcirc_rambank_3_s2,
       subcirc_rambank_3_s3, subcirc_rambank_4_s0, subcirc_rambank_4_s1, subcirc_rambank_4_s2,
       subcirc_rambank_4_s3, subcirc_rambank_5_s0, subcirc_rambank_5_s1, subcirc_rambank_5_s2,
       subcirc_rambank_5_s3, subcirc_rambank_6_s0, subcirc_rambank_6_s1, subcirc_rambank_6_s2,
       subcirc_rambank_6_s3, subcirc_rambank_7_s0, subcirc_rambank_7_s1, subcirc_rambank_7_s2,
       subcirc_rambank_7_s3, subcirc_rambank_8_s0, subcirc_rambank_8_s1, subcirc_rambank_8_s2,
       subcirc_rambank_8_s3, subcirc_rambankoutput_1_s0, subcirc_rambankoutput_1_s1,
       subcirc_rambankoutput_1_s2, subcirc_rambankoutput_1_s3, test_subcirc_matrixadder_1_s0,
       test_subcirc_matrixadder_1_s1, test_subcirc_matrixadder_1_s2, test_subcirc_matrixadder_1_s3,
       test_subcirc_matrixadder_2_s0, test_subcirc_matrixadder_2_s1, test_subcirc_matrixadder_2_s2,
       test_subcirc_matrixadder_2_s3, test_subcirc_matrixadder_3_s0, test_subcirc_matrixadder_3_s1,
       test_subcirc_matrixadder_3_s2, test_subcirc_matrixadder_3_s3, test_subcirc_matrixmultiplier_1_s0,
       test_subcirc_matrixmultiplier_1_s1, test_subcirc_matrixmultiplier_1_s2,
       test_subcirc_matrixmultiplier_1_s3, test_subcirc_matrixmultiplier_1_w0,
       test_subcirc_matrixmultiplier_1_w1, test_subcirc_matrixmultiplier_1_w2,
       test_subcirc_matrixmultiplier_1_w3, test_subcirc_matrixmultiplier_2_s0,
       test_subcirc_matrixmultiplier_2_s1, test_subcirc_matrixmultiplier_2_s2,
       test_subcirc_matrixmultiplier_2_s3, test_subcirc_matrixmultiplier_2_w0,
       test_subcirc_matrixmultiplier_2_w1, test_subcirc_matrixmultiplier_2_w2,
       test_subcirc_matrixmultiplier_2_w3, test_subcirc_matrixmultiplier_3_s0,
       test_subcirc_matrixmultiplier_3_s1, test_subcirc_matrixmultiplier_3_s2,
       test_subcirc_matrixmultiplier_3_s3, test_subcirc_matrixmultiplier_3_w0,
       test_subcirc_matrixmultiplier_3_w1, test_subcirc_matrixmultiplier_3_w2,
       test_subcirc_matrixmultiplier_3_w3, test_subcirc_matrixmultiplier_4_s0,
       test_subcirc_matrixmultiplier_4_s1, test_subcirc_matrixmultiplier_4_s2,
       test_subcirc_matrixmultiplier_4_s3, test_subcirc_matrixmultiplier_4_w0,
       test_subcirc_matrixmultiplier_4_w1, test_subcirc_matrixmultiplier_4_w2,
       test_subcirc_matrixmultiplier_4_w3;

  Counter #(.max('hffff), .width(16)) counter_1 (
    .count(1'b1), .Q(RAM_S_ADDRESS), .up(1'b1), .clk(CLOCK_GLOBAL));  // open: load, D, carry, clr
  // Probe on RAM_A_ADDRESS
  Register #(.width(16)) register_1 (.D(RAM_S_ADDRESS), .Q(register_1_q));  // open: en, clk, clr
  // Probe on counter_4_q
  not not_1 (not_1_out, comparator_3_lt);
  Counter #(.max('h1), .width(1)) counter_2 (
    .count(1'b1), .Q(ACCUMULATOR_CLEAR), .up(1'b1), .clk(CLOCK_GLOBAL));  // open: load, D, carry, clr
  // Probe on counter_5_q
  not not_2 (not_2_out, comparator_1_lt);
  Counter #(.max('h1), .width(1)) counter_3 (
    .count(1'b1), .up(1'b1), .clk(CLOCK_GLOBAL));  // open: load, D, Q, carry, clr
  // Probe on S0
  // Probe on S2
  Counter #(.max('hffff), .width(16)) counter_4 (
    .count(not_1_out), .Q(counter_4_q), .up(1'b1), .clk(CLOCK_GLOBAL), .clr(comparator_4_gt));  // open: load, D, carry
  Counter #(.max('hffff), .width(16)) counter_5 (
    .count(not_2_out), .Q(counter_5_q), .up(1'b1), .clk(CLOCK_GLOBAL), .clr(comparator_2_gt));  // open: load, D, carry
  // Probe on S1
  // Probe on S3
  Counter #(.max('hffff), .width(16)) counter_6 (
    .count(1'b1), .Q(counter_6_q), .up(1'b1), .clk(CLOCK_GLOBAL), .clr(comparator_3_gt));  // open: load, D, carry
  Counter #(.max('hffff), .width(16)) counter_7 (
    .count(1'b1), .Q(counter_7_q), .up(1'b1), .clk(CLOCK_GLOBAL), .clr(comparator_1_gt));  // open: load, D, carry
  // Probe on RAM_B_ADDRESS
  SUBCIRC_RAMBank subcirc_rambank_1 (
    .Address(RAM_A_ADDRESS), .OE(1'b1), .CLK(CLOCK_GLOBAL), .S3(subcirc_rambank_1_s3),
    .S2(subcirc_rambank_1_s2), .S1(subcirc_rambank_1_s1), .S0(subcirc_rambank_1_s0));  // open: D3, D2, D1, D0, WE
  SUBCIRC_RAMBank subcirc_rambank_2 (
    .Address(RAM_A_ADDRESS), .OE(1'b1), .CLK(CLOCK_GLOBAL), .S3(subcirc_rambank_2_s3),
    .S2(subcirc_rambank_2_s2), .S1(subcirc_rambank_2_s1), .S0(subcirc_rambank_2_s0));  // open: D3, D2, D1, D0, WE
  SUBCIRC_RAMBank subcirc_rambank_3 (
    .Address(RAM_A_ADDRESS), .OE(1'b1), .CLK(CLOCK_GLOBAL), .S3(subcirc_rambank_3_s3),
    .S2(subcirc_rambank_3_s2), .S1(subcirc_rambank_3_s1), .S0(subcirc_rambank_3_s0));  // open: D3, D2, D1, D0, WE
  SUBCIRC_RAMBank subcirc_rambank_4 (
    .Address(RAM_A_ADDRESS), .OE(1'b1), .CLK(CLOCK_GLOBAL), .S3(subcirc_rambank_4_s3),
    .S2(subcirc_rambank_4_s2), .S1(subcirc_rambank_4_s1), .S0(subcirc_rambank_4_s0));  // open: D3, D2, D1, D0, WE
  // Probe on COL_ITERCOUNT
  Comparator #(.width(16)) comparator_1 (
    .a(counter_7_q), .b(COL_ITERCOUNT), .gt(comparator_1_gt), .lt(comparator_1_lt));  // open: eq
  Comparator #(.width(16)) comparator_2 (.a(counter_5_q), .b(COL_ITERCOUNT), .gt(comparator_2_gt));  // open: eq, lt
  // Probe on COL_ITERCOUNT
  // Probe on counter_6_q
  Comparator #(.width(16)) comparator_3 (
    .a(counter_6_q), .b(COL_ITERCOUNT), .gt(comparator_3_gt), .lt(comparator_3_lt));  // open: eq
  Comparator #(.width(16)) comparator_4 (.a(counter_4_q), .b(COL_ITERCOUNT), .gt(comparator_4_gt));  // open: eq, lt
  // Probe on counter_7_q
  // Probe on subcirc_rambank_1_s3
  // Probe on subcirc_rambank_3_s3
  Counter #(.max('h4), .width(16)) counter_8 (
    .count(1'b1), .Q(CLOCK_VALUE), .up(1'b1), .clk(CLOCK_GLOBAL));  // open: load, D, carry, clr
  Adder #(.width(16)) adder_1 (.a(counter_4_q), .b(multiplier_1_out), .out(RAM_A_ADDRESS));  // open: cin, cout
  Adder #(.width(16)) adder_2 (.a(counter_6_q), .b(multiplier_1_out), .out(RAM_B_ADDRESS));  // open: cin, cout
  Register #(.width(16)) register_2 (.D(adder_3_out), .en(1'b1), .Q(register_2_q), .clk(CLOCK_GLOBAL));  // open: clr
  SUBCIRC_RAMBank subcirc_rambank_5 (
    .Address(RAM_B_ADDRESS), .OE(1'b1), .CLK(CLOCK_GLOBAL), .S3(subcirc_rambank_5_s3),
    .S2(subcirc_rambank_5_s2), .S1(subcirc_rambank_5_s1), .S0(subcirc_rambank_5_s0));  // open: D3, D2, D1, D0, WE
  SUBCIRC_RAMBank subcirc_rambank_6 (
    .Address(RAM_B_ADDRESS), .OE(1'b1), .CLK(CLOCK_GLOBAL), .S3(subcirc_rambank_6_s3),
    .S2(subcirc_rambank_6_s2), .S1(subcirc_rambank_6_s1), .S0(subcirc_rambank_6_s0));  // open: D3, D2, D1, D0, WE
  SUBCIRC_RAMBank subcirc_rambank_7 (
    .Address(RAM_B_ADDRESS), .OE(1'b1), .CLK(CLOCK_GLOBAL), .S3(subcirc_rambank_7_s3),
    .S2(subcirc_rambank_7_s2), .S1(subcirc_rambank_7_s1), .S0(subcirc_rambank_7_s0));  // open: D3, D2, D1, D0, WE
  SUBCIRC_RAMBank subcirc_rambank_8 (
    .Address(RAM_B_ADDRESS), .OE(1'b1), .CLK(CLOCK_GLOBAL), .S3(subcirc_rambank_8_s3),
    .S2(subcirc_rambank_8_s2), .S1(subcirc_rambank_8_s1), .S0(subcirc_rambank_8_s0));  // open: D3, D2, D1, D0, WE
  Adder #(.width(16)) adder_3 (.a(register_2_q), .b(CLOCK_VALUE), .out(adder_3_out));  // open: cin, cout
  Counter #(.max('hf), .width(16)) counter_9 (
    .count(1'b1), .carry(counter_9_carry[0]), .up(1'b1), .clk(CLOCK_GLOBAL));  // open: load, D, Q, clr
  Register #(.width(16)) register_3 (.D(RAM_S_ADDRESS), .en(1'b1), .Q(register_3_q), .clk(CLOCK_GLOBAL));  // open: clr
  // Probe on subcirc_rambank_5_s3
  TEST_SUBCIRC_MatrixMultiplier test_subcirc_matrixmultiplier_1 (
    .B3(subcirc_rambank_5_s3), .B2(subcirc_rambank_5_s2), .B1(subcirc_rambank_5_s1),
    .B0(subcirc_rambank_5_s0), .A3(subcirc_rambank_1_s3), .A2(subcirc_rambank_1_s2),
    .A1(subcirc_rambank_1_s1), .A0(subcirc_rambank_1_s0), .S0(test_subcirc_matrixmultiplier_1_s0),
    .W0(test_subcirc_matrixmultiplier_1_w0), .S1(test_subcirc_matrixmultiplier_1_s1),
    .W1(test_subcirc_matrixmultiplier_1_w1), .S2(test_subcirc_matrixmultiplier_1_s2),
    .W2(test_subcirc_matrixmultiplier_1_w2), .S3(test_subcirc_matrixmultiplier_1_s3),
    .W3(test_subcirc_matrixmultiplier_1_w3));
  SUBCIRC_MatrixAdder subcirc_matrixadder_1 (
    .B0(test_subcirc_matrixmultiplier_1_s0), .A0(test_subcirc_matrixmultiplier_1_w0),
    .B1(test_subcirc_matrixmultiplier_1_s1), .A1(test_subcirc_matrixmultiplier_1_w1),
    .B2(test_subcirc_matrixmultiplier_1_s2), .A2(test_subcirc_matrixmultiplier_1_w2),
    .B3(test_subcirc_matrixmultiplier_1_s3), .A3(test_subcirc_matrixmultiplier_1_w3),
    .S0(subcirc_matrixadder_1_s0), .S1(subcirc_matrixadder_1_s1), .S2(subcirc_matrixadder_1_s2),
    .S3(subcirc_matrixadder_1_s3));
  TEST_SUBCIRC_MatrixMultiplier test_subcirc_matrixmultiplier_2 (
    .B3(subcirc_rambank_6_s3), .B2(subcirc_rambank_6_s2), .B1(subcirc_rambank_6_s1),
    .B0(subcirc_rambank_6_s0), .A3(subcirc_rambank_2_s3), .A2(subcirc_rambank_2_s2),
    .A1(subcirc_rambank_2_s1), .A0(subcirc_rambank_2_s0), .S0(test_subcirc_matrixmultiplier_2_s0),
    .W0(test_subcirc_matrixmultiplier_2_w0), .S1(test_subcirc_matrixmultiplier_2_s1),
    .W1(test_subcirc_matrixmultiplier_2_w1), .S2(test_subcirc_matrixmultiplier_2_s2),
    .W2(test_subcirc_matrixmultiplier_2_w2), .S3(test_subcirc_matrixmultiplier_2_s3),
    .W3(test_subcirc_matrixmultiplier_2_w3));
  SUBCIRC_MatrixAdder subcirc_matrixadder_2 (
    .B0(test_subcirc_matrixmultiplier_2_s0), .A0(test_subcirc_matrixmultiplier_2_w0),
    .B1(test_subcirc_matrixmultiplier_2_s1), .A1(test_subcirc_matrixmultiplier_2_w1),
    .B2(test_subcirc_matrixmultiplier_2_s2), .A2(test_subcirc_matrixmultiplier_2_w2),
    .B3(test_subcirc_matrixmultiplier_2_s3), .A3(test_subcirc_matrixmultiplier_2_w3),
    .S0(subcirc_matrixadder_2_s0), .S1(subcirc_matrixadder_2_s1), .S2(subcirc_matrixadder_2_s2),
    .S3(subcirc_matrixadder_2_s3));
  TEST_SUBCIRC_MatrixMultiplier test_subcirc_matrixmultiplier_3 (
    .B3(subcirc_rambank_7_s3), .B2(subcirc_rambank_7_s2), .B1(subcirc_rambank_7_s1),
    .B0(subcirc_rambank_7_s0), .A3(subcirc_rambank_3_s3), .A2(subcirc_rambank_3_s2),
    .A1(subcirc_rambank_3_s1), .A0(subcirc_rambank_3_s0), .S0(test_subcirc_matrixmultiplier_3_s0),
    .W0(test_subcirc_matrixmultiplier_3_w0), .S1(test_subcirc_matrixmultiplier_3_s1),
    .W1(test_subcirc_matrixmultiplier_3_w1), .S2(test_subcirc_matrixmultiplier_3_s2),
    .W2(test_subcirc_matrixmultiplier_3_w2), .S3(test_subcirc_matrixmultiplier_3_s3),
    .W3(test_subcirc_matrixmultiplier_3_w3));
  SUBCIRC_MatrixAdder subcirc_matrixadder_3 (
    .B0(test_subcirc_matrixmultiplier_3_s0), .A0(test_subcirc_matrixmultiplier_3_w0),
    .B1(test_subcirc_matrixmultiplier_3_s1), .A1(test_subcirc_matrixmultiplier_3_w1),
    .B2(test_subcirc_matrixmultiplier_3_s2), .A2(test_subcirc_matrixmultiplier_3_w2),
    .B3(test_subcirc_matrixmultiplier_3_s3), .A3(test_subcirc_matrixmultiplier_3_w3),
    .S0(subcirc_matrixadder_3_s0), .S1(subcirc_matrixadder_3_s1), .S2(subcirc_matrixadder_3_s2),
    .S3(subcirc_matrixadder_3_s3));
  TEST_SUBCIRC_MatrixMultiplier test_subcirc_matrixmultiplier_4 (
    .B3(subcirc_rambank_8_s3), .B2(subcirc_rambank_8_s2), .B1(subcirc_rambank_8_s1),
    .B0(subcirc_rambank_8_s0), .A3(subcirc_rambank_4_s3), .A2(subcirc_rambank_4_s2),
    .A1(subcirc_rambank_4_s1), .A0(subcirc_rambank_4_s0), .S0(test_subcirc_matrixmultiplier_4_s0),
    .W0(test_subcirc_matrixmultiplier_4_w0), .S1(test_subcirc_matrixmultiplier_4_s1),
    .W1(test_subcirc_matrixmultiplier_4_w1), .S2(test_subcirc_matrixmultiplier_4_s2),
    .W2(test_subcirc_matrixmultiplier_4_w2), .S3(test_subcirc_matrixmultiplier_4_s3),
    .W3(test_subcirc_matrixmultiplier_4_w3));
  SUBCIRC_MatrixAdder subcirc_matrixadder_4 (
    .B0(test_subcirc_matrixmultiplier_4_s0), .A0(test_subcirc_matrixmultiplier_4_w0),
    .B1(test_subcirc_matrixmultiplier_4_s1), .A1(test_subcirc_matrixmultiplier_4_w1),
    .B2(test_subcirc_matrixmultiplier_4_s2), .A2(test_subcirc_matrixmultiplier_4_w2),
    .B3(test_subcirc_matrixmultiplier_4_s3), .A3(test_subcirc_matrixmultiplier_4_w3),
    .S0(subcirc_matrixadder_4_s0), .S1(subcirc_matrixadder_4_s1), .S2(subcirc_matrixadder_4_s2),
    .S3(subcirc_matrixadder_4_s3));
  // Probe on subcirc_rambank_7_s3
  Register #(.width(16)) register_4 (.D(adder_4_out), .en(1'b1), .Q(register_4_q), .clk(CLOCK_GLOBAL));  // open: clr
  TEST_SUBCIRC_MatrixAdder test_subcirc_matrixadder_1 (
    .B0(subcirc_matrixadder_1_s0), .B1(subcirc_matrixadder_1_s1), .B2(subcirc_matrixadder_1_s2),
    .B3(subcirc_matrixadder_1_s3), .A0(subcirc_matrixadder_2_s0), .A1(subcirc_matrixadder_2_s1),
    .A2(subcirc_matrixadder_2_s2), .A3(subcirc_matrixadder_2_s3), .S0(test_subcirc_matrixadder_1_s0),
    .S1(test_subcirc_matrixadder_1_s1), .S2(test_subcirc_matrixadder_1_s2), .S3(test_subcirc_matrixadder_1_s3));
  TEST_SUBCIRC_MatrixAdder test_subcirc_matrixadder_2 (
    .B0(subcirc_matrixadder_3_s0), .B1(subcirc_matrixadder_3_s1), .B2(subcirc_matrixadder_3_s2),
    .B3(subcirc_matrixadder_3_s3), .A0(subcirc_matrixadder_4_s0), .A1(subcirc_matrixadder_4_s1),
    .A2(subcirc_matrixadder_4_s2), .A3(subcirc_matrixadder_4_s3), .S0(test_subcirc_matrixadder_2_s0),
    .S1(test_subcirc_matrixadder_2_s1), .S2(test_subcirc_matrixadder_2_s2), .S3(test_subcirc_matrixadder_2_s3));
  Multiplier #(.width(16)) multiplier_1 (.a(16'h4), .b(register_4_q), .out(multiplier_1_out));  // open: cin, cout
  Adder #(.width(16)) adder_4 (
    .a(register_4_q), .b({{15{1'b0}}, counter_9_carry[0]}), .out(adder_4_out));  // open: cin, cout
  Clock clock_1 (.out(CLOCK_GLOBAL));
  // Probe on test_subcirc_matrixadder_1_s3
  TEST_SUBCIRC_MatrixAdder test_subcirc_matrixadder_3 (
    .B0(test_subcirc_matrixadder_1_s0), .B1(test_subcirc_matrixadder_1_s1),
    .B2(test_subcirc_matrixadder_1_s2), .B3(test_subcirc_matrixadder_1_s3),
    .A0(test_subcirc_matrixadder_2_s0), .A1(test_subcirc_matrixadder_2_s1),
    .A2(test_subcirc_matrixadder_2_s2), .A3(test_subcirc_matrixadder_2_s3),
    .S0(test_subcirc_matrixadder_3_s0), .S1(test_subcirc_matrixadder_3_s1),
    .S2(test_subcirc_matrixadder_3_s2), .S3(test_subcirc_matrixadder_3_s3));
  SUBCIRC_RAMBankOutput subcirc_rambankoutput_1 (
    .D3(S3), .D2(S2), .D1(S1), .D0(S0), .Address(register_3_q), .WE(1'b1), .CLK(CLOCK_GLOBAL),
    .S3(subcirc_rambankoutput_1_s3), .S2(subcirc_rambankoutput_1_s2), .S1(subcirc_rambankoutput_1_s1),
    .S0(subcirc_rambankoutput_1_s0));  // open: OE
  // Probe on test_subcirc_matrixadder_3_s3
  Accumulator accumulator_1 (
    .Clear(ACCUMULATOR_CLEAR), .Enable(1'b1), .CLK(CLOCK_GLOBAL), .D0(S0), .D1(S1), .D2(S2), .D3(S3),
    .S0(accumulator_1_s0), .S1(accumulator_1_s1), .S2(accumulator_1_s2), .S3(accumulator_1_s3));
  TEST_SUBCIRC_MatrixAdder test_subcirc_matrixadder_4 (
    .B0(accumulator_1_s0), .B1(accumulator_1_s1), .B2(accumulator_1_s2), .B3(accumulator_1_s3),
    .A0(test_subcirc_matrixadder_3_s0), .A1(test_subcirc_matrixadder_3_s1),
    .A2(test_subcirc_matrixadder_3_s2), .A3(test_subcirc_matrixadder_3_s3), .S0(S0), .S1(S1), .S2(S2), .S3(S3));
  Register #(.width(64)) register_5 (.D(S0), .en(DISPLAY_1), .Q(register_5_q), .clk(undriven_2));  // open: clr
  Hex_Digit_Display #(.decimalPoint("false")) hex_digit_display_1 (.value(register_5_q[63:60]));
  Register #(.width(64)) register_6 (.D(S2), .en(DISPLAY_1), .Q(register_6_q), .clk(undriven_2));  // open: clr
  Hex_Digit_Display #(.decimalPoint("false")) hex_digit_display_2 (.value(register_6_q[63:60]));
  Register #(.width(64)) register_7 (.D(S0), .en(DISPLAY_1), .Q(register_7_q), .clk(undriven_2));  // open: clr
  Hex_Digit_Display #(.decimalPoint("false")) hex_digit_display_3 (.value(register_7_q[63:60]));
  Register #(.width(64)) register_8 (.D(S2), .en(DISPLAY_1), .Q(register_8_q), .clk(undriven_2));  // open: clr
  Hex_Digit_Display #(.decimalPoint("false")) hex_digit_display_4 (.value(register_8_q[63:60]));
  Register #(.width(64)) register_9 (.D(S0), .en(DISPLAY_9), .Q(register_9_q), .clk(undriven_3));  // open: clr
  Register #(.width(64)) register_10 (.D(S2), .en(DISPLAY_9), .Q(register_10_q), .clk(undriven_3));  // open: clr
  Register #(.width(64)) register_11 (.D(S0), .en(undriven), .Q(register_11_q), .clk(undriven_4));  // open: clr
  Register #(.width(64)) register_12 (.D(S2), .en(undriven), .Q(register_12_q), .clk(undriven_4));  // open: clr
  Register #(.width(64)) register_13 (.D(S0), .en(DISPLAY_13), .Q(register_13_q), .clk(undriven_8));  // open: clr
  Register #(.width(64)) register_14 (.D(S2), .en(DISPLAY_13), .Q(register_14_q), .clk(undriven_8));  // open: clr
  Register #(.width(64)) register_15 (.D(S0), .en(undriven_5), .Q(register_15_q), .clk(undriven_9));  // open: clr
  Register #(.width(64)) register_16 (.D(S2), .en(undriven_5), .Q(register_16_q), .clk(undriven_9));  // open: clr
  Hex_Digit_Display #(.decimalPoint("false")) hex_digit_display_5 (.value(register_5_q[59:56]));
  Hex_Digit_Display #(.decimalPoint("false")) hex_digit_display_6 (.value(register_5_q[55:52]));
  Hex_Digit_Display #(.decimalPoint("false")) hex_digit_display_7 (.value(register_6_q[59:56]));
  Hex_Digit_Display #(.decimalPoint("false")) hex_digit_display_8 (.value(register_6_q[55:52]));
  Hex_Digit_Display #(.decimalPoint("false")) hex_digit_display_9 (.value(register_7_q[59:56]));
  Hex_Digit_Display #(.decimalPoint("false")) hex_digit_display_10 (.value(register_7_q[55:52]));
  Hex_Digit_Display #(.decimalPoint("false")) hex_digit_display_11 (.value(register_8_q[59:56]));
  Hex_Digit_Display #(.decimalPoint("false")) hex_digit_display_12 (.value(register_8_q[55:52]));
  Hex_Digit_Display #(.decimalPoint("false")) hex_digit_display_13 (.value(register_9_q[63:60]));
  Hex_Digit_Display #(.decimalPoint("false")) hex_digit_display_14 (.value(register_9_q[59:56]));
  Hex_Digit_Display #(.decimalPoint("false")) hex_digit_display_15 (.value(register_10_q[63:60]));
  Hex_Digit_Display #(.decimalPoint("false")) hex_digit_display_16 (.value(register_10_q[59:56]));
  Hex_Digit_Display #(.decimalPoint("false")) hex_digit_display_17 (.value(register_11_q[63:60]));
  Hex_Digit_Display #(.decimalPoint("false")) hex_digit_display_18 (.value(register_11_q[59:56]));
  Hex_Digit_Display #(.decimalPoint("false")) hex_digit_display_19 (.value(register_12_q[63:60]));
  Hex_Digit_Display #(.decimalPoint("false")) hex_digit_display_20 (.value(register_12_q[59:56]));
  Hex_Digit_Display #(.decimalPoint("false")) hex_digit_display_21 (.value(register_13_q[63:60]));
  Hex_Digit_Display #(.decimalPoint("false")) hex_digit_display_22 (.value(register_13_q[59:56]));
  Hex_Digit_Display #(.decimalPoint("false")) hex_digit_display_23 (.value(register_14_q[63:60]));
  Hex_Digit_Display #(.decimalPoint("false")) hex_digit_display_24 (.value(register_14_q[59:56]));
  Hex_Digit_Display #(.decimalPoint("false")) hex_digit_display_25 (.value(register_15_q[63:60]));
  Hex_Digit_Display #(.decimalPoint("false")) hex_digit_display_26 (.value(register_15_q[59:56]));
  Hex_Digit_Display #(.decimalPoint("false")) hex_digit_display_27 (.value(register_16_q[63:60]));
  Hex_Digit_Display #(.decimalPoint("false")) hex_digit_display_28 (.value(register_16_q[59:56]));
  Register #(.width(64)) register_17 (.D(S0), .en(undriven_6), .Q(register_17_q), .clk(undriven_10));  // open: clr
  Hex_Digit_Display #(.decimalPoint("false")) hex_digit_display_29 (.value(register_17_q[63:60]));
  Register #(.width(64)) register_18 (.D(S2), .en(undriven_6), .Q(register_18_q), .clk(undriven_10));  // open: clr
  Hex_Digit_Display #(.decimalPoint("false")) hex_digit_display_30 (.value(register_18_q[63:60]));
  Register #(.width(64)) register_19 (.D(S0), .en(undriven_7), .Q(register_19_q), .clk(undriven_11));  // open: clr
  Hex_Digit_Display #(.decimalPoint("false")) hex_digit_display_31 (.value(register_19_q[63:60]));
  Register #(.width(64)) register_20 (.D(S2), .en(undriven_7), .Q(register_20_q), .clk(undriven_11));  // open: clr
  Hex_Digit_Display #(.decimalPoint("false")) hex_digit_display_32 (.value(register_20_q[63:60]));
  ROM #(.dataWidth(16)) rom_1 (.addr({8{1'b0}}), .data(ACCUMULATOR_ITERCOUNT));
  ROM #(.dataWidth(16)) rom_2 (.addr({8{1'b0}}), .data(COL_ITERCOUNT));
  Hex_Digit_Display #(.decimalPoint("false")) hex_digit_display_33 (.value(register_5_q[51:48]));
  Hex_Digit_Display #(.decimalPoint("false")) hex_digit_display_34 (.value(register_5_q[47:44]));
  Hex_Digit_Display #(.decimalPoint("false")) hex_digit_display_35 (.value(register_6_q[51:48]));
  Hex_Digit_Display #(.decimalPoint("false")) hex_digit_display_36 (.value(register_6_q[47:44]));
  Hex_Digit_Display #(.decimalPoint("false")) hex_digit_display_37 (.value(register_7_q[51:48]));
  Hex_Digit_Display #(.decimalPoint("false")) hex_digit_display_38 (.value(register_7_q[47:44]));
  Hex_Digit_Display #(.decimalPoint("false")) hex_digit_display_39 (.value(register_8_q[51:48]));
  Hex_Digit_Display #(.decimalPoint("false")) hex_digit_display_40 (.value(register_8_q[47:44]));
  Hex_Digit_Display #(.decimalPoint("false")) hex_digit_display_41 (.value(register_9_q[55:52]));
  Hex_Digit_Display #(.decimalPoint("false")) hex_digit_display_42 (.value(register_9_q[51:48]));
  Hex_Digit_Display #(.decimalPoint("false")) hex_digit_display_43 (.value(register_10_q[55:52]));
  Hex_Digit_Display #(.decimalPoint("false")) hex_digit_display_44 (.value(register_10_q[51:48]));
  Hex_Digit_Display #(.decimalPoint("false")) hex_digit_display_45 (.value(register_11_q[55:52]));
  Hex_Digit_Display #(.decimalPoint("false")) hex_digit_display_46 (.value(register_11_q[51:48]));
  Hex_Digit_Display #(.decimalPoint("false")) hex_digit_display_47 (.value(register_12_q[55:52]));
  Hex_Digit_Display #(.decimalPoint("false")) hex_digit_display_48 (.value(register_12_q[51:48]));
  Hex_Digit_Display #(.decimalPoint("false")) hex_digit_display_49 (.value(register_13_q[55:52]));
  Hex_Digit_Display #(.decimalPoint("false")) hex_digit_display_50 (.value(register_13_q[51:48]));
  Hex_Digit_Display #(.decimalPoint("false")) hex_digit_display_51 (.value(register_14_q[55:52]));
  Hex_Digit_Display #(.decimalPoint("false")) hex_digit_display_52 (.value(register_14_q[51:48]));
  Hex_Digit_Display #(.decimalPoint("false")) hex_digit_display_53 (.value(register_15_q[55:52]));
  Hex_Digit_Display #(.decimalPoint("false")) hex_digit_display_54 (.value(register_15_q[51:48]));
  Hex_Digit_Display #(.decimalPoint("false")) hex_digit_display_55 (.value(register_16_q[55:52]));
  Hex_Digit_Display #(.decimalPoint("false")) hex_digit_display_56 (.value(register_16_q[51:48]));
  Hex_Digit_Display #(.decimalPoint("false")) hex_digit_display_57 (.value(register_17_q[59:56]));
  Hex_Digit_Display #(.decimalPoint("false")) hex_digit_display_58 (.value(register_17_q[55:52]));
  Hex_Digit_Display #(.decimalPoint("false")) hex_digit_display_59 (.value(register_18_q[59:56]));
  Hex_Digit_Display #(.decimalPoint("false")) hex_digit_display_60 (.value(register_18_q[55:52]));
  Hex_Digit_Display #(.decimalPoint("false")) hex_digit_display_61 (.value(register_19_q[59:56]));
  Hex_Digit_Display #(.decimalPoint("false")) hex_digit_display_62 (.value(register_19_q[55:52]));
  Hex_Digit_Display #(.decimalPoint("false")) hex_digit_display_63 (.value(register_20_q[59:56]));
  Hex_Digit_Display #(.decimalPoint("false")) hex_digit_display_64 (.value(register_20_q[55:52]));
  Hex_Digit_Display #(.decimalPoint("false")) hex_digit_display_65 (.value(register_5_q[43:40]));
  Hex_Digit_Display #(.decimalPoint("false")) hex_digit_display_66 (.value(register_5_q[39:36]));
  Hex_Digit_Display #(.decimalPoint("false")) hex_digit_display_67 (.value(register_6_q[43:40]));
  Hex_Digit_Display #(.decimalPoint("false")) hex_digit_display_68 (.value(register_6_q[39:36]));
  Hex_Digit_Display #(.decimalPoint("false")) hex_digit_display_69 (.value(register_7_q[43:40]));
  Hex_Digit_Display #(.decimalPoint("false")) hex_digit_display_70 (.value(register_7_q[39:36]));
  Hex_Digit_Display #(.decimalPoint("false")) hex_digit_display_71 (.value(register_8_q[43:40]));
  Hex_Digit_Display #(.decimalPoint("false")) hex_digit_display_72 (.value(register_8_q[39:36]));
  Hex_Digit_Display #(.decimalPoint("false")) hex_digit_display_73 (.value(register_9_q[47:44]));
  Hex_Digit_Display #(.decimalPoint("false")) hex_digit_display_74 (.value(register_9_q[43:40]));
  Hex_Digit_Display #(.decimalPoint("false")) hex_digit_display_75 (.value(register_10_q[47:44]));
  Hex_Digit_Display #(.decimalPoint("false")) hex_digit_display_76 (.value(register_10_q[43:40]));
  Hex_Digit_Display #(.decimalPoint("false")) hex_digit_display_77 (.value(register_11_q[47:44]));
  Hex_Digit_Display #(.decimalPoint("false")) hex_digit_display_78 (.value(register_11_q[43:40]));
  Hex_Digit_Display #(.decimalPoint("false")) hex_digit_display_79 (.value(register_12_q[47:44]));
  Hex_Digit_Display #(.decimalPoint("false")) hex_digit_display_80 (.value(register_12_q[43:40]));
  Hex_Digit_Display #(.decimalPoint("false")) hex_digit_display_81 (.value(register_13_q[47:44]));
  Hex_Digit_Display #(.decimalPoint("false")) hex_digit_display_82 (.value(register_13_q[43:40]));
  Hex_Digit_Display #(.decimalPoint("false")) hex_digit_display_83 (.value(register_14_q[47:44]));
  Hex_Digit_Display #(.decimalPoint("false")) hex_digit_display_84 (.value(register_14_q[43:40]));
  Hex_Digit_Display #(.decimalPoint("false")) hex_digit_display_85 (.value(register_15_q[47:44]));
  Hex_Digit_Display #(.decimalPoint("false")) hex_digit_display_86 (.value(register_15_q[43:40]));
  Hex_Digit_Display #(.decimalPoint("false")) hex_digit_display_87 (.value(register_16_q[47:44]));
  Hex_Digit_Display #(.decimalPoint("false")) hex_digit_display_88 (.value(register_16_q[43:40]));
  Hex_Digit_Display #(.decimalPoint("false")) hex_digit_display_89 (.value(register_17_q[51:48]));
  Hex_Digit_Display #(.decimalPoint("false")) hex_digit_display_90 (.value(register_17_q[47:44]));
  Hex_Digit_Display #(.decimalPoint("false")) hex_digit_display_91 (.value(register_18_q[51:48]));
  Hex_Digit_Display #(.decimalPoint("false")) hex_digit_display_92 (.value(register_18_q[47:44]));
  Hex_Digit_Display #(.decimalPoint("false")) hex_digit_display_93 (.value(register_19_q[51:48]));
  Hex_Digit_Display #(.decimalPoint("false")) hex_digit_display_94 (.value(register_19_q[47:44]));
  Hex_Digit_Display #(.decimalPoint("false")) hex_digit_display_95 (.value(register_20_q[51:48]));
  Hex_Digit_Display #(.decimalPoint("false")) hex_digit_display_96 (.value(register_20_q[47:44]));
  Hex_Digit_Display #(.decimalPoint("false")) hex_digit_display_97 (.value(register_5_q[35:32]));
  Hex_Digit_Display #(.decimalPoint("false")) hex_digit_display_98 (.value(register_5_q[31:28]));
  Hex_Digit_Display #(.decimalPoint("false")) hex_digit_display_99 (.value(register_6_q[35:32]));
  Hex_Digit_Display #(.decimalPoint("false")) hex_digit_display_100 (.value(register_6_q[31:28]));
  Hex_Digit_Display #(.decimalPoint("false")) hex_digit_display_101 (.value(register_7_q[35:32]));
  Hex_Digit_Display #(.decimalPoint("false")) hex_digit_display_102 (.value(register_7_q[31:28]));
  Hex_Digit_Display #(.decimalPoint("false")) hex_digit_display_103 (.value(register_8_q[35:32]));
  Hex_Digit_Display #(.decimalPoint("false")) hex_digit_display_104 (.value(register_8_q[31:28]));
  Hex_Digit_Display #(.decimalPoint("false")) hex_digit_display_105 (.value(register_9_q[39:36]));
  Hex_Digit_Display #(.decimalPoint("false")) hex_digit_display_106 (.value(register_9_q[35:32]));
  Hex_Digit_Display #(.decimalPoint("false")) hex_digit_display_107 (.value(register_10_q[39:36]));
  Hex_Digit_Display #(.decimalPoint("false")) hex_digit_display_108 (.value(register_10_q[35:32]));
  Hex_Digit_Display #(.decimalPoint("false")) hex_digit_display_109 (.value(register_11_q[39:36]));
  Hex_Digit_Display #(.decimalPoint("false")) hex_digit_display_110 (.value(register_11_q[35:32]));
  Hex_Digit_Display #(.decimalPoint("false")) hex_digit_display_111 (.value(register_12_q[39:36]));
  Hex_Digit_Display #(.decimalPoint("false")) hex_digit_display_112 (.value(register_12_q[35:32]));
  Hex_Digit_Display #(.decimalPoint("false")) hex_digit_display_113 (.value(register_13_q[39:36]));
  Hex_Digit_Display #(.decimalPoint("false")) hex_digit_display_114 (.value(register_13_q[35:32]));
  Hex_Digit_Display #(.decimalPoint("false")) hex_digit_display_115 (.value(register_14_q[39:36]));
  Hex_Digit_Display #(.decimalPoint("false")) hex_digit_display_116 (.value(register_14_q[35:32]));
  Hex_Digit_Display #(.decimalPoint("false")) hex_digit_display_117 (.value(register_15_q[39:36]));
  Hex_Digit_Display #(.decimalPoint("false")) hex_digit_display_118 (.value(register_15_q[35:32]));
  Hex_Digit_Display #(.decimalPoint("false")) hex_digit_display_119 (.value(register_16_q[39:36]));
  Hex_Digit_Display #(.decimalPoint("false")) hex_digit_display_120 (.value(register_16_q[35:32]));
  Hex_Digit_Display #(.decimalPoint("false")) hex_digit_display_121 (.value(register_17_q[43:40]));
  Hex_Digit_Display #(.decimalPoint("false")) hex_digit_display_122 (.value(register_17_q[39:36]));
  Hex_Digit_Display #(.decimalPoint("false")) hex_digit_display_123 (.value(register_18_q[43:40]));
  Hex_Digit_Display #(.decimalPoint("false")) hex_digit_display_124 (.value(register_18_q[39:36]));
  Hex_Digit_Display #(.decimalPoint("false")) hex_digit_display_125 (.value(register_19_q[43:40]));
  Hex_Digit_Display #(.decimalPoint("false")) hex_digit_display_126 (.value(register_19_q[39:36]));
  Hex_Digit_Display #(.decimalPoint("false")) hex_digit_display_127 (.value(register_20_q[43:40]));
  Hex_Digit_Display #(.decimalPoint("false")) hex_digit_display_128 (.value(register_20_q[39:36]));
  Hex_Digit_Display #(.decimalPoint("false")) hex_digit_display_129 (.value(register_5_q[27:24]));
  Hex_Digit_Display #(.decimalPoint("false")) hex_digit_display_130 (.value(register_5_q[23:20]));
  Hex_Digit_Display #(.decimalPoint("false")) hex_digit_display_131 (.value(register_6_q[27:24]));
  Hex_Digit_Display #(.decimalPoint("false")) hex_digit_display_132 (.value(register_6_q[23:20]));
  Hex_Digit_Display #(.decimalPoint("false")) hex_digit_display_133 (.value(register_7_q[27:24]));
  Hex_Digit_Display #(.decimalPoint("false")) hex_digit_display_134 (.value(register_7_q[23:20]));
  Hex_Digit_Display #(.decimalPoint("false")) hex_digit_display_135 (.value(register_8_q[27:24]));
  Hex_Digit_Display #(.decimalPoint("false")) hex_digit_display_136 (.value(register_8_q[23:20]));
  Hex_Digit_Display #(.decimalPoint("false")) hex_digit_display_137 (.value(register_9_q[31:28]));
  Hex_Digit_Display #(.decimalPoint("false")) hex_digit_display_138 (.value(register_9_q[27:24]));
  Hex_Digit_Display #(.decimalPoint("false")) hex_digit_display_139 (.value(register_10_q[31:28]));
  Hex_Digit_Display #(.decimalPoint("false")) hex_digit_display_140 (.value(register_10_q[27:24]));
  Hex_Digit_Display #(.decimalPoint("false")) hex_digit_display_141 (.value(register_11_q[31:28]));
  Hex_Digit_Display #(.decimalPoint("false")) hex_digit_display_142 (.value(register_11_q[27:24]));
  Hex_Digit_Display #(.decimalPoint("false")) hex_digit_display_143 (.value(register_12_q[31:28]));
  Hex_Digit_Display #(.decimalPoint("false")) hex_digit_display_144 (.value(register_12_q[27:24]));
  Hex_Digit_Display #(.decimalPoint("false")) hex_digit_display_145 (.value(register_13_q[31:28]));
  Hex_Digit_Display #(.decimalPoint("false")) hex_digit_display_146 (.value(register_13_q[27:24]));
  Hex_Digit_Display #(.decimalPoint("false")) hex_digit_display_147 (.value(register_14_q[31:28]));
  Hex_Digit_Display #(.decimalPoint("false")) hex_digit_display_148 (.value(register_14_q[27:24]));
  Hex_Digit_Display #(.decimalPoint("false")) hex_digit_display_149 (.value(register_15_q[31:28]));
  Hex_Digit_Display #(.decimalPoint("false")) hex_digit_display_150 (.value(register_15_q[27:24]));
  Hex_Digit_Display #(.decimalPoint("false")) hex_digit_display_151 (.value(register_16_q[31:28]));
  Hex_Digit_Display #(.decimalPoint("false")) hex_digit_display_152 (.value(register_16_q[27:24]));
  Hex_Digit_Display #(.decimalPoint("false")) hex_digit_display_153 (.value(register_17_q[35:32]));
  Hex_Digit_Display #(.decimalPoint("false")) hex_digit_display_154 (.value(register_17_q[31:28]));
  Hex_Digit_Display #(.decimalPoint("false")) hex_digit_display_155 (.value(register_18_q[35:32]));
  Hex_Digit_Display #(.decimalPoint("false")) hex_digit_display_156 (.value(register_18_q[31:28]));
  Hex_Digit_Display #(.decimalPoint("false")) hex_digit_display_157 (.value(register_19_q[35:32]));
  Hex_Digit_Display #(.decimalPoint("false")) hex_digit_display_158 (.value(register_19_q[31:28]));
  Hex_Digit_Display #(.decimalPoint("false")) hex_digit_display_159 (.value(register_20_q[35:32]));
  Hex_Digit_Display #(.decimalPoint("false")) hex_digit_display_160 (.value(register_20_q[31:28]));
  Hex_Digit_Display #(.decimalPoint("false")) hex_digit_display_161 (.value(register_5_q[19:16]));
  Hex_Digit_Display #(.decimalPoint("false")) hex_digit_display_162 (.value(register_5_q[15:12]));
  Hex_Digit_Display #(.decimalPoint("false")) hex_digit_display_163 (.value(register_6_q[19:16]));
  Hex_Digit_Display #(.decimalPoint("false")) hex_digit_display_164 (.value(register_6_q[15:12]));
  Hex_Digit_Display #(.decimalPoint("false")) hex_digit_display_165 (.value(register_7_q[19:16]));
  Hex_Digit_Display #(.decimalPoint("false")) hex_digit_display_166 (.value(register_7_q[15:12]));
  Hex_Digit_Display #(.decimalPoint("false")) hex_digit_display_167 (.value(register_8_q[19:16]));
  Hex_Digit_Display #(.decimalPoint("false")) hex_digit_display_168 (.value(register_8_q[15:12]));
  Hex_Digit_Display #(.decimalPoint("false")) hex_digit_display_169 (.value(register_9_q[23:20]));
  Hex_Digit_Display #(.decimalPoint("false")) hex_digit_display_170 (.value(register_9_q[19:16]));
  Hex_Digit_Display #(.decimalPoint("false")) hex_digit_display_171 (.value(register_10_q[23:20]));
  Hex_Digit_Display #(.decimalPoint("false")) hex_digit_display_172 (.value(register_10_q[19:16]));
  Hex_Digit_Display #(.decimalPoint("false")) hex_digit_display_173 (.value(register_11_q[23:20]));
  Hex_Digit_Display #(.decimalPoint("false")) hex_digit_display_174 (.value(register_11_q[19:16]));
  Hex_Digit_Display #(.decimalPoint("false")) hex_digit_display_175 (.value(register_12_q[23:20]));
  Hex_Digit_Display #(.decimalPoint("false")) hex_digit_display_176 (.value(register_12_q[19:16]));
  Hex_Digit_Display #(.decimalPoint("false")) hex_digit_display_177 (.value(register_13_q[23:20]));
  Hex_Digit_Display #(.decimalPoint("false")) hex_digit_display_178 (.value(register_13_q[19:16]));
  Hex_Digit_Display #(.decimalPoint("false")) hex_digit_display_179 (.value(register_14_q[23:20]));
  Hex_Digit_Display #(.decimalPoint("false")) hex_digit_display_180 (.value(register_14_q[19:16]));
  Hex_Digit_Display #(.decimalPoint("false")) hex_digit_display_181 (.value(register_15_q[23:20]));
  Hex_Digit_Display #(.decimalPoint("false")) hex_digit_display_182 (.value(register_15_q[19:16]));
  Hex_Digit_Display #(.decimalPoint("false")) hex_digit_display_183 (.value(register_16_q[23:20]));
  Hex_Digit_Display #(.decimalPoint("false")) hex_digit_display_184 (.value(register_16_q[19:16]));
  Hex_Digit_Display #(.decimalPoint("false")) hex_digit_display_185 (.value(register_17_q[27:24]));
  Hex_Digit_Display #(.decimalPoint("false")) hex_digit_display_186 (.value(register_17_q[23:20]));
  Hex_Digit_Display #(.decimalPoint("false")) hex_digit_display_187 (.value(register_18_q[27:24]));
  Hex_Digit_Display #(.decimalPoint("false")) hex_digit_display_188 (.value(register_18_q[23:20]));
  Hex_Digit_Display #(.decimalPoint("false")) hex_digit_display_189 (.value(register_19_q[27:24]));
  Hex_Digit_Display #(.decimalPoint("false")) hex_digit_display_190 (.value(register_19_q[23:20]));
  Hex_Digit_Display #(.decimalPoint("false")) hex_digit_display_191 (.value(register_20_q[27:24]));
  Hex_Digit_Display #(.decimalPoint("false")) hex_digit_display_192 (.value(register_20_q[23:20]));
  Hex_Digit_Display #(.decimalPoint("false")) hex_digit_display_193 (.value(register_5_q[11:8]));
  Hex_Digit_Display #(.decimalPoint("false")) hex_digit_display_194 (.value(register_5_q[7:4]));
  Hex_Digit_Display #(.decimalPoint("false")) hex_digit_display_195 (.value(register_6_q[11:8]));
  Hex_Digit_Display #(.decimalPoint("false")) hex_digit_display_196 (.value(register_6_q[7:4]));
  Hex_Digit_Display #(.decimalPoint("false")) hex_digit_display_197 (.value(register_7_q[11:8]));
  Hex_Digit_Display #(.decimalPoint("false")) hex_digit_display_198 (.value(register_7_q[7:4]));
  Hex_Digit_Display #(.decimalPoint("false")) hex_digit_display_199 (.value(register_8_q[11:8]));
  Hex_Digit_Display #(.decimalPoint("false")) hex_digit_display_200 (.value(register_8_q[7:4]));
  Hex_Digit_Display #(.decimalPoint("false")) hex_digit_display_201 (.value(register_9_q[15:12]));
  Hex_Digit_Display #(.decimalPoint("false")) hex_digit_display_202 (.value(register_9_q[11:8]));
  Hex_Digit_Display #(.decimalPoint("false")) hex_digit_display_203 (.value(register_10_q[15:12]));
  Hex_Digit_Display #(.decimalPoint("false")) hex_digit_display_204 (.value(register_10_q[11:8]));
  Hex_Digit_Display #(.decimalPoint("false")) hex_digit_display_205 (.value(register_11_q[15:12]));
  Hex_Digit_Display #(.decimalPoint("false")) hex_digit_display_206 (.value(register_11_q[11:8]));
  Hex_Digit_Display #(.decimalPoint("false")) hex_digit_display_207 (.value(register_12_q[15:12]));
  Hex_Digit_Display #(.decimalPoint("false")) hex_digit_display_208 (.value(register_12_q[11:8]));
  Hex_Digit_Display #(.decimalPoint("false")) hex_digit_display_209 (.value(register_13_q[15:12]));
  Hex_Digit_Display #(.decimalPoint("false")) hex_digit_display_210 (.value(register_13_q[11:8]));
  Hex_Digit_Display #(.decimalPoint("false")) hex_digit_display_211 (.value(register_14_q[15:12]));
  Hex_Digit_Display #(.decimalPoint("false")) hex_digit_display_212 (.value(register_14_q[11:8]));
  Hex_Digit_Display #(.decimalPoint("false")) hex_digit_display_213 (.value(register_15_q[15:12]));
  Hex_Digit_Display #(.decimalPoint("false")) hex_digit_display_214 (.value(register_15_q[11:8]));
  Hex_Digit_Display #(.decimalPoint("false")) hex_digit_display_215 (.value(register_16_q[15:12]));
  Hex_Digit_Display #(.decimalPoint("false")) hex_digit_display_216 (.value(register_16_q[11:8]));
  Hex_Digit_Display #(.decimalPoint("false")) hex_digit_display_217 (.value(register_17_q[19:16]));
  Hex_Digit_Display #(.decimalPoint("false")) hex_digit_display_218 (.value(register_17_q[15:12]));
  Hex_Digit_Display #(.decimalPoint("false")) hex_digit_display_219 (.value(register_18_q[19:16]));
  Hex_Digit_Display #(.decimalPoint("false")) hex_digit_display_220 (.value(register_18_q[15:12]));
  Hex_Digit_Display #(.decimalPoint("false")) hex_digit_display_221 (.value(register_19_q[19:16]));
  Hex_Digit_Display #(.decimalPoint("false")) hex_digit_display_222 (.value(register_19_q[15:12]));
  Hex_Digit_Display #(.decimalPoint("false")) hex_digit_display_223 (.value(register_20_q[19:16]));
  Hex_Digit_Display #(.decimalPoint("false")) hex_digit_display_224 (.value(register_20_q[15:12]));
  Hex_Digit_Display #(.decimalPoint("false")) hex_digit_display_225 (.value(register_5_q[3:0]));
  Hex_Digit_Display #(.decimalPoint("false")) hex_digit_display_226 (.value(register_6_q[3:0]));
  Hex_Digit_Display #(.decimalPoint("false")) hex_digit_display_227 (.value(register_7_q[3:0]));
  Hex_Digit_Display #(.decimalPoint("false")) hex_digit_display_228 (.value(register_8_q[3:0]));
  Hex_Digit_Display #(.decimalPoint("false")) hex_digit_display_229 (.value(register_9_q[7:4]));
  Hex_Digit_Display #(.decimalPoint("false")) hex_digit_display_230 (.value(register_9_q[3:0]));
  Hex_Digit_Display #(.decimalPoint("false")) hex_digit_display_231 (.value(register_10_q[7:4]));
  Hex_Digit_Display #(.decimalPoint("false")) hex_digit_display_232 (.value(register_10_q[3:0]));
  Hex_Digit_Display #(.decimalPoint("false")) hex_digit_display_233 (.value(register_11_q[7:4]));
  Hex_Digit_Display #(.decimalPoint("false")) hex_digit_display_234 (.value(register_11_q[3:0]));
  Hex_Digit_Display #(.decimalPoint("false")) hex_digit_display_235 (.value(register_12_q[7:4]));
  Hex_Digit_Display #(.decimalPoint("false")) hex_digit_display_236 (.value(register_12_q[3:0]));
  Hex_Digit_Display #(.decimalPoint("false")) hex_digit_display_237 (.value(register_13_q[7:4]));
  Hex_Digit_Display #(.decimalPoint("false")) hex_digit_display_238 (.value(register_13_q[3:0]));
  Hex_Digit_Display #(.decimalPoint("false")) hex_digit_display_239 (.value(register_14_q[7:4]));
  Hex_Digit_Display #(.decimalPoint("false")) hex_digit_display_240 (.value(register_14_q[3:0]));
  Hex_Digit_Display #(.decimalPoint("false")) hex_digit_display_241 (.value(register_15_q[7:4]));
  Hex_Digit_Display #(.decimalPoint("false")) hex_digit_display_242 (.value(register_15_q[3:0]));
  Hex_Digit_Display #(.decimalPoint("false")) hex_digit_display_243 (.value(register_16_q[7:4]));
  Hex_Digit_Display #(.decimalPoint("false")) hex_digit_display_244 (.value(register_16_q[3:0]));
  Hex_Digit_Display #(.decimalPoint("false")) hex_digit_display_245 (.value(register_17_q[11:8]));
  Hex_Digit_Display #(.decimalPoint("false")) hex_digit_display_246 (.value(register_17_q[7:4]));
  Hex_Digit_Display #(.decimalPoint("false")) hex_digit_display_247 (.value(register_18_q[11:8]));
  Hex_Digit_Display #(.decimalPoint("false")) hex_digit_display_248 (.value(register_18_q[7:4]));
  Hex_Digit_Display #(.decimalPoint("false")) hex_digit_display_249 (.value(register_19_q[11:8]));
  Hex_Digit_Display #(.decimalPoint("false")) hex_digit_display_250 (.value(register_19_q[7:4]));
  Hex_Digit_Display #(.decimalPoint("false")) hex_digit_display_251 (.value(register_20_q[11:8]));
  Hex_Digit_Display #(.decimalPoint("false")) hex_digit_display_252 (.value(register_20_q[7:4]));
  Register #(.width(64)) register_21 (.D(S1), .en(DISPLAY_1), .Q(register_21_q), .clk(undriven_2));  // open: clr
  Register #(.width(64)) register_22 (.D(S3), .en(DISPLAY_1), .Q(register_22_q), .clk(undriven_2));  // open: clr
  Register #(.width(64)) register_23 (.D(S1), .en(DISPLAY_1), .Q(register_23_q), .clk(undriven_2));  // open: clr
  Register #(.width(64)) register_24 (.D(S3), .en(DISPLAY_1), .Q(register_24_q), .clk(undriven_2));  // open: clr
  Register #(.width(64)) register_25 (.D(S1), .en(DISPLAY_9), .Q(register_25_q), .clk(undriven_3));  // open: clr
  Register #(.width(64)) register_26 (.D(S3), .en(DISPLAY_9), .Q(register_26_q), .clk(undriven_3));  // open: clr
  Register #(.width(64)) register_27 (.D(S1), .en(undriven), .Q(register_27_q), .clk(undriven_4));  // open: clr
  Register #(.width(64)) register_28 (.D(S3), .en(undriven), .Q(register_28_q), .clk(undriven_4));  // open: clr
  Hex_Digit_Display #(.decimalPoint("false")) hex_digit_display_253 (.value(register_17_q[3:0]));
  Hex_Digit_Display #(.decimalPoint("false")) hex_digit_display_254 (.value(register_18_q[3:0]));
  Hex_Digit_Display #(.decimalPoint("false")) hex_digit_display_255 (.value(register_19_q[3:0]));
  Hex_Digit_Display #(.decimalPoint("false")) hex_digit_display_256 (.value(register_20_q[3:0]));
  Hex_Digit_Display #(.decimalPoint("false")) hex_digit_display_257 (.value(register_21_q[63:60]));
  Hex_Digit_Display #(.decimalPoint("false")) hex_digit_display_258 (.value(register_21_q[59:56]));
  Hex_Digit_Display #(.decimalPoint("false")) hex_digit_display_259 (.value(register_22_q[63:60]));
  Hex_Digit_Display #(.decimalPoint("false")) hex_digit_display_260 (.value(register_22_q[59:56]));
  Hex_Digit_Display #(.decimalPoint("false")) hex_digit_display_261 (.value(register_23_q[63:60]));
  Hex_Digit_Display #(.decimalPoint("false")) hex_digit_display_262 (.value(register_23_q[59:56]));
  Hex_Digit_Display #(.decimalPoint("false")) hex_digit_display_263 (.value(register_24_q[63:60]));
  Hex_Digit_Display #(.decimalPoint("false")) hex_digit_display_264 (.value(register_24_q[59:56]));
  Hex_Digit_Display #(.decimalPoint("false")) hex_digit_display_265 (.value(register_25_q[63:60]));
  Hex_Digit_Display #(.decimalPoint("false")) hex_digit_display_266 (.value(register_25_q[59:56]));
  Hex_Digit_Display #(.decimalPoint("false")) hex_digit_display_267 (.value(register_26_q[63:60]));
  Hex_Digit_Display #(.decimalPoint("false")) hex_digit_display_268 (.value(register_26_q[59:56]));
  Hex_Digit_Display #(.decimalPoint("false")) hex_digit_display_269 (.value(register_27_q[63:60]));
  Hex_Digit_Display #(.decimalPoint("false")) hex_digit_display_270 (.value(register_27_q[59:56]));
  Hex_Digit_Display #(.decimalPoint("false")) hex_digit_display_271 (.value(register_28_q[63:60]));
  Hex_Digit_Display #(.decimalPoint("false")) hex_digit_display_272 (.value(register_28_q[59:56]));
  Register #(.width(64)) register_29 (.D(S1), .en(DISPLAY_13), .Q(register_29_q), .clk(undriven_8));  // open: clr
  Hex_Digit_Display #(.decimalPoint("false")) hex_digit_display_273 (.value(register_29_q[63:60]));
  Register #(.width(64)) register_30 (.D(S3), .en(DISPLAY_13), .Q(register_30_q), .clk(undriven_8));  // open: clr
  Hex_Digit_Display #(.decimalPoint("false")) hex_digit_display_274 (.value(register_30_q[63:60]));
  Register #(.width(64)) register_31 (.D(S1), .en(undriven_5), .Q(register_31_q), .clk(undriven_9));  // open: clr
  Hex_Digit_Display #(.decimalPoint("false")) hex_digit_display_275 (.value(register_31_q[63:60]));
  Register #(.width(64)) register_32 (.D(S3), .en(undriven_5), .Q(register_32_q), .clk(undriven_9));  // open: clr
  Hex_Digit_Display #(.decimalPoint("false")) hex_digit_display_276 (.value(register_32_q[63:60]));
  Register #(.width(64)) register_33 (.D(S1), .en(undriven_6), .Q(register_33_q), .clk(undriven_10));  // open: clr
  Hex_Digit_Display #(.decimalPoint("false")) hex_digit_display_277 (.value(register_33_q[63:60]));
  Register #(.width(64)) register_34 (.D(S3), .en(undriven_6), .Q(register_34_q), .clk(undriven_10));  // open: clr
  Hex_Digit_Display #(.decimalPoint("false")) hex_digit_display_278 (.value(register_34_q[63:60]));
  Register #(.width(64)) register_35 (.D(S1), .en(undriven_7), .Q(register_35_q), .clk(undriven_11));  // open: clr
  Hex_Digit_Display #(.decimalPoint("false")) hex_digit_display_279 (.value(register_35_q[63:60]));
  Register #(.width(64)) register_36 (.D(S3), .en(undriven_7), .Q(register_36_q), .clk(undriven_11));  // open: clr
  Hex_Digit_Display #(.decimalPoint("false")) hex_digit_display_280 (.value(register_36_q[63:60]));
  Hex_Digit_Display #(.decimalPoint("false")) hex_digit_display_281 (.value(register_21_q[55:52]));
  Hex_Digit_Display #(.decimalPoint("false")) hex_digit_display_282 (.value(register_21_q[51:48]));
  Hex_Digit_Display #(.decimalPoint("false")) hex_digit_display_283 (.value(register_22_q[55:52]));
  Hex_Digit_Display #(.decimalPoint("false")) hex_digit_display_284 (.value(register_22_q[51:48]));
  Hex_Digit_Display #(.decimalPoint("false")) hex_digit_display_285 (.value(register_23_q[55:52]));
  Hex_Digit_Display #(.decimalPoint("false")) hex_digit_display_286 (.value(register_23_q[51:48]));
  Hex_Digit_Display #(.decimalPoint("false")) hex_digit_display_287 (.value(register_24_q[55:52]));
  Hex_Digit_Display #(.decimalPoint("false")) hex_digit_display_288 (.value(register_24_q[51:48]));
  Hex_Digit_Display #(.decimalPoint("false")) hex_digit_display_289 (.value(register_25_q[55:52]));
  Hex_Digit_Display #(.decimalPoint("false")) hex_digit_display_290 (.value(register_25_q[51:48]));
  Hex_Digit_Display #(.decimalPoint("false")) hex_digit_display_291 (.value(register_26_q[55:52]));
  Hex_Digit_Display #(.decimalPoint("false")) hex_digit_display_292 (.value(register_26_q[51:48]));
  Hex_Digit_Display #(.decimalPoint("false")) hex_digit_display_293 (.value(register_27_q[55:52]));
  Hex_Digit_Display #(.decimalPoint("false")) hex_digit_display_294 (.value(register_27_q[51:48]));
  Hex_Digit_Display #(.decimalPoint("false")) hex_digit_display_295 (.value(register_28_q[55:52]));
  Hex_Digit_Display #(.decimalPoint("false")) hex_digit_display_296 (.value(register_28_q[51:48]));
  Hex_Digit_Display #(.decimalPoint("false")) hex_digit_display_297 (.value(register_29_q[59:56]));
  Hex_Digit_Display #(.decimalPoint("false")) hex_digit_display_298 (.value(register_29_q[55:52]));
  Hex_Digit_Display #(.decimalPoint("false")) hex_digit_display_299 (.value(register_30_q[59:56]));
  Hex_Digit_Display #(.decimalPoint("false")) hex_digit_display_300 (.value(register_30_q[55:52]));
  Hex_Digit_Display #(.decimalPoint("false")) hex_digit_display_301 (.value(register_31_q[59:56]));
  Hex_Digit_Display #(.decimalPoint("false")) hex_digit_display_302 (.value(register_31_q[55:52]));
  Hex_Digit_Display #(.decimalPoint("false")) hex_digit_display_303 (.value(register_32_q[59:56]));
  Hex_Digit_Display #(.decimalPoint("false")) hex_digit_display_304 (.value(register_32_q[55:52]));
  Hex_Digit_Display #(.decimalPoint("false")) hex_digit_display_305 (.value(register_33_q[59:56]));
  Hex_Digit_Display #(.decimalPoint("false")) hex_digit_display_306 (.value(register_33_q[55:52]));
  Hex_Digit_Display #(.decimalPoint("false")) hex_digit_display_307 (.value(register_34_q[59:56]));
  Hex_Digit_Display #(.decimalPoint("false")) hex_digit_display_308 (.value(register_34_q[55:52]));
  Hex_Digit_Display #(.decimalPoint("false")) hex_digit_display_309 (.value(register_35_q[59:56]));
  Hex_Digit_Display #(.decimalPoint("false")) hex_digit_display_310 (.value(register_35_q[55:52]));
  Hex_Digit_Display #(.decimalPoint("false")) hex_digit_display_311 (.value(register_36_q[59:56]));
  Hex_Digit_Display #(.decimalPoint("false")) hex_digit_display_312 (.value(register_36_q[55:52]));
  Hex_Digit_Display #(.decimalPoint("false")) hex_digit_display_313 (.value(register_21_q[47:44]));
  Hex_Digit_Display #(.decimalPoint("false")) hex_digit_display_314 (.value(register_21_q[43:40]));
  Hex_Digit_Display #(.decimalPoint("false")) hex_digit_display_315 (.value(register_22_q[47:44]));
  Hex_Digit_Display #(.decimalPoint("false")) hex_digit_display_316 (.value(register_22_q[43:40]));
  Hex_Digit_Display #(.decimalPoint("false")) hex_digit_display_317 (.value(register_23_q[47:44]));
  Hex_Digit_Display #(.decimalPoint("false")) hex_digit_display_318 (.value(register_23_q[43:40]));
  Hex_Digit_Display #(.decimalPoint("false")) hex_digit_display_319 (.value(register_24_q[47:44]));
  Hex_Digit_Display #(.decimalPoint("false")) hex_digit_display_320 (.value(register_24_q[43:40]));
  Hex_Digit_Display #(.decimalPoint("false")) hex_digit_display_321 (.value(register_25_q[47:44]));
  Hex_Digit_Display #(.decimalPoint("false")) hex_digit_display_322 (.value(register_25_q[43:40]));
  Hex_Digit_Display #(.decimalPoint("false")) hex_digit_display_323 (.value(register_26_q[47:44]));
  Hex_Digit_Display #(.decimalPoint("false")) hex_digit_display_324 (.value(register_26_q[43:40]));
  Hex_Digit_Display #(.decimalPoint("false")) hex_digit_display_325 (.value(register_27_q[47:44]));
  Hex_Digit_Display #(.decimalPoint("false")) hex_digit_display_326 (.value(register_27_q[43:40]));
  Hex_Digit_Display #(.decimalPoint("false")) hex_digit_display_327 (.value(register_28_q[47:44]));
  Hex_Digit_Display #(.decimalPoint("false")) hex_digit_display_328 (.value(register_28_q[43:40]));
  Hex_Digit_Display #(.decimalPoint("false")) hex_digit_display_329 (.value(register_29_q[51:48]));
  Hex_Digit_Display #(.decimalPoint("false")) hex_digit_display_330 (.value(register_29_q[47:44]));
  Hex_Digit_Display #(.decimalPoint("false")) hex_digit_display_331 (.value(register_30_q[51:48]));
  Hex_Digit_Display #(.decimalPoint("false")) hex_digit_display_332 (.value(register_30_q[47:44]));
  Hex_Digit_Display #(.decimalPoint("false")) hex_digit_display_333 (.value(register_31_q[51:48]));
  Hex_Digit_Display #(.decimalPoint("false")) hex_digit_display_334 (.value(register_31_q[47:44]));
  Hex_Digit_Display #(.decimalPoint("false")) hex_digit_display_335 (.value(register_32_q[51:48]));
  Hex_Digit_Display #(.decimalPoint("false")) hex_digit_display_336 (.value(register_32_q[47:44]));
  Hex_Digit_Display #(.decimalPoint("false")) hex_digit_display_337 (.value(register_33_q[51:48]));
  Hex_Digit_Display #(.decimalPoint("false")) hex_digit_display_338 (.value(register_33_q[47:44]));
  Hex_Digit_Display #(.decimalPoint("false")) hex_digit_display_339 (.value(register_34_q[51:48]));
  Hex_Digit_Display #(.decimalPoint("false")) hex_digit_display_340 (.value(register_34_q[47:44]));
  Hex_Digit_Display #(.decimalPoint("false")) hex_digit_display_341 (.value(register_35_q[51:48]));
  Hex_Digit_Display #(.decimalPoint("false")) hex_digit_display_342 (.value(register_35_q[47:44]));
  Hex_Digit_Display #(.decimalPoint("false")) hex_digit_display_343 (.value(register_36_q[51:48]));
  Hex_Digit_Display #(.decimalPoint("false")) hex_digit_display_344 (.value(register_36_q[47:44]));
  Hex_Digit_Display #(.decimalPoint("false")) hex_digit_display_345 (.value(register_21_q[39:36]));
  Hex_Digit_Display #(.decimalPoint("false")) hex_digit_display_346 (.value(register_21_q[35:32]));
  Hex_Digit_Display #(.decimalPoint("false")) hex_digit_display_347 (.value(register_22_q[39:36]));
  Hex_Digit_Display #(.decimalPoint("false")) hex_digit_display_348 (.value(register_22_q[35:32]));
  Hex_Digit_Display #(.decimalPoint("false")) hex_digit_display_349 (.value(register_23_q[39:36]));
  Hex_Digit_Display #(.decimalPoint("false")) hex_digit_display_350 (.value(register_23_q[35:32]));
  Hex_Digit_Display #(.decimalPoint("false")) hex_digit_display_351 (.value(register_24_q[39:36]));
  Hex_Digit_Display #(.decimalPoint("false")) hex_digit_display_352 (.value(register_24_q[35:32]));
  Hex_Digit_Display #(.decimalPoint("false")) hex_digit_display_353 (.value(register_25_q[39:36]));
  Hex_Digit_Display #(.decimalPoint("false")) hex_digit_display_354 (.value(register_25_q[35:32]));
  Hex_Digit_Display #(.decimalPoint("false")) hex_digit_display_355 (.value(register_26_q[39:36]));
  Hex_Digit_Display #(.decimalPoint("false")) hex_digit_display_356 (.value(register_26_q[35:32]));
  Hex_Digit_Display #(.decimalPoint("false")) hex_digit_display_357 (.value(register_27_q[39:36]));
  Hex_Digit_Display #(.decimalPoint("false")) hex_digit_display_358 (.value(register_27_q[35:32]));
  Hex_Digit_Display #(.decimalPoint("false")) hex_digit_display_359 (.value(register_28_q[39:36]));
  Hex_Digit_Display #(.decimalPoint("false")) hex_digit_display_360 (.value(register_28_q[35:32]));
  Hex_Digit_Display #(.decimalPoint("false")) hex_digit_display_361 (.value(register_29_q[43:40]));
  Hex_Digit_Display #(.decimalPoint("false")) hex_digit_display_362 (.value(register_29_q[39:36]));
  Hex_Digit_Display #(.decimalPoint("false")) hex_digit_display_363 (.value(register_30_q[43:40]));
  Hex_Digit_Display #(.decimalPoint("false")) hex_digit_display_364 (.value(register_30_q[39:36]));
  Hex_Digit_Display #(.decimalPoint("false")) hex_digit_display_365 (.value(register_31_q[43:40]));
  Hex_Digit_Display #(.decimalPoint("false")) hex_digit_display_366 (.value(register_31_q[39:36]));
  Hex_Digit_Display #(.decimalPoint("false")) hex_digit_display_367 (.value(register_32_q[43:40]));
  Hex_Digit_Display #(.decimalPoint("false")) hex_digit_display_368 (.value(register_32_q[39:36]));
  Hex_Digit_Display #(.decimalPoint("false")) hex_digit_display_369 (.value(register_33_q[43:40]));
  Hex_Digit_Display #(.decimalPoint("false")) hex_digit_display_370 (.value(register_33_q[39:36]));
  Hex_Digit_Display #(.decimalPoint("false")) hex_digit_display_371 (.value(register_34_q[43:40]));
  Hex_Digit_Display #(.decimalPoint("false")) hex_digit_display_372 (.value(register_34_q[39:36]));
  Hex_Digit_Display #(.decimalPoint("false")) hex_digit_display_373 (.value(register_35_q[43:40]));
  Hex_Digit_Display #(.decimalPoint("false")) hex_digit_display_374 (.value(register_35_q[39:36]));
  Hex_Digit_Display #(.decimalPoint("false")) hex_digit_display_375 (.value(register_36_q[43:40]));
  Hex_Digit_Display #(.decimalPoint("false")) hex_digit_display_376 (.value(register_36_q[39:36]));
  Hex_Digit_Display #(.decimalPoint("false")) hex_digit_display_377 (.value(register_21_q[31:28]));
  Hex_Digit_Display #(.decimalPoint("false")) hex_digit_display_378 (.value(register_21_q[27:24]));
  Hex_Digit_Display #(.decimalPoint("false")) hex_digit_display_379 (.value(register_22_q[31:28]));
  Hex_Digit_Display #(.decimalPoint("false")) hex_digit_display_380 (.value(register_22_q[27:24]));
  Hex_Digit_Display #(.decimalPoint("false")) hex_digit_display_381 (.value(register_23_q[31:28]));
  Hex_Digit_Display #(.decimalPoint("false")) hex_digit_display_382 (.value(register_23_q[27:24]));
  Hex_Digit_Display #(.decimalPoint("false")) hex_digit_display_383 (.value(register_24_q[31:28]));
  Hex_Digit_Display #(.decimalPoint("false")) hex_digit_display_384 (.value(register_24_q[27:24]));
  Hex_Digit_Display #(.decimalPoint("false")) hex_digit_display_385 (.value(register_25_q[31:28]));
  Hex_Digit_Display #(.decimalPoint("false")) hex_digit_display_386 (.value(register_25_q[27:24]));
  Hex_Digit_Display #(.decimalPoint("false")) hex_digit_display_387 (.value(register_26_q[31:28]));
  Hex_Digit_Display #(.decimalPoint("false")) hex_digit_display_388 (.value(register_26_q[27:24]));
  Hex_Digit_Display #(.decimalPoint("false")) hex_digit_display_389 (.value(register_27_q[31:28]));
  Hex_Digit_Display #(.decimalPoint("false")) hex_digit_display_390 (.value(register_27_q[27:24]));
  Hex_Digit_Display #(.decimalPoint("false")) hex_digit_display_391 (.value(register_28_q[31:28]));
  Hex_Digit_Display #(.decimalPoint("false")) hex_digit_display_392 (.value(register_28_q[27:24]));
  Hex_Digit_Display #(.decimalPoint("false")) hex_digit_display_393 (.value(register_29_q[35:32]));
  Hex_Digit_Display #(.decimalPoint("false")) hex_digit_display_394 (.value(register_29_q[31:28]));
  Hex_Digit_Display #(.decimalPoint("false")) hex_digit_display_395 (.value(register_30_q[35:32]));
  Hex_Digit_Display #(.decimalPoint("false")) hex_digit_display_396 (.value(register_30_q[31:28]));
  Hex_Digit_Display #(.decimalPoint("false")) hex_digit_display_397 (.value(register_31_q[35:32]));
  Hex_Digit_Display #(.decimalPoint("false")) hex_digit_display_398 (.value(register_31_q[31:28]));
  Hex_Digit_Display #(.decimalPoint("false")) hex_digit_display_399 (.value(register_32_q[35:32]));
  Hex_Digit_Display #(.decimalPoint("false")) hex_digit_display_400 (.value(register_32_q[31:28]));
  Hex_Digit_Display #(.decimalPoint("false")) hex_digit_display_401 (.value(register_33_q[35:32]));
  Hex_Digit_Display #(.decimalPoint("false")) hex_digit_display_402 (.value(register_33_q[31:28]));
  Hex_Digit_Display #(.decimalPoint("false")) hex_digit_display_403 (.value(register_34_q[35:32]));
  Hex_Digit_Display #(.decimalPoint("false")) hex_digit_display_404 (.value(register_34_q[31:28]));
  Hex_Digit_Display #(.decimalPoint("false")) hex_digit_display_405 (.value(register_35_q[35:32]));
  Hex_Digit_Display #(.decimalPoint("false")) hex_digit_display_406 (.value(register_35_q[31:28]));
  Hex_Digit_Display #(.decimalPoint("false")) hex_digit_display_407 (.value(register_36_q[35:32]));
  Hex_Digit_Display #(.decimalPoint("false")) hex_digit_display_408 (.value(register_36_q[31:28]));
  Hex_Digit_Display #(.decimalPoint("false")) hex_digit_display_409 (.value(register_21_q[23:20]));
  Hex_Digit_Display #(.decimalPoint("false")) hex_digit_display_410 (.value(register_21_q[19:16]));
  Hex_Digit_Display #(.decimalPoint("false")) hex_digit_display_411 (.value(register_22_q[23:20]));
  Hex_Digit_Display #(.decimalPoint("false")) hex_digit_display_412 (.value(register_22_q[19:16]));
  Hex_Digit_Display #(.decimalPoint("false")) hex_digit_display_413 (.value(register_23_q[23:20]));
  Hex_Digit_Display #(.decimalPoint("false")) hex_digit_display_414 (.value(register_23_q[19:16]));
  Hex_Digit_Display #(.decimalPoint("false")) hex_digit_display_415 (.value(register_24_q[23:20]));
  Hex_Digit_Display #(.decimalPoint("false")) hex_digit_display_416 (.value(register_24_q[19:16]));
  Hex_Digit_Display #(.decimalPoint("false")) hex_digit_display_417 (.value(register_25_q[23:20]));
  Hex_Digit_Display #(.decimalPoint("false")) hex_digit_display_418 (.value(register_25_q[19:16]));
  Hex_Digit_Display #(.decimalPoint("false")) hex_digit_display_419 (.value(register_26_q[23:20]));
  Hex_Digit_Display #(.decimalPoint("false")) hex_digit_display_420 (.value(register_26_q[19:16]));
  Hex_Digit_Display #(.decimalPoint("false")) hex_digit_display_421 (.value(register_27_q[23:20]));
  Hex_Digit_Display #(.decimalPoint("false")) hex_digit_display_422 (.value(register_27_q[19:16]));
  Hex_Digit_Display #(.decimalPoint("false")) hex_digit_display_423 (.value(register_28_q[23:20]));
  Hex_Digit_Display #(.decimalPoint("false")) hex_digit_display_424 (.value(register_28_q[19:16]));
  Hex_Digit_Display #(.decimalPoint("false")) hex_digit_display_425 (.value(register_29_q[27:24]));
  Hex_Digit_Display #(.decimalPoint("false")) hex_digit_display_426 (.value(register_29_q[23:20]));
  Hex_Digit_Display #(.decimalPoint("false")) hex_digit_display_427 (.value(register_30_q[27:24]));
  Hex_Digit_Display #(.decimalPoint("false")) hex_digit_display_428 (.value(register_30_q[23:20]));
  Hex_Digit_Display #(.decimalPoint("false")) hex_digit_display_429 (.value(register_31_q[27:24]));
  Hex_Digit_Display #(.decimalPoint("false")) hex_digit_display_430 (.value(register_31_q[23:20]));
  Hex_Digit_Display #(.decimalPoint("false")) hex_digit_display_431 (.value(register_32_q[27:24]));
  Hex_Digit_Display #(.decimalPoint("false")) hex_digit_display_432 (.value(register_32_q[23:20]));
  Hex_Digit_Display #(.decimalPoint("false")) hex_digit_display_433 (.value(register_33_q[27:24]));
  Hex_Digit_Display #(.decimalPoint("false")) hex_digit_display_434 (.value(register_33_q[23:20]));
  Hex_Digit_Display #(.decimalPoint("false")) hex_digit_display_435 (.value(register_34_q[27:24]));
  Hex_Digit_Display #(.decimalPoint("false")) hex_digit_display_436 (.value(register_34_q[23:20]));
  Hex_Digit_Display #(.decimalPoint("false")) hex_digit_display_437 (.value(register_35_q[27:24]));
  Hex_Digit_Display #(.decimalPoint("false")) hex_digit_display_438 (.value(register_35_q[23:20]));
  Hex_Digit_Display #(.decimalPoint("false")) hex_digit_display_439 (.value(register_36_q[27:24]));
  Hex_Digit_Display #(.decimalPoint("false")) hex_digit_display_440 (.value(register_36_q[23:20]));
  Hex_Digit_Display #(.decimalPoint("false")) hex_digit_display_441 (.value(register_21_q[15:12]));
  Hex_Digit_Display #(.decimalPoint("false")) hex_digit_display_442 (.value(register_21_q[11:8]));
  Hex_Digit_Display #(.decimalPoint("false")) hex_digit_display_443 (.value(register_22_q[15:12]));
  Hex_Digit_Display #(.decimalPoint("false")) hex_digit_display_444 (.value(register_22_q[11:8]));
  Hex_Digit_Display #(.decimalPoint("false")) hex_digit_display_445 (.value(register_23_q[15:12]));
  Hex_Digit_Display #(.decimalPoint("false")) hex_digit_display_446 (.value(register_23_q[11:8]));
  Hex_Digit_Display #(.decimalPoint("false")) hex_digit_display_447 (.value(register_24_q[15:12]));
  Hex_Digit_Display #(.decimalPoint("false")) hex_digit_display_448 (.value(register_24_q[11:8]));
  Hex_Digit_Display #(.decimalPoint("false")) hex_digit_display_449 (.value(register_25_q[15:12]));
  Hex_Digit_Display #(.decimalPoint("false")) hex_digit_display_450 (.value(register_25_q[11:8]));
  Hex_Digit_Display #(.decimalPoint("false")) hex_digit_display_451 (.value(register_26_q[15:12]));
  Hex_Digit_Display #(.decimalPoint("false")) hex_digit_display_452 (.value(register_26_q[11:8]));
  Hex_Digit_Display #(.decimalPoint("false")) hex_digit_display_453 (.value(register_27_q[15:12]));
  Hex_Digit_Display #(.decimalPoint("false")) hex_digit_display_454 (.value(register_27_q[11:8]));
  Hex_Digit_Display #(.decimalPoint("false")) hex_digit_display_455 (.value(register_28_q[15:12]));
  Hex_Digit_Display #(.decimalPoint("false")) hex_digit_display_456 (.value(register_28_q[11:8]));
  Hex_Digit_Display #(.decimalPoint("false")) hex_digit_display_457 (.value(register_29_q[19:16]));
  Hex_Digit_Display #(.decimalPoint("false")) hex_digit_display_458 (.value(register_29_q[15:12]));
  Hex_Digit_Display #(.decimalPoint("false")) hex_digit_display_459 (.value(register_30_q[19:16]));
  Hex_Digit_Display #(.decimalPoint("false")) hex_digit_display_460 (.value(register_30_q[15:12]));
  Hex_Digit_Display #(.decimalPoint("false")) hex_digit_display_461 (.value(register_31_q[19:16]));
  Hex_Digit_Display #(.decimalPoint("false")) hex_digit_display_462 (.value(register_31_q[15:12]));
  Hex_Digit_Display #(.decimalPoint("false")) hex_digit_display_463 (.value(register_32_q[19:16]));
  Hex_Digit_Display #(.decimalPoint("false")) hex_digit_display_464 (.value(register_32_q[15:12]));
  Hex_Digit_Display #(.decimalPoint("false")) hex_digit_display_465 (.value(register_33_q[19:16]));
  Hex_Digit_Display #(.decimalPoint("false")) hex_digit_display_466 (.value(register_33_q[15:12]));
  Hex_Digit_Display #(.decimalPoint("false")) hex_digit_display_467 (.value(register_34_q[19:16]));
  Hex_Digit_Display #(.decimalPoint("false")) hex_digit_display_468 (.value(register_34_q[15:12]));
  Hex_Digit_Display #(.decimalPoint("false")) hex_digit_display_469 (.value(register_35_q[19:16]));
  Hex_Digit_Display #(.decimalPoint("false")) hex_digit_display_470 (.value(register_35_q[15:12]));
  Hex_Digit_Display #(.decimalPoint("false")) hex_digit_display_471 (.value(register_36_q[19:16]));
  Hex_Digit_Display #(.decimalPoint("false")) hex_digit_display_472 (.value(register_36_q[15:12]));
  Demultiplexer #(.select(4)) demultiplexer_1 (
    .out0(DISPLAY_1), .out1(DISPLAY_2), .out2(DISPLAY_3), .out3(DISPLAY_4), .out4(DISPLAY_5),
    .out5(DISPLAY_6), .out6(DISPLAY_7), .out7(DISPLAY_8), .out8(DISPLAY_9), .out9(DISPLAY_10),
    .out10(DISPLAY_11), .out11(DISPLAY_12), .out12(DISPLAY_13), .out13(DISPLAY_14), .out14(DISPLAY_15),
    .out15(DISPLAY_16), .in(1'b1), .sel(CLOCK_VALUE[3:0]));
  Hex_Digit_Display #(.decimalPoint("false")) hex_digit_display_473 (.value(register_21_q[7:4]));
  Hex_Digit_Display #(.decimalPoint("false")) hex_digit_display_474 (.value(register_21_q[3:0]));
  Hex_Digit_Display #(.decimalPoint("false")) hex_digit_display_475 (.value(register_22_q[7:4]));
  Hex_Digit_Display #(.decimalPoint("false")) hex_digit_display_476 (.value(register_22_q[3:0]));
  Hex_Digit_Display #(.decimalPoint("false")) hex_digit_display_477 (.value(register_23_q[7:4]));
  Hex_Digit_Display #(.decimalPoint("false")) hex_digit_display_478 (.value(register_23_q[3:0]));
  Hex_Digit_Display #(.decimalPoint("false")) hex_digit_display_479 (.value(register_24_q[7:4]));
  Hex_Digit_Display #(.decimalPoint("false")) hex_digit_display_480 (.value(register_24_q[3:0]));
  Hex_Digit_Display #(.decimalPoint("false")) hex_digit_display_481 (.value(register_25_q[7:4]));
  Hex_Digit_Display #(.decimalPoint("false")) hex_digit_display_482 (.value(register_25_q[3:0]));
  Hex_Digit_Display #(.decimalPoint("false")) hex_digit_display_483 (.value(register_26_q[7:4]));
  Hex_Digit_Display #(.decimalPoint("false")) hex_digit_display_484 (.value(register_26_q[3:0]));
  Hex_Digit_Display #(.decimalPoint("false")) hex_digit_display_485 (.value(register_27_q[7:4]));
  Hex_Digit_Display #(.decimalPoint("false")) hex_digit_display_486 (.value(register_27_q[3:0]));
  Hex_Digit_Display #(.decimalPoint("false")) hex_digit_display_487 (.value(register_28_q[7:4]));
  Hex_Digit_Display #(.decimalPoint("false")) hex_digit_display_488 (.value(register_28_q[3:0]));
  Hex_Digit_Display #(.decimalPoint("false")) hex_digit_display_489 (.value(register_29_q[11:8]));
  Hex_Digit_Display #(.decimalPoint("false")) hex_digit_display_490 (.value(register_29_q[7:4]));
  Hex_Digit_Display #(.decimalPoint("false")) hex_digit_display_491 (.value(register_30_q[11:8]));
  Hex_Digit_Display #(.decimalPoint("false")) hex_digit_display_492 (.value(register_30_q[7:4]));
  Hex_Digit_Display #(.decimalPoint("false")) hex_digit_display_493 (.value(register_31_q[11:8]));
  Hex_Digit_Display #(.decimalPoint("false")) hex_digit_display_494 (.value(register_31_q[7:4]));
  Hex_Digit_Display #(.decimalPoint("false")) hex_digit_display_495 (.value(register_32_q[11:8]));
  Hex_Digit_Display #(.decimalPoint("false")) hex_digit_display_496 (.value(register_32_q[7:4]));
  Hex_Digit_Display #(.decimalPoint("false")) hex_digit_display_497 (.value(register_33_q[11:8]));
  Hex_Digit_Display #(.decimalPoint("false")) hex_digit_display_498 (.value(register_33_q[7:4]));
  Hex_Digit_Display #(.decimalPoint("false")) hex_digit_display_499 (.value(register_34_q[11:8]));
  Hex_Digit_Display #(.decimalPoint("false")) hex_digit_display_500 (.value(register_34_q[7:4]));
  Hex_Digit_Display #(.decimalPoint("false")) hex_digit_display_501 (.value(register_35_q[11:8]));
  Hex_Digit_Display #(.decimalPoint("false")) hex_digit_display_502 (.value(register_35_q[7:4]));
  Hex_Digit_Display #(.decimalPoint("false")) hex_digit_display_503 (.value(register_36_q[11:8]));
  Hex_Digit_Display #(.decimalPoint("false")) hex_digit_display_504 (.value(register_36_q[7:4]));
  Hex_Digit_Display #(.decimalPoint("false")) hex_digit_display_505 (.value(register_29_q[3:0]));
  Hex_Digit_Display #(.decimalPoint("false")) hex_digit_display_506 (.value(register_30_q[3:0]));
  Hex_Digit_Display #(.decimalPoint("false")) hex_digit_display_507 (.value(register_31_q[3:0]));
  Hex_Digit_Display #(.decimalPoint("false")) hex_digit_display_508 (.value(register_32_q[3:0]));
  Hex_Digit_Display #(.decimalPoint("false")) hex_digit_display_509 (.value(register_33_q[3:0]));
  Hex_Digit_Display #(.decimalPoint("false")) hex_digit_display_510 (.value(register_34_q[3:0]));
  Hex_Digit_Display #(.decimalPoint("false")) hex_digit_display_511 (.value(register_35_q[3:0]));
  Hex_Digit_Display #(.decimalPoint("false")) hex_digit_display_512 (.value(register_36_q[3:0]));
  Register #(.width(64)) register_37 (.D(S0), .en(DISPLAY_2), .Q(register_37_q), .clk(undriven_14));  // open: clr
  Hex_Digit_Display #(.decimalPoint("false")) hex_digit_display_513 (.value(register_37_q[63:60]));
  Register #(.width(64)) register_38 (.D(S2), .en(DISPLAY_2), .Q(register_38_q), .clk(undriven_14));  // open: clr
  Hex_Digit_Display #(.decimalPoint("false")) hex_digit_display_514 (.value(register_38_q[63:60]));
  Register #(.width(64)) register_39 (.D(S0), .en(DISPLAY_2), .Q(register_39_q), .clk(undriven_14));  // open: clr
  Hex_Digit_Display #(.decimalPoint("false")) hex_digit_display_515 (.value(register_39_q[63:60]));
  Register #(.width(64)) register_40 (.D(S2), .en(DISPLAY_2), .Q(register_40_q), .clk(undriven_14));  // open: clr
  Hex_Digit_Display #(.decimalPoint("false")) hex_digit_display_516 (.value(register_40_q[63:60]));
  Register #(.width(64)) register_41 (.D(S0), .en(undriven_12), .Q(register_41_q), .clk(undriven_15));  // open: clr
  Register #(.width(64)) register_42 (.D(S2), .en(undriven_12), .Q(register_42_q), .clk(undriven_15));  // open: clr
  Register #(.width(64)) register_43 (.D(S0), .en(undriven_13), .Q(register_43_q), .clk(undriven_16));  // open: clr
  Register #(.width(64)) register_44 (.D(S2), .en(undriven_13), .Q(register_44_q), .clk(undriven_16));  // open: clr
  Register #(.width(64)) register_45 (.D(S0), .en(undriven_17), .Q(register_45_q), .clk(undriven_21));  // open: clr
  Register #(.width(64)) register_46 (.D(S2), .en(undriven_17), .Q(register_46_q), .clk(undriven_21));  // open: clr
  Register #(.width(64)) register_47 (.D(S0), .en(undriven_18), .Q(register_47_q), .clk(undriven_22));  // open: clr
  Register #(.width(64)) register_48 (.D(S2), .en(undriven_18), .Q(register_48_q), .clk(undriven_22));  // open: clr
  Hex_Digit_Display #(.decimalPoint("false")) hex_digit_display_517 (.value(register_37_q[59:56]));
  Hex_Digit_Display #(.decimalPoint("false")) hex_digit_display_518 (.value(register_37_q[55:52]));
  Hex_Digit_Display #(.decimalPoint("false")) hex_digit_display_519 (.value(register_38_q[59:56]));
  Hex_Digit_Display #(.decimalPoint("false")) hex_digit_display_520 (.value(register_38_q[55:52]));
  Hex_Digit_Display #(.decimalPoint("false")) hex_digit_display_521 (.value(register_39_q[59:56]));
  Hex_Digit_Display #(.decimalPoint("false")) hex_digit_display_522 (.value(register_39_q[55:52]));
  Hex_Digit_Display #(.decimalPoint("false")) hex_digit_display_523 (.value(register_40_q[59:56]));
  Hex_Digit_Display #(.decimalPoint("false")) hex_digit_display_524 (.value(register_40_q[55:52]));
  Hex_Digit_Display #(.decimalPoint("false")) hex_digit_display_525 (.value(register_41_q[63:60]));
  Hex_Digit_Display #(.decimalPoint("false")) hex_digit_display_526 (.value(register_41_q[59:56]));
  Hex_Digit_Display #(.decimalPoint("false")) hex_digit_display_527 (.value(register_42_q[63:60]));
  Hex_Digit_Display #(.decimalPoint("false")) hex_digit_display_528 (.value(register_42_q[59:56]));
  Hex_Digit_Display #(.decimalPoint("false")) hex_digit_display_529 (.value(register_43_q[63:60]));
  Hex_Digit_Display #(.decimalPoint("false")) hex_digit_display_530 (.value(register_43_q[59:56]));
  Hex_Digit_Display #(.decimalPoint("false")) hex_digit_display_531 (.value(register_44_q[63:60]));
  Hex_Digit_Display #(.decimalPoint("false")) hex_digit_display_532 (.value(register_44_q[59:56]));
  Hex_Digit_Display #(.decimalPoint("false")) hex_digit_display_533 (.value(register_45_q[63:60]));
  Hex_Digit_Display #(.decimalPoint("false")) hex_digit_display_534 (.value(register_45_q[59:56]));
  Hex_Digit_Display #(.decimalPoint("false")) hex_digit_display_535 (.value(register_46_q[63:60]));
  Hex_Digit_Display #(.decimalPoint("false")) hex_digit_display_536 (.value(register_46_q[59:56]));
  Hex_Digit_Display #(.decimalPoint("false")) hex_digit_display_537 (.value(register_47_q[63:60]));
  Hex_Digit_Display #(.decimalPoint("false")) hex_digit_display_538 (.value(register_47_q[59:56]));
  Hex_Digit_Display #(.decimalPoint("false")) hex_digit_display_539 (.value(register_48_q[63:60]));
  Hex_Digit_Display #(.decimalPoint("false")) hex_digit_display_540 (.value(register_48_q[59:56]));
  Register #(.width(64)) register_49 (.D(S0), .en(undriven_19), .Q(register_49_q), .clk(undriven_23));  // open: clr
  Hex_Digit_Display #(.decimalPoint("false")) hex_digit_display_541 (.value(register_49_q[63:60]));
  Register #(.width(64)) register_50 (.D(S2), .en(undriven_19), .Q(register_50_q), .clk(undriven_23));  // open: clr
  Hex_Digit_Display #(.decimalPoint("false")) hex_digit_display_542 (.value(register_50_q[63:60]));
  Register #(.width(64)) register_51 (.D(S0), .en(undriven_20), .Q(register_51_q), .clk(undriven_24));  // open: clr
  Hex_Digit_Display #(.decimalPoint("false")) hex_digit_display_543 (.value(register_51_q[63:60]));
  Register #(.width(64)) register_52 (.D(S2), .en(undriven_20), .Q(register_52_q), .clk(undriven_24));  // open: clr
  Hex_Digit_Display #(.decimalPoint("false")) hex_digit_display_544 (.value(register_52_q[63:60]));
  Hex_Digit_Display #(.decimalPoint("false")) hex_digit_display_545 (.value(register_37_q[51:48]));
  Hex_Digit_Display #(.decimalPoint("false")) hex_digit_display_546 (.value(register_37_q[47:44]));
  Hex_Digit_Display #(.decimalPoint("false")) hex_digit_display_547 (.value(register_38_q[51:48]));
  Hex_Digit_Display #(.decimalPoint("false")) hex_digit_display_548 (.value(register_38_q[47:44]));
  Hex_Digit_Display #(.decimalPoint("false")) hex_digit_display_549 (.value(register_39_q[51:48]));
  Hex_Digit_Display #(.decimalPoint("false")) hex_digit_display_550 (.value(register_39_q[47:44]));
  Hex_Digit_Display #(.decimalPoint("false")) hex_digit_display_551 (.value(register_40_q[51:48]));
  Hex_Digit_Display #(.decimalPoint("false")) hex_digit_display_552 (.value(register_40_q[47:44]));
  Hex_Digit_Display #(.decimalPoint("false")) hex_digit_display_553 (.value(register_41_q[55:52]));
  Hex_Digit_Display #(.decimalPoint("false")) hex_digit_display_554 (.value(register_41_q[51:48]));
  Hex_Digit_Display #(.decimalPoint("false")) hex_digit_display_555 (.value(register_42_q[55:52]));
  Hex_Digit_Display #(.decimalPoint("false")) hex_digit_display_556 (.value(register_42_q[51:48]));
  Hex_Digit_Display #(.decimalPoint("false")) hex_digit_display_557 (.value(register_43_q[55:52]));
  Hex_Digit_Display #(.decimalPoint("false")) hex_digit_display_558 (.value(register_43_q[51:48]));
  Hex_Digit_Display #(.decimalPoint("false")) hex_digit_display_559 (.value(register_44_q[55:52]));
  Hex_Digit_Display #(.decimalPoint("false")) hex_digit_display_560 (.value(register_44_q[51:48]));
  Hex_Digit_Display #(.decimalPoint("false")) hex_digit_display_561 (.value(register_45_q[55:52]));
  Hex_Digit_Display #(.decimalPoint("false")) hex_digit_display_562 (.value(register_45_q[51:48]));
  Hex_Digit_Display #(.decimalPoint("false")) hex_digit_display_563 (.value(register_46_q[55:52]));
  Hex_Digit_Display #(.decimalPoint("false")) hex_digit_display_564 (.value(register_46_q[51:48]));
  Hex_Digit_Display #(.decimalPoint("false")) hex_digit_display_565 (.value(register_47_q[55:52]));
  Hex_Digit_Display #(.decimalPoint("false")) hex_digit_display_566 (.value(register_47_q[51:48]));
  Hex_Digit_Display #(.decimalPoint("false")) hex_digit_display_567 (.value(register_48_q[55:52]));
  Hex_Digit_Display #(.decimalPoint("false")) hex_digit_display_568 (.value(register_48_q[51:48]));
  Hex_Digit_Display #(.decimalPoint("false")) hex_digit_display_569 (.value(register_49_q[59:56]));
  Hex_Digit_Display #(.decimalPoint("false")) hex_digit_display_570 (.value(register_49_q[55:52]));
  Hex_Digit_Display #(.decimalPoint("false")) hex_digit_display_571 (.value(register_50_q[59:56]));
  Hex_Digit_Display #(.decimalPoint("false")) hex_digit_display_572 (.value(register_50_q[55:52]));
  Hex_Digit_Display #(.decimalPoint("false")) hex_digit_display_573 (.value(register_51_q[59:56]));
  Hex_Digit_Display #(.decimalPoint("false")) hex_digit_display_574 (.value(register_51_q[55:52]));
  Hex_Digit_Display #(.decimalPoint("false")) hex_digit_display_575 (.value(register_52_q[59:56]));
  Hex_Digit_Display #(.decimalPoint("false")) hex_digit_display_576 (.value(register_52_q[55:52]));
  Hex_Digit_Display #(.decimalPoint("false")) hex_digit_display_577 (.value(register_37_q[43:40]));
  Hex_Digit_Display #(.decimalPoint("false")) hex_digit_display_578 (.value(register_37_q[39:36]));
  Hex_Digit_Display #(.decimalPoint("false")) hex_digit_display_579 (.value(register_38_q[43:40]));
  Hex_Digit_Display #(.decimalPoint("false")) hex_digit_display_580 (.value(register_38_q[39:36]));
  Hex_Digit_Display #(.decimalPoint("false")) hex_digit_display_581 (.value(register_39_q[43:40]));
  Hex_Digit_Display #(.decimalPoint("false")) hex_digit_display_582 (.value(register_39_q[39:36]));
  Hex_Digit_Display #(.decimalPoint("false")) hex_digit_display_583 (.value(register_40_q[43:40]));
  Hex_Digit_Display #(.decimalPoint("false")) hex_digit_display_584 (.value(register_40_q[39:36]));
  Hex_Digit_Display #(.decimalPoint("false")) hex_digit_display_585 (.value(register_41_q[47:44]));
  Hex_Digit_Display #(.decimalPoint("false")) hex_digit_display_586 (.value(register_41_q[43:40]));
  Hex_Digit_Display #(.decimalPoint("false")) hex_digit_display_587 (.value(register_42_q[47:44]));
  Hex_Digit_Display #(.decimalPoint("false")) hex_digit_display_588 (.value(register_42_q[43:40]));
  Hex_Digit_Display #(.decimalPoint("false")) hex_digit_display_589 (.value(register_43_q[47:44]));
  Hex_Digit_Display #(.decimalPoint("false")) hex_digit_display_590 (.value(register_43_q[43:40]));
  Hex_Digit_Display #(.decimalPoint("false")) hex_digit_display_591 (.value(register_44_q[47:44]));
  Hex_Digit_Display #(.decimalPoint("false")) hex_digit_display_592 (.value(register_44_q[43:40]));
  Hex_Digit_Display #(.decimalPoint("false")) hex_digit_display_593 (.value(register_45_q[47:44]));
  Hex_Digit_Display #(.decimalPoint("false")) hex_digit_display_594 (.value(register_45_q[43:40]));
  Hex_Digit_Display #(.decimalPoint("false")) hex_digit_display_595 (.value(register_46_q[47:44]));
  Hex_Digit_Display #(.decimalPoint("false")) hex_digit_display_596 (.value(register_46_q[43:40]));
  Hex_Digit_Display #(.decimalPoint("false")) hex_digit_display_597 (.value(register_47_q[47:44]));
  Hex_Digit_Display #(.decimalPoint("false")) hex_digit_display_598 (.value(register_47_q[43:40]));
  Hex_Digit_Display #(.decimalPoint("false")) hex_digit_display_599 (.value(register_48_q[47:44]));
  Hex_Digit_Display #(.decimalPoint("false")) hex_digit_display_600 (.value(register_48_q[43:40]));
  Hex_Digit_Display #(.decimalPoint("false")) hex_digit_display_601 (.value(register_49_q[51:48]));
  Hex_Digit_Display #(.decimalPoint("false")) hex_digit_display_602 (.value(register_49_q[47:44]));
  Hex_Digit_Display #(.decimalPoint("false")) hex_digit_display_603 (.value(register_50_q[51:48]));
  Hex_Digit_Display #(.decimalPoint("false")) hex_digit_display_604 (.value(register_50_q[47:44]));
  Hex_Digit_Display #(.decimalPoint("false")) hex_digit_display_605 (.value(register_51_q[51:48]));
  Hex_Digit_Display #(.decimalPoint("false")) hex_digit_display_606 (.value(register_51_q[47:44]));
  Hex_Digit_Display #(.decimalPoint("false")) hex_digit_display_607 (.value(register_52_q[51:48]));
  Hex_Digit_Display #(.decimalPoint("false")) hex_digit_display_608 (.value(register_52_q[47:44]));
  Hex_Digit_Display #(.decimalPoint("false")) hex_digit_display_609 (.value(register_37_q[35:32]));
  Hex_Digit_Display #(.decimalPoint("false")) hex_digit_display_610 (.value(register_37_q[31:28]));
  Hex_Digit_Display #(.decimalPoint("false")) hex_digit_display_611 (.value(register_38_q[35:32]));
  Hex_Digit_Display #(.decimalPoint("false")) hex_digit_display_612 (.value(register_38_q[31:28]));
  Hex_Digit_Display #(.decimalPoint("false")) hex_digit_display_613 (.value(register_39_q[35:32]));
  Hex_Digit_Display #(.decimalPoint("false")) hex_digit_display_614 (.value(register_39_q[31:28]));
  Hex_Digit_Display #(.decimalPoint("false")) hex_digit_display_615 (.value(register_40_q[35:32]));
  Hex_Digit_Display #(.decimalPoint("false")) hex_digit_display_616 (.value(register_40_q[31:28]));
  Hex_Digit_Display #(.decimalPoint("false")) hex_digit_display_617 (.value(register_41_q[39:36]));
  Hex_Digit_Display #(.decimalPoint("false")) hex_digit_display_618 (.value(register_41_q[35:32]));
  Hex_Digit_Display #(.decimalPoint("false")) hex_digit_display_619 (.value(register_42_q[39:36]));
  Hex_Digit_Display #(.decimalPoint("false")) hex_digit_display_620 (.value(register_42_q[35:32]));
  Hex_Digit_Display #(.decimalPoint("false")) hex_digit_display_621 (.value(register_43_q[39:36]));
  Hex_Digit_Display #(.decimalPoint("false")) hex_digit_display_622 (.value(register_43_q[35:32]));
  Hex_Digit_Display #(.decimalPoint("false")) hex_digit_display_623 (.value(register_44_q[39:36]));
  Hex_Digit_Display #(.decimalPoint("false")) hex_digit_display_624 (.value(register_44_q[35:32]));
  Hex_Digit_Display #(.decimalPoint("false")) hex_digit_display_625 (.value(register_45_q[39:36]));
  Hex_Digit_Display #(.decimalPoint("false")) hex_digit_display_626 (.value(register_45_q[35:32]));
  Hex_Digit_Display #(.decimalPoint("false")) hex_digit_display_627 (.value(register_46_q[39:36]));
  Hex_Digit_Display #(.decimalPoint("false")) hex_digit_display_628 (.value(register_46_q[35:32]));
  Hex_Digit_Display #(.decimalPoint("false")) hex_digit_display_629 (.value(register_47_q[39:36]));
  Hex_Digit_Display #(.decimalPoint("false")) hex_digit_display_630 (.value(register_47_q[35:32]));
  Hex_Digit_Display #(.decimalPoint("false")) hex_digit_display_631 (.value(register_48_q[39:36]));
  Hex_Digit_Display #(.decimalPoint("false")) hex_digit_display_632 (.value(register_48_q[35:32]));
  Hex_Digit_Display #(.decimalPoint("false")) hex_digit_display_633 (.value(register_49_q[43:40]));
  Hex_Digit_Display #(.decimalPoint("false")) hex_digit_display_634 (.value(register_49_q[39:36]));
  Hex_Digit_Display #(.decimalPoint("false")) hex_digit_display_635 (.value(register_50_q[43:40]));
  Hex_Digit_Display #(.decimalPoint("false")) hex_digit_display_636 (.value(register_50_q[39:36]));
  Hex_Digit_Display #(.decimalPoint("false")) hex_digit_display_637 (.value(register_51_q[43:40]));
  Hex_Digit_Display #(.decimalPoint("false")) hex_digit_display_638 (.value(register_51_q[39:36]));
  Hex_Digit_Display #(.decimalPoint("false")) hex_digit_display_639 (.value(register_52_q[43:40]));
  Hex_Digit_Display #(.decimalPoint("false")) hex_digit_display_640 (.value(register_52_q[39:36]));
  Hex_Digit_Display #(.decimalPoint("false")) hex_digit_display_641 (.value(register_37_q[27:24]));
  Hex_Digit_Display #(.decimalPoint("false")) hex_digit_display_642 (.value(register_37_q[23:20]));
  Hex_Digit_Display #(.decimalPoint("false")) hex_digit_display_643 (.value(register_38_q[27:24]));
  Hex_Digit_Display #(.decimalPoint("false")) hex_digit_display_644 (.value(register_38_q[23:20]));
  Hex_Digit_Display #(.decimalPoint("false")) hex_digit_display_645 (.value(register_39_q[27:24]));
  Hex_Digit_Display #(.decimalPoint("false")) hex_digit_display_646 (.value(register_39_q[23:20]));
  Hex_Digit_Display #(.decimalPoint("false")) hex_digit_display_647 (.value(register_40_q[27:24]));
  Hex_Digit_Display #(.decimalPoint("false")) hex_digit_display_648 (.value(register_40_q[23:20]));
  Hex_Digit_Display #(.decimalPoint("false")) hex_digit_display_649 (.value(register_41_q[31:28]));
  Hex_Digit_Display #(.decimalPoint("false")) hex_digit_display_650 (.value(register_41_q[27:24]));
  Hex_Digit_Display #(.decimalPoint("false")) hex_digit_display_651 (.value(register_42_q[31:28]));
  Hex_Digit_Display #(.decimalPoint("false")) hex_digit_display_652 (.value(register_42_q[27:24]));
  Hex_Digit_Display #(.decimalPoint("false")) hex_digit_display_653 (.value(register_43_q[31:28]));
  Hex_Digit_Display #(.decimalPoint("false")) hex_digit_display_654 (.value(register_43_q[27:24]));
  Hex_Digit_Display #(.decimalPoint("false")) hex_digit_display_655 (.value(register_44_q[31:28]));
  Hex_Digit_Display #(.decimalPoint("false")) hex_digit_display_656 (.value(register_44_q[27:24]));
  Hex_Digit_Display #(.decimalPoint("false")) hex_digit_display_657 (.value(register_45_q[31:28]));
  Hex_Digit_Display #(.decimalPoint("false")) hex_digit_display_658 (.value(register_45_q[27:24]));
  Hex_Digit_Display #(.decimalPoint("false")) hex_digit_display_659 (.value(register_46_q[31:28]));
  Hex_Digit_Display #(.decimalPoint("false")) hex_digit_display_660 (.value(register_46_q[27:24]));
  Hex_Digit_Display #(.decimalPoint("false")) hex_digit_display_661 (.value(register_47_q[31:28]));
  Hex_Digit_Display #(.decimalPoint("false")) hex_digit_display_662 (.value(register_47_q[27:24]));
  Hex_Digit_Display #(.decimalPoint("false")) hex_digit_display_663 (.value(register_48_q[31:28]));
  Hex_Digit_Display #(.decimalPoint("false")) hex_digit_display_664 (.value(register_48_q[27:24]));
  Hex_Digit_Display #(.decimalPoint("false")) hex_digit_display_665 (.value(register_49_q[35:32]));
  Hex_Digit_Display #(.decimalPoint("false")) hex_digit_display_666 (.value(register_49_q[31:28]));
  Hex_Digit_Display #(.decimalPoint("false")) hex_digit_display_667 (.value(register_50_q[35:32]));
  Hex_Digit_Display #(.decimalPoint("false")) hex_digit_display_668 (.value(register_50_q[31:28]));
  Hex_Digit_Display #(.decimalPoint("false")) hex_digit_display_669 (.value(register_51_q[35:32]));
  Hex_Digit_Display #(.decimalPoint("false")) hex_digit_display_670 (.value(register_51_q[31:28]));
  Hex_Digit_Display #(.decimalPoint("false")) hex_digit_display_671 (.value(register_52_q[35:32]));
  Hex_Digit_Display #(.decimalPoint("false")) hex_digit_display_672 (.value(register_52_q[31:28]));
  Hex_Digit_Display #(.decimalPoint("false")) hex_digit_display_673 (.value(register_37_q[19:16]));
  Hex_Digit_Display #(.decimalPoint("false")) hex_digit_display_674 (.value(register_37_q[15:12]));
  Hex_Digit_Display #(.decimalPoint("false")) hex_digit_display_675 (.value(register_38_q[19:16]));
  Hex_Digit_Display #(.decimalPoint("false")) hex_digit_display_676 (.value(register_38_q[15:12]));
  Hex_Digit_Display #(.decimalPoint("false")) hex_digit_display_677 (.value(register_39_q[19:16]));
  Hex_Digit_Display #(.decimalPoint("false")) hex_digit_display_678 (.value(register_39_q[15:12]));
  Hex_Digit_Display #(.decimalPoint("false")) hex_digit_display_679 (.value(register_40_q[19:16]));
  Hex_Digit_Display #(.decimalPoint("false")) hex_digit_display_680 (.value(register_40_q[15:12]));
  Hex_Digit_Display #(.decimalPoint("false")) hex_digit_display_681 (.value(register_41_q[23:20]));
  Hex_Digit_Display #(.decimalPoint("false")) hex_digit_display_682 (.value(register_41_q[19:16]));
  Hex_Digit_Display #(.decimalPoint("false")) hex_digit_display_683 (.value(register_42_q[23:20]));
  Hex_Digit_Display #(.decimalPoint("false")) hex_digit_display_684 (.value(register_42_q[19:16]));
  Hex_Digit_Display #(.decimalPoint("false")) hex_digit_display_685 (.value(register_43_q[23:20]));
  Hex_Digit_Display #(.decimalPoint("false")) hex_digit_display_686 (.value(register_43_q[19:16]));
  Hex_Digit_Display #(.decimalPoint("false")) hex_digit_display_687 (.value(register_44_q[23:20]));
  Hex_Digit_Display #(.decimalPoint("false")) hex_digit_display_688 (.value(register_44_q[19:16]));
  Hex_Digit_Display #(.decimalPoint("false")) hex_digit_display_689 (.value(register_45_q[23:20]));
  Hex_Digit_Display #(.decimalPoint("false")) hex_digit_display_690 (.value(register_45_q[19:16]));
  Hex_Digit_Display #(.decimalPoint("false")) hex_digit_display_691 (.value(register_46_q[23:20]));
  Hex_Digit_Display #(.decimalPoint("false")) hex_digit_display_692 (.value(register_46_q[19:16]));
  Hex_Digit_Display #(.decimalPoint("false")) hex_digit_display_693 (.value(register_47_q[23:20]));
  Hex_Digit_Display #(.decimalPoint("false")) hex_digit_display_694 (.value(register_47_q[19:16]));
  Hex_Digit_Display #(.decimalPoint("false")) hex_digit_display_695 (.value(register_48_q[23:20]));
  Hex_Digit_Display #(.decimalPoint("false")) hex_digit_display_696 (.value(register_48_q[19:16]));
  Hex_Digit_Display #(.decimalPoint("false")) hex_digit_display_697 (.value(register_49_q[27:24]));
  Hex_Digit_Display #(.decimalPoint("false")) hex_digit_display_698 (.value(register_49_q[23:20]));
  Hex_Digit_Display #(.decimalPoint("false")) hex_digit_display_699 (.value(register_50_q[27:24]));
  Hex_Digit_Display #(.decimalPoint("false")) hex_digit_display_700 (.value(register_50_q[23:20]));
  Hex_Digit_Display #(.decimalPoint("false")) hex_digit_display_701 (.value(register_51_q[27:24]));
  Hex_Digit_Display #(.decimalPoint("false")) hex_digit_display_702 (.value(register_51_q[23:20]));
  Hex_Digit_Display #(.decimalPoint("false")) hex_digit_display_703 (.value(register_52_q[27:24]));
  Hex_Digit_Display #(.decimalPoint("false")) hex_digit_display_704 (.value(register_52_q[23:20]));
  Hex_Digit_Display #(.decimalPoint("false")) hex_digit_display_705 (.value(register_37_q[11:8]));
  Hex_Digit_Display #(.decimalPoint("false")) hex_digit_display_706 (.value(register_37_q[7:4]));
  Hex_Digit_Display #(.decimalPoint("false")) hex_digit_display_707 (.value(register_38_q[11:8]));
  Hex_Digit_Display #(.decimalPoint("false")) hex_digit_display_708 (.value(register_38_q[7:4]));
  Hex_Digit_Display #(.decimalPoint("false")) hex_digit_display_709 (.value(register_39_q[11:8]));
  Hex_Digit_Display #(.decimalPoint("false")) hex_digit_display_710 (.value(register_39_q[7:4]));
  Hex_Digit_Display #(.decimalPoint("false")) hex_digit_display_711 (.value(register_40_q[11:8]));
  Hex_Digit_Display #(.decimalPoint("false")) hex_digit_display_712 (.value(register_40_q[7:4]));
  Hex_Digit_Display #(.decimalPoint("false")) hex_digit_display_713 (.value(register_41_q[15:12]));
  Hex_Digit_Display #(.decimalPoint("false")) hex_digit_display_714 (.value(register_41_q[11:8]));
  Hex_Digit_Display #(.decimalPoint("false")) hex_digit_display_715 (.value(register_42_q[15:12]));
  Hex_Digit_Display #(.decimalPoint("false")) hex_digit_display_716 (.value(register_42_q[11:8]));
  Hex_Digit_Display #(.decimalPoint("false")) hex_digit_display_717 (.value(register_43_q[15:12]));
  Hex_Digit_Display #(.decimalPoint("false")) hex_digit_display_718 (.value(register_43_q[11:8]));
  Hex_Digit_Display #(.decimalPoint("false")) hex_digit_display_719 (.value(register_44_q[15:12]));
  Hex_Digit_Display #(.decimalPoint("false")) hex_digit_display_720 (.value(register_44_q[11:8]));
  Hex_Digit_Display #(.decimalPoint("false")) hex_digit_display_721 (.value(register_45_q[15:12]));
  Hex_Digit_Display #(.decimalPoint("false")) hex_digit_display_722 (.value(register_45_q[11:8]));
  Hex_Digit_Display #(.decimalPoint("false")) hex_digit_display_723 (.value(register_46_q[15:12]));
  Hex_Digit_Display #(.decimalPoint("false")) hex_digit_display_724 (.value(register_46_q[11:8]));
  Hex_Digit_Display #(.decimalPoint("false")) hex_digit_display_725 (.value(register_47_q[15:12]));
  Hex_Digit_Display #(.decimalPoint("false")) hex_digit_display_726 (.value(register_47_q[11:8]));
  Hex_Digit_Display #(.decimalPoint("false")) hex_digit_display_727 (.value(register_48_q[15:12]));
  Hex_Digit_Display #(.decimalPoint("false")) hex_digit_display_728 (.value(register_48_q[11:8]));
  Hex_Digit_Display #(.decimalPoint("false")) hex_digit_display_729 (.value(register_49_q[19:16]));
  Hex_Digit_Display #(.decimalPoint("false")) hex_digit_display_730 (.value(register_49_q[15:12]));
  Hex_Digit_Display #(.decimalPoint("false")) hex_digit_display_731 (.value(register_50_q[19:16]));
  Hex_Digit_Display #(.decimalPoint("false")) hex_digit_display_732 (.value(register_50_q[15:12]));
  Hex_Digit_Display #(.decimalPoint("false")) hex_digit_display_733 (.value(register_51_q[19:16]));
  Hex_Digit_Display #(.decimalPoint("false")) hex_digit_display_734 (.value(register_51_q[15:12]));
  Hex_Digit_Display #(.decimalPoint("false")) hex_digit_display_735 (.value(register_52_q[19:16]));
  Hex_Digit_Display #(.decimalPoint("false")) hex_digit_display_736 (.value(register_52_q[15:12]));
  Hex_Digit_Display #(.decimalPoint("false")) hex_digit_display_737 (.value(register_37_q[3:0]));
  Hex_Digit_Display #(.decimalPoint("false")) hex_digit_display_738 (.value(register_38_q[3:0]));
  Hex_Digit_Display #(.decimalPoint("false")) hex_digit_display_739 (.value(register_39_q[3:0]));
  Hex_Digit_Display #(.decimalPoint("false")) hex_digit_display_740 (.value(register_40_q[3:0]));
  Hex_Digit_Display #(.decimalPoint("false")) hex_digit_display_741 (.value(register_41_q[7:4]));
  Hex_Digit_Display #(.decimalPoint("false")) hex_digit_display_742 (.value(register_41_q[3:0]));
  Hex_Digit_Display #(.decimalPoint("false")) hex_digit_display_743 (.value(register_42_q[7:4]));
  Hex_Digit_Display #(.decimalPoint("false")) hex_digit_display_744 (.value(register_42_q[3:0]));
  Hex_Digit_Display #(.decimalPoint("false")) hex_digit_display_745 (.value(register_43_q[7:4]));
  Hex_Digit_Display #(.decimalPoint("false")) hex_digit_display_746 (.value(register_43_q[3:0]));
  Hex_Digit_Display #(.decimalPoint("false")) hex_digit_display_747 (.value(register_44_q[7:4]));
  Hex_Digit_Display #(.decimalPoint("false")) hex_digit_display_748 (.value(register_44_q[3:0]));
  Hex_Digit_Display #(.decimalPoint("false")) hex_digit_display_749 (.value(register_45_q[7:4]));
  Hex_Digit_Display #(.decimalPoint("false")) hex_digit_display_750 (.value(register_45_q[3:0]));
  Hex_Digit_Display #(.decimalPoint("false")) hex_digit_display_751 (.value(register_46_q[7:4]));
  Hex_Digit_Display #(.decimalPoint("false")) hex_digit_display_752 (.value(register_46_q[3:0]));
  Hex_Digit_Display #(.decimalPoint("false")) hex_digit_display_753 (.value(register_47_q[7:4]));
  Hex_Digit_Display #(.decimalPoint("false")) hex_digit_display_754 (.value(register_47_q[3:0]));
  Hex_Digit_Display #(.decimalPoint("false")) hex_digit_display_755 (.value(register_48_q[7:4]));
  Hex_Digit_Display #(.decimalPoint("false")) hex_digit_display_756 (.value(register_48_q[3:0]));
  Hex_Digit_Display #(.decimalPoint("false")) hex_digit_display_757 (.value(register_49_q[11:8]));
  Hex_Digit_Display #(.decimalPoint("false")) hex_digit_display_758 (.value(register_49_q[7:4]));
  Hex_Digit_Display #(.decimalPoint("false")) hex_digit_display_759 (.value(register_50_q[11:8]));
  Hex_Digit_Display #(.decimalPoint("false")) hex_digit_display_760 (.value(register_50_q[7:4]));
  Hex_Digit_Display #(.decimalPoint("false")) hex_digit_display_761 (.value(register_51_q[11:8]));
  Hex_Digit_Display #(.decimalPoint("false")) hex_digit_display_762 (.value(register_51_q[7:4]));
  Hex_Digit_Display #(.decimalPoint("false")) hex_digit_display_763 (.value(register_52_q[11:8]));
  Hex_Digit_Display #(.decimalPoint("false")) hex_digit_display_764 (.value(register_52_q[7:4]));
  Register #(.width(64)) register_53 (.D(S1), .en(DISPLAY_2), .Q(register_53_q), .clk(undriven_14));  // open: clr
  Register #(.width(64)) register_54 (.D(S3), .en(DISPLAY_2), .Q(register_54_q), .clk(undriven_14));  // open: clr
  Register #(.width(64)) register_55 (.D(S1), .en(DISPLAY_2), .Q(register_55_q), .clk(undriven_14));  // open: clr
  Register #(.width(64)) register_56 (.D(S3), .en(DISPLAY_2), .Q(register_56_q), .clk(undriven_14));  // open: clr
  Register #(.width(64)) register_57 (.D(S1), .en(undriven_12), .Q(register_57_q), .clk(undriven_15));  // open: clr
  Register #(.width(64)) register_58 (.D(S3), .en(undriven_12), .Q(register_58_q), .clk(undriven_15));  // open: clr
  Register #(.width(64)) register_59 (.D(S1), .en(undriven_13), .Q(register_59_q), .clk(undriven_16));  // open: clr
  Register #(.width(64)) register_60 (.D(S3), .en(undriven_13), .Q(register_60_q), .clk(undriven_16));  // open: clr
  Hex_Digit_Display #(.decimalPoint("false")) hex_digit_display_765 (.value(register_49_q[3:0]));
  Hex_Digit_Display #(.decimalPoint("false")) hex_digit_display_766 (.value(register_50_q[3:0]));
  Hex_Digit_Display #(.decimalPoint("false")) hex_digit_display_767 (.value(register_51_q[3:0]));
  Hex_Digit_Display #(.decimalPoint("false")) hex_digit_display_768 (.value(register_52_q[3:0]));
  Hex_Digit_Display #(.decimalPoint("false")) hex_digit_display_769 (.value(register_53_q[63:60]));
  Hex_Digit_Display #(.decimalPoint("false")) hex_digit_display_770 (.value(register_53_q[59:56]));
  Hex_Digit_Display #(.decimalPoint("false")) hex_digit_display_771 (.value(register_54_q[63:60]));
  Hex_Digit_Display #(.decimalPoint("false")) hex_digit_display_772 (.value(register_54_q[59:56]));
  Hex_Digit_Display #(.decimalPoint("false")) hex_digit_display_773 (.value(register_55_q[63:60]));
  Hex_Digit_Display #(.decimalPoint("false")) hex_digit_display_774 (.value(register_55_q[59:56]));
  Hex_Digit_Display #(.decimalPoint("false")) hex_digit_display_775 (.value(register_56_q[63:60]));
  Hex_Digit_Display #(.decimalPoint("false")) hex_digit_display_776 (.value(register_56_q[59:56]));
  Hex_Digit_Display #(.decimalPoint("false")) hex_digit_display_777 (.value(register_57_q[63:60]));
  Hex_Digit_Display #(.decimalPoint("false")) hex_digit_display_778 (.value(register_57_q[59:56]));
  Hex_Digit_Display #(.decimalPoint("false")) hex_digit_display_779 (.value(register_58_q[63:60]));
  Hex_Digit_Display #(.decimalPoint("false")) hex_digit_display_780 (.value(register_58_q[59:56]));
  Hex_Digit_Display #(.decimalPoint("false")) hex_digit_display_781 (.value(register_59_q[63:60]));
  Hex_Digit_Display #(.decimalPoint("false")) hex_digit_display_782 (.value(register_59_q[59:56]));
  Hex_Digit_Display #(.decimalPoint("false")) hex_digit_display_783 (.value(register_60_q[63:60]));
  Hex_Digit_Display #(.decimalPoint("false")) hex_digit_display_784 (.value(register_60_q[59:56]));
  Register #(.width(64)) register_61 (.D(S1), .en(undriven_17), .Q(register_61_q), .clk(undriven_21));  // open: clr
  Hex_Digit_Display #(.decimalPoint("false")) hex_digit_display_785 (.value(register_61_q[63:60]));
  Register #(.width(64)) register_62 (.D(S3), .en(undriven_17), .Q(register_62_q), .clk(undriven_21));  // open: clr
  Hex_Digit_Display #(.decimalPoint("false")) hex_digit_display_786 (.value(register_62_q[63:60]));
  Register #(.width(64)) register_63 (.D(S1), .en(undriven_18), .Q(register_63_q), .clk(undriven_22));  // open: clr
  Hex_Digit_Display #(.decimalPoint("false")) hex_digit_display_787 (.value(register_63_q[63:60]));
  Register #(.width(64)) register_64 (.D(S3), .en(undriven_18), .Q(register_64_q), .clk(undriven_22));  // open: clr
  Hex_Digit_Display #(.decimalPoint("false")) hex_digit_display_788 (.value(register_64_q[63:60]));
  Register #(.width(64)) register_65 (.D(S1), .en(undriven_19), .Q(register_65_q), .clk(undriven_23));  // open: clr
  Hex_Digit_Display #(.decimalPoint("false")) hex_digit_display_789 (.value(register_65_q[63:60]));
  Register #(.width(64)) register_66 (.D(S3), .en(undriven_19), .Q(register_66_q), .clk(undriven_23));  // open: clr
  Hex_Digit_Display #(.decimalPoint("false")) hex_digit_display_790 (.value(register_66_q[63:60]));
  Register #(.width(64)) register_67 (.D(S1), .en(undriven_20), .Q(register_67_q), .clk(undriven_24));  // open: clr
  Hex_Digit_Display #(.decimalPoint("false")) hex_digit_display_791 (.value(register_67_q[63:60]));
  Register #(.width(64)) register_68 (.D(S3), .en(undriven_20), .Q(register_68_q), .clk(undriven_24));  // open: clr
  Hex_Digit_Display #(.decimalPoint("false")) hex_digit_display_792 (.value(register_68_q[63:60]));
  Hex_Digit_Display #(.decimalPoint("false")) hex_digit_display_793 (.value(register_53_q[55:52]));
  Hex_Digit_Display #(.decimalPoint("false")) hex_digit_display_794 (.value(register_53_q[51:48]));
  Hex_Digit_Display #(.decimalPoint("false")) hex_digit_display_795 (.value(register_54_q[55:52]));
  Hex_Digit_Display #(.decimalPoint("false")) hex_digit_display_796 (.value(register_54_q[51:48]));
  Hex_Digit_Display #(.decimalPoint("false")) hex_digit_display_797 (.value(register_55_q[55:52]));
  Hex_Digit_Display #(.decimalPoint("false")) hex_digit_display_798 (.value(register_55_q[51:48]));
  Hex_Digit_Display #(.decimalPoint("false")) hex_digit_display_799 (.value(register_56_q[55:52]));
  Hex_Digit_Display #(.decimalPoint("false")) hex_digit_display_800 (.value(register_56_q[51:48]));
  Hex_Digit_Display #(.decimalPoint("false")) hex_digit_display_801 (.value(register_57_q[55:52]));
  Hex_Digit_Display #(.decimalPoint("false")) hex_digit_display_802 (.value(register_57_q[51:48]));
  Hex_Digit_Display #(.decimalPoint("false")) hex_digit_display_803 (.value(register_58_q[55:52]));
  Hex_Digit_Display #(.decimalPoint("false")) hex_digit_display_804 (.value(register_58_q[51:48]));
  Hex_Digit_Display #(.decimalPoint("false")) hex_digit_display_805 (.value(register_59_q[55:52]));
  Hex_Digit_Display #(.decimalPoint("false")) hex_digit_display_806 (.value(register_59_q[51:48]));
  Hex_Digit_Display #(.decimalPoint("false")) hex_digit_display_807 (.value(register_60_q[55:52]));
  Hex_Digit_Display #(.decimalPoint("false")) hex_digit_display_808 (.value(register_60_q[51:48]));
  Hex_Digit_Display #(.decimalPoint("false")) hex_digit_display_809 (.value(register_61_q[59:56]));
  Hex_Digit_Display #(.decimalPoint("false")) hex_digit_display_810 (.value(register_61_q[55:52]));
  Hex_Digit_Display #(.decimalPoint("false")) hex_digit_display_811 (.value(register_62_q[59:56]));
  Hex_Digit_Display #(.decimalPoint("false")) hex_digit_display_812 (.value(register_62_q[55:52]));
  Hex_Digit_Display #(.decimalPoint("false")) hex_digit_display_813 (.value(register_63_q[59:56]));
  Hex_Digit_Display #(.decimalPoint("false")) hex_digit_display_814 (.value(register_63_q[55:52]));
  Hex_Digit_Display #(.decimalPoint("false")) hex_digit_display_815 (.value(register_64_q[59:56]));
  Hex_Digit_Display #(.decimalPoint("false")) hex_digit_display_816 (.value(register_64_q[55:52]));
  Hex_Digit_Display #(.decimalPoint("false")) hex_digit_display_817 (.value(register_65_q[59:56]));
  Hex_Digit_Display #(.decimalPoint("false")) hex_digit_display_818 (.value(register_65_q[55:52]));
  Hex_Digit_Display #(.decimalPoint("false")) hex_digit_display_819 (.value(register_66_q[59:56]));
  Hex_Digit_Display #(.decimalPoint("false")) hex_digit_display_820 (.value(register_66_q[55:52]));
  Hex_Digit_Display #(.decimalPoint("false")) hex_digit_display_821 (.value(register_67_q[59:56]));
  Hex_Digit_Display #(.decimalPoint("false")) hex_digit_display_822 (.value(register_67_q[55:52]));
  Hex_Digit_Display #(.decimalPoint("false")) hex_digit_display_823 (.value(register_68_q[59:56]));
  Hex_Digit_Display #(.decimalPoint("false")) hex_digit_display_824 (.value(register_68_q[55:52]));
  Hex_Digit_Display #(.decimalPoint("false")) hex_digit_display_825 (.value(register_53_q[47:44]));
  Hex_Digit_Display #(.decimalPoint("false")) hex_digit_display_826 (.value(register_53_q[43:40]));
  Hex_Digit_Display #(.decimalPoint("false")) hex_digit_display_827 (.value(register_54_q[47:44]));
  Hex_Digit_Display #(.decimalPoint("false")) hex_digit_display_828 (.value(register_54_q[43:40]));
  Hex_Digit_Display #(.decimalPoint("false")) hex_digit_display_829 (.value(register_55_q[47:44]));
  Hex_Digit_Display #(.decimalPoint("false")) hex_digit_display_830 (.value(register_55_q[43:40]));
  Hex_Digit_Display #(.decimalPoint("false")) hex_digit_display_831 (.value(register_56_q[47:44]));
  Hex_Digit_Display #(.decimalPoint("false")) hex_digit_display_832 (.value(register_56_q[43:40]));
  Hex_Digit_Display #(.decimalPoint("false")) hex_digit_display_833 (.value(register_57_q[47:44]));
  Hex_Digit_Display #(.decimalPoint("false")) hex_digit_display_834 (.value(register_57_q[43:40]));
  Hex_Digit_Display #(.decimalPoint("false")) hex_digit_display_835 (.value(register_58_q[47:44]));
  Hex_Digit_Display #(.decimalPoint("false")) hex_digit_display_836 (.value(register_58_q[43:40]));
  Hex_Digit_Display #(.decimalPoint("false")) hex_digit_display_837 (.value(register_59_q[47:44]));
  Hex_Digit_Display #(.decimalPoint("false")) hex_digit_display_838 (.value(register_59_q[43:40]));
  Hex_Digit_Display #(.decimalPoint("false")) hex_digit_display_839 (.value(register_60_q[47:44]));
  Hex_Digit_Display #(.decimalPoint("false")) hex_digit_display_840 (.value(register_60_q[43:40]));
  Hex_Digit_Display #(.decimalPoint("false")) hex_digit_display_841 (.value(register_61_q[51:48]));
  Hex_Digit_Display #(.decimalPoint("false")) hex_digit_display_842 (.value(register_61_q[47:44]));
  Hex_Digit_Display #(.decimalPoint("false")) hex_digit_display_843 (.value(register_62_q[51:48]));
  Hex_Digit_Display #(.decimalPoint("false")) hex_digit_display_844 (.value(register_62_q[47:44]));
  Hex_Digit_Display #(.decimalPoint("false")) hex_digit_display_845 (.value(register_63_q[51:48]));
  Hex_Digit_Display #(.decimalPoint("false")) hex_digit_display_846 (.value(register_63_q[47:44]));
  Hex_Digit_Display #(.decimalPoint("false")) hex_digit_display_847 (.value(register_64_q[51:48]));
  Hex_Digit_Display #(.decimalPoint("false")) hex_digit_display_848 (.value(register_64_q[47:44]));
  Hex_Digit_Display #(.decimalPoint("false")) hex_digit_display_849 (.value(register_65_q[51:48]));
  Hex_Digit_Display #(.decimalPoint("false")) hex_digit_display_850 (.value(register_65_q[47:44]));
  Hex_Digit_Display #(.decimalPoint("false")) hex_digit_display_851 (.value(register_66_q[51:48]));
  Hex_Digit_Display #(.decimalPoint("false")) hex_digit_display_852 (.value(register_66_q[47:44]));
  Hex_Digit_Display #(.decimalPoint("false")) hex_digit_display_853 (.value(register_67_q[51:48]));
  Hex_Digit_Display #(.decimalPoint("false")) hex_digit_display_854 (.value(register_67_q[47:44]));
  Hex_Digit_Display #(.decimalPoint("false")) hex_digit_display_855 (.value(register_68_q[51:48]));
  Hex_Digit_Display #(.decimalPoint("false")) hex_digit_display_856 (.value(register_68_q[47:44]));
  Hex_Digit_Display #(.decimalPoint("false")) hex_digit_display_857 (.value(register_53_q[39:36]));
  Hex_Digit_Display #(.decimalPoint("false")) hex_digit_display_858 (.value(register_53_q[35:32]));
  Hex_Digit_Display #(.decimalPoint("false")) hex_digit_display_859 (.value(register_54_q[39:36]));
  Hex_Digit_Display #(.decimalPoint("false")) hex_digit_display_860 (.value(register_54_q[35:32]));
  Hex_Digit_Display #(.decimalPoint("false")) hex_digit_display_861 (.value(register_55_q[39:36]));
  Hex_Digit_Display #(.decimalPoint("false")) hex_digit_display_862 (.value(register_55_q[35:32]));
  Hex_Digit_Display #(.decimalPoint("false")) hex_digit_display_863 (.value(register_56_q[39:36]));
  Hex_Digit_Display #(.decimalPoint("false")) hex_digit_display_864 (.value(register_56_q[35:32]));
  Hex_Digit_Display #(.decimalPoint("false")) hex_digit_display_865 (.value(register_57_q[39:36]));
  Hex_Digit_Display #(.decimalPoint("false")) hex_digit_display_866 (.value(register_57_q[35:32]));
  Hex_Digit_Display #(.decimalPoint("false")) hex_digit_display_867 (.value(register_58_q[39:36]));
  Hex_Digit_Display #(.decimalPoint("false")) hex_digit_display_868 (.value(register_58_q[35:32]));
  Hex_Digit_Display #(.decimalPoint("false")) hex_digit_display_869 (.value(register_59_q[39:36]));
  Hex_Digit_Display #(.decimalPoint("false")) hex_digit_display_870 (.value(register_59_q[35:32]));
  Hex_Digit_Display #(.decimalPoint("false")) hex_digit_display_871 (.value(register_60_q[39:36]));
  Hex_Digit_Display #(.decimalPoint("false")) hex_digit_display_872 (.value(register_60_q[35:32]));
  Hex_Digit_Display #(.decimalPoint("false")) hex_digit_display_873 (.value(register_61_q[43:40]));
  Hex_Digit_Display #(.decimalPoint("false")) hex_digit_display_874 (.value(register_61_q[39:36]));
  Hex_Digit_Display #(.decimalPoint("false")) hex_digit_display_875 (.value(register_62_q[43:40]));
  Hex_Digit_Display #(.decimalPoint("false")) hex_digit_display_876 (.value(register_62_q[39:36]));
  Hex_Digit_Display #(.decimalPoint("false")) hex_digit_display_877 (.value(register_63_q[43:40]));
  Hex_Digit_Display #(.decimalPoint("false")) hex_digit_display_878 (.value(register_63_q[39:36]));
  Hex_Digit_Display #(.decimalPoint("false")) hex_digit_display_879 (.value(register_64_q[43:40]));
  Hex_Digit_Display #(.decimalPoint("false")) hex_digit_display_880 (.value(register_64_q[39:36]));
  Hex_Digit_Display #(.decimalPoint("false")) hex_digit_display_881 (.value(register_65_q[43:40]));
  Hex_Digit_Display #(.decimalPoint("false")) hex_digit_display_882 (.value(register_65_q[39:36]));
  Hex_Digit_Display #(.decimalPoint("false")) hex_digit_display_883 (.value(register_66_q[43:40]));
  Hex_Digit_Display #(.decimalPoint("false")) hex_digit_display_884 (.value(register_66_q[39:36]));
  Hex_Digit_Display #(.decimalPoint("false")) hex_digit_display_885 (.value(register_67_q[43:40]));
  Hex_Digit_Display #(.decimalPoint("false")) hex_digit_display_886 (.value(register_67_q[39:36]));
  Hex_Digit_Display #(.decimalPoint("false")) hex_digit_display_887 (.value(register_68_q[43:40]));
  Hex_Digit_Display #(.decimalPoint("false")) hex_digit_display_888 (.value(register_68_q[39:36]));
  Hex_Digit_Display #(.decimalPoint("false")) hex_digit_display_889 (.value(register_53_q[31:28]));
  Hex_Digit_Display #(.decimalPoint("false")) hex_digit_display_890 (.value(register_53_q[27:24]));
  Hex_Digit_Display #(.decimalPoint("false")) hex_digit_display_891 (.value(register_54_q[31:28]));
  Hex_Digit_Display #(.decimalPoint("false")) hex_digit_display_892 (.value(register_54_q[27:24]));
  Hex_Digit_Display #(.decimalPoint("false")) hex_digit_display_893 (.value(register_55_q[31:28]));
  Hex_Digit_Display #(.decimalPoint("false")) hex_digit_display_894 (.value(register_55_q[27:24]));
  Hex_Digit_Display #(.decimalPoint("false")) hex_digit_display_895 (.value(register_56_q[31:28]));
  Hex_Digit_Display #(.decimalPoint("false")) hex_digit_display_896 (.value(register_56_q[27:24]));
  Hex_Digit_Display #(.decimalPoint("false")) hex_digit_display_897 (.value(register_57_q[31:28]));
  Hex_Digit_Display #(.decimalPoint("false")) hex_digit_display_898 (.value(register_57_q[27:24]));
  Hex_Digit_Display #(.decimalPoint("false")) hex_digit_display_899 (.value(register_58_q[31:28]));
  Hex_Digit_Display #(.decimalPoint("false")) hex_digit_display_900 (.value(register_58_q[27:24]));
  Hex_Digit_Display #(.decimalPoint("false")) hex_digit_display_901 (.value(register_59_q[31:28]));
  Hex_Digit_Display #(.decimalPoint("false")) hex_digit_display_902 (.value(register_59_q[27:24]));
  Hex_Digit_Display #(.decimalPoint("false")) hex_digit_display_903 (.value(register_60_q[31:28]));
  Hex_Digit_Display #(.decimalPoint("false")) hex_digit_display_904 (.value(register_60_q[27:24]));
  Hex_Digit_Display #(.decimalPoint("false")) hex_digit_display_905 (.value(register_61_q[35:32]));
  Hex_Digit_Display #(.decimalPoint("false")) hex_digit_display_906 (.value(register_61_q[31:28]));
  Hex_Digit_Display #(.decimalPoint("false")) hex_digit_display_907 (.value(register_62_q[35:32]));
  Hex_Digit_Display #(.decimalPoint("false")) hex_digit_display_908 (.value(register_62_q[31:28]));
  Hex_Digit_Display #(.decimalPoint("false")) hex_digit_display_909 (.value(register_63_q[35:32]));
  Hex_Digit_Display #(.decimalPoint("false")) hex_digit_display_910 (.value(register_63_q[31:28]));
  Hex_Digit_Display #(.decimalPoint("false")) hex_digit_display_911 (.value(register_64_q[35:32]));
  Hex_Digit_Display #(.decimalPoint("false")) hex_digit_display_912 (.value(register_64_q[31:28]));
  Hex_Digit_Display #(.decimalPoint("false")) hex_digit_display_913 (.value(register_65_q[35:32]));
  Hex_Digit_Display #(.decimalPoint("false")) hex_digit_display_914 (.value(register_65_q[31:28]));
  Hex_Digit_Display #(.decimalPoint("false")) hex_digit_display_915 (.value(register_66_q[35:32]));
  Hex_Digit_Display #(.decimalPoint("false")) hex_digit_display_916 (.value(register_66_q[31:28]));
  Hex_Digit_Display #(.decimalPoint("false")) hex_digit_display_917 (.value(register_67_q[35:32]));
  Hex_Digit_Display #(.decimalPoint("false")) hex_digit_display_918 (.value(register_67_q[31:28]));
  Hex_Digit_Display #(.decimalPoint("false")) hex_digit_display_919 (.value(register_68_q[35:32]));
  Hex_Digit_Display #(.decimalPoint("false")) hex_digit_display_920 (.value(register_68_q[31:28]));
  Hex_Digit_Display #(.decimalPoint("false")) hex_digit_display_921 (.value(register_53_q[23:20]));
  Hex_Digit_Display #(.decimalPoint("false")) hex_digit_display_922 (.value(register_53_q[19:16]));
  Hex_Digit_Display #(.decimalPoint("false")) hex_digit_display_923 (.value(register_54_q[23:20]));
  Hex_Digit_Display #(.decimalPoint("false")) hex_digit_display_924 (.value(register_54_q[19:16]));
  Hex_Digit_Display #(.decimalPoint("false")) hex_digit_display_925 (.value(register_55_q[23:20]));
  Hex_Digit_Display #(.decimalPoint("false")) hex_digit_display_926 (.value(register_55_q[19:16]));
  Hex_Digit_Display #(.decimalPoint("false")) hex_digit_display_927 (.value(register_56_q[23:20]));
  Hex_Digit_Display #(.decimalPoint("false")) hex_digit_display_928 (.value(register_56_q[19:16]));
  Hex_Digit_Display #(.decimalPoint("false")) hex_digit_display_929 (.value(register_57_q[23:20]));
  Hex_Digit_Display #(.decimalPoint("false")) hex_digit_display_930 (.value(register_57_q[19:16]));
  Hex_Digit_Display #(.decimalPoint("false")) hex_digit_display_931 (.value(register_58_q[23:20]));
  Hex_Digit_Display #(.decimalPoint("false")) hex_digit_display_932 (.value(register_58_q[19:16]));
  Hex_Digit_Display #(.decimalPoint("false")) hex_digit_display_933 (.value(register_59_q[23:20]));
  Hex_Digit_Display #(.decimalPoint("false")) hex_digit_display_934 (.value(register_59_q[19:16]));
  Hex_Digit_Display #(.decimalPoint("false")) hex_digit_display_935 (.value(register_60_q[23:20]));
  Hex_Digit_Display #(.decimalPoint("false")) hex_digit_display_936 (.value(register_60_q[19:16]));
  Hex_Digit_Display #(.decimalPoint("false")) hex_digit_display_937 (.value(register_61_q[27:24]));
  Hex_Digit_Display #(.decimalPoint("false")) hex_digit_display_938 (.value(register_61_q[23:20]));
  Hex_Digit_Display #(.decimalPoint("false")) hex_digit_display_939 (.value(register_62_q[27:24]));
  Hex_Digit_Display #(.decimalPoint("false")) hex_digit_display_940 (.value(register_62_q[23:20]));
  Hex_Digit_Display #(.decimalPoint("false")) hex_digit_display_941 (.value(register_63_q[27:24]));
  Hex_Digit_Display #(.decimalPoint("false")) hex_digit_display_942 (.value(register_63_q[23:20]));
  Hex_Digit_Display #(.decimalPoint("false")) hex_digit_display_943 (.value(register_64_q[27:24]));
  Hex_Digit_Display #(.decimalPoint("false")) hex_digit_display_944 (.value(register_64_q[23:20]));
  Hex_Digit_Display #(.decimalPoint("false")) hex_digit_display_945 (.value(register_65_q[27:24]));
  Hex_Digit_Display #(.decimalPoint("false")) hex_digit_display_946 (.value(register_65_q[23:20]));
  Hex_Digit_Display #(.decimalPoint("false")) hex_digit_display_947 (.value(register_66_q[27:24]));
  Hex_Digit_Display #(.decimalPoint("false")) hex_digit_display_948 (.value(register_66_q[23:20]));
  Hex_Digit_Display #(.decimalPoint("false")) hex_digit_display_949 (.value(register_67_q[27:24]));
  Hex_Digit_Display #(.decimalPoint("false")) hex_digit_display_950 (.value(register_67_q[23:20]));
  Hex_Digit_Display #(.decimalPoint("false")) hex_digit_display_951 (.value(register_68_q[27:24]));
  Hex_Digit_Display #(.decimalPoint("false")) hex_digit_display_952 (.value(register_68_q[23:20]));
  Hex_Digit_Display #(.decimalPoint("false")) hex_digit_display_953 (.value(register_53_q[15:12]));
  Hex_Digit_Display #(.decimalPoint("false")) hex_digit_display_954 (.value(register_53_q[11:8]));
  Hex_Digit_Display #(.decimalPoint("false")) hex_digit_display_955 (.value(register_54_q[15:12]));
  Hex_Digit_Display #(.decimalPoint("false")) hex_digit_display_956 (.value(register_54_q[11:8]));
  Hex_Digit_Display #(.decimalPoint("false")) hex_digit_display_957 (.value(register_55_q[15:12]));
  Hex_Digit_Display #(.decimalPoint("false")) hex_digit_display_958 (.value(register_55_q[11:8]));
  Hex_Digit_Display #(.decimalPoint("false")) hex_digit_display_959 (.value(register_56_q[15:12]));
  Hex_Digit_Display #(.decimalPoint("false")) hex_digit_display_960 (.value(register_56_q[11:8]));
  Hex_Digit_Display #(.decimalPoint("false")) hex_digit_display_961 (.value(register_57_q[15:12]));
  Hex_Digit_Display #(.decimalPoint("false")) hex_digit_display_962 (.value(register_57_q[11:8]));
  Hex_Digit_Display #(.decimalPoint("false")) hex_digit_display_963 (.value(register_58_q[15:12]));
  Hex_Digit_Display #(.decimalPoint("false")) hex_digit_display_964 (.value(register_58_q[11:8]));
  Hex_Digit_Display #(.decimalPoint("false")) hex_digit_display_965 (.value(register_59_q[15:12]));
  Hex_Digit_Display #(.decimalPoint("false")) hex_digit_display_966 (.value(register_59_q[11:8]));
  Hex_Digit_Display #(.decimalPoint("false")) hex_digit_display_967 (.value(register_60_q[15:12]));
  Hex_Digit_Display #(.decimalPoint("false")) hex_digit_display_968 (.value(register_60_q[11:8]));
  Hex_Digit_Display #(.decimalPoint("false")) hex_digit_display_969 (.value(register_61_q[19:16]));
  Hex_Digit_Display #(.decimalPoint("false")) hex_digit_display_970 (.value(register_61_q[15:12]));
  Hex_Digit_Display #(.decimalPoint("false")) hex_digit_display_971 (.value(register_62_q[19:16]));
  Hex_Digit_Display #(.decimalPoint("false")) hex_digit_display_972 (.value(register_62_q[15:12]));
  Hex_Digit_Display #(.decimalPoint("false")) hex_digit_display_973 (.value(register_63_q[19:16]));
  Hex_Digit_Display #(.decimalPoint("false")) hex_digit_display_974 (.value(register_63_q[15:12]));
  Hex_Digit_Display #(.decimalPoint("false")) hex_digit_display_975 (.value(register_64_q[19:16]));
  Hex_Digit_Display #(.decimalPoint("false")) hex_digit_display_976 (.value(register_64_q[15:12]));
  Hex_Digit_Display #(.decimalPoint("false")) hex_digit_display_977 (.value(register_65_q[19:16]));
  Hex_Digit_Display #(.decimalPoint("false")) hex_digit_display_978 (.value(register_65_q[15:12]));
  Hex_Digit_Display #(.decimalPoint("false")) hex_digit_display_979 (.value(register_66_q[19:16]));
  Hex_Digit_Display #(.decimalPoint("false")) hex_digit_display_980 (.value(register_66_q[15:12]));
  Hex_Digit_Display #(.decimalPoint("false")) hex_digit_display_981 (.value(register_67_q[19:16]));
  Hex_Digit_Display #(.decimalPoint("false")) hex_digit_display_982 (.value(register_67_q[15:12]));
  Hex_Digit_Display #(.decimalPoint("false")) hex_digit_display_983 (.value(register_68_q[19:16]));
  Hex_Digit_Display #(.decimalPoint("false")) hex_digit_display_984 (.value(register_68_q[15:12]));
  Hex_Digit_Display #(.decimalPoint("false")) hex_digit_display_985 (.value(register_53_q[7:4]));
  Hex_Digit_Display #(.decimalPoint("false")) hex_digit_display_986 (.value(register_53_q[3:0]));
  Hex_Digit_Display #(.decimalPoint("false")) hex_digit_display_987 (.value(register_54_q[7:4]));
  Hex_Digit_Display #(.decimalPoint("false")) hex_digit_display_988 (.value(register_54_q[3:0]));
  Hex_Digit_Display #(.decimalPoint("false")) hex_digit_display_989 (.value(register_55_q[7:4]));
  Hex_Digit_Display #(.decimalPoint("false")) hex_digit_display_990 (.value(register_55_q[3:0]));
  Hex_Digit_Display #(.decimalPoint("false")) hex_digit_display_991 (.value(register_56_q[7:4]));
  Hex_Digit_Display #(.decimalPoint("false")) hex_digit_display_992 (.value(register_56_q[3:0]));
  Hex_Digit_Display #(.decimalPoint("false")) hex_digit_display_993 (.value(register_57_q[7:4]));
  Hex_Digit_Display #(.decimalPoint("false")) hex_digit_display_994 (.value(register_57_q[3:0]));
  Hex_Digit_Display #(.decimalPoint("false")) hex_digit_display_995 (.value(register_58_q[7:4]));
  Hex_Digit_Display #(.decimalPoint("false")) hex_digit_display_996 (.value(register_58_q[3:0]));
  Hex_Digit_Display #(.decimalPoint("false")) hex_digit_display_997 (.value(register_59_q[7:4]));
  Hex_Digit_Display #(.decimalPoint("false")) hex_digit_display_998 (.value(register_59_q[3:0]));
  Hex_Digit_Display #(.decimalPoint("false")) hex_digit_display_999 (.value(register_60_q[7:4]));
  Hex_Digit_Display #(.decimalPoint("false")) hex_digit_display_1000 (.value(register_60_q[3:0]));
  Hex_Digit_Display #(.decimalPoint("false")) hex_digit_display_1001 (.value(register_61_q[11:8]));
  Hex_Digit_Display #(.decimalPoint("false")) hex_digit_display_1002 (.value(register_61_q[7:4]));
  Hex_Digit_Display #(.decimalPoint("false")) hex_digit_display_1003 (.value(register_62_q[11:8]));
  Hex_Digit_Display #(.decimalPoint("false")) hex_digit_display_1004 (.value(register_62_q[7:4]));
  Hex_Digit_Display #(.decimalPoint("false")) hex_digit_display_1005 (.value(register_63_q[11:8]));
  Hex_Digit_Display #(.decimalPoint("false")) hex_digit_display_1006 (.value(register_63_q[7:4]));
  Hex_Digit_Display #(.decimalPoint("false")) hex_digit_display_1007 (.value(register_64_q[11:8]));
  Hex_Digit_Display #(.decimalPoint("false")) hex_digit_display_1008 (.value(register_64_q[7:4]));
  Hex_Digit_Display #(.decimalPoint("false")) hex_digit_display_1009 (.value(register_65_q[11:8]));
  Hex_Digit_Display #(.decimalPoint("false")) hex_digit_display_1010 (.value(register_65_q[7:4]));
  Hex_Digit_Display #(.decimalPoint("false")) hex_digit_display_1011 (.value(register_66_q[11:8]));
  Hex_Digit_Display #(.decimalPoint("false")) hex_digit_display_1012 (.value(register_66_q[7:4]));
  Hex_Digit_Display #(.decimalPoint("false")) hex_digit_display_1013 (.value(register_67_q[11:8]));
  Hex_Digit_Display #(.decimalPoint("false")) hex_digit_display_1014 (.value(register_67_q[7:4]));
  Hex_Digit_Display #(.decimalPoint("false")) hex_digit_display_1015 (.value(register_68_q[11:8]));
  Hex_Digit_Display #(.decimalPoint("false")) hex_digit_display_1016 (.value(register_68_q[7:4]));
  Hex_Digit_Display #(.decimalPoint("false")) hex_digit_display_1017 (.value(register_61_q[3:0]));
  Hex_Digit_Display #(.decimalPoint("false")) hex_digit_display_1018 (.value(register_62_q[3:0]));
  Hex_Digit_Display #(.decimalPoint("false")) hex_digit_display_1019 (.value(register_63_q[3:0]));
  Hex_Digit_Display #(.decimalPoint("false")) hex_digit_display_1020 (.value(register_64_q[3:0]));
  Hex_Digit_Display #(.decimalPoint("false")) hex_digit_display_1021 (.value(register_65_q[3:0]));
  Hex_Digit_Display #(.decimalPoint("false")) hex_digit_display_1022 (.value(register_66_q[3:0]));
  Hex_Digit_Display #(.decimalPoint("false")) hex_digit_display_1023 (.value(register_67_q[3:0]));
  Hex_Digit_Display #(.decimalPoint("false")) hex_digit_display_1024 (.value(register_68_q[3:0]));
  Register #(.width(64)) register_69 (.D(S0), .en(DISPLAY_2), .Q(register_69_q), .clk(undriven_28));  // open: clr
  Hex_Digit_Display #(.decimalPoint("false")) hex_digit_display_1025 (.value(register_69_q[63:60]));
  Register #(.width(64)) register_70 (.D(S2), .en(DISPLAY_2), .Q(register_70_q), .clk(undriven_28));  // open: clr
  Hex_Digit_Display #(.decimalPoint("false")) hex_digit_display_1026 (.value(register_70_q[63:60]));
  Register #(.width(64)) register_71 (.D(S0), .en(undriven_25), .Q(register_71_q), .clk(undriven_29));  // open: clr
  Hex_Digit_Display #(.decimalPoint("false")) hex_digit_display_1027 (.value(register_71_q[63:60]));
  Register #(.width(64)) register_72 (.D(S2), .en(undriven_25), .Q(register_72_q), .clk(undriven_29));  // open: clr
  Hex_Digit_Display #(.decimalPoint("false")) hex_digit_display_1028 (.value(register_72_q[63:60]));
  Register #(.width(64)) register_73 (.D(S0), .en(undriven_26), .Q(register_73_q), .clk(undriven_30));  // open: clr
  Register #(.width(64)) register_74 (.D(S2), .en(undriven_26), .Q(register_74_q), .clk(undriven_30));  // open: clr
  Register #(.width(64)) register_75 (.D(S0), .en(undriven_27), .Q(register_75_q), .clk(undriven_31));  // open: clr
  Register #(.width(64)) register_76 (.D(S2), .en(undriven_27), .Q(register_76_q), .clk(undriven_31));  // open: clr
  Register #(.width(64)) register_77 (.D(S0), .en(undriven_32), .Q(register_77_q), .clk(undriven_36));  // open: clr
  Register #(.width(64)) register_78 (.D(S2), .en(undriven_32), .Q(register_78_q), .clk(undriven_36));  // open: clr
  Register #(.width(64)) register_79 (.D(S0), .en(undriven_33), .Q(register_79_q), .clk(undriven_37));  // open: clr
  Register #(.width(64)) register_80 (.D(S2), .en(undriven_33), .Q(register_80_q), .clk(undriven_37));  // open: clr
  Hex_Digit_Display #(.decimalPoint("false")) hex_digit_display_1029 (.value(register_69_q[59:56]));
  Hex_Digit_Display #(.decimalPoint("false")) hex_digit_display_1030 (.value(register_69_q[55:52]));
  Hex_Digit_Display #(.decimalPoint("false")) hex_digit_display_1031 (.value(register_70_q[59:56]));
  Hex_Digit_Display #(.decimalPoint("false")) hex_digit_display_1032 (.value(register_70_q[55:52]));
  Hex_Digit_Display #(.decimalPoint("false")) hex_digit_display_1033 (.value(register_71_q[59:56]));
  Hex_Digit_Display #(.decimalPoint("false")) hex_digit_display_1034 (.value(register_71_q[55:52]));
  Hex_Digit_Display #(.decimalPoint("false")) hex_digit_display_1035 (.value(register_72_q[59:56]));
  Hex_Digit_Display #(.decimalPoint("false")) hex_digit_display_1036 (.value(register_72_q[55:52]));
  Hex_Digit_Display #(.decimalPoint("false")) hex_digit_display_1037 (.value(register_73_q[63:60]));
  Hex_Digit_Display #(.decimalPoint("false")) hex_digit_display_1038 (.value(register_73_q[59:56]));
  Hex_Digit_Display #(.decimalPoint("false")) hex_digit_display_1039 (.value(register_74_q[63:60]));
  Hex_Digit_Display #(.decimalPoint("false")) hex_digit_display_1040 (.value(register_74_q[59:56]));
  Hex_Digit_Display #(.decimalPoint("false")) hex_digit_display_1041 (.value(register_75_q[63:60]));
  Hex_Digit_Display #(.decimalPoint("false")) hex_digit_display_1042 (.value(register_75_q[59:56]));
  Hex_Digit_Display #(.decimalPoint("false")) hex_digit_display_1043 (.value(register_76_q[63:60]));
  Hex_Digit_Display #(.decimalPoint("false")) hex_digit_display_1044 (.value(register_76_q[59:56]));
  Hex_Digit_Display #(.decimalPoint("false")) hex_digit_display_1045 (.value(register_77_q[63:60]));
  Hex_Digit_Display #(.decimalPoint("false")) hex_digit_display_1046 (.value(register_77_q[59:56]));
  Hex_Digit_Display #(.decimalPoint("false")) hex_digit_display_1047 (.value(register_78_q[63:60]));
  Hex_Digit_Display #(.decimalPoint("false")) hex_digit_display_1048 (.value(register_78_q[59:56]));
  Hex_Digit_Display #(.decimalPoint("false")) hex_digit_display_1049 (.value(register_79_q[63:60]));
  Hex_Digit_Display #(.decimalPoint("false")) hex_digit_display_1050 (.value(register_79_q[59:56]));
  Hex_Digit_Display #(.decimalPoint("false")) hex_digit_display_1051 (.value(register_80_q[63:60]));
  Hex_Digit_Display #(.decimalPoint("false")) hex_digit_display_1052 (.value(register_80_q[59:56]));
  Register #(.width(64)) register_81 (.D(S0), .en(undriven_34), .Q(register_81_q), .clk(undriven_38));  // open: clr
  Hex_Digit_Display #(.decimalPoint("false")) hex_digit_display_1053 (.value(register_81_q[63:60]));
  Register #(.width(64)) register_82 (.D(S2), .en(undriven_34), .Q(register_82_q), .clk(undriven_38));  // open: clr
  Hex_Digit_Display #(.decimalPoint("false")) hex_digit_display_1054 (.value(register_82_q[63:60]));
  Register #(.width(64)) register_83 (.D(S0), .en(undriven_35), .Q(register_83_q), .clk(undriven_39));  // open: clr
  Hex_Digit_Display #(.decimalPoint("false")) hex_digit_display_1055 (.value(register_83_q[63:60]));
  Register #(.width(64)) register_84 (.D(S2), .en(undriven_35), .Q(register_84_q), .clk(undriven_39));  // open: clr
  Hex_Digit_Display #(.decimalPoint("false")) hex_digit_display_1056 (.value(register_84_q[63:60]));
  Hex_Digit_Display #(.decimalPoint("false")) hex_digit_display_1057 (.value(register_69_q[51:48]));
  Hex_Digit_Display #(.decimalPoint("false")) hex_digit_display_1058 (.value(register_69_q[47:44]));
  Hex_Digit_Display #(.decimalPoint("false")) hex_digit_display_1059 (.value(register_70_q[51:48]));
  Hex_Digit_Display #(.decimalPoint("false")) hex_digit_display_1060 (.value(register_70_q[47:44]));
  Hex_Digit_Display #(.decimalPoint("false")) hex_digit_display_1061 (.value(register_71_q[51:48]));
  Hex_Digit_Display #(.decimalPoint("false")) hex_digit_display_1062 (.value(register_71_q[47:44]));
  Hex_Digit_Display #(.decimalPoint("false")) hex_digit_display_1063 (.value(register_72_q[51:48]));
  Hex_Digit_Display #(.decimalPoint("false")) hex_digit_display_1064 (.value(register_72_q[47:44]));
  Hex_Digit_Display #(.decimalPoint("false")) hex_digit_display_1065 (.value(register_73_q[55:52]));
  Hex_Digit_Display #(.decimalPoint("false")) hex_digit_display_1066 (.value(register_73_q[51:48]));
  Hex_Digit_Display #(.decimalPoint("false")) hex_digit_display_1067 (.value(register_74_q[55:52]));
  Hex_Digit_Display #(.decimalPoint("false")) hex_digit_display_1068 (.value(register_74_q[51:48]));
  Hex_Digit_Display #(.decimalPoint("false")) hex_digit_display_1069 (.value(register_75_q[55:52]));
  Hex_Digit_Display #(.decimalPoint("false")) hex_digit_display_1070 (.value(register_75_q[51:48]));
  Hex_Digit_Display #(.decimalPoint("false")) hex_digit_display_1071 (.value(register_76_q[55:52]));
  Hex_Digit_Display #(.decimalPoint("false")) hex_digit_display_1072 (.value(register_76_q[51:48]));
  Hex_Digit_Display #(.decimalPoint("false")) hex_digit_display_1073 (.value(register_77_q[55:52]));
  Hex_Digit_Display #(.decimalPoint("false")) hex_digit_display_1074 (.value(register_77_q[51:48]));
  Hex_Digit_Display #(.decimalPoint("false")) hex_digit_display_1075 (.value(register_78_q[55:52]));
  Hex_Digit_Display #(.decimalPoint("false")) hex_digit_display_1076 (.value(register_78_q[51:48]));
  Hex_Digit_Display #(.decimalPoint("false")) hex_digit_display_1077 (.value(register_79_q[55:52]));
  Hex_Digit_Display #(.decimalPoint("false")) hex_digit_display_1078 (.value(register_79_q[51:48]));
  Hex_Digit_Display #(.decimalPoint("false")) hex_digit_display_1079 (.value(register_80_q[55:52]));
  Hex_Digit_Display #(.decimalPoint("false")) hex_digit_display_1080 (.value(register_80_q[51:48]));
  Hex_Digit_Display #(.decimalPoint("false")) hex_digit_display_1081 (.value(register_81_q[59:56]));
  Hex_Digit_Display #(.decimalPoint("false")) hex_digit_display_1082 (.value(register_81_q[55:52]));
  Hex_Digit_Display #(.decimalPoint("false")) hex_digit_display_1083 (.value(register_82_q[59:56]));
  Hex_Digit_Display #(.decimalPoint("false")) hex_digit_display_1084 (.value(register_82_q[55:52]));
  Hex_Digit_Display #(.decimalPoint("false")) hex_digit_display_1085 (.value(register_83_q[59:56]));
  Hex_Digit_Display #(.decimalPoint("false")) hex_digit_display_1086 (.value(register_83_q[55:52]));
  Hex_Digit_Display #(.decimalPoint("false")) hex_digit_display_1087 (.value(register_84_q[59:56]));
  Hex_Digit_Display #(.decimalPoint("false")) hex_digit_display_1088 (.value(register_84_q[55:52]));
  Hex_Digit_Display #(.decimalPoint("false")) hex_digit_display_1089 (.value(register_69_q[43:40]));
  Hex_Digit_Display #(.decimalPoint("false")) hex_digit_display_1090 (.value(register_69_q[39:36]));
  Hex_Digit_Display #(.decimalPoint("false")) hex_digit_display_1091 (.value(register_70_q[43:40]));
  Hex_Digit_Display #(.decimalPoint("false")) hex_digit_display_1092 (.value(register_70_q[39:36]));
  Hex_Digit_Display #(.decimalPoint("false")) hex_digit_display_1093 (.value(register_71_q[43:40]));
  Hex_Digit_Display #(.decimalPoint("false")) hex_digit_display_1094 (.value(register_71_q[39:36]));
  Hex_Digit_Display #(.decimalPoint("false")) hex_digit_display_1095 (.value(register_72_q[43:40]));
  Hex_Digit_Display #(.decimalPoint("false")) hex_digit_display_1096 (.value(register_72_q[39:36]));
  Hex_Digit_Display #(.decimalPoint("false")) hex_digit_display_1097 (.value(register_73_q[47:44]));
  Hex_Digit_Display #(.decimalPoint("false")) hex_digit_display_1098 (.value(register_73_q[43:40]));
  Hex_Digit_Display #(.decimalPoint("false")) hex_digit_display_1099 (.value(register_74_q[47:44]));
  Hex_Digit_Display #(.decimalPoint("false")) hex_digit_display_1100 (.value(register_74_q[43:40]));
  Hex_Digit_Display #(.decimalPoint("false")) hex_digit_display_1101 (.value(register_75_q[47:44]));
  Hex_Digit_Display #(.decimalPoint("false")) hex_digit_display_1102 (.value(register_75_q[43:40]));
  Hex_Digit_Display #(.decimalPoint("false")) hex_digit_display_1103 (.value(register_76_q[47:44]));
  Hex_Digit_Display #(.decimalPoint("false")) hex_digit_display_1104 (.value(register_76_q[43:40]));
  Hex_Digit_Display #(.decimalPoint("false")) hex_digit_display_1105 (.value(register_77_q[47:44]));
  Hex_Digit_Display #(.decimalPoint("false")) hex_digit_display_1106 (.value(register_77_q[43:40]));
  Hex_Digit_Display #(.decimalPoint("false")) hex_digit_display_1107 (.value(register_78_q[47:44]));
  Hex_Digit_Display #(.decimalPoint("false")) hex_digit_display_1108 (.value(register_78_q[43:40]));
  Hex_Digit_Display #(.decimalPoint("false")) hex_digit_display_1109 (.value(register_79_q[47:44]));
  Hex_Digit_Display #(.decimalPoint("false")) hex_digit_display_1110 (.value(register_79_q[43:40]));
  Hex_Digit_Display #(.decimalPoint("false")) hex_digit_display_1111 (.value(register_80_q[47:44]));
  Hex_Digit_Display #(.decimalPoint("false")) hex_digit_display_1112 (.value(register_80_q[43:40]));
  Hex_Digit_Display #(.decimalPoint("false")) hex_digit_display_1113 (.value(register_81_q[51:48]));
  Hex_Digit_Display #(.decimalPoint("false")) hex_digit_display_1114 (.value(register_81_q[47:44]));
  Hex_Digit_Display #(.decimalPoint("false")) hex_digit_display_1115 (.value(register_82_q[51:48]));
  Hex_Digit_Display #(.decimalPoint("false")) hex_digit_display_1116 (.value(register_82_q[47:44]));
  Hex_Digit_Display #(.decimalPoint("false")) hex_digit_display_1117 (.value(register_83_q[51:48]));
  Hex_Digit_Display #(.decimalPoint("false")) hex_digit_display_1118 (.value(register_83_q[47:44]));
  Hex_Digit_Display #(.decimalPoint("false")) hex_digit_display_1119 (.value(register_84_q[51:48]));
  Hex_Digit_Display #(.decimalPoint("false")) hex_digit_display_1120 (.value(register_84_q[47:44]));
  Hex_Digit_Display #(.decimalPoint("false")) hex_digit_display_1121 (.value(register_69_q[35:32]));
  Hex_Digit_Display #(.decimalPoint("false")) hex_digit_display_1122 (.value(register_69_q[31:28]));
  Hex_Digit_Display #(.decimalPoint("false")) hex_digit_display_1123 (.value(register_70_q[35:32]));
  Hex_Digit_Display #(.decimalPoint("false")) hex_digit_display_1124 (.value(register_70_q[31:28]));
  Hex_Digit_Display #(.decimalPoint("false")) hex_digit_display_1125 (.value(register_71_q[35:32]));
  Hex_Digit_Display #(.decimalPoint("false")) hex_digit_display_1126 (.value(register_71_q[31:28]));
  Hex_Digit_Display #(.decimalPoint("false")) hex_digit_display_1127 (.value(register_72_q[35:32]));
  Hex_Digit_Display #(.decimalPoint("false")) hex_digit_display_1128 (.value(register_72_q[31:28]));
  Hex_Digit_Display #(.decimalPoint("false")) hex_digit_display_1129 (.value(register_73_q[39:36]));
  Hex_Digit_Display #(.decimalPoint("false")) hex_digit_display_1130 (.value(register_73_q[35:32]));
  Hex_Digit_Display #(.decimalPoint("false")) hex_digit_display_1131 (.value(register_74_q[39:36]));
  Hex_Digit_Display #(.decimalPoint("false")) hex_digit_display_1132 (.value(register_74_q[35:32]));
  Hex_Digit_Display #(.decimalPoint("false")) hex_digit_display_1133 (.value(register_75_q[39:36]));
  Hex_Digit_Display #(.decimalPoint("false")) hex_digit_display_1134 (.value(register_75_q[35:32]));
  Hex_Digit_Display #(.decimalPoint("false")) hex_digit_display_1135 (.value(register_76_q[39:36]));
  Hex_Digit_Display #(.decimalPoint("false")) hex_digit_display_1136 (.value(register_76_q[35:32]));
  Hex_Digit_Display #(.decimalPoint("false")) hex_digit_display_1137 (.value(register_77_q[39:36]));
  Hex_Digit_Display #(.decimalPoint("false")) hex_digit_display_1138 (.value(register_77_q[35:32]));
  Hex_Digit_Display #(.decimalPoint("false")) hex_digit_display_1139 (.value(register_78_q[39:36]));
  Hex_Digit_Display #(.decimalPoint("false")) hex_digit_display_1140 (.value(register_78_q[35:32]));
  Hex_Digit_Display #(.decimalPoint("false")) hex_digit_display_1141 (.value(register_79_q[39:36]));
  Hex_Digit_Display #(.decimalPoint("false")) hex_digit_display_1142 (.value(register_79_q[35:32]));
  Hex_Digit_Display #(.decimalPoint("false")) hex_digit_display_1143 (.value(register_80_q[39:36]));
  Hex_Digit_Display #(.decimalPoint("false")) hex_digit_display_1144 (.value(register_80_q[35:32]));
  Hex_Digit_Display #(.decimalPoint("false")) hex_digit_display_1145 (.value(register_81_q[43:40]));
  Hex_Digit_Display #(.decimalPoint("false")) hex_digit_display_1146 (.value(register_81_q[39:36]));
  Hex_Digit_Display #(.decimalPoint("false")) hex_digit_display_1147 (.value(register_82_q[43:40]));
  Hex_Digit_Display #(.decimalPoint("false")) hex_digit_display_1148 (.value(register_82_q[39:36]));
  Hex_Digit_Display #(.decimalPoint("false")) hex_digit_display_1149 (.value(register_83_q[43:40]));
  Hex_Digit_Display #(.decimalPoint("false")) hex_digit_display_1150 (.value(register_83_q[39:36]));
  Hex_Digit_Display #(.decimalPoint("false")) hex_digit_display_1151 (.value(register_84_q[43:40]));
  Hex_Digit_Display #(.decimalPoint("false")) hex_digit_display_1152 (.value(register_84_q[39:36]));
  Hex_Digit_Display #(.decimalPoint("false")) hex_digit_display_1153 (.value(register_69_q[27:24]));
  Hex_Digit_Display #(.decimalPoint("false")) hex_digit_display_1154 (.value(register_69_q[23:20]));
  Hex_Digit_Display #(.decimalPoint("false")) hex_digit_display_1155 (.value(register_70_q[27:24]));
  Hex_Digit_Display #(.decimalPoint("false")) hex_digit_display_1156 (.value(register_70_q[23:20]));
  Hex_Digit_Display #(.decimalPoint("false")) hex_digit_display_1157 (.value(register_71_q[27:24]));
  Hex_Digit_Display #(.decimalPoint("false")) hex_digit_display_1158 (.value(register_71_q[23:20]));
  Hex_Digit_Display #(.decimalPoint("false")) hex_digit_display_1159 (.value(register_72_q[27:24]));
  Hex_Digit_Display #(.decimalPoint("false")) hex_digit_display_1160 (.value(register_72_q[23:20]));
  Hex_Digit_Display #(.decimalPoint("false")) hex_digit_display_1161 (.value(register_73_q[31:28]));
  Hex_Digit_Display #(.decimalPoint("false")) hex_digit_display_1162 (.value(register_73_q[27:24]));
  Hex_Digit_Display #(.decimalPoint("false")) hex_digit_display_1163 (.value(register_74_q[31:28]));
  Hex_Digit_Display #(.decimalPoint("false")) hex_digit_display_1164 (.value(register_74_q[27:24]));
  Hex_Digit_Display #(.decimalPoint("false")) hex_digit_display_1165 (.value(register_75_q[31:28]));
  Hex_Digit_Display #(.decimalPoint("false")) hex_digit_display_1166 (.value(register_75_q[27:24]));
  Hex_Digit_Display #(.decimalPoint("false")) hex_digit_display_1167 (.value(register_76_q[31:28]));
  Hex_Digit_Display #(.decimalPoint("false")) hex_digit_display_1168 (.value(register_76_q[27:24]));
  Hex_Digit_Display #(.decimalPoint("false")) hex_digit_display_1169 (.value(register_77_q[31:28]));
  Hex_Digit_Display #(.decimalPoint("false")) hex_digit_display_1170 (.value(register_77_q[27:24]));
  Hex_Digit_Display #(.decimalPoint("false")) hex_digit_display_1171 (.value(register_78_q[31:28]));
  Hex_Digit_Display #(.decimalPoint("false")) hex_digit_display_1172 (.value(register_78_q[27:24]));
  Hex_Digit_Display #(.decimalPoint("false")) hex_digit_display_1173 (.value(register_79_q[31:28]));
  Hex_Digit_Display #(.decimalPoint("false")) hex_digit_display_1174 (.value(register_79_q[27:24]));
  Hex_Digit_Display #(.decimalPoint("false")) hex_digit_display_1175 (.value(register_80_q[31:28]));
  Hex_Digit_Display #(.decimalPoint("false")) hex_digit_display_1176 (.value(register_80_q[27:24]));
  Hex_Digit_Display #(.decimalPoint("false")) hex_digit_display_1177 (.value(register_81_q[35:32]));
  Hex_Digit_Display #(.decimalPoint("false")) hex_digit_display_1178 (.value(register_81_q[31:28]));
  Hex_Digit_Display #(.decimalPoint("false")) hex_digit_display_1179 (.value(register_82_q[35:32]));
  Hex_Digit_Display #(.decimalPoint("false")) hex_digit_display_1180 (.value(register_82_q[31:28]));
  Hex_Digit_Display #(.decimalPoint("false")) hex_digit_display_1181 (.value(register_83_q[35:32]));
  Hex_Digit_Display #(.decimalPoint("false")) hex_digit_display_1182 (.value(register_83_q[31:28]));
  Hex_Digit_Display #(.decimalPoint("false")) hex_digit_display_1183 (.value(register_84_q[35:32]));
  Hex_Digit_Display #(.decimalPoint("false")) hex_digit_display_1184 (.value(register_84_q[31:28]));
  Hex_Digit_Display #(.decimalPoint("false")) hex_digit_display_1185 (.value(register_69_q[19:16]));
  Hex_Digit_Display #(.decimalPoint("false")) hex_digit_display_1186 (.value(register_69_q[15:12]));
  Hex_Digit_Display #(.decimalPoint("false")) hex_digit_display_1187 (.value(register_70_q[19:16]));
  Hex_Digit_Display #(.decimalPoint("false")) hex_digit_display_1188 (.value(register_70_q[15:12]));
  Hex_Digit_Display #(.decimalPoint("false")) hex_digit_display_1189 (.value(register_71_q[19:16]));
  Hex_Digit_Display #(.decimalPoint("false")) hex_digit_display_1190 (.value(register_71_q[15:12]));
  Hex_Digit_Display #(.decimalPoint("false")) hex_digit_display_1191 (.value(register_72_q[19:16]));
  Hex_Digit_Display #(.decimalPoint("false")) hex_digit_display_1192 (.value(register_72_q[15:12]));
  Hex_Digit_Display #(.decimalPoint("false")) hex_digit_display_1193 (.value(register_73_q[23:20]));
  Hex_Digit_Display #(.decimalPoint("false")) hex_digit_display_1194 (.value(register_73_q[19:16]));
  Hex_Digit_Display #(.decimalPoint("false")) hex_digit_display_1195 (.value(register_74_q[23:20]));
  Hex_Digit_Display #(.decimalPoint("false")) hex_digit_display_1196 (.value(register_74_q[19:16]));
  Hex_Digit_Display #(.decimalPoint("false")) hex_digit_display_1197 (.value(register_75_q[23:20]));
  Hex_Digit_Display #(.decimalPoint("false")) hex_digit_display_1198 (.value(register_75_q[19:16]));
  Hex_Digit_Display #(.decimalPoint("false")) hex_digit_display_1199 (.value(register_76_q[23:20]));
  Hex_Digit_Display #(.decimalPoint("false")) hex_digit_display_1200 (.value(register_76_q[19:16]));
  Hex_Digit_Display #(.decimalPoint("false")) hex_digit_display_1201 (.value(register_77_q[23:20]));
  Hex_Digit_Display #(.decimalPoint("false")) hex_digit_display_1202 (.value(register_77_q[19:16]));
  Hex_Digit_Display #(.decimalPoint("false")) hex_digit_display_1203 (.value(register_78_q[23:20]));
  Hex_Digit_Display #(.decimalPoint("false")) hex_digit_display_1204 (.value(register_78_q[19:16]));
  Hex_Digit_Display #(.decimalPoint("false")) hex_digit_display_1205 (.value(register_79_q[23:20]));
  Hex_Digit_Display #(.decimalPoint("false")) hex_digit_display_1206 (.value(register_79_q[19:16]));
  Hex_Digit_Display #(.decimalPoint("false")) hex_digit_display_1207 (.value(register_80_q[23:20]));
  Hex_Digit_Display #(.decimalPoint("false")) hex_digit_display_1208 (.value(register_80_q[19:16]));
  Hex_Digit_Display #(.decimalPoint("false")) hex_digit_display_1209 (.value(register_81_q[27:24]));
  Hex_Digit_Display #(.decimalPoint("false")) hex_digit_display_1210 (.value(register_81_q[23:20]));
  Hex_Digit_Display #(.decimalPoint("false")) hex_digit_display_1211 (.value(register_82_q[27:24]));
  Hex_Digit_Display #(.decimalPoint("false")) hex_digit_display_1212 (.value(register_82_q[23:20]));
  Hex_Digit_Display #(.decimalPoint("false")) hex_digit_display_1213 (.value(register_83_q[27:24]));
  Hex_Digit_Display #(.decimalPoint("false")) hex_digit_display_1214 (.value(register_83_q[23:20]));
  Hex_Digit_Display #(.decimalPoint("false")) hex_digit_display_1215 (.value(register_84_q[27:24]));
  Hex_Digit_Display #(.decimalPoint("false")) hex_digit_display_1216 (.value(register_84_q[23:20]));
  Hex_Digit_Display #(.decimalPoint("false")) hex_digit_display_1217 (.value(register_69_q[11:8]));
  Hex_Digit_Display #(.decimalPoint("false")) hex_digit_display_1218 (.value(register_69_q[7:4]));
  Hex_Digit_Display #(.decimalPoint("false")) hex_digit_display_1219 (.value(register_70_q[11:8]));
  Hex_Digit_Display #(.decimalPoint("false")) hex_digit_display_1220 (.value(register_70_q[7:4]));
  Hex_Digit_Display #(.decimalPoint("false")) hex_digit_display_1221 (.value(register_71_q[11:8]));
  Hex_Digit_Display #(.decimalPoint("false")) hex_digit_display_1222 (.value(register_71_q[7:4]));
  Hex_Digit_Display #(.decimalPoint("false")) hex_digit_display_1223 (.value(register_72_q[11:8]));
  Hex_Digit_Display #(.decimalPoint("false")) hex_digit_display_1224 (.value(register_72_q[7:4]));
  Hex_Digit_Display #(.decimalPoint("false")) hex_digit_display_1225 (.value(register_73_q[15:12]));
  Hex_Digit_Display #(.decimalPoint("false")) hex_digit_display_1226 (.value(register_73_q[11:8]));
  Hex_Digit_Display #(.decimalPoint("false")) hex_digit_display_1227 (.value(register_74_q[15:12]));
  Hex_Digit_Display #(.decimalPoint("false")) hex_digit_display_1228 (.value(register_74_q[11:8]));
  Hex_Digit_Display #(.decimalPoint("false")) hex_digit_display_1229 (.value(register_75_q[15:12]));
  Hex_Digit_Display #(.decimalPoint("false")) hex_digit_display_1230 (.value(register_75_q[11:8]));
  Hex_Digit_Display #(.decimalPoint("false")) hex_digit_display_1231 (.value(register_76_q[15:12]));
  Hex_Digit_Display #(.decimalPoint("false")) hex_digit_display_1232 (.value(register_76_q[11:8]));
  Hex_Digit_Display #(.decimalPoint("false")) hex_digit_display_1233 (.value(register_77_q[15:12]));
  Hex_Digit_Display #(.decimalPoint("false")) hex_digit_display_1234 (.value(register_77_q[11:8]));
  Hex_Digit_Display #(.decimalPoint("false")) hex_digit_display_1235 (.value(register_78_q[15:12]));
  Hex_Digit_Display #(.decimalPoint("false")) hex_digit_display_1236 (.value(register_78_q[11:8]));
  Hex_Digit_Display #(.decimalPoint("false")) hex_digit_display_1237 (.value(register_79_q[15:12]));
  Hex_Digit_Display #(.decimalPoint("false")) hex_digit_display_1238 (.value(register_79_q[11:8]));
  Hex_Digit_Display #(.decimalPoint("false")) hex_digit_display_1239 (.value(register_80_q[15:12]));
  Hex_Digit_Display #(.decimalPoint("false")) hex_digit_display_1240 (.value(register_80_q[11:8]));
  Hex_Digit_Display #(.decimalPoint("false")) hex_digit_display_1241 (.value(register_81_q[19:16]));
  Hex_Digit_Display #(.decimalPoint("false")) hex_digit_display_1242 (.value(register_81_q[15:12]));
  Hex_Digit_Display #(.decimalPoint("false")) hex_digit_display_1243 (.value(register_82_q[19:16]));
  Hex_Digit_Display #(.decimalPoint("false")) hex_digit_display_1244 (.value(register_82_q[15:12]));
  Hex_Digit_Display #(.decimalPoint("false")) hex_digit_display_1245 (.value(register_83_q[19:16]));
  Hex_Digit_Display #(.decimalPoint("false")) hex_digit_display_1246 (.value(register_83_q[15:12]));
  Hex_Digit_Display #(.decimalPoint("false")) hex_digit_display_1247 (.value(register_84_q[19:16]));
  Hex_Digit_Display #(.decimalPoint("false")) hex_digit_display_1248 (.value(register_84_q[15:12]));
  Hex_Digit_Display #(.decimalPoint("false")) hex_digit_display_1249 (.value(register_69_q[3:0]));
  Hex_Digit_Display #(.decimalPoint("false")) hex_digit_display_1250 (.value(register_70_q[3:0]));
  Hex_Digit_Display #(.decimalPoint("false")) hex_digit_display_1251 (.value(register_71_q[3:0]));
  Hex_Digit_Display #(.decimalPoint("false")) hex_digit_display_1252 (.value(register_72_q[3:0]));
  Hex_Digit_Display #(.decimalPoint("false")) hex_digit_display_1253 (.value(register_73_q[7:4]));
  Hex_Digit_Display #(.decimalPoint("false")) hex_digit_display_1254 (.value(register_73_q[3:0]));
  Hex_Digit_Display #(.decimalPoint("false")) hex_digit_display_1255 (.value(register_74_q[7:4]));
  Hex_Digit_Display #(.decimalPoint("false")) hex_digit_display_1256 (.value(register_74_q[3:0]));
  Hex_Digit_Display #(.decimalPoint("false")) hex_digit_display_1257 (.value(register_75_q[7:4]));
  Hex_Digit_Display #(.decimalPoint("false")) hex_digit_display_1258 (.value(register_75_q[3:0]));
  Hex_Digit_Display #(.decimalPoint("false")) hex_digit_display_1259 (.value(register_76_q[7:4]));
  Hex_Digit_Display #(.decimalPoint("false")) hex_digit_display_1260 (.value(register_76_q[3:0]));
  Hex_Digit_Display #(.decimalPoint("false")) hex_digit_display_1261 (.value(register_77_q[7:4]));
  Hex_Digit_Display #(.decimalPoint("false")) hex_digit_display_1262 (.value(register_77_q[3:0]));
  Hex_Digit_Display #(.decimalPoint("false")) hex_digit_display_1263 (.value(register_78_q[7:4]));
  Hex_Digit_Display #(.decimalPoint("false")) hex_digit_display_1264 (.value(register_78_q[3:0]));
  Hex_Digit_Display #(.decimalPoint("false")) hex_digit_display_1265 (.value(register_79_q[7:4]));
  Hex_Digit_Display #(.decimalPoint("false")) hex_digit_display_1266 (.value(register_79_q[3:0]));
  Hex_Digit_Display #(.decimalPoint("false")) hex_digit_display_1267 (.value(register_80_q[7:4]));
  Hex_Digit_Display #(.decimalPoint("false")) hex_digit_display_1268 (.value(register_80_q[3:0]));
  Hex_Digit_Display #(.decimalPoint("false")) hex_digit_display_1269 (.value(register_81_q[11:8]));
  Hex_Digit_Display #(.decimalPoint("false")) hex_digit_display_1270 (.value(register_81_q[7:4]));
  Hex_Digit_Display #(.decimalPoint("false")) hex_digit_display_1271 (.value(register_82_q[11:8]));
  Hex_Digit_Display #(.decimalPoint("false")) hex_digit_display_1272 (.value(register_82_q[7:4]));
  Hex_Digit_Display #(.decimalPoint("false")) hex_digit_display_1273 (.value(register_83_q[11:8]));
  Hex_Digit_Display #(.decimalPoint("false")) hex_digit_display_1274 (.value(register_83_q[7:4]));
  Hex_Digit_Display #(.decimalPoint("false")) hex_digit_display_1275 (.value(register_84_q[11:8]));
  Hex_Digit_Display #(.decimalPoint("false")) hex_digit_display_1276 (.value(register_84_q[7:4]));
  Register #(.width(64)) register_85 (.D(S1), .en(DISPLAY_2), .Q(register_85_q), .clk(undriven_28));  // open: clr
  Register #(.width(64)) register_86 (.D(S3), .en(DISPLAY_2), .Q(register_86_q), .clk(undriven_28));  // open: clr
  Register #(.width(64)) register_87 (.D(S1), .en(undriven_25), .Q(register_87_q), .clk(undriven_29));  // open: clr
  Register #(.width(64)) register_88 (.D(S3), .en(undriven_25), .Q(register_88_q), .clk(undriven_29));  // open: clr
  Register #(.width(64)) register_89 (.D(S1), .en(undriven_26), .Q(register_89_q), .clk(undriven_30));  // open: clr
  Register #(.width(64)) register_90 (.D(S3), .en(undriven_26), .Q(register_90_q), .clk(undriven_30));  // open: clr
  Register #(.width(64)) register_91 (.D(S1), .en(undriven_27), .Q(register_91_q), .clk(undriven_31));  // open: clr
  Register #(.width(64)) register_92 (.D(S3), .en(undriven_27), .Q(register_92_q), .clk(undriven_31));  // open: clr
  Hex_Digit_Display #(.decimalPoint("false")) hex_digit_display_1277 (.value(register_81_q[3:0]));
  Hex_Digit_Display #(.decimalPoint("false")) hex_digit_display_1278 (.value(register_82_q[3:0]));
  Hex_Digit_Display #(.decimalPoint("false")) hex_digit_display_1279 (.value(register_83_q[3:0]));
  Hex_Digit_Display #(.decimalPoint("false")) hex_digit_display_1280 (.value(register_84_q[3:0]));
  Hex_Digit_Display #(.decimalPoint("false")) hex_digit_display_1281 (.value(register_85_q[63:60]));
  Hex_Digit_Display #(.decimalPoint("false")) hex_digit_display_1282 (.value(register_85_q[59:56]));
  Hex_Digit_Display #(.decimalPoint("false")) hex_digit_display_1283 (.value(register_86_q[63:60]));
  Hex_Digit_Display #(.decimalPoint("false")) hex_digit_display_1284 (.value(register_86_q[59:56]));
  Hex_Digit_Display #(.decimalPoint("false")) hex_digit_display_1285 (.value(register_87_q[63:60]));
  Hex_Digit_Display #(.decimalPoint("false")) hex_digit_display_1286 (.value(register_87_q[59:56]));
  Hex_Digit_Display #(.decimalPoint("false")) hex_digit_display_1287 (.value(register_88_q[63:60]));
  Hex_Digit_Display #(.decimalPoint("false")) hex_digit_display_1288 (.value(register_88_q[59:56]));
  Hex_Digit_Display #(.decimalPoint("false")) hex_digit_display_1289 (.value(register_89_q[63:60]));
  Hex_Digit_Display #(.decimalPoint("false")) hex_digit_display_1290 (.value(register_89_q[59:56]));
  Hex_Digit_Display #(.decimalPoint("false")) hex_digit_display_1291 (.value(register_90_q[63:60]));
  Hex_Digit_Display #(.decimalPoint("false")) hex_digit_display_1292 (.value(register_90_q[59:56]));
  Hex_Digit_Display #(.decimalPoint("false")) hex_digit_display_1293 (.value(register_91_q[63:60]));
  Hex_Digit_Display #(.decimalPoint("false")) hex_digit_display_1294 (.value(register_91_q[59:56]));
  Hex_Digit_Display #(.decimalPoint("false")) hex_digit_display_1295 (.value(register_92_q[63:60]));
  Hex_Digit_Display #(.decimalPoint("false")) hex_digit_display_1296 (.value(register_92_q[59:56]));
  Register #(.width(64)) register_93 (.D(S1), .en(undriven_32), .Q(register_93_q), .clk(undriven_36));  // open: clr
  Hex_Digit_Display #(.decimalPoint("false")) hex_digit_display_1297 (.value(register_93_q[63:60]));
  Register #(.width(64)) register_94 (.D(S3), .en(undriven_32), .Q(register_94_q), .clk(undriven_36));  // open: clr
  Hex_Digit_Display #(.decimalPoint("false")) hex_digit_display_1298 (.value(register_94_q[63:60]));
  Register #(.width(64)) register_95 (.D(S1), .en(undriven_33), .Q(register_95_q), .clk(undriven_37));  // open: clr
  Hex_Digit_Display #(.decimalPoint("false")) hex_digit_display_1299 (.value(register_95_q[63:60]));
  Register #(.width(64)) register_96 (.D(S3), .en(undriven_33), .Q(register_96_q), .clk(undriven_37));  // open: clr
  Hex_Digit_Display #(.decimalPoint("false")) hex_digit_display_1300 (.value(register_96_q[63:60]));
  Register #(.width(64)) register_97 (.D(S1), .en(undriven_34), .Q(register_97_q), .clk(undriven_38));  // open: clr
  Hex_Digit_Display #(.decimalPoint("false")) hex_digit_display_1301 (.value(register_97_q[63:60]));
  Register #(.width(64)) register_98 (.D(S3), .en(undriven_34), .Q(register_98_q), .clk(undriven_38));  // open: clr
  Hex_Digit_Display #(.decimalPoint("false")) hex_digit_display_1302 (.value(register_98_q[63:60]));
  Register #(.width(64)) register_99 (.D(S1), .en(undriven_35), .Q(register_99_q), .clk(undriven_39));  // open: clr
  Hex_Digit_Display #(.decimalPoint("false")) hex_digit_display_1303 (.value(register_99_q[63:60]));
  Register #(.width(64)) register_100 (.D(S3), .en(undriven_35), .Q(register_100_q), .clk(undriven_39));  // open: clr
  Hex_Digit_Display #(.decimalPoint("false")) hex_digit_display_1304 (.value(register_100_q[63:60]));
  Hex_Digit_Display #(.decimalPoint("false")) hex_digit_display_1305 (.value(register_85_q[55:52]));
  Hex_Digit_Display #(.decimalPoint("false")) hex_digit_display_1306 (.value(register_85_q[51:48]));
  Hex_Digit_Display #(.decimalPoint("false")) hex_digit_display_1307 (.value(register_86_q[55:52]));
  Hex_Digit_Display #(.decimalPoint("false")) hex_digit_display_1308 (.value(register_86_q[51:48]));
  Hex_Digit_Display #(.decimalPoint("false")) hex_digit_display_1309 (.value(register_87_q[55:52]));
  Hex_Digit_Display #(.decimalPoint("false")) hex_digit_display_1310 (.value(register_87_q[51:48]));
  Hex_Digit_Display #(.decimalPoint("false")) hex_digit_display_1311 (.value(register_88_q[55:52]));
  Hex_Digit_Display #(.decimalPoint("false")) hex_digit_display_1312 (.value(register_88_q[51:48]));
  Hex_Digit_Display #(.decimalPoint("false")) hex_digit_display_1313 (.value(register_89_q[55:52]));
  Hex_Digit_Display #(.decimalPoint("false")) hex_digit_display_1314 (.value(register_89_q[51:48]));
  Hex_Digit_Display #(.decimalPoint("false")) hex_digit_display_1315 (.value(register_90_q[55:52]));
  Hex_Digit_Display #(.decimalPoint("false")) hex_digit_display_1316 (.value(register_90_q[51:48]));
  Hex_Digit_Display #(.decimalPoint("false")) hex_digit_display_1317 (.value(register_91_q[55:52]));
  Hex_Digit_Display #(.decimalPoint("false")) hex_digit_display_1318 (.value(register_91_q[51:48]));
  Hex_Digit_Display #(.decimalPoint("false")) hex_digit_display_1319 (.value(register_92_q[55:52]));
  Hex_Digit_Display #(.decimalPoint("false")) hex_digit_display_1320 (.value(register_92_q[51:48]));
  Hex_Digit_Display #(.decimalPoint("false")) hex_digit_display_1321 (.value(register_93_q[59:56]));
  Hex_Digit_Display #(.decimalPoint("false")) hex_digit_display_1322 (.value(register_93_q[55:52]));
  Hex_Digit_Display #(.decimalPoint("false")) hex_digit_display_1323 (.value(register_94_q[59:56]));
  Hex_Digit_Display #(.decimalPoint("false")) hex_digit_display_1324 (.value(register_94_q[55:52]));
  Hex_Digit_Display #(.decimalPoint("false")) hex_digit_display_1325 (.value(register_95_q[59:56]));
  Hex_Digit_Display #(.decimalPoint("false")) hex_digit_display_1326 (.value(register_95_q[55:52]));
  Hex_Digit_Display #(.decimalPoint("false")) hex_digit_display_1327 (.value(register_96_q[59:56]));
  Hex_Digit_Display #(.decimalPoint("false")) hex_digit_display_1328 (.value(register_96_q[55:52]));
  Hex_Digit_Display #(.decimalPoint("false")) hex_digit_display_1329 (.value(register_97_q[59:56]));
  Hex_Digit_Display #(.decimalPoint("false")) hex_digit_display_1330 (.value(register_97_q[55:52]));
  Hex_Digit_Display #(.decimalPoint("false")) hex_digit_display_1331 (.value(register_98_q[59:56]));
  Hex_Digit_Display #(.decimalPoint("false")) hex_digit_display_1332 (.value(register_98_q[55:52]));
  Hex_Digit_Display #(.decimalPoint("false")) hex_digit_display_1333 (.value(register_99_q[59:56]));
  Hex_Digit_Display #(.decimalPoint("false")) hex_digit_display_1334 (.value(register_99_q[55:52]));
  Hex_Digit_Display #(.decimalPoint("false")) hex_digit_display_1335 (.value(register_100_q[59:56]));
  Hex_Digit_Display #(.decimalPoint("false")) hex_digit_display_1336 (.value(register_100_q[55:52]));
  Hex_Digit_Display #(.decimalPoint("false")) hex_digit_display_1337 (.value(register_85_q[47:44]));
  Hex_Digit_Display #(.decimalPoint("false")) hex_digit_display_1338 (.value(register_85_q[43:40]));
  Hex_Digit_Display #(.decimalPoint("false")) hex_digit_display_1339 (.value(register_86_q[47:44]));
  Hex_Digit_Display #(.decimalPoint("false")) hex_digit_display_1340 (.value(register_86_q[43:40]));
  Hex_Digit_Display #(.decimalPoint("false")) hex_digit_display_1341 (.value(register_87_q[47:44]));
  Hex_Digit_Display #(.decimalPoint("false")) hex_digit_display_1342 (.value(register_87_q[43:40]));
  Hex_Digit_Display #(.decimalPoint("false")) hex_digit_display_1343 (.value(register_88_q[47:44]));
  Hex_Digit_Display #(.decimalPoint("false")) hex_digit_display_1344 (.value(register_88_q[43:40]));
  Hex_Digit_Display #(.decimalPoint("false")) hex_digit_display_1345 (.value(register_89_q[47:44]));
  Hex_Digit_Display #(.decimalPoint("false")) hex_digit_display_1346 (.value(register_89_q[43:40]));
  Hex_Digit_Display #(.decimalPoint("false")) hex_digit_display_1347 (.value(register_90_q[47:44]));
  Hex_Digit_Display #(.decimalPoint("false")) hex_digit_display_1348 (.value(register_90_q[43:40]));
  Hex_Digit_Display #(.decimalPoint("false")) hex_digit_display_1349 (.value(register_91_q[47:44]));
  Hex_Digit_Display #(.decimalPoint("false")) hex_digit_display_1350 (.value(register_91_q[43:40]));
  Hex_Digit_Display #(.decimalPoint("false")) hex_digit_display_1351 (.value(register_92_q[47:44]));
  Hex_Digit_Display #(.decimalPoint("false")) hex_digit_display_1352 (.value(register_92_q[43:40]));
  Hex_Digit_Display #(.decimalPoint("false")) hex_digit_display_1353 (.value(register_93_q[51:48]));
  Hex_Digit_Display #(.decimalPoint("false")) hex_digit_display_1354 (.value(register_93_q[47:44]));
  Hex_Digit_Display #(.decimalPoint("false")) hex_digit_display_1355 (.value(register_94_q[51:48]));
  Hex_Digit_Display #(.decimalPoint("false")) hex_digit_display_1356 (.value(register_94_q[47:44]));
  Hex_Digit_Display #(.decimalPoint("false")) hex_digit_display_1357 (.value(register_95_q[51:48]));
  Hex_Digit_Display #(.decimalPoint("false")) hex_digit_display_1358 (.value(register_95_q[47:44]));
  Hex_Digit_Display #(.decimalPoint("false")) hex_digit_display_1359 (.value(register_96_q[51:48]));
  Hex_Digit_Display #(.decimalPoint("false")) hex_digit_display_1360 (.value(register_96_q[47:44]));
  Hex_Digit_Display #(.decimalPoint("false")) hex_digit_display_1361 (.value(register_97_q[51:48]));
  Hex_Digit_Display #(.decimalPoint("false")) hex_digit_display_1362 (.value(register_97_q[47:44]));
  Hex_Digit_Display #(.decimalPoint("false")) hex_digit_display_1363 (.value(register_98_q[51:48]));
  Hex_Digit_Display #(.decimalPoint("false")) hex_digit_display_1364 (.value(register_98_q[47:44]));
  Hex_Digit_Display #(.decimalPoint("false")) hex_digit_display_1365 (.value(register_99_q[51:48]));
  Hex_Digit_Display #(.decimalPoint("false")) hex_digit_display_1366 (.value(register_99_q[47:44]));
  Hex_Digit_Display #(.decimalPoint("false")) hex_digit_display_1367 (.value(register_100_q[51:48]));
  Hex_Digit_Display #(.decimalPoint("false")) hex_digit_display_1368 (.value(register_100_q[47:44]));
  Hex_Digit_Display #(.decimalPoint("false")) hex_digit_display_1369 (.value(register_85_q[39:36]));
  Hex_Digit_Display #(.decimalPoint("false")) hex_digit_display_1370 (.value(register_85_q[35:32]));
  Hex_Digit_Display #(.decimalPoint("false")) hex_digit_display_1371 (.value(register_86_q[39:36]));
  Hex_Digit_Display #(.decimalPoint("false")) hex_digit_display_1372 (.value(register_86_q[35:32]));
  Hex_Digit_Display #(.decimalPoint("false")) hex_digit_display_1373 (.value(register_87_q[39:36]));
  Hex_Digit_Display #(.decimalPoint("false")) hex_digit_display_1374 (.value(register_87_q[35:32]));
  Hex_Digit_Display #(.decimalPoint("false")) hex_digit_display_1375 (.value(register_88_q[39:36]));
  Hex_Digit_Display #(.decimalPoint("false")) hex_digit_display_1376 (.value(register_88_q[35:32]));
  Hex_Digit_Display #(.decimalPoint("false")) hex_digit_display_1377 (.value(register_89_q[39:36]));
  Hex_Digit_Display #(.decimalPoint("false")) hex_digit_display_1378 (.value(register_89_q[35:32]));
  Hex_Digit_Display #(.decimalPoint("false")) hex_digit_display_1379 (.value(register_90_q[39:36]));
  Hex_Digit_Display #(.decimalPoint("false")) hex_digit_display_1380 (.value(register_90_q[35:32]));
  Hex_Digit_Display #(.decimalPoint("false")) hex_digit_display_1381 (.value(register_91_q[39:36]));
  Hex_Digit_Display #(.decimalPoint("false")) hex_digit_display_1382 (.value(register_91_q[35:32]));
  Hex_Digit_Display #(.decimalPoint("false")) hex_digit_display_1383 (.value(register_92_q[39:36]));
  Hex_Digit_Display #(.decimalPoint("false")) hex_digit_display_1384 (.value(register_92_q[35:32]));
  Hex_Digit_Display #(.decimalPoint("false")) hex_digit_display_1385 (.value(register_93_q[43:40]));
  Hex_Digit_Display #(.decimalPoint("false")) hex_digit_display_1386 (.value(register_93_q[39:36]));
  Hex_Digit_Display #(.decimalPoint("false")) hex_digit_display_1387 (.value(register_94_q[43:40]));
  Hex_Digit_Display #(.decimalPoint("false")) hex_digit_display_1388 (.value(register_94_q[39:36]));
  Hex_Digit_Display #(.decimalPoint("false")) hex_digit_display_1389 (.value(register_95_q[43:40]));
  Hex_Digit_Display #(.decimalPoint("false")) hex_digit_display_1390 (.value(register_95_q[39:36]));
  Hex_Digit_Display #(.decimalPoint("false")) hex_digit_display_1391 (.value(register_96_q[43:40]));
  Hex_Digit_Display #(.decimalPoint("false")) hex_digit_display_1392 (.value(register_96_q[39:36]));
  Hex_Digit_Display #(.decimalPoint("false")) hex_digit_display_1393 (.value(register_97_q[43:40]));
  Hex_Digit_Display #(.decimalPoint("false")) hex_digit_display_1394 (.value(register_97_q[39:36]));
  Hex_Digit_Display #(.decimalPoint("false")) hex_digit_display_1395 (.value(register_98_q[43:40]));
  Hex_Digit_Display #(.decimalPoint("false")) hex_digit_display_1396 (.value(register_98_q[39:36]));
  Hex_Digit_Display #(.decimalPoint("false")) hex_digit_display_1397 (.value(register_99_q[43:40]));
  Hex_Digit_Display #(.decimalPoint("false")) hex_digit_display_1398 (.value(register_99_q[39:36]));
  Hex_Digit_Display #(.decimalPoint("false")) hex_digit_display_1399 (.value(register_100_q[43:40]));
  Hex_Digit_Display #(.decimalPoint("false")) hex_digit_display_1400 (.value(register_100_q[39:36]));
  Hex_Digit_Display #(.decimalPoint("false")) hex_digit_display_1401 (.value(register_85_q[31:28]));
  Hex_Digit_Display #(.decimalPoint("false")) hex_digit_display_1402 (.value(register_85_q[27:24]));
  Hex_Digit_Display #(.decimalPoint("false")) hex_digit_display_1403 (.value(register_86_q[31:28]));
  Hex_Digit_Display #(.decimalPoint("false")) hex_digit_display_1404 (.value(register_86_q[27:24]));
  Hex_Digit_Display #(.decimalPoint("false")) hex_digit_display_1405 (.value(register_87_q[31:28]));
  Hex_Digit_Display #(.decimalPoint("false")) hex_digit_display_1406 (.value(register_87_q[27:24]));
  Hex_Digit_Display #(.decimalPoint("false")) hex_digit_display_1407 (.value(register_88_q[31:28]));
  Hex_Digit_Display #(.decimalPoint("false")) hex_digit_display_1408 (.value(register_88_q[27:24]));
  Hex_Digit_Display #(.decimalPoint("false")) hex_digit_display_1409 (.value(register_89_q[31:28]));
  Hex_Digit_Display #(.decimalPoint("false")) hex_digit_display_1410 (.value(register_89_q[27:24]));
  Hex_Digit_Display #(.decimalPoint("false")) hex_digit_display_1411 (.value(register_90_q[31:28]));
  Hex_Digit_Display #(.decimalPoint("false")) hex_digit_display_1412 (.value(register_90_q[27:24]));
  Hex_Digit_Display #(.decimalPoint("false")) hex_digit_display_1413 (.value(register_91_q[31:28]));
  Hex_Digit_Display #(.decimalPoint("false")) hex_digit_display_1414 (.value(register_91_q[27:24]));
  Hex_Digit_Display #(.decimalPoint("false")) hex_digit_display_1415 (.value(register_92_q[31:28]));
  Hex_Digit_Display #(.decimalPoint("false")) hex_digit_display_1416 (.value(register_92_q[27:24]));
  Hex_Digit_Display #(.decimalPoint("false")) hex_digit_display_1417 (.value(register_93_q[35:32]));
  Hex_Digit_Display #(.decimalPoint("false")) hex_digit_display_1418 (.value(register_93_q[31:28]));
  Hex_Digit_Display #(.decimalPoint("false")) hex_digit_display_1419 (.value(register_94_q[35:32]));
  Hex_Digit_Display #(.decimalPoint("false")) hex_digit_display_1420 (.value(register_94_q[31:28]));
  Hex_Digit_Display #(.decimalPoint("false")) hex_digit_display_1421 (.value(register_95_q[35:32]));
  Hex_Digit_Display #(.decimalPoint("false")) hex_digit_display_1422 (.value(register_95_q[31:28]));
  Hex_Digit_Display #(.decimalPoint("false")) hex_digit_display_1423 (.value(register_96_q[35:32]));
  Hex_Digit_Display #(.decimalPoint("false")) hex_digit_display_1424 (.value(register_96_q[31:28]));
  Hex_Digit_Display #(.decimalPoint("false")) hex_digit_display_1425 (.value(register_97_q[35:32]));
  Hex_Digit_Display #(.decimalPoint("false")) hex_digit_display_1426 (.value(register_97_q[31:28]));
  Hex_Digit_Display #(.decimalPoint("false")) hex_digit_display_1427 (.value(register_98_q[35:32]));
  Hex_Digit_Display #(.decimalPoint("false")) hex_digit_display_1428 (.value(register_98_q[31:28]));
  Hex_Digit_Display #(.decimalPoint("false")) hex_digit_display_1429 (.value(register_99_q[35:32]));
  Hex_Digit_Display #(.decimalPoint("false")) hex_digit_display_1430 (.value(register_99_q[31:28]));
  Hex_Digit_Display #(.decimalPoint("false")) hex_digit_display_1431 (.value(register_100_q[35:32]));
  Hex_Digit_Display #(.decimalPoint("false")) hex_digit_display_1432 (.value(register_100_q[31:28]));
  Hex_Digit_Display #(.decimalPoint("false")) hex_digit_display_1433 (.value(register_85_q[23:20]));
  Hex_Digit_Display #(.decimalPoint("false")) hex_digit_display_1434 (.value(register_85_q[19:16]));
  Hex_Digit_Display #(.decimalPoint("false")) hex_digit_display_1435 (.value(register_86_q[23:20]));
  Hex_Digit_Display #(.decimalPoint("false")) hex_digit_display_1436 (.value(register_86_q[19:16]));
  Hex_Digit_Display #(.decimalPoint("false")) hex_digit_display_1437 (.value(register_87_q[23:20]));
  Hex_Digit_Display #(.decimalPoint("false")) hex_digit_display_1438 (.value(register_87_q[19:16]));
  Hex_Digit_Display #(.decimalPoint("false")) hex_digit_display_1439 (.value(register_88_q[23:20]));
  Hex_Digit_Display #(.decimalPoint("false")) hex_digit_display_1440 (.value(register_88_q[19:16]));
  Hex_Digit_Display #(.decimalPoint("false")) hex_digit_display_1441 (.value(register_89_q[23:20]));
  Hex_Digit_Display #(.decimalPoint("false")) hex_digit_display_1442 (.value(register_89_q[19:16]));
  Hex_Digit_Display #(.decimalPoint("false")) hex_digit_display_1443 (.value(register_90_q[23:20]));
  Hex_Digit_Display #(.decimalPoint("false")) hex_digit_display_1444 (.value(register_90_q[19:16]));
  Hex_Digit_Display #(.decimalPoint("false")) hex_digit_display_1445 (.value(register_91_q[23:20]));
  Hex_Digit_Display #(.decimalPoint("false")) hex_digit_display_1446 (.value(register_91_q[19:16]));
  Hex_Digit_Display #(.decimalPoint("false")) hex_digit_display_1447 (.value(register_92_q[23:20]));
  Hex_Digit_Display #(.decimalPoint("false")) hex_digit_display_1448 (.value(register_92_q[19:16]));
  Hex_Digit_Display #(.decimalPoint("false")) hex_digit_display_1449 (.value(register_93_q[27:24]));
  Hex_Digit_Display #(.decimalPoint("false")) hex_digit_display_1450 (.value(register_93_q[23:20]));
  Hex_Digit_Display #(.decimalPoint("false")) hex_digit_display_1451 (.value(register_94_q[27:24]));
  Hex_Digit_Display #(.decimalPoint("false")) hex_digit_display_1452 (.value(register_94_q[23:20]));
  Hex_Digit_Display #(.decimalPoint("false")) hex_digit_display_1453 (.value(register_95_q[27:24]));
  Hex_Digit_Display #(.decimalPoint("false")) hex_digit_display_1454 (.value(register_95_q[23:20]));
  Hex_Digit_Display #(.decimalPoint("false")) hex_digit_display_1455 (.value(register_96_q[27:24]));
  Hex_Digit_Display #(.decimalPoint("false")) hex_digit_display_1456 (.value(register_96_q[23:20]));
  Hex_Digit_Display #(.decimalPoint("false")) hex_digit_display_1457 (.value(register_97_q[27:24]));
  Hex_Digit_Display #(.decimalPoint("false")) hex_digit_display_1458 (.value(register_97_q[23:20]));
  Hex_Digit_Display #(.decimalPoint("false")) hex_digit_display_1459 (.value(register_98_q[27:24]));
  Hex_Digit_Display #(.decimalPoint("false")) hex_digit_display_1460 (.value(register_98_q[23:20]));
  Hex_Digit_Display #(.decimalPoint("false")) hex_digit_display_1461 (.value(register_99_q[27:24]));
  Hex_Digit_Display #(.decimalPoint("false")) hex_digit_display_1462 (.value(register_99_q[23:20]));
  Hex_Digit_Display #(.decimalPoint("false")) hex_digit_display_1463 (.value(register_100_q[27:24]));
  Hex_Digit_Display #(.decimalPoint("false")) hex_digit_display_1464 (.value(register_100_q[23:20]));
  Hex_Digit_Display #(.decimalPoint("false")) hex_digit_display_1465 (.value(register_85_q[15:12]));
  Hex_Digit_Display #(.decimalPoint("false")) hex_digit_display_1466 (.value(register_85_q[11:8]));
  Hex_Digit_Display #(.decimalPoint("false")) hex_digit_display_1467 (.value(register_86_q[15:12]));
  Hex_Digit_Display #(.decimalPoint("false")) hex_digit_display_1468 (.value(register_86_q[11:8]));
  Hex_Digit_Display #(.decimalPoint("false")) hex_digit_display_1469 (.value(register_87_q[15:12]));
  Hex_Digit_Display #(.decimalPoint("false")) hex_digit_display_1470 (.value(register_87_q[11:8]));
  Hex_Digit_Display #(.decimalPoint("false")) hex_digit_display_1471 (.value(register_88_q[15:12]));
  Hex_Digit_Display #(.decimalPoint("false")) hex_digit_display_1472 (.value(register_88_q[11:8]));
  Hex_Digit_Display #(.decimalPoint("false")) hex_digit_display_1473 (.value(register_89_q[15:12]));
  Hex_Digit_Display #(.decimalPoint("false")) hex_digit_display_1474 (.value(register_89_q[11:8]));
  Hex_Digit_Display #(.decimalPoint("false")) hex_digit_display_1475 (.value(register_90_q[15:12]));
  Hex_Digit_Display #(.decimalPoint("false")) hex_digit_display_1476 (.value(register_90_q[11:8]));
  Hex_Digit_Display #(.decimalPoint("false")) hex_digit_display_1477 (.value(register_91_q[15:12]));
  Hex_Digit_Display #(.decimalPoint("false")) hex_digit_display_1478 (.value(register_91_q[11:8]));
  Hex_Digit_Display #(.decimalPoint("false")) hex_digit_display_1479 (.value(register_92_q[15:12]));
  Hex_Digit_Display #(.decimalPoint("false")) hex_digit_display_1480 (.value(register_92_q[11:8]));
  Hex_Digit_Display #(.decimalPoint("false")) hex_digit_display_1481 (.value(register_93_q[19:16]));
  Hex_Digit_Display #(.decimalPoint("false")) hex_digit_display_1482 (.value(register_93_q[15:12]));
  Hex_Digit_Display #(.decimalPoint("false")) hex_digit_display_1483 (.value(register_94_q[19:16]));
  Hex_Digit_Display #(.decimalPoint("false")) hex_digit_display_1484 (.value(register_94_q[15:12]));
  Hex_Digit_Display #(.decimalPoint("false")) hex_digit_display_1485 (.value(register_95_q[19:16]));
  Hex_Digit_Display #(.decimalPoint("false")) hex_digit_display_1486 (.value(register_95_q[15:12]));
  Hex_Digit_Display #(.decimalPoint("false")) hex_digit_display_1487 (.value(register_96_q[19:16]));
  Hex_Digit_Display #(.decimalPoint("false")) hex_digit_display_1488 (.value(register_96_q[15:12]));
  Hex_Digit_Display #(.decimalPoint("false")) hex_digit_display_1489 (.value(register_97_q[19:16]));
  Hex_Digit_Display #(.decimalPoint("false")) hex_digit_display_1490 (.value(register_97_q[15:12]));
  Hex_Digit_Display #(.decimalPoint("false")) hex_digit_display_1491 (.value(register_98_q[19:16]));
  Hex_Digit_Display #(.decimalPoint("false")) hex_digit_display_1492 (.value(register_98_q[15:12]));
  Hex_Digit_Display #(.decimalPoint("false")) hex_digit_display_1493 (.value(register_99_q[19:16]));
  Hex_Digit_Display #(.decimalPoint("false")) hex_digit_display_1494 (.value(register_99_q[15:12]));
  Hex_Digit_Display #(.decimalPoint("false")) hex_digit_display_1495 (.value(register_100_q[19:16]));
  Hex_Digit_Display #(.decimalPoint("false")) hex_digit_display_1496 (.value(register_100_q[15:12]));
  Hex_Digit_Display #(.decimalPoint("false")) hex_digit_display_1497 (.value(register_85_q[7:4]));
  Hex_Digit_Display #(.decimalPoint("false")) hex_digit_display_1498 (.value(register_85_q[3:0]));
  Hex_Digit_Display #(.decimalPoint("false")) hex_digit_display_1499 (.value(register_86_q[7:4]));
  Hex_Digit_Display #(.decimalPoint("false")) hex_digit_display_1500 (.value(register_86_q[3:0]));
  Hex_Digit_Display #(.decimalPoint("false")) hex_digit_display_1501 (.value(register_87_q[7:4]));
  Hex_Digit_Display #(.decimalPoint("false")) hex_digit_display_1502 (.value(register_87_q[3:0]));
  Hex_Digit_Display #(.decimalPoint("false")) hex_digit_display_1503 (.value(register_88_q[7:4]));
  Hex_Digit_Display #(.decimalPoint("false")) hex_digit_display_1504 (.value(register_88_q[3:0]));
  Hex_Digit_Display #(.decimalPoint("false")) hex_digit_display_1505 (.value(register_89_q[7:4]));
  Hex_Digit_Display #(.decimalPoint("false")) hex_digit_display_1506 (.value(register_89_q[3:0]));
  Hex_Digit_Display #(.decimalPoint("false")) hex_digit_display_1507 (.value(register_90_q[7:4]));
  Hex_Digit_Display #(.decimalPoint("false")) hex_digit_display_1508 (.value(register_90_q[3:0]));
  Hex_Digit_Display #(.decimalPoint("false")) hex_digit_display_1509 (.value(register_91_q[7:4]));
  Hex_Digit_Display #(.decimalPoint("false")) hex_digit_display_1510 (.value(register_91_q[3:0]));
  Hex_Digit_Display #(.decimalPoint("false")) hex_digit_display_1511 (.value(register_92_q[7:4]));
  Hex_Digit_Display #(.decimalPoint("false")) hex_digit_display_1512 (.value(register_92_q[3:0]));
  Hex_Digit_Display #(.decimalPoint("false")) hex_digit_display_1513 (.value(register_93_q[11:8]));
  Hex_Digit_Display #(.decimalPoint("false")) hex_digit_display_1514 (.value(register_93_q[7:4]));
  Hex_Digit_Display #(.decimalPoint("false")) hex_digit_display_1515 (.value(register_94_q[11:8]));
  Hex_Digit_Display #(.decimalPoint("false")) hex_digit_display_1516 (.value(register_94_q[7:4]));
  Hex_Digit_Display #(.decimalPoint("false")) hex_digit_display_1517 (.value(register_95_q[11:8]));
  Hex_Digit_Display #(.decimalPoint("false")) hex_digit_display_1518 (.value(register_95_q[7:4]));
  Hex_Digit_Display #(.decimalPoint("false")) hex_digit_display_1519 (.value(register_96_q[11:8]));
  Hex_Digit_Display #(.decimalPoint("false")) hex_digit_display_1520 (.value(register_96_q[7:4]));
  Hex_Digit_Display #(.decimalPoint("false")) hex_digit_display_1521 (.value(register_97_q[11:8]));
  Hex_Digit_Display #(.decimalPoint("false")) hex_digit_display_1522 (.value(register_97_q[7:4]));
  Hex_Digit_Display #(.decimalPoint("false")) hex_digit_display_1523 (.value(register_98_q[11:8]));
  Hex_Digit_Display #(.decimalPoint("false")) hex_digit_display_1524 (.value(register_98_q[7:4]));
  Hex_Digit_Display #(.decimalPoint("false")) hex_digit_display_1525 (.value(register_99_q[11:8]));
  Hex_Digit_Display #(.decimalPoint("false")) hex_digit_display_1526 (.value(register_99_q[7:4]));
  Hex_Digit_Display #(.decimalPoint("false")) hex_digit_display_1527 (.value(register_100_q[11:8]));
  Hex_Digit_Display #(.decimalPoint("false")) hex_digit_display_1528 (.value(register_100_q[7:4]));
  Hex_Digit_Display #(.decimalPoint("false")) hex_digit_display_1529 (.value(register_93_q[3:0]));
  Hex_Digit_Display #(.decimalPoint("false")) hex_digit_display_1530 (.value(register_94_q[3:0]));
  Hex_Digit_Display #(.decimalPoint("false")) hex_digit_display_1531 (.value(register_95_q[3:0]));
  Hex_Digit_Display #(.decimalPoint("false")) hex_digit_display_1532 (.value(register_96_q[3:0]));
  Hex_Digit_Display #(.decimalPoint("false")) hex_digit_display_1533 (.value(register_97_q[3:0]));
  Hex_Digit_Display #(.decimalPoint("false")) hex_digit_display_1534 (.value(register_98_q[3:0]));
  Hex_Digit_Display #(.decimalPoint("false")) hex_digit_display_1535 (.value(register_99_q[3:0]));
  Hex_Digit_Display #(.decimalPoint("false")) hex_digit_display_1536 (.value(register_100_q[3:0]));
  Register #(.width(64)) register_101 (.D(S0), .en(undriven_40), .Q(register_101_q), .clk(undriven_44));  // open: clr
  Hex_Digit_Display #(.decimalPoint("false")) hex_digit_display_1537 (.value(register_101_q[63:60]));
  Register #(.width(64)) register_102 (.D(S2), .en(undriven_40), .Q(register_102_q), .clk(undriven_44));  // open: clr
  Hex_Digit_Display #(.decimalPoint("false")) hex_digit_display_1538 (.value(register_102_q[63:60]));
  Register #(.width(64)) register_103 (.D(S0), .en(undriven_41), .Q(register_103_q), .clk(undriven_45));  // open: clr
  Hex_Digit_Display #(.decimalPoint("false")) hex_digit_display_1539 (.value(register_103_q[63:60]));
  Register #(.width(64)) register_104 (.D(S2), .en(undriven_41), .Q(register_104_q), .clk(undriven_45));  // open: clr
  Hex_Digit_Display #(.decimalPoint("false")) hex_digit_display_1540 (.value(register_104_q[63:60]));
  Register #(.width(64)) register_105 (.D(S0), .en(undriven_42), .Q(register_105_q), .clk(undriven_46));  // open: clr
  Register #(.width(64)) register_106 (.D(S2), .en(undriven_42), .Q(register_106_q), .clk(undriven_46));  // open: clr
  Register #(.width(64)) register_107 (.D(S0), .en(undriven_43), .Q(register_107_q), .clk(undriven_47));  // open: clr
  Register #(.width(64)) register_108 (.D(S2), .en(undriven_43), .Q(register_108_q), .clk(undriven_47));  // open: clr
  Register #(.width(64)) register_109 (.D(S0), .en(undriven_48), .Q(register_109_q), .clk(undriven_52));  // open: clr
  Register #(.width(64)) register_110 (.D(S2), .en(undriven_48), .Q(register_110_q), .clk(undriven_52));  // open: clr
  Register #(.width(64)) register_111 (.D(S0), .en(undriven_49), .Q(register_111_q), .clk(undriven_53));  // open: clr
  Register #(.width(64)) register_112 (.D(S2), .en(undriven_49), .Q(register_112_q), .clk(undriven_53));  // open: clr
  Hex_Digit_Display #(.decimalPoint("false")) hex_digit_display_1541 (.value(register_101_q[59:56]));
  Hex_Digit_Display #(.decimalPoint("false")) hex_digit_display_1542 (.value(register_101_q[55:52]));
  Hex_Digit_Display #(.decimalPoint("false")) hex_digit_display_1543 (.value(register_102_q[59:56]));
  Hex_Digit_Display #(.decimalPoint("false")) hex_digit_display_1544 (.value(register_102_q[55:52]));
  Hex_Digit_Display #(.decimalPoint("false")) hex_digit_display_1545 (.value(register_103_q[59:56]));
  Hex_Digit_Display #(.decimalPoint("false")) hex_digit_display_1546 (.value(register_103_q[55:52]));
  Hex_Digit_Display #(.decimalPoint("false")) hex_digit_display_1547 (.value(register_104_q[59:56]));
  Hex_Digit_Display #(.decimalPoint("false")) hex_digit_display_1548 (.value(register_104_q[55:52]));
  Hex_Digit_Display #(.decimalPoint("false")) hex_digit_display_1549 (.value(register_105_q[63:60]));
  Hex_Digit_Display #(.decimalPoint("false")) hex_digit_display_1550 (.value(register_105_q[59:56]));
  Hex_Digit_Display #(.decimalPoint("false")) hex_digit_display_1551 (.value(register_106_q[63:60]));
  Hex_Digit_Display #(.decimalPoint("false")) hex_digit_display_1552 (.value(register_106_q[59:56]));
  Hex_Digit_Display #(.decimalPoint("false")) hex_digit_display_1553 (.value(register_107_q[63:60]));
  Hex_Digit_Display #(.decimalPoint("false")) hex_digit_display_1554 (.value(register_107_q[59:56]));
  Hex_Digit_Display #(.decimalPoint("false")) hex_digit_display_1555 (.value(register_108_q[63:60]));
  Hex_Digit_Display #(.decimalPoint("false")) hex_digit_display_1556 (.value(register_108_q[59:56]));
  Hex_Digit_Display #(.decimalPoint("false")) hex_digit_display_1557 (.value(register_109_q[63:60]));
  Hex_Digit_Display #(.decimalPoint("false")) hex_digit_display_1558 (.value(register_109_q[59:56]));
  Hex_Digit_Display #(.decimalPoint("false")) hex_digit_display_1559 (.value(register_110_q[63:60]));
  Hex_Digit_Display #(.decimalPoint("false")) hex_digit_display_1560 (.value(register_110_q[59:56]));
  Hex_Digit_Display #(.decimalPoint("false")) hex_digit_display_1561 (.value(register_111_q[63:60]));
  Hex_Digit_Display #(.decimalPoint("false")) hex_digit_display_1562 (.value(register_111_q[59:56]));
  Hex_Digit_Display #(.decimalPoint("false")) hex_digit_display_1563 (.value(register_112_q[63:60]));
  Hex_Digit_Display #(.decimalPoint("false")) hex_digit_display_1564 (.value(register_112_q[59:56]));
  Register #(.width(64)) register_113 (.D(S0), .en(undriven_50), .Q(register_113_q), .clk(undriven_54));  // open: clr
  Hex_Digit_Display #(.decimalPoint("false")) hex_digit_display_1565 (.value(register_113_q[63:60]));
  Register #(.width(64)) register_114 (.D(S2), .en(undriven_50), .Q(register_114_q), .clk(undriven_54));  // open: clr
  Hex_Digit_Display #(.decimalPoint("false")) hex_digit_display_1566 (.value(register_114_q[63:60]));
  Register #(.width(64)) register_115 (.D(S0), .en(undriven_51), .Q(register_115_q), .clk(undriven_55));  // open: clr
  Hex_Digit_Display #(.decimalPoint("false")) hex_digit_display_1567 (.value(register_115_q[63:60]));
  Register #(.width(64)) register_116 (.D(S2), .en(undriven_51), .Q(register_116_q), .clk(undriven_55));  // open: clr
  Hex_Digit_Display #(.decimalPoint("false")) hex_digit_display_1568 (.value(register_116_q[63:60]));
  Hex_Digit_Display #(.decimalPoint("false")) hex_digit_display_1569 (.value(register_101_q[51:48]));
  Hex_Digit_Display #(.decimalPoint("false")) hex_digit_display_1570 (.value(register_101_q[47:44]));
  Hex_Digit_Display #(.decimalPoint("false")) hex_digit_display_1571 (.value(register_102_q[51:48]));
  Hex_Digit_Display #(.decimalPoint("false")) hex_digit_display_1572 (.value(register_102_q[47:44]));
  Hex_Digit_Display #(.decimalPoint("false")) hex_digit_display_1573 (.value(register_103_q[51:48]));
  Hex_Digit_Display #(.decimalPoint("false")) hex_digit_display_1574 (.value(register_103_q[47:44]));
  Hex_Digit_Display #(.decimalPoint("false")) hex_digit_display_1575 (.value(register_104_q[51:48]));
  Hex_Digit_Display #(.decimalPoint("false")) hex_digit_display_1576 (.value(register_104_q[47:44]));
  Hex_Digit_Display #(.decimalPoint("false")) hex_digit_display_1577 (.value(register_105_q[55:52]));
  Hex_Digit_Display #(.decimalPoint("false")) hex_digit_display_1578 (.value(register_105_q[51:48]));
  Hex_Digit_Display #(.decimalPoint("false")) hex_digit_display_1579 (.value(register_106_q[55:52]));
  Hex_Digit_Display #(.decimalPoint("false")) hex_digit_display_1580 (.value(register_106_q[51:48]));
  Hex_Digit_Display #(.decimalPoint("false")) hex_digit_display_1581 (.value(register_107_q[55:52]));
  Hex_Digit_Display #(.decimalPoint("false")) hex_digit_display_1582 (.value(register_107_q[51:48]));
  Hex_Digit_Display #(.decimalPoint("false")) hex_digit_display_1583 (.value(register_108_q[55:52]));
  Hex_Digit_Display #(.decimalPoint("false")) hex_digit_display_1584 (.value(register_108_q[51:48]));
  Hex_Digit_Display #(.decimalPoint("false")) hex_digit_display_1585 (.value(register_109_q[55:52]));
  Hex_Digit_Display #(.decimalPoint("false")) hex_digit_display_1586 (.value(register_109_q[51:48]));
  Hex_Digit_Display #(.decimalPoint("false")) hex_digit_display_1587 (.value(register_110_q[55:52]));
  Hex_Digit_Display #(.decimalPoint("false")) hex_digit_display_1588 (.value(register_110_q[51:48]));
  Hex_Digit_Display #(.decimalPoint("false")) hex_digit_display_1589 (.value(register_111_q[55:52]));
  Hex_Digit_Display #(.decimalPoint("false")) hex_digit_display_1590 (.value(register_111_q[51:48]));
  Hex_Digit_Display #(.decimalPoint("false")) hex_digit_display_1591 (.value(register_112_q[55:52]));
  Hex_Digit_Display #(.decimalPoint("false")) hex_digit_display_1592 (.value(register_112_q[51:48]));
  Hex_Digit_Display #(.decimalPoint("false")) hex_digit_display_1593 (.value(register_113_q[59:56]));
  Hex_Digit_Display #(.decimalPoint("false")) hex_digit_display_1594 (.value(register_113_q[55:52]));
  Hex_Digit_Display #(.decimalPoint("false")) hex_digit_display_1595 (.value(register_114_q[59:56]));
  Hex_Digit_Display #(.decimalPoint("false")) hex_digit_display_1596 (.value(register_114_q[55:52]));
  Hex_Digit_Display #(.decimalPoint("false")) hex_digit_display_1597 (.value(register_115_q[59:56]));
  Hex_Digit_Display #(.decimalPoint("false")) hex_digit_display_1598 (.value(register_115_q[55:52]));
  Hex_Digit_Display #(.decimalPoint("false")) hex_digit_display_1599 (.value(register_116_q[59:56]));
  Hex_Digit_Display #(.decimalPoint("false")) hex_digit_display_1600 (.value(register_116_q[55:52]));
  Hex_Digit_Display #(.decimalPoint("false")) hex_digit_display_1601 (.value(register_101_q[43:40]));
  Hex_Digit_Display #(.decimalPoint("false")) hex_digit_display_1602 (.value(register_101_q[39:36]));
  Hex_Digit_Display #(.decimalPoint("false")) hex_digit_display_1603 (.value(register_102_q[43:40]));
  Hex_Digit_Display #(.decimalPoint("false")) hex_digit_display_1604 (.value(register_102_q[39:36]));
  Hex_Digit_Display #(.decimalPoint("false")) hex_digit_display_1605 (.value(register_103_q[43:40]));
  Hex_Digit_Display #(.decimalPoint("false")) hex_digit_display_1606 (.value(register_103_q[39:36]));
  Hex_Digit_Display #(.decimalPoint("false")) hex_digit_display_1607 (.value(register_104_q[43:40]));
  Hex_Digit_Display #(.decimalPoint("false")) hex_digit_display_1608 (.value(register_104_q[39:36]));
  Hex_Digit_Display #(.decimalPoint("false")) hex_digit_display_1609 (.value(register_105_q[47:44]));
  Hex_Digit_Display #(.decimalPoint("false")) hex_digit_display_1610 (.value(register_105_q[43:40]));
  Hex_Digit_Display #(.decimalPoint("false")) hex_digit_display_1611 (.value(register_106_q[47:44]));
  Hex_Digit_Display #(.decimalPoint("false")) hex_digit_display_1612 (.value(register_106_q[43:40]));
  Hex_Digit_Display #(.decimalPoint("false")) hex_digit_display_1613 (.value(register_107_q[47:44]));
  Hex_Digit_Display #(.decimalPoint("false")) hex_digit_display_1614 (.value(register_107_q[43:40]));
  Hex_Digit_Display #(.decimalPoint("false")) hex_digit_display_1615 (.value(register_108_q[47:44]));
  Hex_Digit_Display #(.decimalPoint("false")) hex_digit_display_1616 (.value(register_108_q[43:40]));
  Hex_Digit_Display #(.decimalPoint("false")) hex_digit_display_1617 (.value(register_109_q[47:44]));
  Hex_Digit_Display #(.decimalPoint("false")) hex_digit_display_1618 (.value(register_109_q[43:40]));
  Hex_Digit_Display #(.decimalPoint("false")) hex_digit_display_1619 (.value(register_110_q[47:44]));
  Hex_Digit_Display #(.decimalPoint("false")) hex_digit_display_1620 (.value(register_110_q[43:40]));
  Hex_Digit_Display #(.decimalPoint("false")) hex_digit_display_1621 (.value(register_111_q[47:44]));
  Hex_Digit_Display #(.decimalPoint("false")) hex_digit_display_1622 (.value(register_111_q[43:40]));
  Hex_Digit_Display #(.decimalPoint("false")) hex_digit_display_1623 (.value(register_112_q[47:44]));
  Hex_Digit_Display #(.decimalPoint("false")) hex_digit_display_1624 (.value(register_112_q[43:40]));
  Hex_Digit_Display #(.decimalPoint("false")) hex_digit_display_1625 (.value(register_113_q[51:48]));
  Hex_Digit_Display #(.decimalPoint("false")) hex_digit_display_1626 (.value(register_113_q[47:44]));
  Hex_Digit_Display #(.decimalPoint("false")) hex_digit_display_1627 (.value(register_114_q[51:48]));
  Hex_Digit_Display #(.decimalPoint("false")) hex_digit_display_1628 (.value(register_114_q[47:44]));
  Hex_Digit_Display #(.decimalPoint("false")) hex_digit_display_1629 (.value(register_115_q[51:48]));
  Hex_Digit_Display #(.decimalPoint("false")) hex_digit_display_1630 (.value(register_115_q[47:44]));
  Hex_Digit_Display #(.decimalPoint("false")) hex_digit_display_1631 (.value(register_116_q[51:48]));
  Hex_Digit_Display #(.decimalPoint("false")) hex_digit_display_1632 (.value(register_116_q[47:44]));
  Hex_Digit_Display #(.decimalPoint("false")) hex_digit_display_1633 (.value(register_101_q[35:32]));
  Hex_Digit_Display #(.decimalPoint("false")) hex_digit_display_1634 (.value(register_101_q[31:28]));
  Hex_Digit_Display #(.decimalPoint("false")) hex_digit_display_1635 (.value(register_102_q[35:32]));
  Hex_Digit_Display #(.decimalPoint("false")) hex_digit_display_1636 (.value(register_102_q[31:28]));
  Hex_Digit_Display #(.decimalPoint("false")) hex_digit_display_1637 (.value(register_103_q[35:32]));
  Hex_Digit_Display #(.decimalPoint("false")) hex_digit_display_1638 (.value(register_103_q[31:28]));
  Hex_Digit_Display #(.decimalPoint("false")) hex_digit_display_1639 (.value(register_104_q[35:32]));
  Hex_Digit_Display #(.decimalPoint("false")) hex_digit_display_1640 (.value(register_104_q[31:28]));
  Hex_Digit_Display #(.decimalPoint("false")) hex_digit_display_1641 (.value(register_105_q[39:36]));
  Hex_Digit_Display #(.decimalPoint("false")) hex_digit_display_1642 (.value(register_105_q[35:32]));
  Hex_Digit_Display #(.decimalPoint("false")) hex_digit_display_1643 (.value(register_106_q[39:36]));
  Hex_Digit_Display #(.decimalPoint("false")) hex_digit_display_1644 (.value(register_106_q[35:32]));
  Hex_Digit_Display #(.decimalPoint("false")) hex_digit_display_1645 (.value(register_107_q[39:36]));
  Hex_Digit_Display #(.decimalPoint("false")) hex_digit_display_1646 (.value(register_107_q[35:32]));
  Hex_Digit_Display #(.decimalPoint("false")) hex_digit_display_1647 (.value(register_108_q[39:36]));
  Hex_Digit_Display #(.decimalPoint("false")) hex_digit_display_1648 (.value(register_108_q[35:32]));
  Hex_Digit_Display #(.decimalPoint("false")) hex_digit_display_1649 (.value(register_109_q[39:36]));
  Hex_Digit_Display #(.decimalPoint("false")) hex_digit_display_1650 (.value(register_109_q[35:32]));
  Hex_Digit_Display #(.decimalPoint("false")) hex_digit_display_1651 (.value(register_110_q[39:36]));
  Hex_Digit_Display #(.decimalPoint("false")) hex_digit_display_1652 (.value(register_110_q[35:32]));
  Hex_Digit_Display #(.decimalPoint("false")) hex_digit_display_1653 (.value(register_111_q[39:36]));
  Hex_Digit_Display #(.decimalPoint("false")) hex_digit_display_1654 (.value(register_111_q[35:32]));
  Hex_Digit_Display #(.decimalPoint("false")) hex_digit_display_1655 (.value(register_112_q[39:36]));
  Hex_Digit_Display #(.decimalPoint("false")) hex_digit_display_1656 (.value(register_112_q[35:32]));
  Hex_Digit_Display #(.decimalPoint("false")) hex_digit_display_1657 (.value(register_113_q[43:40]));
  Hex_Digit_Display #(.decimalPoint("false")) hex_digit_display_1658 (.value(register_113_q[39:36]));
  Hex_Digit_Display #(.decimalPoint("false")) hex_digit_display_1659 (.value(register_114_q[43:40]));
  Hex_Digit_Display #(.decimalPoint("false")) hex_digit_display_1660 (.value(register_114_q[39:36]));
  Hex_Digit_Display #(.decimalPoint("false")) hex_digit_display_1661 (.value(register_115_q[43:40]));
  Hex_Digit_Display #(.decimalPoint("false")) hex_digit_display_1662 (.value(register_115_q[39:36]));
  Hex_Digit_Display #(.decimalPoint("false")) hex_digit_display_1663 (.value(register_116_q[43:40]));
  Hex_Digit_Display #(.decimalPoint("false")) hex_digit_display_1664 (.value(register_116_q[39:36]));
  Hex_Digit_Display #(.decimalPoint("false")) hex_digit_display_1665 (.value(register_101_q[27:24]));
  Hex_Digit_Display #(.decimalPoint("false")) hex_digit_display_1666 (.value(register_101_q[23:20]));
  Hex_Digit_Display #(.decimalPoint("false")) hex_digit_display_1667 (.value(register_102_q[27:24]));
  Hex_Digit_Display #(.decimalPoint("false")) hex_digit_display_1668 (.value(register_102_q[23:20]));
  Hex_Digit_Display #(.decimalPoint("false")) hex_digit_display_1669 (.value(register_103_q[27:24]));
  Hex_Digit_Display #(.decimalPoint("false")) hex_digit_display_1670 (.value(register_103_q[23:20]));
  Hex_Digit_Display #(.decimalPoint("false")) hex_digit_display_1671 (.value(register_104_q[27:24]));
  Hex_Digit_Display #(.decimalPoint("false")) hex_digit_display_1672 (.value(register_104_q[23:20]));
  Hex_Digit_Display #(.decimalPoint("false")) hex_digit_display_1673 (.value(register_105_q[31:28]));
  Hex_Digit_Display #(.decimalPoint("false")) hex_digit_display_1674 (.value(register_105_q[27:24]));
  Hex_Digit_Display #(.decimalPoint("false")) hex_digit_display_1675 (.value(register_106_q[31:28]));
  Hex_Digit_Display #(.decimalPoint("false")) hex_digit_display_1676 (.value(register_106_q[27:24]));
  Hex_Digit_Display #(.decimalPoint("false")) hex_digit_display_1677 (.value(register_107_q[31:28]));
  Hex_Digit_Display #(.decimalPoint("false")) hex_digit_display_1678 (.value(register_107_q[27:24]));
  Hex_Digit_Display #(.decimalPoint("false")) hex_digit_display_1679 (.value(register_108_q[31:28]));
  Hex_Digit_Display #(.decimalPoint("false")) hex_digit_display_1680 (.value(register_108_q[27:24]));
  Hex_Digit_Display #(.decimalPoint("false")) hex_digit_display_1681 (.value(register_109_q[31:28]));
  Hex_Digit_Display #(.decimalPoint("false")) hex_digit_display_1682 (.value(register_109_q[27:24]));
  Hex_Digit_Display #(.decimalPoint("false")) hex_digit_display_1683 (.value(register_110_q[31:28]));
  Hex_Digit_Display #(.decimalPoint("false")) hex_digit_display_1684 (.value(register_110_q[27:24]));
  Hex_Digit_Display #(.decimalPoint("false")) hex_digit_display_1685 (.value(register_111_q[31:28]));
  Hex_Digit_Display #(.decimalPoint("false")) hex_digit_display_1686 (.value(register_111_q[27:24]));
  Hex_Digit_Display #(.decimalPoint("false")) hex_digit_display_1687 (.value(register_112_q[31:28]));
  Hex_Digit_Display #(.decimalPoint("false")) hex_digit_display_1688 (.value(register_112_q[27:24]));
  Hex_Digit_Display #(.decimalPoint("false")) hex_digit_display_1689 (.value(register_113_q[35:32]));
  Hex_Digit_Display #(.decimalPoint("false")) hex_digit_display_1690 (.value(register_113_q[31:28]));
  Hex_Digit_Display #(.decimalPoint("false")) hex_digit_display_1691 (.value(register_114_q[35:32]));
  Hex_Digit_Display #(.decimalPoint("false")) hex_digit_display_1692 (.value(register_114_q[31:28]));
  Hex_Digit_Display #(.decimalPoint("false")) hex_digit_display_1693 (.value(register_115_q[35:32]));
  Hex_Digit_Display #(.decimalPoint("false")) hex_digit_display_1694 (.value(register_115_q[31:28]));
  Hex_Digit_Display #(.decimalPoint("false")) hex_digit_display_1695 (.value(register_116_q[35:32]));
  Hex_Digit_Display #(.decimalPoint("false")) hex_digit_display_1696 (.value(register_116_q[31:28]));
  Hex_Digit_Display #(.decimalPoint("false")) hex_digit_display_1697 (.value(register_101_q[19:16]));
  Hex_Digit_Display #(.decimalPoint("false")) hex_digit_display_1698 (.value(register_101_q[15:12]));
  Hex_Digit_Display #(.decimalPoint("false")) hex_digit_display_1699 (.value(register_102_q[19:16]));
  Hex_Digit_Display #(.decimalPoint("false")) hex_digit_display_1700 (.value(register_102_q[15:12]));
  Hex_Digit_Display #(.decimalPoint("false")) hex_digit_display_1701 (.value(register_103_q[19:16]));
  Hex_Digit_Display #(.decimalPoint("false")) hex_digit_display_1702 (.value(register_103_q[15:12]));
  Hex_Digit_Display #(.decimalPoint("false")) hex_digit_display_1703 (.value(register_104_q[19:16]));
  Hex_Digit_Display #(.decimalPoint("false")) hex_digit_display_1704 (.value(register_104_q[15:12]));
  Hex_Digit_Display #(.decimalPoint("false")) hex_digit_display_1705 (.value(register_105_q[23:20]));
  Hex_Digit_Display #(.decimalPoint("false")) hex_digit_display_1706 (.value(register_105_q[19:16]));
  Hex_Digit_Display #(.decimalPoint("false")) hex_digit_display_1707 (.value(register_106_q[23:20]));
  Hex_Digit_Display #(.decimalPoint("false")) hex_digit_display_1708 (.value(register_106_q[19:16]));
  Hex_Digit_Display #(.decimalPoint("false")) hex_digit_display_1709 (.value(register_107_q[23:20]));
  Hex_Digit_Display #(.decimalPoint("false")) hex_digit_display_1710 (.value(register_107_q[19:16]));
  Hex_Digit_Display #(.decimalPoint("false")) hex_digit_display_1711 (.value(register_108_q[23:20]));
  Hex_Digit_Display #(.decimalPoint("false")) hex_digit_display_1712 (.value(register_108_q[19:16]));
  Hex_Digit_Display #(.decimalPoint("false")) hex_digit_display_1713 (.value(register_109_q[23:20]));
  Hex_Digit_Display #(.decimalPoint("false")) hex_digit_display_1714 (.value(register_109_q[19:16]));
  Hex_Digit_Display #(.decimalPoint("false")) hex_digit_display_1715 (.value(register_110_q[23:20]));
  Hex_Digit_Display #(.decimalPoint("false")) hex_digit_display_1716 (.value(register_110_q[19:16]));
  Hex_Digit_Display #(.decimalPoint("false")) hex_digit_display_1717 (.value(register_111_q[23:20]));
  Hex_Digit_Display #(.decimalPoint("false")) hex_digit_display_1718 (.value(register_111_q[19:16]));
  Hex_Digit_Display #(.decimalPoint("false")) hex_digit_display_1719 (.value(register_112_q[23:20]));
  Hex_Digit_Display #(.decimalPoint("false")) hex_digit_display_1720 (.value(register_112_q[19:16]));
  Hex_Digit_Display #(.decimalPoint("false")) hex_digit_display_1721 (.value(register_113_q[27:24]));
  Hex_Digit_Display #(.decimalPoint("false")) hex_digit_display_1722 (.value(register_113_q[23:20]));
  Hex_Digit_Display #(.decimalPoint("false")) hex_digit_display_1723 (.value(register_114_q[27:24]));
  Hex_Digit_Display #(.decimalPoint("false")) hex_digit_display_1724 (.value(register_114_q[23:20]));
  Hex_Digit_Display #(.decimalPoint("false")) hex_digit_display_1725 (.value(register_115_q[27:24]));
  Hex_Digit_Display #(.decimalPoint("false")) hex_digit_display_1726 (.value(register_115_q[23:20]));
  Hex_Digit_Display #(.decimalPoint("false")) hex_digit_display_1727 (.value(register_116_q[27:24]));
  Hex_Digit_Display #(.decimalPoint("false")) hex_digit_display_1728 (.value(register_116_q[23:20]));
  Hex_Digit_Display #(.decimalPoint("false")) hex_digit_display_1729 (.value(register_101_q[11:8]));
  Hex_Digit_Display #(.decimalPoint("false")) hex_digit_display_1730 (.value(register_101_q[7:4]));
  Hex_Digit_Display #(.decimalPoint("false")) hex_digit_display_1731 (.value(register_102_q[11:8]));
  Hex_Digit_Display #(.decimalPoint("false")) hex_digit_display_1732 (.value(register_102_q[7:4]));
  Hex_Digit_Display #(.decimalPoint("false")) hex_digit_display_1733 (.value(register_103_q[11:8]));
  Hex_Digit_Display #(.decimalPoint("false")) hex_digit_display_1734 (.value(register_103_q[7:4]));
  Hex_Digit_Display #(.decimalPoint("false")) hex_digit_display_1735 (.value(register_104_q[11:8]));
  Hex_Digit_Display #(.decimalPoint("false")) hex_digit_display_1736 (.value(register_104_q[7:4]));
  Hex_Digit_Display #(.decimalPoint("false")) hex_digit_display_1737 (.value(register_105_q[15:12]));
  Hex_Digit_Display #(.decimalPoint("false")) hex_digit_display_1738 (.value(register_105_q[11:8]));
  Hex_Digit_Display #(.decimalPoint("false")) hex_digit_display_1739 (.value(register_106_q[15:12]));
  Hex_Digit_Display #(.decimalPoint("false")) hex_digit_display_1740 (.value(register_106_q[11:8]));
  Hex_Digit_Display #(.decimalPoint("false")) hex_digit_display_1741 (.value(register_107_q[15:12]));
  Hex_Digit_Display #(.decimalPoint("false")) hex_digit_display_1742 (.value(register_107_q[11:8]));
  Hex_Digit_Display #(.decimalPoint("false")) hex_digit_display_1743 (.value(register_108_q[15:12]));
  Hex_Digit_Display #(.decimalPoint("false")) hex_digit_display_1744 (.value(register_108_q[11:8]));
  Hex_Digit_Display #(.decimalPoint("false")) hex_digit_display_1745 (.value(register_109_q[15:12]));
  Hex_Digit_Display #(.decimalPoint("false")) hex_digit_display_1746 (.value(register_109_q[11:8]));
  Hex_Digit_Display #(.decimalPoint("false")) hex_digit_display_1747 (.value(register_110_q[15:12]));
  Hex_Digit_Display #(.decimalPoint("false")) hex_digit_display_1748 (.value(register_110_q[11:8]));
  Hex_Digit_Display #(.decimalPoint("false")) hex_digit_display_1749 (.value(register_111_q[15:12]));
  Hex_Digit_Display #(.decimalPoint("false")) hex_digit_display_1750 (.value(register_111_q[11:8]));
  Hex_Digit_Display #(.decimalPoint("false")) hex_digit_display_1751 (.value(register_112_q[15:12]));
  Hex_Digit_Display #(.decimalPoint("false")) hex_digit_display_1752 (.value(register_112_q[11:8]));
  Hex_Digit_Display #(.decimalPoint("false")) hex_digit_display_1753 (.value(register_113_q[19:16]));
  Hex_Digit_Display #(.decimalPoint("false")) hex_digit_display_1754 (.value(register_113_q[15:12]));
  Hex_Digit_Display #(.decimalPoint("false")) hex_digit_display_1755 (.value(register_114_q[19:16]));
  Hex_Digit_Display #(.decimalPoint("false")) hex_digit_display_1756 (.value(register_114_q[15:12]));
  Hex_Digit_Display #(.decimalPoint("false")) hex_digit_display_1757 (.value(register_115_q[19:16]));
  Hex_Digit_Display #(.decimalPoint("false")) hex_digit_display_1758 (.value(register_115_q[15:12]));
  Hex_Digit_Display #(.decimalPoint("false")) hex_digit_display_1759 (.value(register_116_q[19:16]));
  Hex_Digit_Display #(.decimalPoint("false")) hex_digit_display_1760 (.value(register_116_q[15:12]));
  Hex_Digit_Display #(.decimalPoint("false")) hex_digit_display_1761 (.value(register_101_q[3:0]));
  Hex_Digit_Display #(.decimalPoint("false")) hex_digit_display_1762 (.value(register_102_q[3:0]));
  Hex_Digit_Display #(.decimalPoint("false")) hex_digit_display_1763 (.value(register_103_q[3:0]));
  Hex_Digit_Display #(.decimalPoint("false")) hex_digit_display_1764 (.value(register_104_q[3:0]));
  Hex_Digit_Display #(.decimalPoint("false")) hex_digit_display_1765 (.value(register_105_q[7:4]));
  Hex_Digit_Display #(.decimalPoint("false")) hex_digit_display_1766 (.value(register_105_q[3:0]));
  Hex_Digit_Display #(.decimalPoint("false")) hex_digit_display_1767 (.value(register_106_q[7:4]));
  Hex_Digit_Display #(.decimalPoint("false")) hex_digit_display_1768 (.value(register_106_q[3:0]));
  Hex_Digit_Display #(.decimalPoint("false")) hex_digit_display_1769 (.value(register_107_q[7:4]));
  Hex_Digit_Display #(.decimalPoint("false")) hex_digit_display_1770 (.value(register_107_q[3:0]));
  Hex_Digit_Display #(.decimalPoint("false")) hex_digit_display_1771 (.value(register_108_q[7:4]));
  Hex_Digit_Display #(.decimalPoint("false")) hex_digit_display_1772 (.value(register_108_q[3:0]));
  Hex_Digit_Display #(.decimalPoint("false")) hex_digit_display_1773 (.value(register_109_q[7:4]));
  Hex_Digit_Display #(.decimalPoint("false")) hex_digit_display_1774 (.value(register_109_q[3:0]));
  Hex_Digit_Display #(.decimalPoint("false")) hex_digit_display_1775 (.value(register_110_q[7:4]));
  Hex_Digit_Display #(.decimalPoint("false")) hex_digit_display_1776 (.value(register_110_q[3:0]));
  Hex_Digit_Display #(.decimalPoint("false")) hex_digit_display_1777 (.value(register_111_q[7:4]));
  Hex_Digit_Display #(.decimalPoint("false")) hex_digit_display_1778 (.value(register_111_q[3:0]));
  Hex_Digit_Display #(.decimalPoint("false")) hex_digit_display_1779 (.value(register_112_q[7:4]));
  Hex_Digit_Display #(.decimalPoint("false")) hex_digit_display_1780 (.value(register_112_q[3:0]));
  Hex_Digit_Display #(.decimalPoint("false")) hex_digit_display_1781 (.value(register_113_q[11:8]));
  Hex_Digit_Display #(.decimalPoint("false")) hex_digit_display_1782 (.value(register_113_q[7:4]));
  Hex_Digit_Display #(.decimalPoint("false")) hex_digit_display_1783 (.value(register_114_q[11:8]));
  Hex_Digit_Display #(.decimalPoint("false")) hex_digit_display_1784 (.value(register_114_q[7:4]));
  Hex_Digit_Display #(.decimalPoint("false")) hex_digit_display_1785 (.value(register_115_q[11:8]));
  Hex_Digit_Display #(.decimalPoint("false")) hex_digit_display_1786 (.value(register_115_q[7:4]));
  Hex_Digit_Display #(.decimalPoint("false")) hex_digit_display_1787 (.value(register_116_q[11:8]));
  Hex_Digit_Display #(.decimalPoint("false")) hex_digit_display_1788 (.value(register_116_q[7:4]));
  Register #(.width(64)) register_117 (.D(S1), .en(undriven_40), .Q(register_117_q), .clk(undriven_44));  // open: clr
  Register #(.width(64)) register_118 (.D(S3), .en(undriven_40), .Q(register_118_q), .clk(undriven_44));  // open: clr
  Register #(.width(64)) register_119 (.D(S1), .en(undriven_41), .Q(register_119_q), .clk(undriven_45));  // open: clr
  Register #(.width(64)) register_120 (.D(S3), .en(undriven_41), .Q(register_120_q), .clk(undriven_45));  // open: clr
  Register #(.width(64)) register_121 (.D(S1), .en(undriven_42), .Q(register_121_q), .clk(undriven_46));  // open: clr
  Register #(.width(64)) register_122 (.D(S3), .en(undriven_42), .Q(register_122_q), .clk(undriven_46));  // open: clr
  Register #(.width(64)) register_123 (.D(S1), .en(undriven_43), .Q(register_123_q), .clk(undriven_47));  // open: clr
  Register #(.width(64)) register_124 (.D(S3), .en(undriven_43), .Q(register_124_q), .clk(undriven_47));  // open: clr
  Hex_Digit_Display #(.decimalPoint("false")) hex_digit_display_1789 (.value(register_113_q[3:0]));
  Hex_Digit_Display #(.decimalPoint("false")) hex_digit_display_1790 (.value(register_114_q[3:0]));
  Hex_Digit_Display #(.decimalPoint("false")) hex_digit_display_1791 (.value(register_115_q[3:0]));
  Hex_Digit_Display #(.decimalPoint("false")) hex_digit_display_1792 (.value(register_116_q[3:0]));
  Hex_Digit_Display #(.decimalPoint("false")) hex_digit_display_1793 (.value(register_117_q[63:60]));
  Hex_Digit_Display #(.decimalPoint("false")) hex_digit_display_1794 (.value(register_117_q[59:56]));
  Hex_Digit_Display #(.decimalPoint("false")) hex_digit_display_1795 (.value(register_118_q[63:60]));
  Hex_Digit_Display #(.decimalPoint("false")) hex_digit_display_1796 (.value(register_118_q[59:56]));
  Hex_Digit_Display #(.decimalPoint("false")) hex_digit_display_1797 (.value(register_119_q[63:60]));
  Hex_Digit_Display #(.decimalPoint("false")) hex_digit_display_1798 (.value(register_119_q[59:56]));
  Hex_Digit_Display #(.decimalPoint("false")) hex_digit_display_1799 (.value(register_120_q[63:60]));
  Hex_Digit_Display #(.decimalPoint("false")) hex_digit_display_1800 (.value(register_120_q[59:56]));
  Hex_Digit_Display #(.decimalPoint("false")) hex_digit_display_1801 (.value(register_121_q[63:60]));
  Hex_Digit_Display #(.decimalPoint("false")) hex_digit_display_1802 (.value(register_121_q[59:56]));
  Hex_Digit_Display #(.decimalPoint("false")) hex_digit_display_1803 (.value(register_122_q[63:60]));
  Hex_Digit_Display #(.decimalPoint("false")) hex_digit_display_1804 (.value(register_122_q[59:56]));
  Hex_Digit_Display #(.decimalPoint("false")) hex_digit_display_1805 (.value(register_123_q[63:60]));
  Hex_Digit_Display #(.decimalPoint("false")) hex_digit_display_1806 (.value(register_123_q[59:56]));
  Hex_Digit_Display #(.decimalPoint("false")) hex_digit_display_1807 (.value(register_124_q[63:60]));
  Hex_Digit_Display #(.decimalPoint("false")) hex_digit_display_1808 (.value(register_124_q[59:56]));
  Register #(.width(64)) register_125 (.D(S1), .en(undriven_48), .Q(register_125_q), .clk(undriven_52));  // open: clr
  Hex_Digit_Display #(.decimalPoint("false")) hex_digit_display_1809 (.value(register_125_q[63:60]));
  Register #(.width(64)) register_126 (.D(S3), .en(undriven_48), .Q(register_126_q), .clk(undriven_52));  // open: clr
  Hex_Digit_Display #(.decimalPoint("false")) hex_digit_display_1810 (.value(register_126_q[63:60]));
  Register #(.width(64)) register_127 (.D(S1), .en(undriven_49), .Q(register_127_q), .clk(undriven_53));  // open: clr
  Hex_Digit_Display #(.decimalPoint("false")) hex_digit_display_1811 (.value(register_127_q[63:60]));
  Register #(.width(64)) register_128 (.D(S3), .en(undriven_49), .Q(register_128_q), .clk(undriven_53));  // open: clr
  Hex_Digit_Display #(.decimalPoint("false")) hex_digit_display_1812 (.value(register_128_q[63:60]));
  Register #(.width(64)) register_129 (.D(S1), .en(undriven_50), .Q(register_129_q), .clk(undriven_54));  // open: clr
  Hex_Digit_Display #(.decimalPoint("false")) hex_digit_display_1813 (.value(register_129_q[63:60]));
  Register #(.width(64)) register_130 (.D(S3), .en(undriven_50), .Q(register_130_q), .clk(undriven_54));  // open: clr
  Hex_Digit_Display #(.decimalPoint("false")) hex_digit_display_1814 (.value(register_130_q[63:60]));
  Register #(.width(64)) register_131 (.D(S1), .en(undriven_51), .Q(register_131_q), .clk(undriven_55));  // open: clr
  Hex_Digit_Display #(.decimalPoint("false")) hex_digit_display_1815 (.value(register_131_q[63:60]));
  Register #(.width(64)) register_132 (.D(S3), .en(undriven_51), .Q(register_132_q), .clk(undriven_55));  // open: clr
  Hex_Digit_Display #(.decimalPoint("false")) hex_digit_display_1816 (.value(register_132_q[63:60]));
  Hex_Digit_Display #(.decimalPoint("false")) hex_digit_display_1817 (.value(register_117_q[55:52]));
  Hex_Digit_Display #(.decimalPoint("false")) hex_digit_display_1818 (.value(register_117_q[51:48]));
  Hex_Digit_Display #(.decimalPoint("false")) hex_digit_display_1819 (.value(register_118_q[55:52]));
  Hex_Digit_Display #(.decimalPoint("false")) hex_digit_display_1820 (.value(register_118_q[51:48]));
  Hex_Digit_Display #(.decimalPoint("false")) hex_digit_display_1821 (.value(register_119_q[55:52]));
  Hex_Digit_Display #(.decimalPoint("false")) hex_digit_display_1822 (.value(register_119_q[51:48]));
  Hex_Digit_Display #(.decimalPoint("false")) hex_digit_display_1823 (.value(register_120_q[55:52]));
  Hex_Digit_Display #(.decimalPoint("false")) hex_digit_display_1824 (.value(register_120_q[51:48]));
  Hex_Digit_Display #(.decimalPoint("false")) hex_digit_display_1825 (.value(register_121_q[55:52]));
  Hex_Digit_Display #(.decimalPoint("false")) hex_digit_display_1826 (.value(register_121_q[51:48]));
  Hex_Digit_Display #(.decimalPoint("false")) hex_digit_display_1827 (.value(register_122_q[55:52]));
  Hex_Digit_Display #(.decimalPoint("false")) hex_digit_display_1828 (.value(register_122_q[51:48]));
  Hex_Digit_Display #(.decimalPoint("false")) hex_digit_display_1829 (.value(register_123_q[55:52]));
  Hex_Digit_Display #(.decimalPoint("false")) hex_digit_display_1830 (.value(register_123_q[51:48]));
  Hex_Digit_Display #(.decimalPoint("false")) hex_digit_display_1831 (.value(register_124_q[55:52]));
  Hex_Digit_Display #(.decimalPoint("false")) hex_digit_display_1832 (.value(register_124_q[51:48]));
  Hex_Digit_Display #(.decimalPoint("false")) hex_digit_display_1833 (.value(register_125_q[59:56]));
  Hex_Digit_Display #(.decimalPoint("false")) hex_digit_display_1834 (.value(register_125_q[55:52]));
  Hex_Digit_Display #(.decimalPoint("false")) hex_digit_display_1835 (.value(register_126_q[59:56]));
  Hex_Digit_Display #(.decimalPoint("false")) hex_digit_display_1836 (.value(register_126_q[55:52]));
  Hex_Digit_Display #(.decimalPoint("false")) hex_digit_display_1837 (.value(register_127_q[59:56]));
  Hex_Digit_Display #(.decimalPoint("false")) hex_digit_display_1838 (.value(register_127_q[55:52]));
  Hex_Digit_Display #(.decimalPoint("false")) hex_digit_display_1839 (.value(register_128_q[59:56]));
  Hex_Digit_Display #(.decimalPoint("false")) hex_digit_display_1840 (.value(register_128_q[55:52]));
  Hex_Digit_Display #(.decimalPoint("false")) hex_digit_display_1841 (.value(register_129_q[59:56]));
  Hex_Digit_Display #(.decimalPoint("false")) hex_digit_display_1842 (.value(register_129_q[55:52]));
  Hex_Digit_Display #(.decimalPoint("false")) hex_digit_display_1843 (.value(register_130_q[59:56]));
  Hex_Digit_Display #(.decimalPoint("false")) hex_digit_display_1844 (.value(register_130_q[55:52]));
  Hex_Digit_Display #(.decimalPoint("false")) hex_digit_display_1845 (.value(register_131_q[59:56]));
  Hex_Digit_Display #(.decimalPoint("false")) hex_digit_display_1846 (.value(register_131_q[55:52]));
  Hex_Digit_Display #(.decimalPoint("false")) hex_digit_display_1847 (.value(register_132_q[59:56]));
  Hex_Digit_Display #(.decimalPoint("false")) hex_digit_display_1848 (.value(register_132_q[55:52]));
  Hex_Digit_Display #(.decimalPoint("false")) hex_digit_display_1849 (.value(register_117_q[47:44]));
  Hex_Digit_Display #(.decimalPoint("false")) hex_digit_display_1850 (.value(register_117_q[43:40]));
  Hex_Digit_Display #(.decimalPoint("false")) hex_digit_display_1851 (.value(register_118_q[47:44]));
  Hex_Digit_Display #(.decimalPoint("false")) hex_digit_display_1852 (.value(register_118_q[43:40]));
  Hex_Digit_Display #(.decimalPoint("false")) hex_digit_display_1853 (.value(register_119_q[47:44]));
  Hex_Digit_Display #(.decimalPoint("false")) hex_digit_display_1854 (.value(register_119_q[43:40]));
  Hex_Digit_Display #(.decimalPoint("false")) hex_digit_display_1855 (.value(register_120_q[47:44]));
  Hex_Digit_Display #(.decimalPoint("false")) hex_digit_display_1856 (.value(register_120_q[43:40]));
  Hex_Digit_Display #(.decimalPoint("false")) hex_digit_display_1857 (.value(register_121_q[47:44]));
  Hex_Digit_Display #(.decimalPoint("false")) hex_digit_display_1858 (.value(register_121_q[43:40]));
  Hex_Digit_Display #(.decimalPoint("false")) hex_digit_display_1859 (.value(register_122_q[47:44]));
  Hex_Digit_Display #(.decimalPoint("false")) hex_digit_display_1860 (.value(register_122_q[43:40]));
  Hex_Digit_Display #(.decimalPoint("false")) hex_digit_display_1861 (.value(register_123_q[47:44]));
  Hex_Digit_Display #(.decimalPoint("false")) hex_digit_display_1862 (.value(register_123_q[43:40]));
  Hex_Digit_Display #(.decimalPoint("false")) hex_digit_display_1863 (.value(register_124_q[47:44]));
  Hex_Digit_Display #(.decimalPoint("false")) hex_digit_display_1864 (.value(register_124_q[43:40]));
  Hex_Digit_Display #(.decimalPoint("false")) hex_digit_display_1865 (.value(register_125_q[51:48]));
  Hex_Digit_Display #(.decimalPoint("false")) hex_digit_display_1866 (.value(register_125_q[47:44]));
  Hex_Digit_Display #(.decimalPoint("false")) hex_digit_display_1867 (.value(register_126_q[51:48]));
  Hex_Digit_Display #(.decimalPoint("false")) hex_digit_display_1868 (.value(register_126_q[47:44]));
  Hex_Digit_Display #(.decimalPoint("false")) hex_digit_display_1869 (.value(register_127_q[51:48]));
  Hex_Digit_Display #(.decimalPoint("false")) hex_digit_display_1870 (.value(register_127_q[47:44]));
  Hex_Digit_Display #(.decimalPoint("false")) hex_digit_display_1871 (.value(register_128_q[51:48]));
  Hex_Digit_Display #(.decimalPoint("false")) hex_digit_display_1872 (.value(register_128_q[47:44]));
  Hex_Digit_Display #(.decimalPoint("false")) hex_digit_display_1873 (.value(register_129_q[51:48]));
  Hex_Digit_Display #(.decimalPoint("false")) hex_digit_display_1874 (.value(register_129_q[47:44]));
  Hex_Digit_Display #(.decimalPoint("false")) hex_digit_display_1875 (.value(register_130_q[51:48]));
  Hex_Digit_Display #(.decimalPoint("false")) hex_digit_display_1876 (.value(register_130_q[47:44]));
  Hex_Digit_Display #(.decimalPoint("false")) hex_digit_display_1877 (.value(register_131_q[51:48]));
  Hex_Digit_Display #(.decimalPoint("false")) hex_digit_display_1878 (.value(register_131_q[47:44]));
  Hex_Digit_Display #(.decimalPoint("false")) hex_digit_display_1879 (.value(register_132_q[51:48]));
  Hex_Digit_Display #(.decimalPoint("false")) hex_digit_display_1880 (.value(register_132_q[47:44]));
  Hex_Digit_Display #(.decimalPoint("false")) hex_digit_display_1881 (.value(register_117_q[39:36]));
  Hex_Digit_Display #(.decimalPoint("false")) hex_digit_display_1882 (.value(register_117_q[35:32]));
  Hex_Digit_Display #(.decimalPoint("false")) hex_digit_display_1883 (.value(register_118_q[39:36]));
  Hex_Digit_Display #(.decimalPoint("false")) hex_digit_display_1884 (.value(register_118_q[35:32]));
  Hex_Digit_Display #(.decimalPoint("false")) hex_digit_display_1885 (.value(register_119_q[39:36]));
  Hex_Digit_Display #(.decimalPoint("false")) hex_digit_display_1886 (.value(register_119_q[35:32]));
  Hex_Digit_Display #(.decimalPoint("false")) hex_digit_display_1887 (.value(register_120_q[39:36]));
  Hex_Digit_Display #(.decimalPoint("false")) hex_digit_display_1888 (.value(register_120_q[35:32]));
  Hex_Digit_Display #(.decimalPoint("false")) hex_digit_display_1889 (.value(register_121_q[39:36]));
  Hex_Digit_Display #(.decimalPoint("false")) hex_digit_display_1890 (.value(register_121_q[35:32]));
  Hex_Digit_Display #(.decimalPoint("false")) hex_digit_display_1891 (.value(register_122_q[39:36]));
  Hex_Digit_Display #(.decimalPoint("false")) hex_digit_display_1892 (.value(register_122_q[35:32]));
  Hex_Digit_Display #(.decimalPoint("false")) hex_digit_display_1893 (.value(register_123_q[39:36]));
  Hex_Digit_Display #(.decimalPoint("false")) hex_digit_display_1894 (.value(register_123_q[35:32]));
  Hex_Digit_Display #(.decimalPoint("false")) hex_digit_display_1895 (.value(register_124_q[39:36]));
  Hex_Digit_Display #(.decimalPoint("false")) hex_digit_display_1896 (.value(register_124_q[35:32]));
  Hex_Digit_Display #(.decimalPoint("false")) hex_digit_display_1897 (.value(register_125_q[43:40]));
  Hex_Digit_Display #(.decimalPoint("false")) hex_digit_display_1898 (.value(register_125_q[39:36]));
  Hex_Digit_Display #(.decimalPoint("false")) hex_digit_display_1899 (.value(register_126_q[43:40]));
  Hex_Digit_Display #(.decimalPoint("false")) hex_digit_display_1900 (.value(register_126_q[39:36]));
  Hex_Digit_Display #(.decimalPoint("false")) hex_digit_display_1901 (.value(register_127_q[43:40]));
  Hex_Digit_Display #(.decimalPoint("false")) hex_digit_display_1902 (.value(register_127_q[39:36]));
  Hex_Digit_Display #(.decimalPoint("false")) hex_digit_display_1903 (.value(register_128_q[43:40]));
  Hex_Digit_Display #(.decimalPoint("false")) hex_digit_display_1904 (.value(register_128_q[39:36]));
  Hex_Digit_Display #(.decimalPoint("false")) hex_digit_display_1905 (.value(register_129_q[43:40]));
  Hex_Digit_Display #(.decimalPoint("false")) hex_digit_display_1906 (.value(register_129_q[39:36]));
  Hex_Digit_Display #(.decimalPoint("false")) hex_digit_display_1907 (.value(register_130_q[43:40]));
  Hex_Digit_Display #(.decimalPoint("false")) hex_digit_display_1908 (.value(register_130_q[39:36]));
  Hex_Digit_Display #(.decimalPoint("false")) hex_digit_display_1909 (.value(register_131_q[43:40]));
  Hex_Digit_Display #(.decimalPoint("false")) hex_digit_display_1910 (.value(register_131_q[39:36]));
  Hex_Digit_Display #(.decimalPoint("false")) hex_digit_display_1911 (.value(register_132_q[43:40]));
  Hex_Digit_Display #(.decimalPoint("false")) hex_digit_display_1912 (.value(register_132_q[39:36]));
  Hex_Digit_Display #(.decimalPoint("false")) hex_digit_display_1913 (.value(register_117_q[31:28]));
  Hex_Digit_Display #(.decimalPoint("false")) hex_digit_display_1914 (.value(register_117_q[27:24]));
  Hex_Digit_Display #(.decimalPoint("false")) hex_digit_display_1915 (.value(register_118_q[31:28]));
  Hex_Digit_Display #(.decimalPoint("false")) hex_digit_display_1916 (.value(register_118_q[27:24]));
  Hex_Digit_Display #(.decimalPoint("false")) hex_digit_display_1917 (.value(register_119_q[31:28]));
  Hex_Digit_Display #(.decimalPoint("false")) hex_digit_display_1918 (.value(register_119_q[27:24]));
  Hex_Digit_Display #(.decimalPoint("false")) hex_digit_display_1919 (.value(register_120_q[31:28]));
  Hex_Digit_Display #(.decimalPoint("false")) hex_digit_display_1920 (.value(register_120_q[27:24]));
  Hex_Digit_Display #(.decimalPoint("false")) hex_digit_display_1921 (.value(register_121_q[31:28]));
  Hex_Digit_Display #(.decimalPoint("false")) hex_digit_display_1922 (.value(register_121_q[27:24]));
  Hex_Digit_Display #(.decimalPoint("false")) hex_digit_display_1923 (.value(register_122_q[31:28]));
  Hex_Digit_Display #(.decimalPoint("false")) hex_digit_display_1924 (.value(register_122_q[27:24]));
  Hex_Digit_Display #(.decimalPoint("false")) hex_digit_display_1925 (.value(register_123_q[31:28]));
  Hex_Digit_Display #(.decimalPoint("false")) hex_digit_display_1926 (.value(register_123_q[27:24]));
  Hex_Digit_Display #(.decimalPoint("false")) hex_digit_display_1927 (.value(register_124_q[31:28]));
  Hex_Digit_Display #(.decimalPoint("false")) hex_digit_display_1928 (.value(register_124_q[27:24]));
  Hex_Digit_Display #(.decimalPoint("false")) hex_digit_display_1929 (.value(register_125_q[35:32]));
  Hex_Digit_Display #(.decimalPoint("false")) hex_digit_display_1930 (.value(register_125_q[31:28]));
  Hex_Digit_Display #(.decimalPoint("false")) hex_digit_display_1931 (.value(register_126_q[35:32]));
  Hex_Digit_Display #(.decimalPoint("false")) hex_digit_display_1932 (.value(register_126_q[31:28]));
  Hex_Digit_Display #(.decimalPoint("false")) hex_digit_display_1933 (.value(register_127_q[35:32]));
  Hex_Digit_Display #(.decimalPoint("false")) hex_digit_display_1934 (.value(register_127_q[31:28]));
  Hex_Digit_Display #(.decimalPoint("false")) hex_digit_display_1935 (.value(register_128_q[35:32]));
  Hex_Digit_Display #(.decimalPoint("false")) hex_digit_display_1936 (.value(register_128_q[31:28]));
  Hex_Digit_Display #(.decimalPoint("false")) hex_digit_display_1937 (.value(register_129_q[35:32]));
  Hex_Digit_Display #(.decimalPoint("false")) hex_digit_display_1938 (.value(register_129_q[31:28]));
  Hex_Digit_Display #(.decimalPoint("false")) hex_digit_display_1939 (.value(register_130_q[35:32]));
  Hex_Digit_Display #(.decimalPoint("false")) hex_digit_display_1940 (.value(register_130_q[31:28]));
  Hex_Digit_Display #(.decimalPoint("false")) hex_digit_display_1941 (.value(register_131_q[35:32]));
  Hex_Digit_Display #(.decimalPoint("false")) hex_digit_display_1942 (.value(register_131_q[31:28]));
  Hex_Digit_Display #(.decimalPoint("false")) hex_digit_display_1943 (.value(register_132_q[35:32]));
  Hex_Digit_Display #(.decimalPoint("false")) hex_digit_display_1944 (.value(register_132_q[31:28]));
  Hex_Digit_Display #(.decimalPoint("false")) hex_digit_display_1945 (.value(register_117_q[23:20]));
  Hex_Digit_Display #(.decimalPoint("false")) hex_digit_display_1946 (.value(register_117_q[19:16]));
  Hex_Digit_Display #(.decimalPoint("false")) hex_digit_display_1947 (.value(register_118_q[23:20]));
  Hex_Digit_Display #(.decimalPoint("false")) hex_digit_display_1948 (.value(register_118_q[19:16]));
  Hex_Digit_Display #(.decimalPoint("false")) hex_digit_display_1949 (.value(register_119_q[23:20]));
  Hex_Digit_Display #(.decimalPoint("false")) hex_digit_display_1950 (.value(register_119_q[19:16]));
  Hex_Digit_Display #(.decimalPoint("false")) hex_digit_display_1951 (.value(register_120_q[23:20]));
  Hex_Digit_Display #(.decimalPoint("false")) hex_digit_display_1952 (.value(register_120_q[19:16]));
  Hex_Digit_Display #(.decimalPoint("false")) hex_digit_display_1953 (.value(register_121_q[23:20]));
  Hex_Digit_Display #(.decimalPoint("false")) hex_digit_display_1954 (.value(register_121_q[19:16]));
  Hex_Digit_Display #(.decimalPoint("false")) hex_digit_display_1955 (.value(register_122_q[23:20]));
  Hex_Digit_Display #(.decimalPoint("false")) hex_digit_display_1956 (.value(register_122_q[19:16]));
  Hex_Digit_Display #(.decimalPoint("false")) hex_digit_display_1957 (.value(register_123_q[23:20]));
  Hex_Digit_Display #(.decimalPoint("false")) hex_digit_display_1958 (.value(register_123_q[19:16]));
  Hex_Digit_Display #(.decimalPoint("false")) hex_digit_display_1959 (.value(register_124_q[23:20]));
  Hex_Digit_Display #(.decimalPoint("false")) hex_digit_display_1960 (.value(register_124_q[19:16]));
  Hex_Digit_Display #(.decimalPoint("false")) hex_digit_display_1961 (.value(register_125_q[27:24]));
  Hex_Digit_Display #(.decimalPoint("false")) hex_digit_display_1962 (.value(register_125_q[23:20]));
  Hex_Digit_Display #(.decimalPoint("false")) hex_digit_display_1963 (.value(register_126_q[27:24]));
  Hex_Digit_Display #(.decimalPoint("false")) hex_digit_display_1964 (.value(register_126_q[23:20]));
  Hex_Digit_Display #(.decimalPoint("false")) hex_digit_display_1965 (.value(register_127_q[27:24]));
  Hex_Digit_Display #(.decimalPoint("false")) hex_digit_display_1966 (.value(register_127_q[23:20]));
  Hex_Digit_Display #(.decimalPoint("false")) hex_digit_display_1967 (.value(register_128_q[27:24]));
  Hex_Digit_Display #(.decimalPoint("false")) hex_digit_display_1968 (.value(register_128_q[23:20]));
  Hex_Digit_Display #(.decimalPoint("false")) hex_digit_display_1969 (.value(register_129_q[27:24]));
  Hex_Digit_Display #(.decimalPoint("false")) hex_digit_display_1970 (.value(register_129_q[23:20]));
  Hex_Digit_Display #(.decimalPoint("false")) hex_digit_display_1971 (.value(register_130_q[27:24]));
  Hex_Digit_Display #(.decimalPoint("false")) hex_digit_display_1972 (.value(register_130_q[23:20]));
  Hex_Digit_Display #(.decimalPoint("false")) hex_digit_display_1973 (.value(register_131_q[27:24]));
  Hex_Digit_Display #(.decimalPoint("false")) hex_digit_display_1974 (.value(register_131_q[23:20]));
  Hex_Digit_Display #(.decimalPoint("false")) hex_digit_display_1975 (.value(register_132_q[27:24]));
  Hex_Digit_Display #(.decimalPoint("false")) hex_digit_display_1976 (.value(register_132_q[23:20]));
  Hex_Digit_Display #(.decimalPoint("false")) hex_digit_display_1977 (.value(register_117_q[15:12]));
  Hex_Digit_Display #(.decimalPoint("false")) hex_digit_display_1978 (.value(register_117_q[11:8]));
  Hex_Digit_Display #(.decimalPoint("false")) hex_digit_display_1979 (.value(register_118_q[15:12]));
  Hex_Digit_Display #(.decimalPoint("false")) hex_digit_display_1980 (.value(register_118_q[11:8]));
  Hex_Digit_Display #(.decimalPoint("false")) hex_digit_display_1981 (.value(register_119_q[15:12]));
  Hex_Digit_Display #(.decimalPoint("false")) hex_digit_display_1982 (.value(register_119_q[11:8]));
  Hex_Digit_Display #(.decimalPoint("false")) hex_digit_display_1983 (.value(register_120_q[15:12]));
  Hex_Digit_Display #(.decimalPoint("false")) hex_digit_display_1984 (.value(register_120_q[11:8]));
  Hex_Digit_Display #(.decimalPoint("false")) hex_digit_display_1985 (.value(register_121_q[15:12]));
  Hex_Digit_Display #(.decimalPoint("false")) hex_digit_display_1986 (.value(register_121_q[11:8]));
  Hex_Digit_Display #(.decimalPoint("false")) hex_digit_display_1987 (.value(register_122_q[15:12]));
  Hex_Digit_Display #(.decimalPoint("false")) hex_digit_display_1988 (.value(register_122_q[11:8]));
  Hex_Digit_Display #(.decimalPoint("false")) hex_digit_display_1989 (.value(register_123_q[15:12]));
  Hex_Digit_Display #(.decimalPoint("false")) hex_digit_display_1990 (.value(register_123_q[11:8]));
  Hex_Digit_Display #(.decimalPoint("false")) hex_digit_display_1991 (.value(register_124_q[15:12]));
  Hex_Digit_Display #(.decimalPoint("false")) hex_digit_display_1992 (.value(register_124_q[11:8]));
  Hex_Digit_Display #(.decimalPoint("false")) hex_digit_display_1993 (.value(register_125_q[19:16]));
  Hex_Digit_Display #(.decimalPoint("false")) hex_digit_display_1994 (.value(register_125_q[15:12]));
  Hex_Digit_Display #(.decimalPoint("false")) hex_digit_display_1995 (.value(register_126_q[19:16]));
  Hex_Digit_Display #(.decimalPoint("false")) hex_digit_display_1996 (.value(register_126_q[15:12]));
  Hex_Digit_Display #(.decimalPoint("false")) hex_digit_display_1997 (.value(register_127_q[19:16]));
  Hex_Digit_Display #(.decimalPoint("false")) hex_digit_display_1998 (.value(register_127_q[15:12]));
  Hex_Digit_Display #(.decimalPoint("false")) hex_digit_display_1999 (.value(register_128_q[19:16]));
  Hex_Digit_Display #(.decimalPoint("false")) hex_digit_display_2000 (.value(register_128_q[15:12]));
  Hex_Digit_Display #(.decimalPoint("false")) hex_digit_display_2001 (.value(register_129_q[19:16]));
  Hex_Digit_Display #(.decimalPoint("false")) hex_digit_display_2002 (.value(register_129_q[15:12]));
  Hex_Digit_Display #(.decimalPoint("false")) hex_digit_display_2003 (.value(register_130_q[19:16]));
  Hex_Digit_Display #(.decimalPoint("false")) hex_digit_display_2004 (.value(register_130_q[15:12]));
  Hex_Digit_Display #(.decimalPoint("false")) hex_digit_display_2005 (.value(register_131_q[19:16]));
  Hex_Digit_Display #(.decimalPoint("false")) hex_digit_display_2006 (.value(register_131_q[15:12]));
  Hex_Digit_Display #(.decimalPoint("false")) hex_digit_display_2007 (.value(register_132_q[19:16]));
  Hex_Digit_Display #(.decimalPoint("false")) hex_digit_display_2008 (.value(register_132_q[15:12]));
  Hex_Digit_Display #(.decimalPoint("false")) hex_digit_display_2009 (.value(register_117_q[7:4]));
  Hex_Digit_Display #(.decimalPoint("false")) hex_digit_display_2010 (.value(register_117_q[3:0]));
  Hex_Digit_Display #(.decimalPoint("false")) hex_digit_display_2011 (.value(register_118_q[7:4]));
  Hex_Digit_Display #(.decimalPoint("false")) hex_digit_display_2012 (.value(register_118_q[3:0]));
  Hex_Digit_Display #(.decimalPoint("false")) hex_digit_display_2013 (.value(register_119_q[7:4]));
  Hex_Digit_Display #(.decimalPoint("false")) hex_digit_display_2014 (.value(register_119_q[3:0]));
  Hex_Digit_Display #(.decimalPoint("false")) hex_digit_display_2015 (.value(register_120_q[7:4]));
  Hex_Digit_Display #(.decimalPoint("false")) hex_digit_display_2016 (.value(register_120_q[3:0]));
  Hex_Digit_Display #(.decimalPoint("false")) hex_digit_display_2017 (.value(register_121_q[7:4]));
  Hex_Digit_Display #(.decimalPoint("false")) hex_digit_display_2018 (.value(register_121_q[3:0]));
  Hex_Digit_Display #(.decimalPoint("false")) hex_digit_display_2019 (.value(register_122_q[7:4]));
  Hex_Digit_Display #(.decimalPoint("false")) hex_digit_display_2020 (.value(register_122_q[3:0]));
  Hex_Digit_Display #(.decimalPoint("false")) hex_digit_display_2021 (.value(register_123_q[7:4]));
  Hex_Digit_Display #(.decimalPoint("false")) hex_digit_display_2022 (.value(register_123_q[3:0]));
  Hex_Digit_Display #(.decimalPoint("false")) hex_digit_display_2023 (.value(register_124_q[7:4]));
  Hex_Digit_Display #(.decimalPoint("false")) hex_digit_display_2024 (.value(register_124_q[3:0]));
  Hex_Digit_Display #(.decimalPoint("false")) hex_digit_display_2025 (.value(register_125_q[11:8]));
  Hex_Digit_Display #(.decimalPoint("false")) hex_digit_display_2026 (.value(register_125_q[7:4]));
  Hex_Digit_Display #(.decimalPoint("false")) hex_digit_display_2027 (.value(register_126_q[11:8]));
  Hex_Digit_Display #(.decimalPoint("false")) hex_digit_display_2028 (.value(register_126_q[7:4]));
  Hex_Digit_Display #(.decimalPoint("false")) hex_digit_display_2029 (.value(register_127_q[11:8]));
  Hex_Digit_Display #(.decimalPoint("false")) hex_digit_display_2030 (.value(register_127_q[7:4]));
  Hex_Digit_Display #(.decimalPoint("false")) hex_digit_display_2031 (.value(register_128_q[11:8]));
  Hex_Digit_Display #(.decimalPoint("false")) hex_digit_display_2032 (.value(register_128_q[7:4]));
  Hex_Digit_Display #(.decimalPoint("false")) hex_digit_display_2033 (.value(register_129_q[11:8]));
  Hex_Digit_Display #(.decimalPoint("false")) hex_digit_display_2034 (.value(register_129_q[7:4]));
  Hex_Digit_Display #(.decimalPoint("false")) hex_digit_display_2035 (.value(register_130_q[11:8]));
  Hex_Digit_Display #(.decimalPoint("false")) hex_digit_display_2036 (.value(register_130_q[7:4]));
  Hex_Digit_Display #(.decimalPoint("false")) hex_digit_display_2037 (.value(register_131_q[11:8]));
  Hex_Digit_Display #(.decimalPoint("false")) hex_digit_display_2038 (.value(register_131_q[7:4]));
  Hex_Digit_Display #(.decimalPoint("false")) hex_digit_display_2039 (.value(register_132_q[11:8]));
  Hex_Digit_Display #(.decimalPoint("false")) hex_digit_display_2040 (.value(register_132_q[7:4]));
  Hex_Digit_Display #(.decimalPoint("false")) hex_digit_display_2041 (.value(register_125_q[3:0]));
  Hex_Digit_Display #(.decimalPoint("false")) hex_digit_display_2042 (.value(register_126_q[3:0]));
  Hex_Digit_Display #(.decimalPoint("false")) hex_digit_display_2043 (.value(register_127_q[3:0]));
  Hex_Digit_Display #(.decimalPoint("false")) hex_digit_display_2044 (.value(register_128_q[3:0]));
  Hex_Digit_Display #(.decimalPoint("false")) hex_digit_display_2045 (.value(register_129_q[3:0]));
  Hex_Digit_Display #(.decimalPoint("false")) hex_digit_display_2046 (.value(register_130_q[3:0]));
  Hex_Digit_Display #(.decimalPoint("false")) hex_digit_display_2047 (.value(register_131_q[3:0]));
  Hex_Digit_Display #(.decimalPoint("false")) hex_digit_display_2048 (.value(register_132_q[3:0]));

  // Notes on the sheet:
  //   Pipelined
  //   Written based on a 16x16
  //   Currently only supports multiplying a single NxN (8x8)
  //   Quick and dirty for trying out 8x8
  //   The Tiled Matrix multiplication unit
  //   Quick and dirty for trying out 8x8
  //   Constant High Bit
  //   Control Unit
  //   RAM A Addresses
  //   RAM A Addresses
  //   Row[0][0]
  //   Row[0][1]
  //   Row[0][2]
  //   Row[0][3]
  //   A
  //   A
  //   RAM B Addresses
  //   RAM B Addresses
  //   Col[0][0]
  //   Col[0][1]
  //   Col[0][2]
  //   Col[0][3]
  //   B
  //   B
  //   AW
  //   Partal Sum
  //   BY
  //   AW
  //   Partal Sum
  //   BY
  //   O
  //   Complete 8x8 Element Sum
  //   contents of rom_2 (hex, n*v repeats v):
  //   3
  //   Iterations for Each Tile, since RAMS can hold one row and one colmun of 8x8 Matrix, N/8 would be the value here
  //   Configuration RAM, Holds Matrix Size (N/4)[0], Data Type (0: int64, 1: float64)[1]
  //   N-1, for 8x8 Matrix, do 3 here. i.e 8/2 -1, N/2 -1
endmodule

module Accumulator (
  input  Clear,
  input  Enable,
  input  CLK,
  input  [63:0] D0,
  input  [63:0] D1,
  input  [63:0] D2,
  input  [63:0] D3,
  output [63:0] S0,
  output [63:0] S1,
  output [63:0] S2,
  output [63:0] S3
);

  Register #(.width(64)) register_1 (.D(D0), .en(Enable), .Q(S0), .clk(CLK), .clr(Clear));
  Register #(.width(64)) register_2 (.D(D1), .en(Enable), .Q(S1), .clk(CLK), .clr(Clear));
  Register #(.width(64)) register_3 (.D(D2), .en(Enable), .Q(S2), .clk(CLK), .clr(Clear));
  Register #(.width(64)) register_4 (.D(D3), .en(Enable), .Q(S3), .clk(CLK), .clr(Clear));
endmodule

module MainAssemblyUnbounded (
);

  wire CLOCK_GLOBAL, demultiplexer_1_out0, demultiplexer_1_out1, demultiplexer_1_out2, demultiplexer_1_out3,
       DISPLAY_9, DISPLAY_10, DISPLAY_11, DISPLAY_12, DISPLAY_13, DISPLAY_14, DISPLAY_15, DISPLAY_16, EN_0,
       EN_1, EN_2, EN_3, EN_4, EN_5, EN_6, EN_7, register_3_q;
  wire [15:0] adder_1_out, ADDRESSS_A, CLOCK_VALUE, counter_2_q, register_1_q;
  wire [63:0] ram_1_dout, registerbank_1_p1, registerbank_1_p2, registerbank_1_p3, registerbank_1_p4,
       registerbank_2_p1, registerbank_2_p2, registerbank_2_p3, registerbank_2_p4, registerbank_3_p1,
       registerbank_3_p2, registerbank_3_p3, registerbank_3_p4, registerbank_4_p1, registerbank_4_p2,
       registerbank_4_p3, registerbank_4_p4, registerbank_5_s0, registerbank_5_s1, registerbank_5_s2,
       registerbank_5_s3, registerbank_6_s0, registerbank_6_s1, registerbank_6_s2, registerbank_6_s3,
       subcirc_delay_1_s0, subcirc_delay_1_s1, subcirc_delay_1_s2, subcirc_delay_1_s3, subcirc_delay_1_s4,
       subcirc_delay_1_s5, subcirc_delay_1_s6, subcirc_delay_1_s7, test_subcirc_matrixmultiplier_1_s0,
       test_subcirc_matrixmultiplier_1_s1, test_subcirc_matrixmultiplier_1_s2,
       test_subcirc_matrixmultiplier_1_s3, test_subcirc_matrixmultiplier_1_w0,
       test_subcirc_matrixmultiplier_1_w1, test_subcirc_matrixmultiplier_1_w2,
       test_subcirc_matrixmultiplier_1_w3, test_subcirc_matrixmultiplier_2_s0,
       test_subcirc_matrixmultiplier_2_s1, test_subcirc_matrixmultiplier_2_s2,
       test_subcirc_matrixmultiplier_2_s3, test_subcirc_matrixmultiplier_2_w0,
       test_subcirc_matrixmultiplier_2_w1, test_subcirc_matrixmultiplier_2_w2,
       test_subcirc_matrixmultiplier_2_w3;

  RAM #(.addrWidth(16), .dataWidth(64), .\type ("nonvolatile")) ram_1 (
    .addr(ADDRESSS_A), .oe(1'b1), .clk(CLOCK_GLOBAL), .dout(ram_1_dout));  // open: we, din
  RAM ram_2 ();  // open: addr, we, oe, clk, din, dout
  Clock clock_1 (.out(CLOCK_GLOBAL));
  // RegisterBank registerbank_1: pin names not known; wires that end beside it: registerbank_1_p1, registerbank_1_p2, registerbank_1_p3, registerbank_1_p4
  // RegisterBank registerbank_2: pin names not known; wires that end beside it: registerbank_2_p1, registerbank_2_p2, registerbank_2_p3, registerbank_2_p4
  Counter #(.max('hffff), .width(16)) counter_1 (
    .count(1'b1), .Q(ADDRESSS_A), .up(1'b1), .clk(CLOCK_GLOBAL));  // open: load, D, carry, clr
  // RegisterBank registerbank_3: pin names not known; wires that end beside it: registerbank_3_p1, registerbank_3_p2, registerbank_3_p3, registerbank_3_p4
  // RegisterBank registerbank_4: pin names not known; wires that end beside it: registerbank_4_p1, registerbank_4_p2, registerbank_4_p3, registerbank_4_p4
  TEST_SUBCIRC_MatrixMultiplier test_subcirc_matrixmultiplier_1 (
    .B3(registerbank_3_p4), .B2(registerbank_3_p3), .B1(registerbank_3_p2), .B0(registerbank_3_p1),
    .A3(registerbank_1_p1), .A2(registerbank_1_p2), .A1(registerbank_1_p3), .A0(registerbank_1_p4),
    .S0(test_subcirc_matrixmultiplier_1_s0), .W0(test_subcirc_matrixmultiplier_1_w0),
    .S1(test_subcirc_matrixmultiplier_1_s1), .W1(test_subcirc_matrixmultiplier_1_w1),
    .S2(test_subcirc_matrixmultiplier_1_s2), .W2(test_subcirc_matrixmultiplier_1_w2),
    .S3(test_subcirc_matrixmultiplier_1_s3), .W3(test_subcirc_matrixmultiplier_1_w3));
  TEST_SUBCIRC_MatrixAdder test_subcirc_matrixadder_1 (
    .B0(test_subcirc_matrixmultiplier_1_s0), .B1(test_subcirc_matrixmultiplier_1_w0),
    .B2(test_subcirc_matrixmultiplier_1_s1), .B3(test_subcirc_matrixmultiplier_1_w1),
    .A0(test_subcirc_matrixmultiplier_1_s2), .A1(test_subcirc_matrixmultiplier_1_w2),
    .A2(test_subcirc_matrixmultiplier_1_s3), .A3(test_subcirc_matrixmultiplier_1_w3));  // open: S0, S1, S2, S3
  TEST_SUBCIRC_MatrixMultiplier test_subcirc_matrixmultiplier_2 (
    .B3(registerbank_4_p4), .B2(registerbank_4_p3), .B1(registerbank_4_p2), .B0(registerbank_4_p1),
    .A3(registerbank_2_p1), .A2(registerbank_2_p2), .A1(registerbank_2_p3), .A0(registerbank_2_p4),
    .S0(test_subcirc_matrixmultiplier_2_s0), .W0(test_subcirc_matrixmultiplier_2_w0),
    .S1(test_subcirc_matrixmultiplier_2_s1), .W1(test_subcirc_matrixmultiplier_2_w1),
    .S2(test_subcirc_matrixmultiplier_2_s2), .W2(test_subcirc_matrixmultiplier_2_w2),
    .S3(test_subcirc_matrixmultiplier_2_s3), .W3(test_subcirc_matrixmultiplier_2_w3));
  TEST_SUBCIRC_MatrixAdder test_subcirc_matrixadder_2 (
    .B0(test_subcirc_matrixmultiplier_2_s0), .B1(test_subcirc_matrixmultiplier_2_w0),
    .B2(test_subcirc_matrixmultiplier_2_s1), .B3(test_subcirc_matrixmultiplier_2_w1),
    .A0(test_subcirc_matrixmultiplier_2_s2), .A1(test_subcirc_matrixmultiplier_2_w2),
    .A2(test_subcirc_matrixmultiplier_2_s3), .A3(test_subcirc_matrixmultiplier_2_w3));  // open: S0, S1, S2, S3
  Counter #(.max('hffff), .width(16)) counter_2 (
    .count(1'b1), .Q(counter_2_q), .up(1'b1), .clk(CLOCK_GLOBAL));  // open: load, D, carry, clr
  Register #(.width(16)) register_1 (.D(adder_1_out), .en(1'b1), .Q(register_1_q), .clk(CLOCK_GLOBAL));  // open: clr
  Adder #(.width(16)) adder_1 (.a(register_1_q), .b(counter_2_q), .out(adder_1_out));  // open: cin, cout
  Register #(.width(16)) register_2 (.D(counter_2_q), .en(1'b1), .Q(CLOCK_VALUE), .clk(CLOCK_GLOBAL));  // open: clr
  RegisterBank registerbank_5 (
    .D3(ram_1_dout), .D2(ram_1_dout), .D1(ram_1_dout), .D0(ram_1_dout), .CLK(CLOCK_GLOBAL), .EN3(EN_3),
    .EN2(EN_2), .EN1(EN_1), .EN0(EN_0), .S3(registerbank_5_s3), .S2(registerbank_5_s2),
    .S1(registerbank_5_s1), .S0(registerbank_5_s0));  // open: CLEAR
  RegisterBank registerbank_6 (
    .D3(ram_1_dout), .D2(ram_1_dout), .D1(ram_1_dout), .D0(ram_1_dout), .CLK(CLOCK_GLOBAL), .EN3(EN_7),
    .EN2(EN_6), .EN1(EN_5), .EN0(EN_4), .S3(registerbank_6_s3), .S2(registerbank_6_s2),
    .S1(registerbank_6_s1), .S0(registerbank_6_s0));  // open: CLEAR
  Demultiplexer #(.select(4)) demultiplexer_1 (
    .out0(demultiplexer_1_out0), .out1(demultiplexer_1_out1), .out2(demultiplexer_1_out2),
    .out3(demultiplexer_1_out3), .out4(EN_4), .out5(EN_5), .out6(EN_6), .out7(EN_7), .out8(DISPLAY_9),
    .out9(DISPLAY_10), .out10(DISPLAY_11), .out11(DISPLAY_12), .out12(DISPLAY_13), .out13(DISPLAY_14),
    .out14(DISPLAY_15), .out15(DISPLAY_16), .sel(CLOCK_VALUE[3:0]));  // open: in
  SUBCIRC_Delay subcirc_delay_1 (
    .D4(registerbank_5_s3), .D5(registerbank_5_s2), .D6(registerbank_5_s1), .D7(registerbank_5_s0),
    .D0(registerbank_6_s3), .D1(registerbank_6_s2), .D2(registerbank_6_s1), .D3(registerbank_6_s0),
    .EN(1'b1), .CLK(CLOCK_GLOBAL), .S7(subcirc_delay_1_s7), .S6(subcirc_delay_1_s6), .S5(subcirc_delay_1_s5),
    .S4(subcirc_delay_1_s4), .S3(subcirc_delay_1_s3), .S2(subcirc_delay_1_s2), .S1(subcirc_delay_1_s1),
    .S0(subcirc_delay_1_s0));
  Register #(.width(1)) register_3 (.D(1'b1), .en(1'b1), .Q(register_3_q), .clk(CLOCK_GLOBAL));  // open: clr
  Demultiplexer #(.select(2)) demultiplexer_2 (
    .out0(EN_0), .out1(EN_1), .out2(EN_2), .out3(EN_3), .in(1'b1), .sel(CLOCK_VALUE[1:0]));
  // Probe on subcirc_delay_1_s7
  // Probe on subcirc_delay_1_s6
  // Probe on subcirc_delay_1_s5
  // Probe on subcirc_delay_1_s4
  // Probe on subcirc_delay_1_s3
  // Probe on subcirc_delay_1_s2
  // Probe on subcirc_delay_1_s1
  // Probe on subcirc_delay_1_s0
endmodule

module RegisterBank (
  input  [63:0] D3,
  input  [63:0] D2,
  input  [63:0] D1,
  input  [63:0] D0,
  input  CLEAR,
  input  CLK,
  input  EN3,
  input  EN2,
  input  EN1,
  input  EN0,
  output [63:0] S3,
  output [63:0] S2,
  output [63:0] S1,
  output [63:0] S0
);

  Register #(.width(64)) register_1 (.D(D3), .en(EN3), .Q(S3), .clk(CLK), .clr(CLEAR));
  Register #(.width(64)) register_2 (.D(D2), .en(EN2), .Q(S2), .clk(CLK), .clr(CLEAR));
  Register #(.width(64)) register_3 (.D(D1), .en(EN1), .Q(S1), .clk(CLK), .clr(CLEAR));
  Register #(.width(64)) register_4 (.D(D0), .en(EN0), .Q(S0), .clk(CLK), .clr(CLEAR));
endmodule

module SUBCIRC_Delay (
  input  EN,
  input  CLK,
  input  [63:0] D4,
  input  [63:0] D5,
  input  [63:0] D6,
  input  [63:0] D7,
  input  [63:0] D0,
  input  [63:0] D1,
  input  [63:0] D2,
  input  [63:0] D3,
  output [63:0] S7,
  output [63:0] S6,
  output [63:0] S5,
  output [63:0] S4,
  output [63:0] S3,
  output [63:0] S2,
  output [63:0] S1,
  output [63:0] S0
);

  wire [63:0] register_1_q, register_2_q, register_3_q, register_4_q, register_6_q, register_7_q,
       register_8_q, register_9_q, register_10_q, register_11_q, register_13_q, register_14_q, register_16_q,
       register_17_q, register_18_q, register_19_q, register_20_q, register_21_q, register_24_q,
       register_25_q, register_27_q;

  Register #(.width(64)) register_1 (.D(D4), .en(EN), .Q(register_1_q), .clk(CLK));  // open: clr
  Register #(.width(64)) register_2 (.D(D5), .en(EN), .Q(register_2_q), .clk(CLK));  // open: clr
  Register #(.width(64)) register_3 (.D(D6), .en(EN), .Q(register_3_q), .clk(CLK));  // open: clr
  Register #(.width(64)) register_4 (.D(D7), .en(EN), .Q(register_4_q), .clk(CLK));  // open: clr
  Register #(.width(64)) register_5 (.D(D1), .en(EN), .Q(S1), .clk(CLK));  // open: clr
  Register #(.width(64)) register_6 (.D(D2), .en(EN), .Q(register_6_q), .clk(CLK));  // open: clr
  Register #(.width(64)) register_7 (.D(D3), .en(EN), .Q(register_7_q), .clk(CLK));  // open: clr
  Register #(.width(64)) register_8 (.D(register_1_q), .en(EN), .Q(register_8_q), .clk(CLK));  // open: clr
  Register #(.width(64)) register_9 (.D(register_2_q), .en(EN), .Q(register_9_q), .clk(CLK));  // open: clr
  Register #(.width(64)) register_10 (.D(register_3_q), .en(EN), .Q(register_10_q), .clk(CLK));  // open: clr
  Register #(.width(64)) register_11 (.D(register_4_q), .en(EN), .Q(register_11_q), .clk(CLK));  // open: clr
  Register #(.width(64)) register_12 (.D(register_6_q), .en(EN), .Q(S2), .clk(CLK));  // open: clr
  Register #(.width(64)) register_13 (.D(register_7_q), .en(EN), .Q(register_13_q), .clk(CLK));  // open: clr
  Register #(.width(64)) register_14 (.D(register_8_q), .en(EN), .Q(register_14_q), .clk(CLK));  // open: clr
  Register #(.width(64)) register_15 (.D(register_14_q), .en(EN), .Q(S4), .clk(CLK));  // open: clr
  Register #(.width(64)) register_16 (.D(register_9_q), .en(EN), .Q(register_16_q), .clk(CLK));  // open: clr
  Register #(.width(64)) register_17 (.D(register_16_q), .en(EN), .Q(register_17_q), .clk(CLK));  // open: clr
  Register #(.width(64)) register_18 (.D(register_10_q), .en(EN), .Q(register_18_q), .clk(CLK));  // open: clr
  Register #(.width(64)) register_19 (.D(register_18_q), .en(EN), .Q(register_19_q), .clk(CLK));  // open: clr
  Register #(.width(64)) register_20 (.D(register_11_q), .en(EN), .Q(register_20_q), .clk(CLK));  // open: clr
  Register #(.width(64)) register_21 (.D(register_20_q), .en(EN), .Q(register_21_q), .clk(CLK));  // open: clr
  Register #(.width(64)) register_22 (.D(register_13_q), .en(EN), .Q(S3), .clk(CLK));  // open: clr
  Register #(.width(64)) register_23 (.D(register_17_q), .en(EN), .Q(S5), .clk(CLK));  // open: clr
  Register #(.width(64)) register_24 (.D(register_19_q), .en(EN), .Q(register_24_q), .clk(CLK));  // open: clr
  Register #(.width(64)) register_25 (.D(register_21_q), .en(EN), .Q(register_25_q), .clk(CLK));  // open: clr
  Register #(.width(64)) register_26 (.D(register_24_q), .en(EN), .Q(S6), .clk(CLK));  // open: clr
  Register #(.width(64)) register_27 (.D(register_25_q), .en(EN), .Q(register_27_q), .clk(CLK));  // open: clr
  Register #(.width(64)) register_28 (.D(register_27_q), .en(EN), .Q(S7), .clk(CLK));  // open: clr

  assign S0 = D0;
endmodule

module TEST_RAM_MULTICYCLE (
);

  wire CLOCK_GLOBAL, dataramcontroller_1_oe, dataramcontroller_2_oe, dataramcontroller_3_oe,
       dataramcontroller_4_oe;
  wire [7:0] ram_1_dout, ram_2_dout, ram_3_dout, ram_4_dout;
  wire [15:0] dataramcontroller_1_a, dataramcontroller_2_a, dataramcontroller_3_a, dataramcontroller_4_a;

  Clock clock_1 (.out(CLOCK_GLOBAL));
  RAM #(.addrWidth(16), .asyncread("true"), .trigger("falling"), .\type ("nonvolatile")) ram_1 (
    .addr(dataramcontroller_1_a), .oe(dataramcontroller_1_oe), .clk(CLOCK_GLOBAL), .dout(ram_1_dout));  // open: we, din
  DataRAMController dataramcontroller_1 (
    .SHIFT({16{1'b0}}), .CLK(CLOCK_GLOBAL), .A(dataramcontroller_1_a), .OE(dataramcontroller_1_oe));
  RAM #(.addrWidth(16), .asyncread("true"), .trigger("falling"), .\type ("nonvolatile")) ram_2 (
    .addr(dataramcontroller_2_a), .oe(dataramcontroller_2_oe), .clk(CLOCK_GLOBAL), .dout(ram_2_dout));  // open: we, din
  DataRAMController dataramcontroller_2 (
    .SHIFT(16'h3), .CLK(CLOCK_GLOBAL), .A(dataramcontroller_2_a), .OE(dataramcontroller_2_oe));
  RAM #(.addrWidth(16), .asyncread("true"), .trigger("falling"), .\type ("nonvolatile")) ram_3 (
    .addr(dataramcontroller_3_a), .oe(dataramcontroller_3_oe), .clk(CLOCK_GLOBAL), .dout(ram_3_dout));  // open: we, din
  DataRAMController dataramcontroller_3 (
    .SHIFT(16'h7), .CLK(CLOCK_GLOBAL), .A(dataramcontroller_3_a), .OE(dataramcontroller_3_oe));
  RAM #(.addrWidth(16), .asyncread("true"), .trigger("falling"), .\type ("nonvolatile")) ram_4 (
    .addr(dataramcontroller_4_a), .oe(dataramcontroller_4_oe), .clk(CLOCK_GLOBAL), .dout(ram_4_dout));  // open: we, din
  DataRAMController dataramcontroller_4 (
    .SHIFT(16'h15), .CLK(CLOCK_GLOBAL), .A(dataramcontroller_4_a), .OE(dataramcontroller_4_oe));
  // Probe on ram_1_dout
  // Probe on ram_2_dout
  // Probe on ram_3_dout
  // Probe on ram_4_dout
endmodule

module Assembly8x8 (
  input  [63:0] D3,
  input  [63:0] D2,
  input  [63:0] D1,
  input  [63:0] D0,
  input  CLEAR,
  input  CLK,
  input  EN2,
  input  EN0,
  output [63:0] S3,
  output [63:0] S2,
  output [63:0] S1,
  output [63:0] S0
);

  wire clock_2_out, CLOCK_GLOBAL, not_1_out, not_2_out;
  wire [15:0] undriven, undriven_2;
  wire [63:0] rambankedged_1_r0, rambankedged_1_r1, S0_t, S1_t, S2_t, S3_t;

  Clock clock_1 (.out(CLOCK_GLOBAL));
  Clock clock_2 (.out(clock_2_out));
  RAMBankEdged rambankedged_1 (
    .OFFSET(undriven), .CLK(clock_2_out), .R0(rambankedged_1_r0), .R1(rambankedged_1_r1));  // open: R2, R3
  RegisterBankEdgedPaired registerbankedgedpaired_1 (
    .D3(rambankedged_1_r1), .D2(rambankedged_1_r1), .D1(rambankedged_1_r0), .D0(rambankedged_1_r0),
    .CLK(clock_2_out), .EN2(1'b1), .EN0(1'b1), .S3(S3_t), .S2(S2_t), .S1(S1_t), .S0(S0_t));  // open: CLEAR
  // RegisterBankEdged registerbankedged_1: pin names not known
  // RegisterBankEdged registerbankedged_2: pin names not known
  // RegisterBankEdged registerbankedged_3: pin names not known
  // RegisterBankEdged registerbankedged_4: pin names not known
  // RegisterBankEdged registerbankedged_5: pin names not known
  // RegisterBankEdged registerbankedged_6: pin names not known
  // RegisterBankEdged registerbankedged_7: pin names not known
  RAMBankEdged rambankedged_2 (.OFFSET(undriven_2), .CLK(clock_2_out));  // open: R0, R1, R2, R3
  // Probe on S0_t
  // Probe on S2_t
  // RegisterBankEdged registerbankedged_8: pin names not known
  // RegisterBankEdged registerbankedged_9: pin names not known
  // RegisterBankEdged registerbankedged_10: pin names not known
  // RegisterBankEdged registerbankedged_11: pin names not known
  // RegisterBankEdged registerbankedged_12: pin names not known
  // RegisterBankEdged registerbankedged_13: pin names not known
  // RegisterBankEdged registerbankedged_14: pin names not known
  // RegisterBankEdged registerbankedged_15: pin names not known
  // Probe on S1_t
  // Probe on S3_t
  not not_1 (not_1_out, EN2);
  not not_2 (not_2_out, EN0);
  Register #(.width(64)) register_1 (.D(D3), .en(not_1_out), .Q(S3), .clk(CLK), .clr(CLEAR));
  Register #(.trigger("falling"), .width(64)) register_2 (.D(D2), .en(EN2), .Q(S2), .clk(CLK), .clr(CLEAR));
  Register #(.width(64)) register_3 (.D(D1), .en(not_2_out), .Q(S1), .clk(CLK), .clr(CLEAR));
  Register #(.trigger("falling"), .width(64)) register_4 (.D(D0), .en(EN0), .Q(S0), .clk(CLK), .clr(CLEAR));

  // Notes on the sheet:
  //   A
  //   WE
  //   B
  //   WE
endmodule

module RegisterBankEdged (
  input  [63:0] D3,
  input  [63:0] D2,
  input  [63:0] D1,
  input  [63:0] D0,
  input  CLEAR,
  input  CLK,
  input  EN3,
  input  EN2,
  input  EN1,
  input  EN0,
  output [63:0] S3,
  output [63:0] S2,
  output [63:0] S1,
  output [63:0] S0
);

  Register #(.width(64)) register_1 (.D(D3), .en(EN3), .Q(S3), .clk(CLK), .clr(CLEAR));
  Register #(.trigger("falling"), .width(64)) register_2 (.D(D2), .en(EN2), .Q(S2), .clk(CLK), .clr(CLEAR));
  Register #(.width(64)) register_3 (.D(D1), .en(EN1), .Q(S1), .clk(CLK), .clr(CLEAR));
  Register #(.trigger("falling"), .width(64)) register_4 (.D(D0), .en(EN0), .Q(S0), .clk(CLK), .clr(CLEAR));
endmodule

module RAMBankEdged (
  input  [15:0] OFFSET,
  input  CLK,
  output [63:0] R0,
  output [63:0] R1,
  output [63:0] R2,
  output [63:0] R3
);

  wire dataramcontroller_1_oe, dataramcontroller_2_oe, dataramcontroller_3_oe, dataramcontroller_4_oe;
  wire [15:0] adder_1_out, adder_2_out, adder_3_out, adder_4_out, dataramcontroller_1_a,
       dataramcontroller_2_a, dataramcontroller_3_a, dataramcontroller_4_a;

  DataRAMController dataramcontroller_1 (
    .SHIFT({16{1'b0}}), .CLK(CLK), .A(dataramcontroller_1_a), .OE(dataramcontroller_1_oe));
  DataRAMController dataramcontroller_2 (
    .SHIFT(16'h1), .CLK(CLK), .A(dataramcontroller_2_a), .OE(dataramcontroller_2_oe));
  DataRAMController dataramcontroller_3 (
    .SHIFT(16'h2), .CLK(CLK), .A(dataramcontroller_3_a), .OE(dataramcontroller_3_oe));
  DataRAMController dataramcontroller_4 (
    .SHIFT(16'h3), .CLK(CLK), .A(dataramcontroller_4_a), .OE(dataramcontroller_4_oe));
  RAM #(.addrWidth(16), .asyncread("true"), .dataWidth(64), .trigger("falling"), .\type ("nonvolatile")) ram_1 (
    .addr(adder_1_out), .oe(dataramcontroller_1_oe), .clk(CLK), .dout(R0));  // open: we, din
  Adder #(.width(16)) adder_1 (.a(OFFSET), .b(dataramcontroller_1_a), .out(adder_1_out));  // open: cin, cout
  RAM #(.addrWidth(16), .asyncread("true"), .dataWidth(64), .trigger("falling"), .\type ("nonvolatile")) ram_2 (
    .addr(adder_2_out), .oe(dataramcontroller_2_oe), .clk(CLK), .dout(R1));  // open: we, din
  Adder #(.width(16)) adder_2 (.a(OFFSET), .b(dataramcontroller_2_a), .out(adder_2_out));  // open: cin, cout
  RAM #(.addrWidth(16), .asyncread("true"), .dataWidth(64), .trigger("falling"), .\type ("nonvolatile")) ram_3 (
    .addr(adder_3_out), .oe(dataramcontroller_3_oe), .clk(CLK), .dout(R2));  // open: we, din
  Adder #(.width(16)) adder_3 (.a(OFFSET), .b(dataramcontroller_3_a), .out(adder_3_out));  // open: cin, cout
  RAM #(.addrWidth(16), .asyncread("true"), .dataWidth(64), .trigger("falling"), .\type ("nonvolatile")) ram_4 (
    .addr(adder_4_out), .oe(dataramcontroller_4_oe), .clk(CLK), .dout(R3));  // open: we, din
  Adder #(.width(16)) adder_4 (.a(OFFSET), .b(dataramcontroller_4_a), .out(adder_4_out));  // open: cin, cout

  // Other names for the same wires on the sheet: CLOCK_GLOBAL = CLK
endmodule

module RegisterBankEdgedPaired (
  input  [63:0] D3,
  input  [63:0] D2,
  input  [63:0] D1,
  input  [63:0] D0,
  input  CLEAR,
  input  CLK,
  input  EN2,
  input  EN0,
  output [63:0] S3,
  output [63:0] S2,
  output [63:0] S1,
  output [63:0] S0
);

  wire not_1_out, not_2_out;

  not not_1 (not_1_out, EN2);
  not not_2 (not_2_out, EN0);
  Register #(.width(64)) register_1 (.D(D3), .en(not_1_out), .Q(S3), .clk(CLK), .clr(CLEAR));
  Register #(.trigger("falling"), .width(64)) register_2 (.D(D2), .en(EN2), .Q(S2), .clk(CLK), .clr(CLEAR));
  Register #(.width(64)) register_3 (.D(D1), .en(not_2_out), .Q(S1), .clk(CLK), .clr(CLEAR));
  Register #(.trigger("falling"), .width(64)) register_4 (.D(D0), .en(EN0), .Q(S0), .clk(CLK), .clr(CLEAR));
endmodule
