// Logisim project release_v2.circ as structural Verilog
module DEPRECATED_RegisterBankEdged (
  input  [63:0] D3,
  input  [63:0] D2,
  input  [63:0] D1,
  input  [63:0] D0,
  input  CLEAR,
  input  CLK,
  input  EN3,
  input  EN2,
  input  EN1,
  input  EN0,
  output [63:0] S3,
  output [63:0] S2,
  output [63:0] S1,
  output [63:0] S0
);

  Register #(.width(64)) register_1 (.D(D3), .en(EN3), .Q(S3), .clk(CLK), .clr(CLEAR));
  Register #(.trigger("falling"), .width(64)) register_2 (.D(D2), .en(EN2), .Q(S2), .clk(CLK), .clr(CLEAR));
  Register #(.width(64)) register_3 (.D(D1), .en(EN1), .Q(S1), .clk(CLK), .clr(CLEAR));
  Register #(.trigger("falling"), .width(64)) register_4 (.D(D0), .en(EN0), .Q(S0), .clk(CLK), .clr(CLEAR));
endmodule

module Accumulator (
  input  Clear,
  input  Enable,
  input  CLK,
  input  [63:0] A0,
  input  [63:0] A1,
  input  [63:0] A2,
  input  [63:0] A3,
  output [63:0] S0,
  output [63:0] S1,
  output [63:0] S2,
  output [63:0] S3
);

  wire [63:0] matrixadder_1_s0, matrixadder_1_s1, matrixadder_1_s2, matrixadder_1_s3;

  Register #(.width(64)) register_1 (.D(matrixadder_1_s3), .en(Enable), .Q(S0), .clk(CLK), .clr(Clear));
  Register #(.width(64)) register_2 (.D(matrixadder_1_s2), .en(Enable), .Q(S1), .clk(CLK), .clr(Clear));
  Register #(.width(64)) register_3 (.D(matrixadder_1_s1), .en(Enable), .Q(S2), .clk(CLK), .clr(Clear));
  Register #(.width(64)) register_4 (.D(matrixadder_1_s0), .en(Enable), .Q(S3), .clk(CLK), .clr(Clear));
  MatrixAdder matrixadder_1 (
    .B0(S0), .B1(S1), .B2(S2), .B3(S3), .A0(A0), .A1(A1), .A2(A2), .A3(A3), .S0(matrixadder_1_s0),
    .S1(matrixadder_1_s1), .S2(matrixadder_1_s2), .S3(matrixadder_1_s3));
endmodule

module MatrixMultiplier (
  input  [63:0] A3,
  input  [63:0] A2,
  input  [63:0] A1,
  input  [63:0] A0,
  input  P,
  input  [63:0] B3,
  input  [63:0] B2,
  input  [63:0] B1,
  input  [63:0] B0,
  output [63:0] S0,
  output [63:0] S1,
  output [63:0] S2,
  output [63:0] S3,
  output [63:0] W0,
  output [63:0] W1,
  output [63:0] W2,
  output [63:0] W3
);

  wire [63:0] multiplier_1_out, multiplier_2_out, multiplier_3_out, multiplier_4_out, multiplier_5_out,
       multiplier_6_out, multiplier_7_out, multiplier_8_out;

  Multiplier #(.width(64)) multiplier_1 (.a(A0), .b(B0), .out(multiplier_1_out));  // open: cin, cout
  Multiplier #(.width(64)) multiplier_2 (.a(A0), .b(B1), .out(multiplier_2_out));  // open: cin, cout
  Multiplier #(.width(64)) multiplier_3 (.a(A2), .b(B0), .out(multiplier_3_out));  // open: cin, cout
  Multiplier #(.width(64)) multiplier_4 (.a(A2), .b(B1), .out(multiplier_4_out));  // open: cin, cout
  Multiplier #(.width(64)) multiplier_5 (.a(A1), .b(B2), .out(multiplier_5_out));  // open: cin, cout
  Multiplier #(.width(64)) multiplier_6 (.a(A1), .b(B3), .out(multiplier_6_out));  // open: cin, cout
  Multiplier #(.width(64)) multiplier_7 (.a(A3), .b(B2), .out(multiplier_7_out));  // open: cin, cout
  Multiplier #(.width(64)) multiplier_8 (.a(A3), .b(B3), .out(multiplier_8_out));  // open: cin, cout
  Multiplexer #(.width(64)) multiplexer_1 (.in0(multiplier_1_out), .in1(A0), .out(S0), .sel(P));
  Multiplexer #(.width(64)) multiplexer_2 (.in0(multiplier_2_out), .in1(A1), .out(S1), .sel(P));
  Multiplexer #(.width(64)) multiplexer_3 (.in0(multiplier_3_out), .in1(A2), .out(S2), .sel(P));
  Multiplexer #(.width(64)) multiplexer_4 (.in0(multiplier_4_out), .in1(A3), .out(S3), .sel(P));
  Multiplexer #(.width(64)) multiplexer_5 (.in0(multiplier_5_out), .in1(B0), .out(W0), .sel(P));
  Multiplexer #(.width(64)) multiplexer_6 (.in0(multiplier_6_out), .in1(B1), .out(W1), .sel(P));
  Multiplexer #(.width(64)) multiplexer_7 (.in0(multiplier_7_out), .in1(B2), .out(W2), .sel(P));
  Multiplexer #(.width(64)) multiplexer_8 (.in0(multiplier_8_out), .in1(B3), .out(W3), .sel(P));

  // Notes on the sheet:
  //   Acts as a Partial Multiplication Node
  //   Supports Partial Matrix Multiplication where A*B = S1, S2 where S = S1+S2
  //   When passthrough is asserted 1, values pass unchanged
  //   A0B0
  //   A0B1
  //   A2B0
  //   A2B1
  //   A1B2
  //   A1B3
  //   A3B2
  //   A3B3
endmodule

module SUBCIRC_HalfCycleCounter (
  input  [15:0] SHIFT,
  input  CLK,
  input  Clear,
  output [15:0] A
);

  wire [15:0] adder_1_out, counter_1_q, multiplexer_1_out, multiplier_1_out;

  Counter #(.max('hffff), .trigger("falling"), .width(16)) counter_1 (
    .count(1'b1), .Q(counter_1_q), .up(1'b1), .clk(CLK), .clr(Clear));  // open: load, D, carry
  Multiplier #(.width(16)) multiplier_1 (.a(counter_1_q), .b(16'h2), .out(multiplier_1_out));  // open: cin, cout
  Multiplexer #(.width(16)) multiplexer_1 (
    .in0(multiplier_1_out), .in1(adder_1_out), .out(multiplexer_1_out), .sel(CLK));
  Adder #(.width(16)) adder_1 (.a(multiplier_1_out), .b(16'h1), .out(adder_1_out));  // open: cin, cout
  Adder #(.width(16)) adder_2 (.a(SHIFT), .b(multiplexer_1_out), .out(A));  // open: cin, cout

  // Notes on the sheet:
  //   Credits for doing with 1 counter goes to Ali
endmodule

module MatrixAdder (
  input  [63:0] B0,
  input  [63:0] B1,
  input  [63:0] B2,
  input  [63:0] B3,
  input  [63:0] A0,
  input  [63:0] A1,
  input  [63:0] A2,
  input  [63:0] A3,
  output [63:0] S0,
  output [63:0] S1,
  output [63:0] S2,
  output [63:0] S3
);

  Adder #(.width(64)) adder_1 (.a(B0), .b(A0), .out(S0));  // open: cin, cout
  Adder #(.width(64)) adder_2 (.a(B1), .b(A1), .out(S1));  // open: cin, cout
  Adder #(.width(64)) adder_3 (.a(B2), .b(A2), .out(S2));  // open: cin, cout
  Adder #(.width(64)) adder_4 (.a(B3), .b(A3), .out(S3));  // open: cin, cout

  // Notes on the sheet:
  //   Acts as a addition Node
endmodule

module DEPRECATED_PARALLEL_Assembly (
);

  wire ACCUMULATOR_CLEAR, CLOCK_GLOBAL, EN_11_12_A, EN_11_12_B, EN_13_14_A, EN_15_16_A, EN_17_18_A,
       EN_21_22_A, EN_21_22_B, EN_23_24_A, EN_25_26_A, EN_27_28_A, EN_31_32_B, EN_41_42_B, EN_51_52_B,
       EN_61_62_B, EN_71_72_B, EN_81_82_B, ENABLE_IRAM_COUNTER, ENABLE_ROW_COUNTER, I_BlockLoad, I_BlockMove,
       I_BlockStore, I_DIM, I_Execute, I_Halt, I_Loop, I_MatrixAdd, INPUT_REG_CLEAR, MM_PASSTHROUGH,
       not_1_out, not_2_out, not_3_out, not_4_out, not_5_out, not_6_out, not_7_out, not_8_out, not_9_out,
       not_10_out, not_11_out, not_12_out, not_13_out, not_14_out, not_15_out, not_16_out, not_17_out,
       not_18_out, not_19_out, OR_WE, RESET_IRAM_COUNTER, RESET_ROM_STEP, RESET_ROW_COUNTER, UO_INUPUT_0,
       UO_INUPUT_1, UO_INUPUT_2, UO_INUPUT_3;
  wire [3:0] OP_GLOBAL, subcirc_instructionsplitter_1_flag;
  wire [7:0] STEP_COUNT, subcirc_instructionsplitter_1_addressa, subcirc_instructionsplitter_1_addressb,
       undriven, undriven_2;
  wire [15:0] counter_1_q, register_1_q, register_2_q, undriven_3;
  wire [15:8] controlunit_1_control_a, controlunit_1_control_b;
  wire [23:0] ram_2_dout;
  wire [63:0] accumulator_1_s0, accumulator_1_s1, accumulator_1_s2, accumulator_1_s3, accumulator_2_s0,
       accumulator_2_s1, accumulator_2_s2, accumulator_2_s3, accumulator_3_s0, accumulator_3_s1,
       accumulator_3_s2, accumulator_3_s3, accumulator_4_s0, accumulator_4_s1, accumulator_4_s2,
       accumulator_4_s3, controlled_buffer_1_out, controlled_buffer_2_out, controlled_buffer_3_out,
       controlled_buffer_4_out, matrixadder_1_s0, matrixadder_1_s1, matrixadder_1_s2, matrixadder_1_s3,
       matrixadder_2_s0, matrixadder_2_s1, matrixadder_2_s2, matrixadder_2_s3, matrixadder_3_s0,
       matrixadder_3_s1, matrixadder_3_s2, matrixadder_3_s3, matrixadder_4_s0, matrixadder_4_s1,
       matrixadder_4_s2, matrixadder_4_s3, matrixadder_5_s0, matrixadder_5_s1, matrixadder_5_s2,
       matrixadder_5_s3, matrixadder_6_s0, matrixadder_6_s1, matrixadder_6_s2, matrixadder_6_s3,
       matrixadder_7_s0, matrixadder_7_s1, matrixadder_7_s2, matrixadder_7_s3, matrixadder_8_s0,
       matrixadder_8_s1, matrixadder_8_s2, matrixadder_8_s3, matrixadder_9_s0, matrixadder_9_s1,
       matrixadder_9_s2, matrixadder_9_s3, matrixadder_10_s0, matrixadder_10_s1, matrixadder_10_s2,
       matrixadder_10_s3, matrixadder_11_s0, matrixadder_11_s1, matrixadder_11_s2, matrixadder_11_s3,
       matrixadder_12_s0, matrixadder_12_s1, matrixadder_12_s2, matrixadder_12_s3, matrixmultiplier_1_s0,
       matrixmultiplier_1_s1, matrixmultiplier_1_s2, matrixmultiplier_1_s3, matrixmultiplier_1_w0,
       matrixmultiplier_1_w1, matrixmultiplier_1_w2, matrixmultiplier_1_w3, matrixmultiplier_2_s0,
       matrixmultiplier_2_s1, matrixmultiplier_2_s2, matrixmultiplier_2_s3, matrixmultiplier_2_w0,
       matrixmultiplier_2_w1, matrixmultiplier_2_w2, matrixmultiplier_2_w3, matrixmultiplier_3_s0,
       matrixmultiplier_3_s1, matrixmultiplier_3_s2, matrixmultiplier_3_s3, matrixmultiplier_3_w0,
       matrixmultiplier_3_w1, matrixmultiplier_3_w2, matrixmultiplier_3_w3, matrixmultiplier_4_s0,
       matrixmultiplier_4_s1, matrixmultiplier_4_s2, matrixmultiplier_4_s3, matrixmultiplier_4_w0,
       matrixmultiplier_4_w1, matrixmultiplier_4_w2, matrixmultiplier_4_w3, matrixmultiplier_5_s0,
       matrixmultiplier_5_s1, matrixmultiplier_5_s2, matrixmultiplier_5_s3, matrixmultiplier_5_w0,
       matrixmultiplier_5_w1, matrixmultiplier_5_w2, matrixmultiplier_5_w3, matrixmultiplier_6_s0,
       matrixmultiplier_6_s1, matrixmultiplier_6_s2, matrixmultiplier_6_s3, matrixmultiplier_6_w0,
       matrixmultiplier_6_w1, matrixmultiplier_6_w2, matrixmultiplier_6_w3, matrixmultiplier_7_s0,
       matrixmultiplier_7_s1, matrixmultiplier_7_s2, matrixmultiplier_7_s3, matrixmultiplier_7_w0,
       matrixmultiplier_7_w1, matrixmultiplier_7_w2, matrixmultiplier_7_w3, matrixmultiplier_8_s0,
       matrixmultiplier_8_s1, matrixmultiplier_8_s2, matrixmultiplier_8_s3, matrixmultiplier_8_w0,
       matrixmultiplier_8_w1, matrixmultiplier_8_w2, matrixmultiplier_8_w3, ram_3_dout, ram_4_dout,
       ram_5_dout, ram_6_dout, rambankedged_1_p3, rambankedged_1_p4, rambankedged_2_p3, rambankedged_2_p4,
       registerbankedged_1_s0, registerbankedged_1_s1, registerbankedged_1_s2, registerbankedged_1_s3,
       registerbankedged_2_s0, registerbankedged_2_s1, registerbankedged_2_s2, registerbankedged_2_s3,
       registerbankedged_3_s0, registerbankedged_3_s1, registerbankedged_3_s2, registerbankedged_3_s3,
       registerbankedged_4_s0, registerbankedged_4_s1, registerbankedged_4_s2, registerbankedged_4_s3,
       registerbankedged_5_s0, registerbankedged_5_s1, registerbankedged_5_s2, registerbankedged_5_s3,
       registerbankedged_6_s0, registerbankedged_6_s1, registerbankedged_6_s2, registerbankedged_6_s3,
       registerbankedged_7_s0, registerbankedged_7_s1, registerbankedged_7_s2, registerbankedged_7_s3,
       registerbankedged_8_s0, registerbankedged_8_s1, registerbankedged_8_s2, registerbankedged_8_s3,
       registerbankedged_9_s0, registerbankedged_9_s1, registerbankedged_9_s2, registerbankedged_9_s3,
       registerbankedged_10_s0, registerbankedged_10_s1, registerbankedged_10_s2, registerbankedged_10_s3,
       registerbankedged_11_s0, registerbankedged_11_s1, registerbankedged_11_s2, registerbankedged_11_s3,
       registerbankedged_12_s0, registerbankedged_12_s1, registerbankedged_12_s2, registerbankedged_12_s3,
       registerbankedged_13_s0, registerbankedged_13_s1, registerbankedged_13_s2, registerbankedged_13_s3,
       registerbankedged_14_s0, registerbankedged_14_s1, registerbankedged_14_s2, registerbankedged_14_s3,
       registerbankedged_15_s0, registerbankedged_15_s1, registerbankedged_15_s2, registerbankedged_15_s3,
       registerbankedged_16_s0, registerbankedged_16_s1, registerbankedged_16_s2, registerbankedged_16_s3,
       rom_1_data, S0, S1, S2, S3;

  Clock clock_1 (.out(CLOCK_GLOBAL));
  Register #(.width(16)) register_1 (
    .D({{8{1'b0}}, undriven}), .en(1'b1), .Q(register_1_q), .clk(CLOCK_GLOBAL));  // open: clr
  Register #(.width(16)) register_2 (
    .D({{8{1'b0}}, undriven_2}), .en(1'b1), .Q(register_2_q), .clk(CLOCK_GLOBAL));  // open: clr
  // Probe on S0
  // Probe on S2
  Counter #(.max('hffff), .width(16)) counter_1 (
    .count(ENABLE_IRAM_COUNTER), .Q(counter_1_q), .up(1'b1), .clk(CLOCK_GLOBAL), .clr(RESET_IRAM_COUNTER));  // open: load, D, carry
  // Probe on {OP_GLOBAL, STEP_COUNT}
  // Probe on S1
  // Probe on S3
  // Probe on rambankedged_1_p3
  // Probe on rambankedged_2_p3
  // RAMBankEdged rambankedged_1: pin names not known; wires that end beside it: register_1_q, CLOCK_GLOBAL, rambankedged_1_p3, rambankedged_1_p4
  // RAMBankEdged rambankedged_2: pin names not known; wires that end beside it: register_2_q, CLOCK_GLOBAL, rambankedged_2_p3, rambankedged_2_p4
  SUBCIRC_ROMController subcirc_romcontroller_1 (
    .RESET(RESET_ROM_STEP), .CLK(CLOCK_GLOBAL), .A(STEP_COUNT));  // open: SHIFT
  RAM #(.addrWidth(16), .dataWidth(64)) ram_1 ();  // open: addr, we, oe, clk, din, dout
  RegisterBankEdged registerbankedged_1 (
    .CLEAR(INPUT_REG_CLEAR), .CLK(CLOCK_GLOBAL), .EN0(EN_11_12_A), .EN1(EN_11_12_A), .EN3(EN_21_22_A),
    .EN2(EN_21_22_A), .D(rambankedged_1_p3), .S3(registerbankedged_1_s3), .S2(registerbankedged_1_s2),
    .S1(registerbankedged_1_s1), .S0(registerbankedged_1_s0));
  RegisterBankEdged registerbankedged_2 (
    .CLEAR(INPUT_REG_CLEAR), .CLK(CLOCK_GLOBAL), .EN0(EN_13_14_A), .EN1(EN_13_14_A), .EN3(EN_23_24_A),
    .EN2(EN_23_24_A), .D(rambankedged_1_p3), .S3(registerbankedged_2_s3), .S2(registerbankedged_2_s2),
    .S1(registerbankedged_2_s1), .S0(registerbankedged_2_s0));
  RegisterBankEdged registerbankedged_3 (
    .CLEAR(INPUT_REG_CLEAR), .CLK(CLOCK_GLOBAL), .EN0(EN_15_16_A), .EN1(EN_15_16_A), .EN3(EN_25_26_A),
    .EN2(EN_25_26_A), .D(rambankedged_1_p3), .S3(registerbankedged_3_s3), .S2(registerbankedged_3_s2),
    .S1(registerbankedged_3_s1), .S0(registerbankedged_3_s0));
  RegisterBankEdged registerbankedged_4 (
    .CLEAR(INPUT_REG_CLEAR), .CLK(CLOCK_GLOBAL), .EN0(EN_17_18_A), .EN1(EN_17_18_A), .EN3(EN_27_28_A),
    .EN2(EN_27_28_A), .D(rambankedged_1_p3), .S3(registerbankedged_4_s3), .S2(registerbankedged_4_s2),
    .S1(registerbankedged_4_s1), .S0(registerbankedged_4_s0));
  RegisterBankEdged registerbankedged_5 (
    .CLEAR(INPUT_REG_CLEAR), .CLK(CLOCK_GLOBAL), .EN0(EN_11_12_A), .EN1(EN_11_12_A), .EN3(EN_21_22_A),
    .EN2(EN_21_22_A), .D(rambankedged_1_p4), .S3(registerbankedged_5_s3), .S2(registerbankedged_5_s2),
    .S1(registerbankedged_5_s1), .S0(registerbankedged_5_s0));
  RegisterBankEdged registerbankedged_6 (
    .CLEAR(INPUT_REG_CLEAR), .CLK(CLOCK_GLOBAL), .EN0(EN_13_14_A), .EN1(EN_13_14_A), .EN3(EN_23_24_A),
    .EN2(EN_23_24_A), .D(rambankedged_1_p4), .S3(registerbankedged_6_s3), .S2(registerbankedged_6_s2),
    .S1(registerbankedged_6_s1), .S0(registerbankedged_6_s0));
  RegisterBankEdged registerbankedged_7 (
    .CLEAR(INPUT_REG_CLEAR), .CLK(CLOCK_GLOBAL), .EN0(EN_15_16_A), .EN1(EN_15_16_A), .EN3(EN_25_26_A),
    .EN2(EN_25_26_A), .D(rambankedged_1_p4), .S3(registerbankedged_7_s3), .S2(registerbankedged_7_s2),
    .S1(registerbankedged_7_s1), .S0(registerbankedged_7_s0));
  RegisterBankEdged registerbankedged_8 (
    .CLEAR(INPUT_REG_CLEAR), .CLK(CLOCK_GLOBAL), .EN0(EN_17_18_A), .EN1(EN_17_18_A), .EN3(EN_27_28_A),
    .EN2(EN_27_28_A), .D(rambankedged_1_p4), .S3(registerbankedged_8_s3), .S2(registerbankedged_8_s2),
    .S1(registerbankedged_8_s1), .S0(registerbankedged_8_s0));
  Counter #(.max('hffff), .width(16)) counter_2 (
    .count(ENABLE_ROW_COUNTER), .Q(counter_1_q), .up(1'b1), .clk(CLOCK_GLOBAL), .clr(RESET_ROW_COUNTER));  // open: load, D, carry
  // Probe on registerbankedged_1_s3
  // Probe on registerbankedged_1_s2
  // Probe on registerbankedged_1_s1
  // Probe on registerbankedged_1_s0
  RegisterBankEdged registerbankedged_9 (
    .CLEAR(INPUT_REG_CLEAR), .CLK(CLOCK_GLOBAL), .EN0(EN_11_12_B), .EN1(EN_11_12_B), .EN3(EN_21_22_B),
    .EN2(EN_21_22_B), .D(rambankedged_2_p3), .S3(registerbankedged_9_s3), .S2(registerbankedged_9_s2),
    .S1(registerbankedged_9_s1), .S0(registerbankedged_9_s0));
  RegisterBankEdged registerbankedged_10 (
    .CLEAR(INPUT_REG_CLEAR), .CLK(CLOCK_GLOBAL), .EN0(EN_31_32_B), .EN1(EN_31_32_B), .EN3(EN_41_42_B),
    .EN2(EN_41_42_B), .D(rambankedged_2_p3), .S3(registerbankedged_10_s3), .S2(registerbankedged_10_s2),
    .S1(registerbankedged_10_s1), .S0(registerbankedged_10_s0));
  RegisterBankEdged registerbankedged_11 (
    .CLEAR(INPUT_REG_CLEAR), .CLK(CLOCK_GLOBAL), .EN0(EN_51_52_B), .EN1(EN_51_52_B), .EN3(EN_61_62_B),
    .EN2(EN_61_62_B), .D(rambankedged_2_p3), .S3(registerbankedged_11_s3), .S2(registerbankedged_11_s2),
    .S1(registerbankedged_11_s1), .S0(registerbankedged_11_s0));
  RegisterBankEdged registerbankedged_12 (
    .CLEAR(INPUT_REG_CLEAR), .CLK(CLOCK_GLOBAL), .EN0(EN_71_72_B), .EN1(EN_71_72_B), .EN3(EN_81_82_B),
    .EN2(EN_81_82_B), .D(rambankedged_2_p3), .S3(registerbankedged_12_s3), .S2(registerbankedged_12_s2),
    .S1(registerbankedged_12_s1), .S0(registerbankedged_12_s0));
  RegisterBankEdged registerbankedged_13 (
    .CLEAR(INPUT_REG_CLEAR), .CLK(CLOCK_GLOBAL), .EN0(EN_11_12_B), .EN1(EN_11_12_B), .EN3(EN_21_22_B),
    .EN2(EN_21_22_B), .D(rambankedged_2_p4), .S3(registerbankedged_13_s3), .S2(registerbankedged_13_s2),
    .S1(registerbankedged_13_s1), .S0(registerbankedged_13_s0));
  RegisterBankEdged registerbankedged_14 (
    .CLEAR(INPUT_REG_CLEAR), .CLK(CLOCK_GLOBAL), .EN0(EN_31_32_B), .EN1(EN_31_32_B), .EN3(EN_41_42_B),
    .EN2(EN_41_42_B), .D(rambankedged_2_p4), .S3(registerbankedged_14_s3), .S2(registerbankedged_14_s2),
    .S1(registerbankedged_14_s1), .S0(registerbankedged_14_s0));
  RegisterBankEdged registerbankedged_15 (
    .CLEAR(INPUT_REG_CLEAR), .CLK(CLOCK_GLOBAL), .EN0(EN_51_52_B), .EN1(EN_51_52_B), .EN3(EN_61_62_B),
    .EN2(EN_61_62_B), .D(rambankedged_2_p4), .S3(registerbankedged_15_s3), .S2(registerbankedged_15_s2),
    .S1(registerbankedged_15_s1), .S0(registerbankedged_15_s0));
  RegisterBankEdged registerbankedged_16 (
    .CLEAR(INPUT_REG_CLEAR), .CLK(CLOCK_GLOBAL), .EN0(EN_71_72_B), .EN1(EN_71_72_B), .EN3(EN_81_82_B),
    .EN2(EN_81_82_B), .D(rambankedged_2_p4), .S3(registerbankedged_16_s3), .S2(registerbankedged_16_s2),
    .S1(registerbankedged_16_s1), .S0(registerbankedged_16_s0));
  ROM #(.addrWidth(12), .dataWidth(64)) rom_1 (.addr({OP_GLOBAL, STEP_COUNT}), .data(rom_1_data));
  RAM #(.addrWidth(16), .dataWidth(24), .\type ("nonvolatile")) ram_2 (
    .addr(counter_1_q), .oe(1'b1), .clk(CLOCK_GLOBAL), .dout(ram_2_dout));  // open: we, din
  MatrixMultiplier matrixmultiplier_1 (
    .A3(registerbankedged_1_s3), .A2(registerbankedged_1_s2), .A1(registerbankedged_1_s1),
    .A0(registerbankedged_1_s0), .P(MM_PASSTHROUGH), .B3(registerbankedged_9_s3),
    .B2(registerbankedged_9_s2), .B1(registerbankedged_9_s1), .B0(registerbankedged_9_s0),
    .S0(matrixmultiplier_1_s0), .S1(matrixmultiplier_1_s1), .S2(matrixmultiplier_1_s2),
    .S3(matrixmultiplier_1_s3), .W0(matrixmultiplier_1_w0), .W1(matrixmultiplier_1_w1),
    .W2(matrixmultiplier_1_w2), .W3(matrixmultiplier_1_w3));
  MatrixMultiplier matrixmultiplier_2 (
    .A3(registerbankedged_2_s3), .A2(registerbankedged_2_s2), .A1(registerbankedged_2_s1),
    .A0(registerbankedged_2_s0), .P(MM_PASSTHROUGH), .B3(registerbankedged_10_s3),
    .B2(registerbankedged_10_s2), .B1(registerbankedged_10_s1), .B0(registerbankedged_10_s0),
    .S0(matrixmultiplier_2_s0), .S1(matrixmultiplier_2_s1), .S2(matrixmultiplier_2_s2),
    .S3(matrixmultiplier_2_s3), .W0(matrixmultiplier_2_w0), .W1(matrixmultiplier_2_w1),
    .W2(matrixmultiplier_2_w2), .W3(matrixmultiplier_2_w3));
  MatrixMultiplier matrixmultiplier_3 (
    .A3(registerbankedged_3_s3), .A2(registerbankedged_3_s2), .A1(registerbankedged_3_s1),
    .A0(registerbankedged_3_s0), .P(MM_PASSTHROUGH), .B3(registerbankedged_11_s3),
    .B2(registerbankedged_11_s2), .B1(registerbankedged_11_s1), .B0(registerbankedged_11_s0),
    .S0(matrixmultiplier_3_s0), .S1(matrixmultiplier_3_s1), .S2(matrixmultiplier_3_s2),
    .S3(matrixmultiplier_3_s3), .W0(matrixmultiplier_3_w0), .W1(matrixmultiplier_3_w1),
    .W2(matrixmultiplier_3_w2), .W3(matrixmultiplier_3_w3));
  MatrixMultiplier matrixmultiplier_4 (
    .A3(registerbankedged_4_s3), .A2(registerbankedged_4_s2), .A1(registerbankedged_4_s1),
    .A0(registerbankedged_4_s0), .P(MM_PASSTHROUGH), .B3(registerbankedged_12_s3),
    .B2(registerbankedged_12_s2), .B1(registerbankedged_12_s1), .B0(registerbankedged_12_s0),
    .S0(matrixmultiplier_4_s0), .S1(matrixmultiplier_4_s1), .S2(matrixmultiplier_4_s2),
    .S3(matrixmultiplier_4_s3), .W0(matrixmultiplier_4_w0), .W1(matrixmultiplier_4_w1),
    .W2(matrixmultiplier_4_w2), .W3(matrixmultiplier_4_w3));
  MatrixMultiplier matrixmultiplier_5 (
    .A3(registerbankedged_5_s3), .A2(registerbankedged_5_s2), .A1(registerbankedged_5_s1),
    .A0(registerbankedged_5_s0), .P(MM_PASSTHROUGH), .B3(registerbankedged_13_s3),
    .B2(registerbankedged_13_s2), .B1(registerbankedged_13_s1), .B0(registerbankedged_13_s0),
    .S0(matrixmultiplier_5_s0), .S1(matrixmultiplier_5_s1), .S2(matrixmultiplier_5_s2),
    .S3(matrixmultiplier_5_s3), .W0(matrixmultiplier_5_w0), .W1(matrixmultiplier_5_w1),
    .W2(matrixmultiplier_5_w2), .W3(matrixmultiplier_5_w3));
  MatrixMultiplier matrixmultiplier_6 (
    .A3(registerbankedged_6_s3), .A2(registerbankedged_6_s2), .A1(registerbankedged_6_s1),
    .A0(registerbankedged_6_s0), .P(MM_PASSTHROUGH), .B3(registerbankedged_14_s3),
    .B2(registerbankedged_14_s2), .B1(registerbankedged_14_s1), .B0(registerbankedged_14_s0),
    .S0(matrixmultiplier_6_s0), .S1(matrixmultiplier_6_s1), .S2(matrixmultiplier_6_s2),
    .S3(matrixmultiplier_6_s3), .W0(matrixmultiplier_6_w0), .W1(matrixmultiplier_6_w1),
    .W2(matrixmultiplier_6_w2), .W3(matrixmultiplier_6_w3));
  MatrixMultiplier matrixmultiplier_7 (
    .A3(registerbankedged_7_s3), .A2(registerbankedged_7_s2), .A1(registerbankedged_7_s1),
    .A0(registerbankedged_7_s0), .P(MM_PASSTHROUGH), .B3(registerbankedged_15_s3),
    .B2(registerbankedged_15_s2), .B1(registerbankedged_15_s1), .B0(registerbankedged_15_s0),
    .S0(matrixmultiplier_7_s0), .S1(matrixmultiplier_7_s1), .S2(matrixmultiplier_7_s2),
    .S3(matrixmultiplier_7_s3), .W0(matrixmultiplier_7_w0), .W1(matrixmultiplier_7_w1),
    .W2(matrixmultiplier_7_w2), .W3(matrixmultiplier_7_w3));
  MatrixMultiplier matrixmultiplier_8 (
    .A3(registerbankedged_8_s3), .A2(registerbankedged_8_s2), .A1(registerbankedged_8_s1),
    .A0(registerbankedged_8_s0), .P(MM_PASSTHROUGH), .B3(registerbankedged_16_s3),
    .B2(registerbankedged_16_s2), .B1(registerbankedged_16_s1), .B0(registerbankedged_16_s0),
    .S0(matrixmultiplier_8_s0), .S1(matrixmultiplier_8_s1), .S2(matrixmultiplier_8_s2),
    .S3(matrixmultiplier_8_s3), .W0(matrixmultiplier_8_w0), .W1(matrixmultiplier_8_w1),
    .W2(matrixmultiplier_8_w2), .W3(matrixmultiplier_8_w3));
  // Probe on rom_1_data
  MatrixAdder matrixadder_1 (
    .B0(matrixmultiplier_1_s0), .B1(matrixmultiplier_1_s1), .B2(matrixmultiplier_1_s2),
    .B3(matrixmultiplier_1_s3), .A0(matrixmultiplier_1_w0), .A1(matrixmultiplier_1_w1),
    .A2(matrixmultiplier_1_w2), .A3(matrixmultiplier_1_w3), .S0(matrixadder_1_s0), .S1(matrixadder_1_s1),
    .S2(matrixadder_1_s2), .S3(matrixadder_1_s3));
  MatrixAdder matrixadder_2 (
    .B0(matrixmultiplier_2_s0), .B1(matrixmultiplier_2_s1), .B2(matrixmultiplier_2_s2),
    .B3(matrixmultiplier_2_s3), .A0(matrixmultiplier_2_w0), .A1(matrixmultiplier_2_w1),
    .A2(matrixmultiplier_2_w2), .A3(matrixmultiplier_2_w3), .S0(matrixadder_2_s0), .S1(matrixadder_2_s1),
    .S2(matrixadder_2_s2), .S3(matrixadder_2_s3));
  MatrixAdder matrixadder_3 (
    .B0(matrixmultiplier_3_s0), .B1(matrixmultiplier_3_s1), .B2(matrixmultiplier_3_s2),
    .B3(matrixmultiplier_3_s3), .A0(matrixmultiplier_3_w0), .A1(matrixmultiplier_3_w1),
    .A2(matrixmultiplier_3_w2), .A3(matrixmultiplier_3_w3), .S0(matrixadder_3_s0), .S1(matrixadder_3_s1),
    .S2(matrixadder_3_s2), .S3(matrixadder_3_s3));
  MatrixAdder matrixadder_4 (
    .B0(matrixmultiplier_4_s0), .B1(matrixmultiplier_4_s1), .B2(matrixmultiplier_4_s2),
    .B3(matrixmultiplier_4_s3), .A0(matrixmultiplier_4_w0), .A1(matrixmultiplier_4_w1),
    .A2(matrixmultiplier_4_w2), .A3(matrixmultiplier_4_w3), .S0(matrixadder_4_s0), .S1(matrixadder_4_s1),
    .S2(matrixadder_4_s2), .S3(matrixadder_4_s3));
  MatrixAdder matrixadder_5 (
    .B0(matrixmultiplier_5_s0), .B1(matrixmultiplier_5_s1), .B2(matrixmultiplier_5_s2),
    .B3(matrixmultiplier_5_s3), .A0(matrixmultiplier_5_w0), .A1(matrixmultiplier_5_w1),
    .A2(matrixmultiplier_5_w2), .A3(matrixmultiplier_5_w3), .S0(matrixadder_5_s0), .S1(matrixadder_5_s1),
    .S2(matrixadder_5_s2), .S3(matrixadder_5_s3));
  MatrixAdder matrixadder_6 (
    .B0(matrixmultiplier_6_s0), .B1(matrixmultiplier_6_s1), .B2(matrixmultiplier_6_s2),
    .B3(matrixmultiplier_6_s3), .A0(matrixmultiplier_6_w0), .A1(matrixmultiplier_6_w1),
    .A2(matrixmultiplier_6_w2), .A3(matrixmultiplier_6_w3), .S0(matrixadder_6_s0), .S1(matrixadder_6_s1),
    .S2(matrixadder_6_s2), .S3(matrixadder_6_s3));
  MatrixAdder matrixadder_7 (
    .B0(matrixmultiplier_7_s0), .B1(matrixmultiplier_7_s1), .B2(matrixmultiplier_7_s2),
    .B3(matrixmultiplier_7_s3), .A0(matrixmultiplier_7_w0), .A1(matrixmultiplier_7_w1),
    .A2(matrixmultiplier_7_w2), .A3(matrixmultiplier_7_w3), .S0(matrixadder_7_s0), .S1(matrixadder_7_s1),
    .S2(matrixadder_7_s2), .S3(matrixadder_7_s3));
  MatrixAdder matrixadder_8 (
    .B0(matrixmultiplier_8_s0), .B1(matrixmultiplier_8_s1), .B2(matrixmultiplier_8_s2),
    .B3(matrixmultiplier_8_s3), .A0(matrixmultiplier_8_w0), .A1(matrixmultiplier_8_w1),
    .A2(matrixmultiplier_8_w2), .A3(matrixmultiplier_8_w3), .S0(matrixadder_8_s0), .S1(matrixadder_8_s1),
    .S2(matrixadder_8_s2), .S3(matrixadder_8_s3));
  MatrixAdder matrixadder_9 (
    .B0(matrixadder_1_s0), .B1(matrixadder_1_s1), .B2(matrixadder_1_s2), .B3(matrixadder_1_s3),
    .A0(matrixadder_2_s0), .A1(matrixadder_2_s1), .A2(matrixadder_2_s2), .A3(matrixadder_2_s3),
    .S0(matrixadder_9_s0), .S1(matrixadder_9_s1), .S2(matrixadder_9_s2), .S3(matrixadder_9_s3));
  MatrixAdder matrixadder_10 (
    .B0(matrixadder_3_s0), .B1(matrixadder_3_s1), .B2(matrixadder_3_s2), .B3(matrixadder_3_s3),
    .A0(matrixadder_4_s0), .A1(matrixadder_4_s1), .A2(matrixadder_4_s2), .A3(matrixadder_4_s3),
    .S0(matrixadder_10_s0), .S1(matrixadder_10_s1), .S2(matrixadder_10_s2), .S3(matrixadder_10_s3));
  MatrixAdder matrixadder_11 (
    .B0(matrixadder_5_s0), .B1(matrixadder_5_s1), .B2(matrixadder_5_s2), .B3(matrixadder_5_s3),
    .A0(matrixadder_6_s0), .A1(matrixadder_6_s1), .A2(matrixadder_6_s2), .A3(matrixadder_6_s3),
    .S0(matrixadder_11_s0), .S1(matrixadder_11_s1), .S2(matrixadder_11_s2), .S3(matrixadder_11_s3));
  MatrixAdder matrixadder_12 (
    .B0(matrixadder_7_s0), .B1(matrixadder_7_s1), .B2(matrixadder_7_s2), .B3(matrixadder_7_s3),
    .A0(matrixadder_8_s0), .A1(matrixadder_8_s1), .A2(matrixadder_8_s2), .A3(matrixadder_8_s3),
    .S0(matrixadder_12_s0), .S1(matrixadder_12_s1), .S2(matrixadder_12_s2), .S3(matrixadder_12_s3));
  // Probe on {controlunit_1_control_a, EN_27_28_A, EN_17_18_A, EN_25_26_A, EN_15_16_A, EN_23_24_A, EN_13_14_A, EN_21_22_A, EN_11_12_A}
  ControlUnit controlunit_1 (
    .ROM_INPUT(rom_1_data), .OP(OP_GLOBAL), .FLAG(subcirc_instructionsplitter_1_flag),
    .AddressA(subcirc_instructionsplitter_1_addressa), .AddressB(subcirc_instructionsplitter_1_addressb),
    .STEP_COUNT(STEP_COUNT),
    .Control_A({controlunit_1_control_a, EN_27_28_A, EN_17_18_A, EN_25_26_A, EN_15_16_A, EN_23_24_A, EN_13_14_A, EN_21_22_A, EN_11_12_A}),
    .Control_B({controlunit_1_control_b, EN_81_82_B, EN_71_72_B, EN_61_62_B, EN_51_52_B, EN_41_42_B, EN_31_32_B, EN_21_22_B, EN_11_12_B}));  // open: CLK, PINS
  SUBCIRC_InstructionSplitter subcirc_instructionsplitter_1 (
    .I(ram_2_dout), .AddressB(subcirc_instructionsplitter_1_addressb),
    .AddressA(subcirc_instructionsplitter_1_addressa), .OP(OP_GLOBAL),
    .Flag(subcirc_instructionsplitter_1_flag));
  Accumulator accumulator_1 (
    .Clear(ACCUMULATOR_CLEAR), .Enable(1'b1), .CLK(CLOCK_GLOBAL), .A0(matrixadder_9_s0),
    .A1(matrixadder_9_s1), .A2(matrixadder_9_s2), .A3(matrixadder_9_s3), .S0(accumulator_1_s0),
    .S1(accumulator_1_s1), .S2(accumulator_1_s2), .S3(accumulator_1_s3));
  Accumulator accumulator_2 (
    .Clear(ACCUMULATOR_CLEAR), .Enable(1'b1), .CLK(CLOCK_GLOBAL), .A0(matrixadder_10_s0),
    .A1(matrixadder_10_s1), .A2(matrixadder_10_s2), .A3(matrixadder_10_s3), .S0(accumulator_2_s0),
    .S1(accumulator_2_s1), .S2(accumulator_2_s2), .S3(accumulator_2_s3));
  Accumulator accumulator_3 (
    .Clear(ACCUMULATOR_CLEAR), .Enable(1'b1), .CLK(CLOCK_GLOBAL), .A0(matrixadder_11_s0),
    .A1(matrixadder_11_s1), .A2(matrixadder_11_s2), .A3(matrixadder_11_s3), .S0(accumulator_3_s0),
    .S1(accumulator_3_s1), .S2(accumulator_3_s2), .S3(accumulator_3_s3));
  Accumulator accumulator_4 (
    .Clear(ACCUMULATOR_CLEAR), .Enable(1'b1), .CLK(CLOCK_GLOBAL), .A0(matrixadder_12_s0),
    .A1(matrixadder_12_s1), .A2(matrixadder_12_s2), .A3(matrixadder_12_s3), .S0(accumulator_4_s0),
    .S1(accumulator_4_s1), .S2(accumulator_4_s2), .S3(accumulator_4_s3));
  assign controlled_buffer_1_out = UO_INUPUT_0 ? accumulator_1_s0 : 64'bz;  // Controlled_Buffer controlled_buffer_1
  assign controlled_buffer_2_out = UO_INUPUT_0 ? accumulator_1_s1 : 64'bz;  // Controlled_Buffer controlled_buffer_2
  assign controlled_buffer_3_out = UO_INUPUT_0 ? accumulator_1_s2 : 64'bz;  // Controlled_Buffer controlled_buffer_3
  assign controlled_buffer_4_out = UO_INUPUT_0 ? accumulator_1_s3 : 64'bz;  // Controlled_Buffer controlled_buffer_4
  assign controlled_buffer_1_out = UO_INUPUT_1 ? accumulator_2_s0 : 64'bz;  // Controlled_Buffer controlled_buffer_5
  assign controlled_buffer_2_out = UO_INUPUT_1 ? accumulator_2_s1 : 64'bz;  // Controlled_Buffer controlled_buffer_6
  assign controlled_buffer_3_out = UO_INUPUT_1 ? accumulator_2_s2 : 64'bz;  // Controlled_Buffer controlled_buffer_7
  assign controlled_buffer_4_out = UO_INUPUT_1 ? accumulator_2_s3 : 64'bz;  // Controlled_Buffer controlled_buffer_8
  assign controlled_buffer_1_out = UO_INUPUT_2 ? accumulator_3_s0 : 64'bz;  // Controlled_Buffer controlled_buffer_9
  assign controlled_buffer_2_out = UO_INUPUT_2 ? accumulator_3_s1 : 64'bz;  // Controlled_Buffer controlled_buffer_10
  assign controlled_buffer_3_out = UO_INUPUT_2 ? accumulator_3_s2 : 64'bz;  // Controlled_Buffer controlled_buffer_11
  assign controlled_buffer_4_out = UO_INUPUT_2 ? accumulator_3_s3 : 64'bz;  // Controlled_Buffer controlled_buffer_12
  assign controlled_buffer_1_out = UO_INUPUT_3 ? accumulator_4_s0 : 64'bz;  // Controlled_Buffer controlled_buffer_13
  assign controlled_buffer_2_out = UO_INUPUT_3 ? accumulator_4_s1 : 64'bz;  // Controlled_Buffer controlled_buffer_14
  assign controlled_buffer_3_out = UO_INUPUT_3 ? accumulator_4_s2 : 64'bz;  // Controlled_Buffer controlled_buffer_15
  assign controlled_buffer_4_out = UO_INUPUT_3 ? accumulator_4_s3 : 64'bz;  // Controlled_Buffer controlled_buffer_16
  Register #(.width(4)) OuterDimA (
    .D(subcirc_instructionsplitter_1_addressa[3:0]), .en(I_DIM), .clk(CLOCK_GLOBAL));  // open: Q, clr
  Register #(.width(4)) DIM (.D(subcirc_instructionsplitter_1_flag), .en(I_DIM), .clk(CLOCK_GLOBAL));  // open: Q, clr
  Register #(.width(4)) OuterDimB (
    .D(subcirc_instructionsplitter_1_addressb[3:0]), .en(I_DIM), .clk(CLOCK_GLOBAL));  // open: Q, clr
  RAM #(.addrWidth(16), .dataWidth(64)) ram_3 (
    .addr(undriven_3), .we(OR_WE), .clk(CLOCK_GLOBAL), .din(controlled_buffer_1_out), .dout(ram_3_dout));  // open: oe
  RAM #(.addrWidth(16), .dataWidth(64)) ram_4 (
    .addr(undriven_3), .we(OR_WE), .clk(CLOCK_GLOBAL), .din(controlled_buffer_2_out), .dout(ram_4_dout));  // open: oe
  RAM #(.addrWidth(16), .dataWidth(64)) ram_5 (
    .addr(undriven_3), .we(OR_WE), .clk(CLOCK_GLOBAL), .din(controlled_buffer_3_out), .dout(ram_5_dout));  // open: oe
  RAM #(.addrWidth(16), .dataWidth(64)) ram_6 (
    .addr(undriven_3), .we(OR_WE), .clk(CLOCK_GLOBAL), .din(controlled_buffer_4_out), .dout(ram_6_dout));  // open: oe
  not not_1 (not_1_out, OP_GLOBAL[0]);
  not not_2 (not_2_out, OP_GLOBAL[2]);
  not not_3 (not_3_out, OP_GLOBAL[3]);
  not not_4 (not_4_out, OP_GLOBAL[2]);
  not not_5 (not_5_out, OP_GLOBAL[3]);
  not not_6 (not_6_out, OP_GLOBAL[0]);
  not not_7 (not_7_out, OP_GLOBAL[1]);
  not not_8 (not_8_out, OP_GLOBAL[3]);
  and and_1 (I_BlockLoad, not_1_out, OP_GLOBAL[1], not_2_out, not_3_out);
  and and_2 (I_Execute, OP_GLOBAL[0], OP_GLOBAL[1], not_4_out, not_5_out);
  and and_3 (I_BlockStore, not_6_out, not_7_out, OP_GLOBAL[2], not_8_out);
  not not_9 (not_9_out, OP_GLOBAL[1]);
  not not_10 (not_10_out, OP_GLOBAL[3]);
  not not_11 (not_11_out, OP_GLOBAL[0]);
  not not_12 (not_12_out, OP_GLOBAL[3]);
  not not_13 (not_13_out, OP_GLOBAL[0]);
  and and_4 (I_BlockMove, OP_GLOBAL[0], not_9_out, OP_GLOBAL[2], not_10_out);
  and and_5 (I_MatrixAdd, not_11_out, OP_GLOBAL[1], OP_GLOBAL[2], not_12_out);
  and and_6 (I_Loop, not_13_out, OP_GLOBAL[1], OP_GLOBAL[2], OP_GLOBAL[3]);
  not not_14 (not_14_out, OP_GLOBAL[0]);
  not not_15 (not_15_out, OP_GLOBAL[1]);
  not not_16 (not_16_out, OP_GLOBAL[2]);
  not not_17 (not_17_out, OP_GLOBAL[1]);
  not not_18 (not_18_out, OP_GLOBAL[2]);
  not not_19 (not_19_out, OP_GLOBAL[3]);
  and and_7 (I_Halt, not_14_out, not_15_out, not_16_out, OP_GLOBAL[3]);
  and and_8 (I_DIM, OP_GLOBAL[0], not_17_out, not_18_out, not_19_out);

  // Notes on the sheet:
  //   Preview
  //   Clock Counter
  //   Internal System uses 16 Bit Addresses, 
  //   ROM Address
  //   Make first 8 MSB (0000 0000) + Address to get desired results
  //   8 - Bit step counter (OP+STEP_COUNT = 12 Bits) (count up to 2^12 Cycles)
  //   RAM Bank A
  //   RAM Bank B
  //   Input Bus
  //   ROM Step Counter
  //   Final Output RAM
  //   A11 A12 A21 A22
  //   A11 A12 A21 A22
  //   Register Bank A
  //   Triggered 1/2 Clock Cycle
  //   Control Unit
  //   |
  //   |
  //   |
  //   |
  //   |
  //   |
  //   |
  //   |
  //   |
  //   |
  //   |
  //   |
  //   |
  //   |
  //   Register Bank B
  //   B11 B12 B21 B22
  //   OP + Step Counter = 12 Bit
  //   contents of rom_1 (hex, n*v repeats v):
  //   1 1 4 4 10 10 40 40 2 2 8 8 20 20 80 80
  //   Instruction RAM / C
  //   (i) Should not be controlled since ENABLE_IRAM_COUNTER can be set to 0 which will hold IRAM instruction
  //   Calculate 16x16 Multiplication
  //   1x 16x2 Row and 1x 16x2 Colmun (8 2x2) => 1 2x2
  //   Micro Code ROM
  //   AW+BY+CX+DZ
  //   AW+BY+CX+DZ
  //   (i) Should have 8 Terms, but since 1 Term is a 2x2 we get 8/2 Terms
  //   DIM Instruction
  //   A11 A12 A21 A22
  //   Unified Output Bus
  //   Block Load Instruction
  //   Execute Instruction
  //   Block Store Instruction
  //   Unified Memory
  //   Block Move Instruction
  //   Matrix Add Instruction
  //   Loop Instruction
  //   Halt Instruction
  //   DIM Instruction
endmodule

module DEPRECATED_ControlUnit (
  input  [63:0] ROM_INPUT,
  input  [7:0] AddressA,
  input  [7:0] AddressB,
  input  [7:0] STEP_COUNT,
  input  [3:0] OP,
  input  [3:0] FLAG
);
endmodule

module SUBCIRC_InstructionSplitter (
  input  [23:0] I,
  output [7:0] AddressB,
  output [7:0] AddressA,
  output [3:0] OP,
  output [3:0] Flag
);


  assign AddressA = I[15:8];
  assign AddressB = I[7:0];
  assign Flag = I[23:20];
  assign OP = I[19:16];

  // Notes on the sheet:
  //   Testing Splitter
endmodule

module RAMBankEdged (
  input  CLK,
  input  WE,
  input  OE,
  input  [15:0] A0,
  input  [15:0] A1,
  input  [63:0] D0,
  input  [63:0] D1,
  output [63:0] R0,
  output [63:0] R1
);

  RAM #(.addrWidth(16), .asyncread("true"), .dataWidth(64), .trigger("falling"), .\type ("nonvolatile")) ram_1 (
    .addr(A0), .we(WE), .oe(OE), .clk(CLK), .din(D0), .dout(R0));
  RAM #(.addrWidth(16), .asyncread("true"), .dataWidth(64), .trigger("falling"), .\type ("nonvolatile")) ram_2 (
    .addr(A1), .we(WE), .oe(OE), .clk(CLK), .din(D1), .dout(R1));
endmodule

module RegisterBankEdged (
  input  CLEAR,
  input  CLK,
  input  EN0,
  input  EN1,
  input  EN3,
  input  EN2,
  input  [63:0] D,
  output [63:0] S3,
  output [63:0] S2,
  output [63:0] S1,
  output [63:0] S0
);

  Register #(.width(64)) register_1 (.D(D), .en(EN3), .Q(S3), .clk(CLK), .clr(CLEAR));
  Register #(.trigger("falling"), .width(64)) register_2 (.D(D), .en(EN2), .Q(S2), .clk(CLK), .clr(CLEAR));
  Register #(.width(64)) register_3 (.D(D), .en(EN1), .Q(S1), .clk(CLK), .clr(CLEAR));
  Register #(.trigger("falling"), .width(64)) register_4 (.D(D), .en(EN0), .Q(S0), .clk(CLK), .clr(CLEAR));
endmodule

module DEPECRATED_MatrixMultiplier (
  input  [63:0] B0,
  input  [63:0] A0,
  input  [63:0] B1,
  input  [63:0] A1,
  input  [63:0] B2,
  input  [63:0] A2,
  input  [63:0] B3,
  input  [63:0] A3,
  output [63:0] S0,
  output [63:0] S1,
  output [63:0] S2,
  output [63:0] S3,
  output [63:0] W0,
  output [63:0] W1,
  output [63:0] W2,
  output [63:0] W3
);

  Multiplier #(.width(64)) multiplier_1 (.a(A0), .b(B0), .out(S0));  // open: cin, cout
  Multiplier #(.width(64)) multiplier_2 (.a(A0), .b(B1), .out(S1));  // open: cin, cout
  Multiplier #(.width(64)) multiplier_3 (.a(A2), .b(B0), .out(S2));  // open: cin, cout
  Multiplier #(.width(64)) multiplier_4 (.a(A2), .b(B1), .out(S3));  // open: cin, cout
  Multiplier #(.width(64)) multiplier_5 (.a(A1), .b(B2), .out(W0));  // open: cin, cout
  Multiplier #(.width(64)) multiplier_6 (.a(A1), .b(B3), .out(W1));  // open: cin, cout
  Multiplier #(.width(64)) multiplier_7 (.a(A3), .b(B2), .out(W2));  // open: cin, cout
  Multiplier #(.width(64)) multiplier_8 (.a(A3), .b(B3), .out(W3));  // open: cin, cout

  // Notes on the sheet:
  //   Acts as a Partial Multiplication Node
  //   Supports Partial Matrix Multiplication where A*B = S1, S2 where S = S1+S2
  //   A0B0
  //   A0B1
  //   A2B0
  //   A2B1
  //   A1B2
  //   A1B3
  //   A3B2
  //   A3B3
endmodule

module ControlUnit (
  input  [63:0] ROM_INPUT,
  input  [3:0] OP,
  input  [3:0] FLAG,
  input  [7:0] AddressA,
  input  [7:0] AddressB,
  input  [7:0] STEP_COUNT,
  input  CLK,
  output [15:0] Control_A,
  output [15:0] Control_B,
  output [31:0] PINS
);

  // Probe on ROM_INPUT

  assign Control_A = ROM_INPUT[15:0];
  assign Control_B = ROM_INPUT[31:16];
  assign PINS = ROM_INPUT[63:32];

  // Other names for the same wires on the sheet: clock_local = CLK

  // Notes on the sheet:
  //   0000 0000 _ 0000 0000 _ 0000 0000 _ 0000 0000 _ 1010 0000 _ 0000 0000 _ 0000 0000 _ 0000 0000
endmodule

module SCRATCHPAD (
  input  in_1,
  input  in_2
);

  wire clock_1_out, clock_2_out, clock_3_out, clock_4_out, clock_5_out, comparator_1_eq, comparator_2_eq,
       comparator_3_gt, comparator_3_lt, comparator_4_gt, comparator_5_gt, comparator_5_lt, comparator_6_eq,
       comparator_7_eq, comparator_7_gt, comparator_8_eq, comparator_9_eq, comparator_10_eq, decoder_1_out0,
       decoder_1_out1, decoder_1_out2, decoder_1_out3, decoder_1_out4, decoder_1_out5, decoder_1_out6,
       decoder_1_out7, not_1_out, not_2_out, subcirc_halfcyclecounter_1_p1, subcirc_halfcyclecounter_1_p2,
       subcirc_halfcyclecounter_2_p1, subcirc_halfcyclecounter_2_p2, undriven, undriven_2;
  wire [0:0] counter_7_carry, counter_8_carry;
  wire [2:0] counter_1_q, register_3_q, register_4_q, register_5_q, register_8_q;
  wire [7:0] adder_1_out, adder_7_out, adder_9_out, counter_6_q, multiplier_1_out, multiplier_3_out,
       multiplier_7_out, register_20_q;
  wire [15:0] adder_2_out, adder_8_out, adder_10_out, adder_11_out, adder_12_out, adder_13_out, adder_14_out,
       adder_15_out, counter_2_q, counter_3_q, counter_4_q, counter_5_q, multiplier_2_out, multiplier_4_out,
       multiplier_5_out, multiplier_6_out, multiplier_8_out, multiplier_9_out, multiplier_10_out,
       multiplier_11_out, RAM_A_ADDRESS, RAM_B_ADDRESS, register_21_q, register_22_q, register_23_q,
       register_24_q, subcirc_halfcyclecounter_1_p3, subcirc_halfcyclecounter_2_p3;
  wire [23:0] ram_3_dout;
  wire [63:0] matrixadder_1_s0, matrixadder_1_s1, matrixadder_1_s2, matrixadder_1_s3, matrixadder_2_s0,
       matrixadder_2_s1, matrixadder_2_s2, matrixadder_2_s3, matrixmultiplier_1_s0, matrixmultiplier_1_s1,
       matrixmultiplier_1_s2, matrixmultiplier_1_s3, matrixmultiplier_1_w0, matrixmultiplier_1_w1,
       matrixmultiplier_1_w2, matrixmultiplier_2_s0, matrixmultiplier_2_s1, matrixmultiplier_2_s2,
       matrixmultiplier_2_s3, matrixmultiplier_2_w0, matrixmultiplier_2_w1, matrixmultiplier_2_w2,
       matrixmultiplier_2_w3, ram_1_dout, register_1_q, register_2_q, register_6_q, register_7_q,
       register_9_q, register_10_q, register_11_q, register_12_q, register_13_q, register_14_q,
       register_15_q, register_16_q, register_17_q, register_18_q, register_19_q;

  Counter #(.max('h7), .width(3)) counter_1 (
    .count(1'b1), .Q(counter_1_q), .up(1'b1), .clk(clock_1_out));  // open: load, D, carry, clr
  RAM #(.addrWidth(3), .asyncread("true"), .dataWidth(64), .\type ("nonvolatile")) ram_1 (
    .addr(counter_1_q), .oe(1'b1), .clk(clock_1_out), .dout(ram_1_dout));  // open: we, din
  Decoder #(.select(3)) decoder_1 (
    .out0(decoder_1_out0), .out1(decoder_1_out1), .out2(decoder_1_out2), .out3(decoder_1_out3),
    .out4(decoder_1_out4), .out5(decoder_1_out5), .out6(decoder_1_out6), .out7(decoder_1_out7),
    .sel(counter_1_q), .en(1'b1));
  Clock clock_1 (.out(clock_1_out));
  Register #(.width(64)) register_1 (
    .D(ram_1_dout), .en(decoder_1_out0), .Q(register_1_q), .clk(clock_1_out));  // open: clr
  Register #(.width(64)) register_2 (
    .D(ram_1_dout), .en(decoder_1_out4), .Q(register_2_q), .clk(clock_1_out));  // open: clr
  Register #(.width(3)) register_3 (.D(counter_1_q), .en(1'b1), .Q(register_3_q), .clk(clock_1_out));  // open: clr
  Register #(.width(3)) register_4 (.D(register_3_q), .en(1'b1), .Q(register_4_q), .clk(clock_1_out));  // open: clr
  Register #(.width(3)) register_5 (.D(register_4_q), .en(1'b1), .Q(register_5_q), .clk(clock_1_out));  // open: clr
  Register #(.width(64)) register_6 (
    .D(ram_1_dout), .en(decoder_1_out1), .Q(register_6_q), .clk(clock_1_out));  // open: clr
  Register #(.width(64)) register_7 (
    .D(ram_1_dout), .en(decoder_1_out5), .Q(register_7_q), .clk(clock_1_out));  // open: clr
  Register #(.width(3)) register_8 (.D(register_5_q), .en(1'b1), .Q(register_8_q), .clk(clock_1_out));  // open: clr
  Register #(.width(64)) register_9 (
    .D(ram_1_dout), .en(decoder_1_out2), .Q(register_9_q), .clk(clock_1_out));  // open: clr
  Register #(.width(64)) register_10 (
    .D(ram_1_dout), .en(decoder_1_out6), .Q(register_10_q), .clk(clock_1_out));  // open: clr
  // Probe on counter_2_q
  not not_1 (not_1_out, comparator_3_lt);
  // Probe on counter_3_q
  not not_2 (not_2_out, comparator_5_lt);
  Register #(.width(64)) register_11 (
    .D(ram_1_dout), .en(decoder_1_out3), .Q(register_11_q), .clk(clock_1_out));  // open: clr
  Register #(.width(64)) register_12 (
    .D(ram_1_dout), .en(decoder_1_out7), .Q(register_12_q), .clk(clock_1_out));  // open: clr
  Counter #(.max('hffff), .width(16)) counter_2 (
    .count(not_1_out), .Q(counter_2_q), .up(1'b1), .clk(clock_3_out), .clr(comparator_4_gt));  // open: load, D, carry
  Counter #(.max('hffff), .width(16)) counter_3 (
    .count(not_2_out), .Q(counter_3_q), .up(1'b1), .clk(clock_4_out), .clr(comparator_6_eq));  // open: load, D, carry
  Comparator comparator_1 (.a(8'h4), .b(multiplier_1_out), .eq(comparator_1_eq));  // open: gt, lt
  Counter #(.max('hffff), .width(16)) counter_4 (
    .count(1'b1), .Q(counter_4_q), .up(1'b1), .clk(clock_3_out), .clr(comparator_3_gt));  // open: load, D, carry
  Counter #(.max('hffff), .width(16)) counter_5 (
    .count(1'b1), .Q(counter_5_q), .up(1'b1), .clk(clock_4_out), .clr(comparator_5_gt));  // open: load, D, carry
  Multiplier multiplier_1 (.a(register_20_q), .b(8'h2), .out(multiplier_1_out));  // open: cin, cout
  Multiplier #(.width(16)) multiplier_2 (.a(register_23_q), .b(16'h2), .out(multiplier_2_out));  // open: cin, cout
  Comparator #(.width(16)) comparator_2 (.a(16'h4), .b(multiplier_2_out), .eq(comparator_2_eq));  // open: gt, lt
  MatrixMultiplier matrixmultiplier_1 (
    .A3(register_11_q), .A2(register_9_q), .A1(register_6_q), .A0(register_1_q), .B3(register_12_q),
    .B2(register_10_q), .B1(register_7_q), .B0(register_2_q), .S0(matrixmultiplier_1_s0),
    .S1(matrixmultiplier_1_s1), .S2(matrixmultiplier_1_s2), .S3(matrixmultiplier_1_s3),
    .W0(matrixmultiplier_1_w0), .W1(matrixmultiplier_1_w1), .W2(matrixmultiplier_1_w2));  // open: P, W3
  MatrixMultiplier matrixmultiplier_2 (
    .A3(64'h8), .A2(64'h7), .A1(64'h6), .A0(64'h5), .P(in_2), .B3(64'h4), .B2(64'h3), .B1(64'h2), .B0(64'h1),
    .S0(matrixmultiplier_2_s0), .S1(matrixmultiplier_2_s1), .S2(matrixmultiplier_2_s2),
    .S3(matrixmultiplier_2_s3), .W0(matrixmultiplier_2_w0), .W1(matrixmultiplier_2_w1),
    .W2(matrixmultiplier_2_w2), .W3(matrixmultiplier_2_w3));
  MatrixAdder matrixadder_1 (
    .B0(matrixmultiplier_2_s0), .B1(matrixmultiplier_2_s1), .B2(matrixmultiplier_2_s2),
    .B3(matrixmultiplier_2_s3), .A0(matrixmultiplier_2_w0), .A1(matrixmultiplier_2_w1),
    .A2(matrixmultiplier_2_w2), .A3(matrixmultiplier_2_w3), .S0(matrixadder_1_s0), .S1(matrixadder_1_s1),
    .S2(matrixadder_1_s2), .S3(matrixadder_1_s3));
  // Probe on counter_4_q
  Comparator #(.width(16)) comparator_3 (
    .a(counter_4_q), .b(16'h5), .gt(comparator_3_gt), .lt(comparator_3_lt));  // open: eq
  Comparator #(.width(16)) comparator_4 (.a(counter_2_q), .b(16'h5), .gt(comparator_4_gt));  // open: eq, lt
  // Probe on 16'h5
  // Probe on counter_5_q
  Comparator #(.width(16)) comparator_5 (
    .a(counter_5_q), .b(16'h5), .gt(comparator_5_gt), .lt(comparator_5_lt));  // open: eq
  Comparator #(.width(16)) comparator_6 (.a(counter_3_q), .b(16'h4), .eq(comparator_6_eq));  // open: gt, lt
  // Probe on 16'h4
  MatrixAdder matrixadder_2 (
    .B0(matrixmultiplier_1_s0), .B1(matrixmultiplier_1_s1), .B2(matrixmultiplier_1_s2),
    .B3(matrixmultiplier_1_s3), .A0(matrixmultiplier_1_w0), .A1(matrixmultiplier_1_w1),
    .A2(matrixmultiplier_1_w2), .S0(matrixadder_2_s0), .S1(matrixadder_2_s1), .S2(matrixadder_2_s2),
    .S3(matrixadder_2_s3));  // open: A3
  // Probe on matrixadder_1_s0
  // Probe on matrixadder_1_s2
  // Probe on adder_1_out
  Adder adder_1 (.a(adder_7_out), .b(8'h6), .out(adder_1_out));  // open: cin, cout
  Adder #(.width(16)) adder_2 (.a(adder_8_out), .b(16'h6), .out(adder_2_out));  // open: cin, cout
  Register #(.width(64)) register_13 (
    .D(matrixadder_2_s0), .en(1'b1), .Q(register_13_q), .clk(clock_1_out));  // open: clr
  Register #(.width(64)) register_14 (
    .D(matrixadder_2_s1), .en(1'b1), .Q(register_14_q), .clk(clock_1_out));  // open: clr
  Register #(.width(64)) register_15 (
    .D(matrixadder_2_s2), .en(1'b1), .Q(register_15_q), .clk(clock_1_out));  // open: clr
  Register #(.width(64)) register_16 (
    .D(matrixadder_2_s3), .en(1'b1), .Q(register_16_q), .clk(clock_1_out));  // open: clr
  // Probe on adder_2_out
  Register #(.width(64)) register_17 (
    .D(register_13_q), .en(undriven), .Q(register_17_q), .clk(undriven_2));  // open: clr
  Register #(.width(64)) register_18 (
    .D(register_17_q), .en(undriven), .Q(register_18_q), .clk(undriven_2));  // open: clr
  // Probe on matrixadder_1_s1
  // Probe on matrixadder_1_s3
  Adder #(.width(16)) adder_3 (.a(counter_2_q), .b({16{1'b0}}), .out(RAM_A_ADDRESS));  // open: cin, cout
  Adder #(.width(16)) adder_4 (.a(counter_4_q), .b({16{1'b0}}), .out(RAM_B_ADDRESS));  // open: cin, cout
  Adder #(.width(16)) adder_5 (.a(counter_3_q), .b({16{1'b0}}));  // open: out, cin, cout
  Adder #(.width(16)) adder_6 (.a(counter_5_q), .b({16{1'b0}}));  // open: out, cin, cout
  // Probe on counter_6_q
  Counter counter_6 (
    .count(1'b1), .Q(counter_6_q), .clk(clock_5_out), .clr(comparator_7_gt));  // open: load, D, carry, up
  // SUBCIRC_HalfCycleCounter subcirc_halfcyclecounter_1: pin names not known; wires that end beside it: subcirc_halfcyclecounter_1_p1, subcirc_halfcyclecounter_1_p2, subcirc_halfcyclecounter_1_p3
  Register #(.width(64)) register_19 (
    .D(register_18_q), .en(undriven), .Q(register_19_q), .clk(undriven_2));  // open: clr
  Counter #(.max('h1), .width(16)) counter_7 (
    .count(1'b1), .carry(counter_7_carry[0]), .up(1'b1), .clk(clock_3_out));  // open: load, D, Q, clr
  Adder adder_7 (.a(multiplier_7_out), .b(counter_6_q), .out(adder_7_out));  // open: cin, cout
  Register register_20 (
    .D(adder_9_out), .en(comparator_7_eq), .Q(register_20_q), .clk(clock_5_out), .clr(comparator_1_eq));
  Comparator comparator_7 (.a(counter_6_q), .b(8'h5), .gt(comparator_7_gt), .eq(comparator_7_eq));  // open: lt
  Adder #(.width(16)) adder_8 (
    .a(multiplier_8_out), .b(subcirc_halfcyclecounter_1_p3), .out(adder_8_out));  // open: cin, cout
  // Probe on subcirc_halfcyclecounter_1_p3
  Comparator #(.width(16)) comparator_8 (
    .a(subcirc_halfcyclecounter_1_p3), .b(16'h5), .gt(subcirc_halfcyclecounter_1_p2), .eq(comparator_8_eq));  // open: lt
  Clock clock_2 (.out(clock_2_out));
  Register #(.width(16)) register_21 (.D(adder_10_out), .en(1'b1), .Q(register_21_q), .clk(clock_3_out));  // open: clr
  Register #(.width(16)) register_22 (.D(adder_11_out), .en(1'b1), .Q(register_22_q), .clk(clock_4_out));  // open: clr
  Counter #(.max('h1), .width(16)) counter_8 (
    .count(1'b1), .carry(counter_8_carry[0]), .up(1'b1), .clk(clock_4_out));  // open: load, D, Q, clr
  // Probe on adder_7_out
  Adder adder_9 (.a(register_20_q), .b(8'h1), .out(adder_9_out));  // open: cin, cout
  Multiplier multiplier_3 (.a(8'h2), .b(8'h6), .out(multiplier_3_out));  // open: cin, cout
  // Probe on adder_8_out
  Register #(.trigger("falling"), .width(16)) register_23 (
    .D(adder_12_out), .en(comparator_8_eq), .Q(register_23_q), .clk(subcirc_halfcyclecounter_1_p1),
    .clr(comparator_2_eq));
  Multiplier #(.width(16)) multiplier_4 (.a(16'h2), .b(register_21_q), .out(multiplier_4_out));  // open: cin, cout
  Adder #(.width(16)) adder_10 (
    .a(register_21_q), .b({{15{1'b0}}, counter_7_carry[0]}), .out(adder_10_out));  // open: cin, cout
  Clock clock_3 (.out(clock_3_out));
  Multiplier #(.width(16)) multiplier_5 (.a(16'h2), .b(register_22_q), .out(multiplier_5_out));  // open: cin, cout
  Adder #(.width(16)) adder_11 (
    .a(register_22_q), .b({{15{1'b0}}, counter_8_carry[0]}), .out(adder_11_out));  // open: cin, cout
  Clock clock_4 (.out(clock_4_out));
  Clock clock_5 (.out(clock_5_out));
  Adder #(.width(16)) adder_12 (.a(register_23_q), .b(16'h1), .out(adder_12_out));  // open: cin, cout
  Multiplier #(.width(16)) multiplier_6 (.a(16'h2), .b(16'h6), .out(multiplier_6_out));  // open: cin, cout
  RAM #(.addrWidth(3), .asyncread("true"), .dataWidth(64), .\type ("nonvolatile")) ram_2 (.addr(register_8_q));  // open: we, oe, clk, din, dout
  RAM #(.addrWidth(16), .dataWidth(24), .\type ("nonvolatile")) ram_3 (
    .addr({16{1'b0}}), .oe(in_1), .clk(clock_2_out), .dout(ram_3_dout));  // open: we, din
  Multiplier multiplier_7 (.a(register_20_q), .b(multiplier_3_out), .out(multiplier_7_out));  // open: cin, cout
  Multiplier #(.width(16)) multiplier_8 (
    .a(register_23_q), .b(multiplier_6_out), .out(multiplier_8_out));  // open: cin, cout
  Clock clock_6 (.out(subcirc_halfcyclecounter_1_p1));
  // Probe on multiplier_7_out
  // Probe on multiplier_8_out
  // Probe on ram_3_dout
  Comparator #(.width(16)) comparator_9 (.a(16'h2), .b(multiplier_9_out), .eq(comparator_9_eq));  // open: gt, lt
  Multiplier #(.width(16)) multiplier_9 (.a(register_24_q), .b(16'h2), .out(multiplier_9_out));  // open: cin, cout
  // Probe on adder_13_out
  Adder #(.width(16)) adder_13 (.a(adder_14_out), .b(16'h2), .out(adder_13_out));  // open: cin, cout
  // Probe on subcirc_halfcyclecounter_2_p3
  // SUBCIRC_HalfCycleCounter subcirc_halfcyclecounter_2: pin names not known; wires that end beside it: subcirc_halfcyclecounter_2_p1, subcirc_halfcyclecounter_2_p2, subcirc_halfcyclecounter_2_p3
  Adder #(.width(16)) adder_14 (
    .a(multiplier_11_out), .b(subcirc_halfcyclecounter_2_p3), .out(adder_14_out));  // open: cin, cout
  Register #(.trigger("falling"), .width(16)) register_24 (
    .D(adder_15_out), .en(comparator_10_eq), .Q(register_24_q), .clk(subcirc_halfcyclecounter_2_p1),
    .clr(comparator_9_eq));
  Comparator #(.width(16)) comparator_10 (
    .a(subcirc_halfcyclecounter_2_p3), .b(16'h1), .gt(subcirc_halfcyclecounter_2_p2), .eq(comparator_10_eq));  // open: lt
  // Probe on adder_14_out
  Adder #(.width(16)) adder_15 (.a(register_24_q), .b(16'h1), .out(adder_15_out));  // open: cin, cout
  Multiplier #(.width(16)) multiplier_10 (.a(16'h2), .b(16'h2), .out(multiplier_10_out));  // open: cin, cout
  Clock clock_7 (.out(subcirc_halfcyclecounter_2_p1));
  Multiplier #(.width(16)) multiplier_11 (
    .a(register_24_q), .b(multiplier_10_out), .out(multiplier_11_out));  // open: cin, cout
  // Probe on multiplier_11_out

  // Notes on the sheet:
  //   Currently only supports multiplying a single NxN (8x8)
  //   Currently only supports multiplying a single NxN (8x8)
  //   Currently only supports multiplying a single NxN (8x8)
  //   Currently only supports multiplying a single NxN (8x8)
  //   RAM A Addresses
  //   ROW Number
  //   RAM B Addresses
  //   SUB Iteration Number
  //   X+k
  //   X+k
  //   X
  //   X
  //   2K
  //   2K
  //   N
  //   K
  //   K-1
  //   N
  //   K
  //   K-1
  //   WORKING TESTED
  //   X+k
  //   X
  //   2K
  //   N
  //   K
  //   K-1
endmodule

module SUBCIRC_ROMController (
  input  [7:0] SHIFT,
  input  RESET,
  input  CLK,
  output [7:0] A
);

  wire [7:0] adder_1_out, counter_1_q, multiplexer_1_out, multiplier_1_out;

  Counter #(.trigger("falling")) counter_1 (
    .count(1'b1), .Q(counter_1_q), .up(1'b1), .clk(CLK), .clr(RESET));  // open: load, D, carry
  Multiplier multiplier_1 (.a(counter_1_q), .b(8'h2), .out(multiplier_1_out));  // open: cin, cout
  Multiplexer #(.width(8)) multiplexer_1 (
    .in0(multiplier_1_out), .in1(adder_1_out), .out(multiplexer_1_out), .sel(CLK));
  Adder adder_1 (.a(multiplier_1_out), .b(8'h1), .out(adder_1_out));  // open: cin, cout
  Adder adder_2 (.a(SHIFT), .b(multiplexer_1_out), .out(A));  // open: cin, cout
endmodule

module DEPRECATED_Assembly (
);

  wire ACCUMULATOR_CLEAR, CLOCK_GLOBAL, EN_11_12_A, EN_11_12_B, EN_13_14_A, EN_15_16_A, EN_17_18_A,
       EN_21_22_A, EN_21_22_B, EN_23_24_A, EN_25_26_A, EN_27_28_A, EN_31_32_B, EN_41_42_B, EN_51_52_B,
       EN_61_62_B, EN_71_72_B, EN_81_82_B, ENABLE_IRAM_COUNTER, RESET_IRAM_COUNTER, RESET_ROM_STEP;
  wire [3:0] OP_GLOBAL, subcirc_instructionsplitter_1_flag;
  wire [7:0] STEP_COUNT, subcirc_instructionsplitter_1_addressa, subcirc_instructionsplitter_1_addressb;
  wire [15:0] counter_1_q, register_1_q, register_2_q;
  wire [15:8] controlunit_1_control_a, controlunit_1_control_b;
  wire [63:0] matrixadder_1_s0, matrixadder_1_s1, matrixadder_1_s2, matrixadder_1_s3, matrixadder_2_s0,
       matrixadder_2_s1, matrixadder_2_s2, matrixadder_2_s3, matrixadder_3_s0, matrixadder_3_s1,
       matrixadder_3_s2, matrixadder_3_s3, matrixadder_4_s0, matrixadder_4_s1, matrixadder_4_s2,
       matrixadder_4_s3, matrixadder_5_s0, matrixadder_5_s1, matrixadder_5_s2, matrixadder_5_s3,
       matrixadder_6_s0, matrixadder_6_s1, matrixadder_6_s2, matrixadder_6_s3, matrixadder_7_s0,
       matrixadder_7_s1, matrixadder_7_s2, matrixadder_7_s3, matrixadder_8_s0, matrixadder_8_s1,
       matrixadder_8_s2, matrixadder_8_s3, matrixadder_9_s0, matrixadder_9_s1, matrixadder_9_s2,
       matrixadder_9_s3, matrixadder_10_s0, matrixadder_10_s1, matrixadder_10_s2, matrixadder_10_s3,
       matrixadder_11_s0, matrixadder_11_s1, matrixadder_11_s2, matrixadder_11_s3, matrixadder_12_s0,
       matrixadder_12_s1, matrixadder_12_s2, matrixadder_12_s3, matrixadder_13_s0, matrixadder_13_s1,
       matrixadder_13_s2, matrixadder_13_s3, matrixadder_14_s0, matrixadder_14_s1, matrixadder_14_s2,
       matrixadder_14_s3, matrixadder_15_s0, matrixadder_15_s1, matrixadder_15_s2, matrixadder_15_s3,
       matrixmultiplier_1_s0, matrixmultiplier_1_s1, matrixmultiplier_1_s2, matrixmultiplier_1_s3,
       matrixmultiplier_1_w0, matrixmultiplier_1_w1, matrixmultiplier_1_w2, matrixmultiplier_1_w3,
       matrixmultiplier_2_s0, matrixmultiplier_2_s1, matrixmultiplier_2_s2, matrixmultiplier_2_s3,
       matrixmultiplier_2_w0, matrixmultiplier_2_w1, matrixmultiplier_2_w2, matrixmultiplier_2_w3,
       matrixmultiplier_3_s0, matrixmultiplier_3_s1, matrixmultiplier_3_s2, matrixmultiplier_3_s3,
       matrixmultiplier_3_w0, matrixmultiplier_3_w1, matrixmultiplier_3_w2, matrixmultiplier_3_w3,
       matrixmultiplier_4_s0, matrixmultiplier_4_s1, matrixmultiplier_4_s2, matrixmultiplier_4_s3,
       matrixmultiplier_4_w0, matrixmultiplier_4_w1, matrixmultiplier_4_w2, matrixmultiplier_4_w3,
       matrixmultiplier_5_s0, matrixmultiplier_5_s1, matrixmultiplier_5_s2, matrixmultiplier_5_s3,
       matrixmultiplier_5_w0, matrixmultiplier_5_w1, matrixmultiplier_5_w2, matrixmultiplier_5_w3,
       matrixmultiplier_6_s0, matrixmultiplier_6_s1, matrixmultiplier_6_s2, matrixmultiplier_6_s3,
       matrixmultiplier_6_w0, matrixmultiplier_6_w1, matrixmultiplier_6_w2, matrixmultiplier_6_w3,
       matrixmultiplier_7_s0, matrixmultiplier_7_s1, matrixmultiplier_7_s2, matrixmultiplier_7_s3,
       matrixmultiplier_7_w0, matrixmultiplier_7_w1, matrixmultiplier_7_w2, matrixmultiplier_7_w3,
       matrixmultiplier_8_s0, matrixmultiplier_8_s1, matrixmultiplier_8_s2, matrixmultiplier_8_s3,
       matrixmultiplier_8_w0, matrixmultiplier_8_w1, matrixmultiplier_8_w2, matrixmultiplier_8_w3,
       ram_1_dout, rambankedged_1_p3, rambankedged_1_p4, rambankedged_2_p3, rambankedged_2_p4,
       registerbankedged_1_s0, registerbankedged_1_s1, registerbankedged_1_s2, registerbankedged_1_s3,
       registerbankedged_2_s0, registerbankedged_2_s1, registerbankedged_2_s2, registerbankedged_2_s3,
       registerbankedged_3_s0, registerbankedged_3_s1, registerbankedged_3_s2, registerbankedged_3_s3,
       registerbankedged_4_s0, registerbankedged_4_s1, registerbankedged_4_s2, registerbankedged_4_s3,
       registerbankedged_5_s0, registerbankedged_5_s1, registerbankedged_5_s2, registerbankedged_5_s3,
       registerbankedged_6_s0, registerbankedged_6_s1, registerbankedged_6_s2, registerbankedged_6_s3,
       registerbankedged_7_s0, registerbankedged_7_s1, registerbankedged_7_s2, registerbankedged_7_s3,
       registerbankedged_8_s0, registerbankedged_8_s1, registerbankedged_8_s2, registerbankedged_8_s3,
       registerbankedged_9_s0, registerbankedged_9_s1, registerbankedged_9_s2, registerbankedged_9_s3,
       registerbankedged_10_s0, registerbankedged_10_s1, registerbankedged_10_s2, registerbankedged_10_s3,
       registerbankedged_11_s0, registerbankedged_11_s1, registerbankedged_11_s2, registerbankedged_11_s3,
       registerbankedged_12_s0, registerbankedged_12_s1, registerbankedged_12_s2, registerbankedged_12_s3,
       registerbankedged_13_s0, registerbankedged_13_s1, registerbankedged_13_s2, registerbankedged_13_s3,
       registerbankedged_14_s0, registerbankedged_14_s1, registerbankedged_14_s2, registerbankedged_14_s3,
       registerbankedged_15_s0, registerbankedged_15_s1, registerbankedged_15_s2, registerbankedged_15_s3,
       registerbankedged_16_s0, registerbankedged_16_s1, registerbankedged_16_s2, registerbankedged_16_s3,
       rom_1_data, S0, S1, S2, S3;

  Clock clock_1 (.out(CLOCK_GLOBAL));
  Register #(.width(16)) register_1 (.Q(register_1_q), .clk(CLOCK_GLOBAL));  // open: D, en, clr
  Register #(.width(16)) register_2 (.Q(register_2_q), .clk(CLOCK_GLOBAL));  // open: D, en, clr
  // Probe on S0
  // Probe on S2
  Counter #(.max('hffff), .width(16)) counter_1 (
    .count(ENABLE_IRAM_COUNTER), .Q(counter_1_q), .up(1'b1), .clk(CLOCK_GLOBAL), .clr(RESET_IRAM_COUNTER));  // open: load, D, carry
  // Probe on {OP_GLOBAL, STEP_COUNT}
  // Probe on S1
  // Probe on S3
  // Probe on rambankedged_1_p3
  // Probe on rambankedged_2_p3
  // RAMBankEdged rambankedged_1: pin names not known; wires that end beside it: register_1_q, CLOCK_GLOBAL, rambankedged_1_p3, rambankedged_1_p4
  // RAMBankEdged rambankedged_2: pin names not known; wires that end beside it: register_2_q, CLOCK_GLOBAL, rambankedged_2_p3, rambankedged_2_p4
  SUBCIRC_ROMController subcirc_romcontroller_1 (
    .RESET(RESET_ROM_STEP), .CLK(CLOCK_GLOBAL), .A(STEP_COUNT));  // open: SHIFT
  RegisterBankEdged registerbankedged_1 (
    .CLK(CLOCK_GLOBAL), .EN0(EN_11_12_A), .EN1(EN_11_12_A), .EN3(EN_21_22_A), .EN2(EN_21_22_A),
    .D(rambankedged_1_p3), .S3(registerbankedged_1_s3), .S2(registerbankedged_1_s2),
    .S1(registerbankedged_1_s1), .S0(registerbankedged_1_s0));  // open: CLEAR
  RegisterBankEdged registerbankedged_2 (
    .CLK(CLOCK_GLOBAL), .EN0(EN_13_14_A), .EN1(EN_13_14_A), .EN3(EN_23_24_A), .EN2(EN_23_24_A),
    .D(rambankedged_1_p3), .S3(registerbankedged_2_s3), .S2(registerbankedged_2_s2),
    .S1(registerbankedged_2_s1), .S0(registerbankedged_2_s0));  // open: CLEAR
  RegisterBankEdged registerbankedged_3 (
    .CLK(CLOCK_GLOBAL), .EN0(EN_15_16_A), .EN1(EN_15_16_A), .EN3(EN_25_26_A), .EN2(EN_25_26_A),
    .D(rambankedged_1_p3), .S3(registerbankedged_3_s3), .S2(registerbankedged_3_s2),
    .S1(registerbankedged_3_s1), .S0(registerbankedged_3_s0));  // open: CLEAR
  RegisterBankEdged registerbankedged_4 (
    .CLK(CLOCK_GLOBAL), .EN0(EN_17_18_A), .EN1(EN_17_18_A), .EN3(EN_27_28_A), .EN2(EN_27_28_A),
    .D(rambankedged_1_p3), .S3(registerbankedged_4_s3), .S2(registerbankedged_4_s2),
    .S1(registerbankedged_4_s1), .S0(registerbankedged_4_s0));  // open: CLEAR
  RegisterBankEdged registerbankedged_5 (
    .CLK(CLOCK_GLOBAL), .EN0(EN_11_12_A), .EN1(EN_11_12_A), .EN3(EN_21_22_A), .EN2(EN_21_22_A),
    .D(rambankedged_1_p4), .S3(registerbankedged_5_s3), .S2(registerbankedged_5_s2),
    .S1(registerbankedged_5_s1), .S0(registerbankedged_5_s0));  // open: CLEAR
  RegisterBankEdged registerbankedged_6 (
    .CLK(CLOCK_GLOBAL), .EN0(EN_13_14_A), .EN1(EN_13_14_A), .EN3(EN_23_24_A), .EN2(EN_23_24_A),
    .D(rambankedged_1_p4), .S3(registerbankedged_6_s3), .S2(registerbankedged_6_s2),
    .S1(registerbankedged_6_s1), .S0(registerbankedged_6_s0));  // open: CLEAR
  RegisterBankEdged registerbankedged_7 (
    .CLK(CLOCK_GLOBAL), .EN0(EN_15_16_A), .EN1(EN_15_16_A), .EN3(EN_25_26_A), .EN2(EN_25_26_A),
    .D(rambankedged_1_p4), .S3(registerbankedged_7_s3), .S2(registerbankedged_7_s2),
    .S1(registerbankedged_7_s1), .S0(registerbankedged_7_s0));  // open: CLEAR
  RegisterBankEdged registerbankedged_8 (
    .CLK(CLOCK_GLOBAL), .EN0(EN_17_18_A), .EN1(EN_17_18_A), .EN3(EN_27_28_A), .EN2(EN_27_28_A),
    .D(rambankedged_1_p4), .S3(registerbankedged_8_s3), .S2(registerbankedged_8_s2),
    .S1(registerbankedged_8_s1), .S0(registerbankedged_8_s0));  // open: CLEAR
  // Probe on registerbankedged_1_s3
  // Probe on registerbankedged_1_s2
  // Probe on registerbankedged_1_s1
  // Probe on registerbankedged_1_s0
  RegisterBankEdged registerbankedged_9 (
    .CLK(CLOCK_GLOBAL), .EN0(EN_11_12_B), .EN1(EN_11_12_B), .EN3(EN_21_22_B), .EN2(EN_21_22_B),
    .D(rambankedged_2_p3), .S3(registerbankedged_9_s3), .S2(registerbankedged_9_s2),
    .S1(registerbankedged_9_s1), .S0(registerbankedged_9_s0));  // open: CLEAR
  RegisterBankEdged registerbankedged_10 (
    .CLK(CLOCK_GLOBAL), .EN0(EN_31_32_B), .EN1(EN_31_32_B), .EN3(EN_41_42_B), .EN2(EN_41_42_B),
    .D(rambankedged_2_p3), .S3(registerbankedged_10_s3), .S2(registerbankedged_10_s2),
    .S1(registerbankedged_10_s1), .S0(registerbankedged_10_s0));  // open: CLEAR
  RegisterBankEdged registerbankedged_11 (
    .CLK(CLOCK_GLOBAL), .EN0(EN_51_52_B), .EN1(EN_51_52_B), .EN3(EN_61_62_B), .EN2(EN_61_62_B),
    .D(rambankedged_2_p3), .S3(registerbankedged_11_s3), .S2(registerbankedged_11_s2),
    .S1(registerbankedged_11_s1), .S0(registerbankedged_11_s0));  // open: CLEAR
  RegisterBankEdged registerbankedged_12 (
    .CLK(CLOCK_GLOBAL), .EN0(EN_71_72_B), .EN1(EN_71_72_B), .EN3(EN_81_82_B), .EN2(EN_81_82_B),
    .D(rambankedged_2_p3), .S3(registerbankedged_12_s3), .S2(registerbankedged_12_s2),
    .S1(registerbankedged_12_s1), .S0(registerbankedged_12_s0));  // open: CLEAR
  RegisterBankEdged registerbankedged_13 (
    .CLK(CLOCK_GLOBAL), .EN0(EN_11_12_B), .EN1(EN_11_12_B), .EN3(EN_21_22_B), .EN2(EN_21_22_B),
    .D(rambankedged_2_p4), .S3(registerbankedged_13_s3), .S2(registerbankedged_13_s2),
    .S1(registerbankedged_13_s1), .S0(registerbankedged_13_s0));  // open: CLEAR
  RegisterBankEdged registerbankedged_14 (
    .CLK(CLOCK_GLOBAL), .EN0(EN_31_32_B), .EN1(EN_31_32_B), .EN3(EN_41_42_B), .EN2(EN_41_42_B),
    .D(rambankedged_2_p4), .S3(registerbankedged_14_s3), .S2(registerbankedged_14_s2),
    .S1(registerbankedged_14_s1), .S0(registerbankedged_14_s0));  // open: CLEAR
  RegisterBankEdged registerbankedged_15 (
    .CLK(CLOCK_GLOBAL), .EN0(EN_51_52_B), .EN1(EN_51_52_B), .EN3(EN_61_62_B), .EN2(EN_61_62_B),
    .D(rambankedged_2_p4), .S3(registerbankedged_15_s3), .S2(registerbankedged_15_s2),
    .S1(registerbankedged_15_s1), .S0(registerbankedged_15_s0));  // open: CLEAR
  RegisterBankEdged registerbankedged_16 (
    .CLEAR(CLOCK_GLOBAL), .CLK(CLOCK_GLOBAL), .EN0(EN_71_72_B), .EN1(EN_71_72_B), .EN3(EN_81_82_B),
    .EN2(EN_81_82_B), .D(rambankedged_2_p4), .S3(registerbankedged_16_s3), .S2(registerbankedged_16_s2),
    .S1(registerbankedged_16_s1), .S0(registerbankedged_16_s0));
  ROM #(.addrWidth(12), .dataWidth(64)) rom_1 (.addr({OP_GLOBAL, STEP_COUNT}), .data(rom_1_data));
  RAM #(.addrWidth(16), .dataWidth(64), .\type ("nonvolatile")) ram_1 (
    .addr(counter_1_q), .oe(1'b1), .clk(CLOCK_GLOBAL), .dout(ram_1_dout));  // open: we, din
  // Probe on rom_1_data
  // Probe on {controlunit_1_control_a, EN_27_28_A, EN_17_18_A, EN_25_26_A, EN_15_16_A, EN_23_24_A, EN_13_14_A, EN_21_22_A, EN_11_12_A}
  Register #(.width(4)) DIM ();  // open: D, en, Q, clk, clr
  MatrixMultiplier matrixmultiplier_1 (
    .A3(registerbankedged_1_s3), .A2(registerbankedged_1_s2), .A1(registerbankedged_1_s1),
    .A0(registerbankedged_1_s0), .B3(registerbankedged_9_s3), .B2(registerbankedged_9_s2),
    .B1(registerbankedged_9_s1), .B0(registerbankedged_9_s0), .S0(matrixmultiplier_1_s0),
    .S1(matrixmultiplier_1_s1), .S2(matrixmultiplier_1_s2), .S3(matrixmultiplier_1_s3),
    .W0(matrixmultiplier_1_w0), .W1(matrixmultiplier_1_w1), .W2(matrixmultiplier_1_w2),
    .W3(matrixmultiplier_1_w3));  // open: P
  MatrixAdder matrixadder_1 (
    .B0(matrixmultiplier_1_s0), .B1(matrixmultiplier_1_s1), .B2(matrixmultiplier_1_s2),
    .B3(matrixmultiplier_1_s3), .A0(matrixmultiplier_1_w0), .A1(matrixmultiplier_1_w1),
    .A2(matrixmultiplier_1_w2), .A3(matrixmultiplier_1_w3), .S0(matrixadder_1_s0), .S1(matrixadder_1_s1),
    .S2(matrixadder_1_s2), .S3(matrixadder_1_s3));
  MatrixMultiplier matrixmultiplier_2 (
    .A3(registerbankedged_2_s3), .A2(registerbankedged_2_s2), .A1(registerbankedged_2_s1),
    .A0(registerbankedged_2_s0), .B3(registerbankedged_10_s3), .B2(registerbankedged_10_s2),
    .B1(registerbankedged_10_s1), .B0(registerbankedged_10_s0), .S0(matrixmultiplier_2_s0),
    .S1(matrixmultiplier_2_s1), .S2(matrixmultiplier_2_s2), .S3(matrixmultiplier_2_s3),
    .W0(matrixmultiplier_2_w0), .W1(matrixmultiplier_2_w1), .W2(matrixmultiplier_2_w2),
    .W3(matrixmultiplier_2_w3));  // open: P
  MatrixAdder matrixadder_2 (
    .B0(matrixmultiplier_2_s0), .B1(matrixmultiplier_2_s1), .B2(matrixmultiplier_2_s2),
    .B3(matrixmultiplier_2_s3), .A0(matrixmultiplier_2_w0), .A1(matrixmultiplier_2_w1),
    .A2(matrixmultiplier_2_w2), .A3(matrixmultiplier_2_w3), .S0(matrixadder_2_s0), .S1(matrixadder_2_s1),
    .S2(matrixadder_2_s2), .S3(matrixadder_2_s3));
  MatrixMultiplier matrixmultiplier_3 (
    .A3(registerbankedged_3_s3), .A2(registerbankedged_3_s2), .A1(registerbankedged_3_s1),
    .A0(registerbankedged_3_s0), .B3(registerbankedged_11_s3), .B2(registerbankedged_11_s2),
    .B1(registerbankedged_11_s1), .B0(registerbankedged_11_s0), .S0(matrixmultiplier_3_s0),
    .S1(matrixmultiplier_3_s1), .S2(matrixmultiplier_3_s2), .S3(matrixmultiplier_3_s3),
    .W0(matrixmultiplier_3_w0), .W1(matrixmultiplier_3_w1), .W2(matrixmultiplier_3_w2),
    .W3(matrixmultiplier_3_w3));  // open: P
  MatrixAdder matrixadder_3 (
    .B0(matrixmultiplier_3_s0), .B1(matrixmultiplier_3_s1), .B2(matrixmultiplier_3_s2),
    .B3(matrixmultiplier_3_s3), .A0(matrixmultiplier_3_w0), .A1(matrixmultiplier_3_w1),
    .A2(matrixmultiplier_3_w2), .A3(matrixmultiplier_3_w3), .S0(matrixadder_3_s0), .S1(matrixadder_3_s1),
    .S2(matrixadder_3_s2), .S3(matrixadder_3_s3));
  MatrixMultiplier matrixmultiplier_4 (
    .A3(registerbankedged_4_s3), .A2(registerbankedged_4_s2), .A1(registerbankedged_4_s1),
    .A0(registerbankedged_4_s0), .B3(registerbankedged_12_s3), .B2(registerbankedged_12_s2),
    .B1(registerbankedged_12_s1), .B0(registerbankedged_12_s0), .S0(matrixmultiplier_4_s0),
    .S1(matrixmultiplier_4_s1), .S2(matrixmultiplier_4_s2), .S3(matrixmultiplier_4_s3),
    .W0(matrixmultiplier_4_w0), .W1(matrixmultiplier_4_w1), .W2(matrixmultiplier_4_w2),
    .W3(matrixmultiplier_4_w3));  // open: P
  MatrixAdder matrixadder_4 (
    .B0(matrixmultiplier_4_s0), .B1(matrixmultiplier_4_s1), .B2(matrixmultiplier_4_s2),
    .B3(matrixmultiplier_4_s3), .A0(matrixmultiplier_4_w0), .A1(matrixmultiplier_4_w1),
    .A2(matrixmultiplier_4_w2), .A3(matrixmultiplier_4_w3), .S0(matrixadder_4_s0), .S1(matrixadder_4_s1),
    .S2(matrixadder_4_s2), .S3(matrixadder_4_s3));
  MatrixMultiplier matrixmultiplier_5 (
    .A3(registerbankedged_5_s3), .A2(registerbankedged_5_s2), .A1(registerbankedged_5_s1),
    .A0(registerbankedged_5_s0), .B3(registerbankedged_13_s3), .B2(registerbankedged_13_s2),
    .B1(registerbankedged_13_s1), .B0(registerbankedged_13_s0), .S0(matrixmultiplier_5_s0),
    .S1(matrixmultiplier_5_s1), .S2(matrixmultiplier_5_s2), .S3(matrixmultiplier_5_s3),
    .W0(matrixmultiplier_5_w0), .W1(matrixmultiplier_5_w1), .W2(matrixmultiplier_5_w2),
    .W3(matrixmultiplier_5_w3));  // open: P
  MatrixAdder matrixadder_5 (
    .B0(matrixmultiplier_5_s0), .B1(matrixmultiplier_5_s1), .B2(matrixmultiplier_5_s2),
    .B3(matrixmultiplier_5_s3), .A0(matrixmultiplier_5_w0), .A1(matrixmultiplier_5_w1),
    .A2(matrixmultiplier_5_w2), .A3(matrixmultiplier_5_w3), .S0(matrixadder_5_s0), .S1(matrixadder_5_s1),
    .S2(matrixadder_5_s2), .S3(matrixadder_5_s3));
  MatrixMultiplier matrixmultiplier_6 (
    .A3(registerbankedged_6_s3), .A2(registerbankedged_6_s2), .A1(registerbankedged_6_s1),
    .A0(registerbankedged_6_s0), .B3(registerbankedged_14_s3), .B2(registerbankedged_14_s2),
    .B1(registerbankedged_14_s1), .B0(registerbankedged_14_s0), .S0(matrixmultiplier_6_s0),
    .S1(matrixmultiplier_6_s1), .S2(matrixmultiplier_6_s2), .S3(matrixmultiplier_6_s3),
    .W0(matrixmultiplier_6_w0), .W1(matrixmultiplier_6_w1), .W2(matrixmultiplier_6_w2),
    .W3(matrixmultiplier_6_w3));  // open: P
  MatrixAdder matrixadder_6 (
    .B0(matrixmultiplier_6_s0), .B1(matrixmultiplier_6_s1), .B2(matrixmultiplier_6_s2),
    .B3(matrixmultiplier_6_s3), .A0(matrixmultiplier_6_w0), .A1(matrixmultiplier_6_w1),
    .A2(matrixmultiplier_6_w2), .A3(matrixmultiplier_6_w3), .S0(matrixadder_6_s0), .S1(matrixadder_6_s1),
    .S2(matrixadder_6_s2), .S3(matrixadder_6_s3));
  MatrixMultiplier matrixmultiplier_7 (
    .A3(registerbankedged_7_s3), .A2(registerbankedged_7_s2), .A1(registerbankedged_7_s1),
    .A0(registerbankedged_7_s0), .B3(registerbankedged_15_s3), .B2(registerbankedged_15_s2),
    .B1(registerbankedged_15_s1), .B0(registerbankedged_15_s0), .S0(matrixmultiplier_7_s0),
    .S1(matrixmultiplier_7_s1), .S2(matrixmultiplier_7_s2), .S3(matrixmultiplier_7_s3),
    .W0(matrixmultiplier_7_w0), .W1(matrixmultiplier_7_w1), .W2(matrixmultiplier_7_w2),
    .W3(matrixmultiplier_7_w3));  // open: P
  MatrixAdder matrixadder_7 (
    .B0(matrixmultiplier_7_s0), .B1(matrixmultiplier_7_s1), .B2(matrixmultiplier_7_s2),
    .B3(matrixmultiplier_7_s3), .A0(matrixmultiplier_7_w0), .A1(matrixmultiplier_7_w1),
    .A2(matrixmultiplier_7_w2), .A3(matrixmultiplier_7_w3), .S0(matrixadder_7_s0), .S1(matrixadder_7_s1),
    .S2(matrixadder_7_s2), .S3(matrixadder_7_s3));
  MatrixMultiplier matrixmultiplier_8 (
    .A3(registerbankedged_8_s3), .A2(registerbankedged_8_s2), .A1(registerbankedged_8_s1),
    .A0(registerbankedged_8_s0), .B3(registerbankedged_16_s3), .B2(registerbankedged_16_s2),
    .B1(registerbankedged_16_s1), .B0(registerbankedged_16_s0), .S0(matrixmultiplier_8_s0),
    .S1(matrixmultiplier_8_s1), .S2(matrixmultiplier_8_s2), .S3(matrixmultiplier_8_s3),
    .W0(matrixmultiplier_8_w0), .W1(matrixmultiplier_8_w1), .W2(matrixmultiplier_8_w2),
    .W3(matrixmultiplier_8_w3));  // open: P
  MatrixAdder matrixadder_8 (
    .B0(matrixmultiplier_8_s0), .B1(matrixmultiplier_8_s1), .B2(matrixmultiplier_8_s2),
    .B3(matrixmultiplier_8_s3), .A0(matrixmultiplier_8_w0), .A1(matrixmultiplier_8_w1),
    .A2(matrixmultiplier_8_w2), .A3(matrixmultiplier_8_w3), .S0(matrixadder_8_s0), .S1(matrixadder_8_s1),
    .S2(matrixadder_8_s2), .S3(matrixadder_8_s3));
  ControlUnit controlunit_1 (
    .ROM_INPUT(rom_1_data), .OP(OP_GLOBAL), .FLAG(subcirc_instructionsplitter_1_flag),
    .AddressA(subcirc_instructionsplitter_1_addressa), .AddressB(subcirc_instructionsplitter_1_addressb),
    .STEP_COUNT(STEP_COUNT),
    .Control_A({controlunit_1_control_a, EN_27_28_A, EN_17_18_A, EN_25_26_A, EN_15_16_A, EN_23_24_A, EN_13_14_A, EN_21_22_A, EN_11_12_A}),
    .Control_B({controlunit_1_control_b, EN_81_82_B, EN_71_72_B, EN_61_62_B, EN_51_52_B, EN_41_42_B, EN_31_32_B, EN_21_22_B, EN_11_12_B}));  // open: CLK, PINS
  SUBCIRC_InstructionSplitter subcirc_instructionsplitter_1 (
    .I(ram_1_dout[23:0]), .AddressB(subcirc_instructionsplitter_1_addressb),
    .AddressA(subcirc_instructionsplitter_1_addressa), .OP(OP_GLOBAL),
    .Flag(subcirc_instructionsplitter_1_flag));
  MatrixAdder matrixadder_9 (
    .B0(matrixadder_1_s0), .B1(matrixadder_1_s1), .B2(matrixadder_1_s2), .B3(matrixadder_1_s3),
    .A0(matrixadder_2_s0), .A1(matrixadder_2_s1), .A2(matrixadder_2_s2), .A3(matrixadder_2_s3),
    .S0(matrixadder_9_s0), .S1(matrixadder_9_s1), .S2(matrixadder_9_s2), .S3(matrixadder_9_s3));
  MatrixAdder matrixadder_10 (
    .B0(matrixadder_3_s0), .B1(matrixadder_3_s1), .B2(matrixadder_3_s2), .B3(matrixadder_3_s3),
    .A0(matrixadder_4_s0), .A1(matrixadder_4_s1), .A2(matrixadder_4_s2), .A3(matrixadder_4_s3),
    .S0(matrixadder_10_s0), .S1(matrixadder_10_s1), .S2(matrixadder_10_s2), .S3(matrixadder_10_s3));
  MatrixAdder matrixadder_11 (
    .B0(matrixadder_5_s0), .B1(matrixadder_5_s1), .B2(matrixadder_5_s2), .B3(matrixadder_5_s3),
    .A0(matrixadder_6_s0), .A1(matrixadder_6_s1), .A2(matrixadder_6_s2), .A3(matrixadder_6_s3),
    .S0(matrixadder_11_s0), .S1(matrixadder_11_s1), .S2(matrixadder_11_s2), .S3(matrixadder_11_s3));
  MatrixAdder matrixadder_12 (
    .B0(matrixadder_7_s0), .B1(matrixadder_7_s1), .B2(matrixadder_7_s2), .B3(matrixadder_7_s3),
    .A0(matrixadder_8_s0), .A1(matrixadder_8_s1), .A2(matrixadder_8_s2), .A3(matrixadder_8_s3),
    .S0(matrixadder_12_s0), .S1(matrixadder_12_s1), .S2(matrixadder_12_s2), .S3(matrixadder_12_s3));
  MatrixAdder matrixadder_13 (
    .B0(matrixadder_9_s0), .B1(matrixadder_9_s1), .B2(matrixadder_9_s2), .B3(matrixadder_9_s3),
    .A0(matrixadder_10_s0), .A1(matrixadder_10_s1), .A2(matrixadder_10_s2), .A3(matrixadder_10_s3),
    .S0(matrixadder_13_s0), .S1(matrixadder_13_s1), .S2(matrixadder_13_s2), .S3(matrixadder_13_s3));
  MatrixAdder matrixadder_14 (
    .B0(matrixadder_11_s0), .B1(matrixadder_11_s1), .B2(matrixadder_11_s2), .B3(matrixadder_11_s3),
    .A0(matrixadder_12_s0), .A1(matrixadder_12_s1), .A2(matrixadder_12_s2), .A3(matrixadder_12_s3),
    .S0(matrixadder_14_s0), .S1(matrixadder_14_s1), .S2(matrixadder_14_s2), .S3(matrixadder_14_s3));
  MatrixAdder matrixadder_15 (
    .B0(matrixadder_13_s0), .B1(matrixadder_13_s1), .B2(matrixadder_13_s2), .B3(matrixadder_13_s3),
    .A0(matrixadder_14_s0), .A1(matrixadder_14_s1), .A2(matrixadder_14_s2), .A3(matrixadder_14_s3),
    .S0(matrixadder_15_s0), .S1(matrixadder_15_s1), .S2(matrixadder_15_s2), .S3(matrixadder_15_s3));
  Accumulator accumulator_1 (
    .Clear(ACCUMULATOR_CLEAR), .Enable(1'b1), .CLK(CLOCK_GLOBAL), .A0(matrixadder_15_s0),
    .A1(matrixadder_15_s1), .A2(matrixadder_15_s2), .A3(matrixadder_15_s3), .S0(S0), .S1(S1), .S2(S2), .S3(S3));
  Register #(.width(64)) register_3 (.D(S0), .en(1'b1), .clk(CLOCK_GLOBAL));  // open: Q, clr
  Register #(.width(64)) register_4 (.D(S2), .en(1'b1), .clk(CLOCK_GLOBAL));  // open: Q, clr
  Register #(.width(64)) register_5 (.D(S1), .en(1'b1), .clk(CLOCK_GLOBAL));  // open: Q, clr
  Register #(.width(64)) register_6 (.D(S3), .en(1'b1), .clk(CLOCK_GLOBAL));  // open: Q, clr
  // Pins of 24 and 64 bits meet at ram_1_dout

  // Notes on the sheet:
  //   Preview
  //   Clock Counter
  //   ROM Address
  //   RAM Bank A
  //   RAM Bank B
  //   ROM Step Counter
  //   A11 A12 A21 A22
  //   A11 A12 A21 A22
  //   8 - Bit step counter (OP+STEP_COUNT = 12 Bits) (count up to 2^12 Cycles)
  //   Register Bank A
  //   Triggered 1/2 Clock Cycle
  //   Register Bank B
  //   B11 B12 B21 B22
  //   OP + Step Counter = 12 Bit
  //   contents of rom_1 (hex, n*v repeats v):
  //   1 1 4 4 10 10 40 40 2 2 8 8 20 20 80 80
  //   Instruction RAM / C
  //   (i) Should not be controlled since ENABLE_IRAM_COUNTER can be set to 0 which will hold IRAM instruction
  //   Control Unit
  //   Micro Code ROM
  //   (i) Should have 8 Terms, but since 1 Term is a 2x2 we get 8/2 Terms
  //   Calculate 16x16 Multiplication
  //   1x 16x2 Row and 1x 16x2 Colmun (8 2x2) => 1 2x2
  //   AW+BY+CX+DZ
  //   AW+BY+CX+DZ
  //   ------------------------------------------------------------------------------------------------------------------------------------------------------------------------------------------------------
  //   Accumulator - Will reset after every cycle for 16x16 Multiplication
  //   A11 A12 A21 A22
endmodule

module SUBCIRC_DataRAMASequencer (
  input  [15:0] SHIFT,
  input  CLK,
  input  [15:0] N,
  input  [15:0] K,
  output [15:0] R0,
  output [15:0] R1
);

  wire comparator_1_eq, comparator_1_gt, comparator_2_eq;
  wire [15:0] adder_1_out, adder_2_out, adder_3_out, adder_4_out, multiplier_1_out, multiplier_2_out,
       register_1_q, subcirc_halfcyclecounter_1_a, subtractor_1_out;

  Register #(.trigger("falling"), .width(16)) register_1 (
    .D(adder_1_out), .en(comparator_1_eq), .Q(register_1_q), .clk(CLK), .clr(comparator_2_eq));
  Subtractor #(.width(16)) subtractor_1 (.a(K), .b(16'h1), .out(subtractor_1_out));  // open: bin, bout
  Multiplier #(.width(16)) multiplier_1 (.a(16'h2), .b(K), .out(multiplier_1_out));  // open: cin, cout
  Adder #(.width(16)) adder_1 (.a(16'h1), .b(register_1_q), .out(adder_1_out));  // open: cin, cout
  Multiplier #(.width(16)) multiplier_2 (
    .a(register_1_q), .b(multiplier_1_out), .out(multiplier_2_out));  // open: cin, cout
  SUBCIRC_HalfCycleCounter subcirc_halfcyclecounter_1 (
    .CLK(CLK), .Clear(comparator_1_gt), .A(subcirc_halfcyclecounter_1_a));  // open: SHIFT
  // Probe on adder_2_out
  Adder #(.width(16)) adder_2 (
    .a(multiplier_2_out), .b(subcirc_halfcyclecounter_1_a), .out(adder_2_out));  // open: cin, cout
  Comparator #(.width(16)) comparator_1 (
    .a(subcirc_halfcyclecounter_1_a), .b(subtractor_1_out), .gt(comparator_1_gt), .eq(comparator_1_eq));  // open: lt
  Adder #(.width(16)) adder_3 (.a(register_1_q), .b(16'h2), .out(adder_3_out));  // open: cin, cout
  Comparator #(.width(16)) comparator_2 (.a(adder_3_out), .b(N), .eq(comparator_2_eq));  // open: gt, lt
  Adder #(.width(16)) adder_4 (.a(adder_2_out), .b(K), .out(adder_4_out));  // open: cin, cout
  // Probe on adder_4_out
  // Probe on N
  // Probe on K
  // Probe on subtractor_1_out
  Adder #(.width(16)) adder_5 (.a(SHIFT), .b(adder_2_out), .out(R0));  // open: cin, cout
  Adder #(.width(16)) adder_6 (.a(SHIFT), .b(adder_4_out), .out(R1));  // open: cin, cout

  // Notes on the sheet:
  //   After K increment multiplier input
  //   K-1
  //   2K
  //   Shifting using RAMController not possible
  //   Async, so it clears right after it becomes 6
  //   X
  //   X+K
endmodule
module Assembly (
);

  wire ACCUMULATOR_CLEAR, CLOCK_GLOBAL, DRAM_OE, DRAM_WE, EN_11_12_A, EN_11_12_B, EN_13_14_A, EN_15_16_A,
       EN_17_18_A, EN_21_22_A, EN_21_22_B, EN_23_24_A, EN_25_26_A, EN_27_28_A, EN_31_32_B, EN_41_42_B,
       EN_51_52_B, EN_61_62_B, EN_71_72_B, EN_81_82_B, ENABLE_IRAM_COUNTER, I_BlockLoad, I_BlockMove,
       I_BlockStore, I_DIM, I_Execute, I_Halt, I_Loop, I_MatrixAdd, INPUT_REG_CLEAR, IRAM_OE, MM_PASSTHROUGH,
       not_1_out, not_2_out, not_3_out, not_4_out, not_5_out, not_6_out, not_7_out, not_8_out, not_9_out,
       not_10_out, not_11_out, not_12_out, not_13_out, not_14_out, not_15_out, not_16_out, not_17_out,
       not_18_out, not_19_out, ORAM_WE, RESET_IRAM_COUNTER, RESET_ROM_STEP;
  wire [3:0] DIMK_GLOBAL, DIMN_A_GLOBAL, DIMN_B_GLOBAL, OP_GLOBAL, subcirc_instructionsplitter_1_flag;
  wire [7:0] AddressA, AddressB, STEP_COUNT, subcirc_instructionsplitter_1_addressa,
       subcirc_instructionsplitter_1_addressb;
  wire [15:0] counter_1_q, register_1_q, register_2_q, subcirc_dataramasequencer_1_r0,
       subcirc_dataramasequencer_1_r1, subcirc_datarambsequencer_1_r0, subcirc_datarambsequencer_1_r1,
       undriven;
  wire [15:8] controlunit_1_control_a, controlunit_1_control_b;
  wire [23:0] ram_2_dout;
  wire [31:10] controlunit_1_pins;
  wire [63:0] matrixadder_1_s0, matrixadder_1_s1, matrixadder_1_s2, matrixadder_1_s3, matrixadder_2_s0,
       matrixadder_2_s1, matrixadder_2_s2, matrixadder_2_s3, matrixadder_3_s0, matrixadder_3_s1,
       matrixadder_3_s2, matrixadder_3_s3, matrixadder_4_s0, matrixadder_4_s1, matrixadder_4_s2,
       matrixadder_4_s3, matrixadder_5_s0, matrixadder_5_s1, matrixadder_5_s2, matrixadder_5_s3,
       matrixadder_6_s0, matrixadder_6_s1, matrixadder_6_s2, matrixadder_6_s3, matrixadder_7_s0,
       matrixadder_7_s1, matrixadder_7_s2, matrixadder_7_s3, matrixadder_8_s0, matrixadder_8_s1,
       matrixadder_8_s2, matrixadder_8_s3, matrixadder_9_s0, matrixadder_9_s1, matrixadder_9_s2,
       matrixadder_9_s3, matrixadder_10_s0, matrixadder_10_s1, matrixadder_10_s2, matrixadder_10_s3,
       matrixadder_11_s0, matrixadder_11_s1, matrixadder_11_s2, matrixadder_11_s3, matrixadder_12_s0,
       matrixadder_12_s1, matrixadder_12_s2, matrixadder_12_s3, matrixadder_13_s0, matrixadder_13_s1,
       matrixadder_13_s2, matrixadder_13_s3, matrixadder_14_s0, matrixadder_14_s1, matrixadder_14_s2,
       matrixadder_14_s3, matrixadder_15_s0, matrixadder_15_s1, matrixadder_15_s2, matrixadder_15_s3,
       matrixmultiplier_1_s0, matrixmultiplier_1_s1, matrixmultiplier_1_s2, matrixmultiplier_1_s3,
       matrixmultiplier_1_w0, matrixmultiplier_1_w1, matrixmultiplier_1_w2, matrixmultiplier_1_w3,
       matrixmultiplier_2_s0, matrixmultiplier_2_s1, matrixmultiplier_2_s2, matrixmultiplier_2_s3,
       matrixmultiplier_2_w0, matrixmultiplier_2_w1, matrixmultiplier_2_w2, matrixmultiplier_2_w3,
       matrixmultiplier_3_s0, matrixmultiplier_3_s1, matrixmultiplier_3_s2, matrixmultiplier_3_s3,
       matrixmultiplier_3_w0, matrixmultiplier_3_w1, matrixmultiplier_3_w2, matrixmultiplier_3_w3,
       matrixmultiplier_4_s0, matrixmultiplier_4_s1, matrixmultiplier_4_s2, matrixmultiplier_4_s3,
       matrixmultiplier_4_w0, matrixmultiplier_4_w1, matrixmultiplier_4_w2, matrixmultiplier_4_w3,
       matrixmultiplier_5_s0, matrixmultiplier_5_s1, matrixmultiplier_5_s2, matrixmultiplier_5_s3,
       matrixmultiplier_5_w0, matrixmultiplier_5_w1, matrixmultiplier_5_w2, matrixmultiplier_5_w3,
       matrixmultiplier_6_s0, matrixmultiplier_6_s1, matrixmultiplier_6_s2, matrixmultiplier_6_s3,
       matrixmultiplier_6_w0, matrixmultiplier_6_w1, matrixmultiplier_6_w2, matrixmultiplier_6_w3,
       matrixmultiplier_7_s0, matrixmultiplier_7_s1, matrixmultiplier_7_s2, matrixmultiplier_7_s3,
       matrixmultiplier_7_w0, matrixmultiplier_7_w1, matrixmultiplier_7_w2, matrixmultiplier_7_w3,
       matrixmultiplier_8_s0, matrixmultiplier_8_s1, matrixmultiplier_8_s2, matrixmultiplier_8_s3,
       matrixmultiplier_8_w0, matrixmultiplier_8_w1, matrixmultiplier_8_w2, matrixmultiplier_8_w3,
       ram_3_dout, ram_4_dout, ram_5_dout, ram_6_dout, rambankedged_1_r0, rambankedged_1_r1,
       rambankedged_2_r0, rambankedged_2_r1, registerbankedged_1_s0, registerbankedged_1_s1,
       registerbankedged_1_s2, registerbankedged_1_s3, registerbankedged_2_s0, registerbankedged_2_s1,
       registerbankedged_2_s2, registerbankedged_2_s3, registerbankedged_3_s0, registerbankedged_3_s1,
       registerbankedged_3_s2, registerbankedged_3_s3, registerbankedged_4_s0, registerbankedged_4_s1,
       registerbankedged_4_s2, registerbankedged_4_s3, registerbankedged_5_s0, registerbankedged_5_s1,
       registerbankedged_5_s2, registerbankedged_5_s3, registerbankedged_6_s0, registerbankedged_6_s1,
       registerbankedged_6_s2, registerbankedged_6_s3, registerbankedged_7_s0, registerbankedged_7_s1,
       registerbankedged_7_s2, registerbankedged_7_s3, registerbankedged_8_s0, registerbankedged_8_s1,
       registerbankedged_8_s2, registerbankedged_8_s3, registerbankedged_9_s0, registerbankedged_9_s1,
       registerbankedged_9_s2, registerbankedged_9_s3, registerbankedged_10_s0, registerbankedged_10_s1,
       registerbankedged_10_s2, registerbankedged_10_s3, registerbankedged_11_s0, registerbankedged_11_s1,
       registerbankedged_11_s2, registerbankedged_11_s3, registerbankedged_12_s0, registerbankedged_12_s1,
       registerbankedged_12_s2, registerbankedged_12_s3, registerbankedged_13_s0, registerbankedged_13_s1,
       registerbankedged_13_s2, registerbankedged_13_s3, registerbankedged_14_s0, registerbankedged_14_s1,
       registerbankedged_14_s2, registerbankedged_14_s3, registerbankedged_15_s0, registerbankedged_15_s1,
       registerbankedged_15_s2, registerbankedged_15_s3, registerbankedged_16_s0, registerbankedged_16_s1,
       registerbankedged_16_s2, registerbankedged_16_s3, rom_1_data, S0, S1, S2, S3;

  Clock clock_1 (.out(CLOCK_GLOBAL));
  Hex_Digit_Display hex_digit_display_1 ();  // open: value, dp
  Hex_Digit_Display hex_digit_display_2 ();  // open: value, dp
  Hex_Digit_Display hex_digit_display_3 ();  // open: value, dp
  Hex_Digit_Display hex_digit_display_4 ();  // open: value, dp
  Hex_Digit_Display hex_digit_display_5 ();  // open: value, dp
  // Probe on {{8{1'b0}}, AddressA}
  Hex_Digit_Display hex_digit_display_6 ();  // open: value, dp
  Register #(.width(16)) register_1 (
    .D({{8{1'b0}}, AddressA}), .en(1'b1), .Q(register_1_q), .clk(CLOCK_GLOBAL));  // open: clr
  Register #(.width(16)) register_2 (
    .D({{8{1'b0}}, AddressB}), .en(1'b1), .Q(register_2_q), .clk(CLOCK_GLOBAL));  // open: clr
  SUBCIRC_DataRAMASequencer subcirc_dataramasequencer_1 (
    .SHIFT(register_1_q), .CLK(CLOCK_GLOBAL), .N({{12{1'b0}}, DIMN_A_GLOBAL}), .K({{12{1'b0}}, DIMK_GLOBAL}),
    .R0(subcirc_dataramasequencer_1_r0), .R1(subcirc_dataramasequencer_1_r1));
  SUBCIRC_DataRAMBSequencer subcirc_datarambsequencer_1 (
    .SHIFT(register_2_q), .CLK(CLOCK_GLOBAL), .N({{12{1'b0}}, DIMN_B_GLOBAL}), .K({{12{1'b0}}, DIMK_GLOBAL}),
    .R0(subcirc_datarambsequencer_1_r0), .R1(subcirc_datarambsequencer_1_r1));
  // Probe on subcirc_dataramasequencer_1_r0
  Counter #(.max('hffff), .width(16)) counter_1 (
    .count(ENABLE_IRAM_COUNTER), .Q(counter_1_q), .up(1'b1), .clk(CLOCK_GLOBAL), .clr(RESET_IRAM_COUNTER));  // open: load, D, carry
  // Probe on S0
  // Probe on S2
  // Probe on rambankedged_1_r0
  // Probe on rambankedged_1_r1
  // Probe on rambankedged_2_r0
  // Probe on rambankedged_2_r1
  RAMBankEdged rambankedged_1 (
    .CLK(CLOCK_GLOBAL), .WE(DRAM_WE), .OE(DRAM_OE), .A0(subcirc_dataramasequencer_1_r0),
    .A1(subcirc_dataramasequencer_1_r1), .R0(rambankedged_1_r0), .R1(rambankedged_1_r1));  // open: D0, D1
  RAMBankEdged rambankedged_2 (
    .CLK(CLOCK_GLOBAL), .WE(DRAM_WE), .OE(DRAM_OE), .A0(subcirc_datarambsequencer_1_r0),
    .A1(subcirc_datarambsequencer_1_r1), .R0(rambankedged_2_r0), .R1(rambankedged_2_r1));  // open: D0, D1
  // Probe on {OP_GLOBAL, STEP_COUNT}
  // Probe on S1
  // Probe on S3
  SUBCIRC_ROMController subcirc_romcontroller_1 (
    .RESET(RESET_ROM_STEP), .CLK(CLOCK_GLOBAL), .A(STEP_COUNT));  // open: SHIFT
  RAM #(.addrWidth(16), .dataWidth(64)) ram_1 ();  // open: addr, we, oe, clk, din, dout
  RegisterBankEdged registerbankedged_1 (
    .CLEAR(INPUT_REG_CLEAR), .CLK(CLOCK_GLOBAL), .EN0(EN_11_12_A), .EN1(EN_11_12_A), .EN3(EN_21_22_A),
    .EN2(EN_21_22_A), .D(rambankedged_1_r0), .S3(registerbankedged_1_s3), .S2(registerbankedged_1_s2),
    .S1(registerbankedged_1_s1), .S0(registerbankedged_1_s0));
  RegisterBankEdged registerbankedged_2 (
    .CLEAR(INPUT_REG_CLEAR), .CLK(CLOCK_GLOBAL), .EN0(EN_13_14_A), .EN1(EN_13_14_A), .EN3(EN_23_24_A),
    .EN2(EN_23_24_A), .D(rambankedged_1_r0), .S3(registerbankedged_2_s3), .S2(registerbankedged_2_s2),
    .S1(registerbankedged_2_s1), .S0(registerbankedged_2_s0));
  RegisterBankEdged registerbankedged_3 (
    .CLEAR(INPUT_REG_CLEAR), .CLK(CLOCK_GLOBAL), .EN0(EN_15_16_A), .EN1(EN_15_16_A), .EN3(EN_25_26_A),
    .EN2(EN_25_26_A), .D(rambankedged_1_r0), .S3(registerbankedged_3_s3), .S2(registerbankedged_3_s2),
    .S1(registerbankedged_3_s1), .S0(registerbankedged_3_s0));
  RegisterBankEdged registerbankedged_4 (
    .CLEAR(INPUT_REG_CLEAR), .CLK(CLOCK_GLOBAL), .EN0(EN_17_18_A), .EN1(EN_17_18_A), .EN3(EN_27_28_A),
    .EN2(EN_27_28_A), .D(rambankedged_1_r0), .S3(registerbankedged_4_s3), .S2(registerbankedged_4_s2),
    .S1(registerbankedged_4_s1), .S0(registerbankedged_4_s0));
  RegisterBankEdged registerbankedged_5 (
    .CLEAR(INPUT_REG_CLEAR), .CLK(CLOCK_GLOBAL), .EN0(EN_11_12_A), .EN1(EN_11_12_A), .EN3(EN_21_22_A),
    .EN2(EN_21_22_A), .D(rambankedged_1_r1), .S3(registerbankedged_5_s3), .S2(registerbankedged_5_s2),
    .S1(registerbankedged_5_s1), .S0(registerbankedged_5_s0));
  RegisterBankEdged registerbankedged_6 (
    .CLEAR(INPUT_REG_CLEAR), .CLK(CLOCK_GLOBAL), .EN0(EN_13_14_A), .EN1(EN_13_14_A), .EN3(EN_23_24_A),
    .EN2(EN_23_24_A), .D(rambankedged_1_r1), .S3(registerbankedged_6_s3), .S2(registerbankedged_6_s2),
    .S1(registerbankedged_6_s1), .S0(registerbankedged_6_s0));
  RegisterBankEdged registerbankedged_7 (
    .CLEAR(INPUT_REG_CLEAR), .CLK(CLOCK_GLOBAL), .EN0(EN_15_16_A), .EN1(EN_15_16_A), .EN3(EN_25_26_A),
    .EN2(EN_25_26_A), .D(rambankedged_1_r1), .S3(registerbankedged_7_s3), .S2(registerbankedged_7_s2),
    .S1(registerbankedged_7_s1), .S0(registerbankedged_7_s0));
  RegisterBankEdged registerbankedged_8 (
    .CLEAR(INPUT_REG_CLEAR), .CLK(CLOCK_GLOBAL), .EN0(EN_17_18_A), .EN1(EN_17_18_A), .EN3(EN_27_28_A),
    .EN2(EN_27_28_A), .D(rambankedged_1_r1), .S3(registerbankedged_8_s3), .S2(registerbankedged_8_s2),
    .S1(registerbankedged_8_s1), .S0(registerbankedged_8_s0));
  // Probe on registerbankedged_1_s3
  // Probe on registerbankedged_1_s2
  // Probe on registerbankedged_1_s1
  // Probe on registerbankedged_1_s0
  RegisterBankEdged registerbankedged_9 (
    .CLEAR(INPUT_REG_CLEAR), .CLK(CLOCK_GLOBAL), .EN0(EN_11_12_B), .EN1(EN_11_12_B), .EN3(EN_21_22_B),
    .EN2(EN_21_22_B), .D(rambankedged_2_r0), .S3(registerbankedged_9_s3), .S2(registerbankedged_9_s2),
    .S1(registerbankedged_9_s1), .S0(registerbankedged_9_s0));
  RegisterBankEdged registerbankedged_10 (
    .CLEAR(INPUT_REG_CLEAR), .CLK(CLOCK_GLOBAL), .EN0(EN_31_32_B), .EN1(EN_31_32_B), .EN3(EN_41_42_B),
    .EN2(EN_41_42_B), .D(rambankedged_2_r0), .S3(registerbankedged_10_s3), .S2(registerbankedged_10_s2),
    .S1(registerbankedged_10_s1), .S0(registerbankedged_10_s0));
  RegisterBankEdged registerbankedged_11 (
    .CLEAR(INPUT_REG_CLEAR), .CLK(CLOCK_GLOBAL), .EN0(EN_51_52_B), .EN1(EN_51_52_B), .EN3(EN_61_62_B),
    .EN2(EN_61_62_B), .D(rambankedged_2_r0), .S3(registerbankedged_11_s3), .S2(registerbankedged_11_s2),
    .S1(registerbankedged_11_s1), .S0(registerbankedged_11_s0));
  RegisterBankEdged registerbankedged_12 (
    .CLEAR(INPUT_REG_CLEAR), .CLK(CLOCK_GLOBAL), .EN0(EN_71_72_B), .EN1(EN_71_72_B), .EN3(EN_81_82_B),
    .EN2(EN_81_82_B), .D(rambankedged_2_r0), .S3(registerbankedged_12_s3), .S2(registerbankedged_12_s2),
    .S1(registerbankedged_12_s1), .S0(registerbankedged_12_s0));
  RegisterBankEdged registerbankedged_13 (
    .CLEAR(INPUT_REG_CLEAR), .CLK(CLOCK_GLOBAL), .EN0(EN_11_12_B), .EN1(EN_11_12_B), .EN3(EN_21_22_B),
    .EN2(EN_21_22_B), .D(rambankedged_2_r1), .S3(registerbankedged_13_s3), .S2(registerbankedged_13_s2),
    .S1(registerbankedged_13_s1), .S0(registerbankedged_13_s0));
  RegisterBankEdged registerbankedged_14 (
    .CLEAR(INPUT_REG_CLEAR), .CLK(CLOCK_GLOBAL), .EN0(EN_31_32_B), .EN1(EN_31_32_B), .EN3(EN_41_42_B),
    .EN2(EN_41_42_B), .D(rambankedged_2_r1), .S3(registerbankedged_14_s3), .S2(registerbankedged_14_s2),
    .S1(registerbankedged_14_s1), .S0(registerbankedged_14_s0));
  RegisterBankEdged registerbankedged_15 (
    .CLEAR(INPUT_REG_CLEAR), .CLK(CLOCK_GLOBAL), .EN0(EN_51_52_B), .EN1(EN_51_52_B), .EN3(EN_61_62_B),
    .EN2(EN_61_62_B), .D(rambankedged_2_r1), .S3(registerbankedged_15_s3), .S2(registerbankedged_15_s2),
    .S1(registerbankedged_15_s1), .S0(registerbankedged_15_s0));
  RegisterBankEdged registerbankedged_16 (
    .CLEAR(INPUT_REG_CLEAR), .CLK(CLOCK_GLOBAL), .EN0(EN_71_72_B), .EN1(EN_71_72_B), .EN3(EN_81_82_B),
    .EN2(EN_81_82_B), .D(rambankedged_2_r1), .S3(registerbankedged_16_s3), .S2(registerbankedged_16_s2),
    .S1(registerbankedged_16_s1), .S0(registerbankedged_16_s0));
  // Probe on STEP_COUNT
  ROM #(.addrWidth(12), .dataWidth(64)) rom_1 (.addr({OP_GLOBAL, STEP_COUNT}), .data(rom_1_data));
  // Probe on OP_GLOBAL
  RAM #(.addrWidth(16), .dataWidth(24), .\type ("nonvolatile")) ram_2 (
    .addr(counter_1_q), .oe(IRAM_OE), .clk(CLOCK_GLOBAL), .dout(ram_2_dout));  // open: we, din
  // Probe on rom_1_data
  MatrixMultiplier matrixmultiplier_1 (
    .A3(registerbankedged_1_s3), .A2(registerbankedged_1_s2), .A1(registerbankedged_1_s1),
    .A0(registerbankedged_1_s0), .P(MM_PASSTHROUGH), .B3(registerbankedged_9_s3),
    .B2(registerbankedged_9_s2), .B1(registerbankedged_9_s1), .B0(registerbankedged_9_s0),
    .S0(matrixmultiplier_1_s0), .S1(matrixmultiplier_1_s1), .S2(matrixmultiplier_1_s2),
    .S3(matrixmultiplier_1_s3), .W0(matrixmultiplier_1_w0), .W1(matrixmultiplier_1_w1),
    .W2(matrixmultiplier_1_w2), .W3(matrixmultiplier_1_w3));
  MatrixAdder matrixadder_1 (
    .B0(matrixmultiplier_1_s0), .B1(matrixmultiplier_1_s1), .B2(matrixmultiplier_1_s2),
    .B3(matrixmultiplier_1_s3), .A0(matrixmultiplier_1_w0), .A1(matrixmultiplier_1_w1),
    .A2(matrixmultiplier_1_w2), .A3(matrixmultiplier_1_w3), .S0(matrixadder_1_s0), .S1(matrixadder_1_s1),
    .S2(matrixadder_1_s2), .S3(matrixadder_1_s3));
  MatrixMultiplier matrixmultiplier_2 (
    .A3(registerbankedged_2_s3), .A2(registerbankedged_2_s2), .A1(registerbankedged_2_s1),
    .A0(registerbankedged_2_s0), .P(MM_PASSTHROUGH), .B3(registerbankedged_10_s3),
    .B2(registerbankedged_10_s2), .B1(registerbankedged_10_s1), .B0(registerbankedged_10_s0),
    .S0(matrixmultiplier_2_s0), .S1(matrixmultiplier_2_s1), .S2(matrixmultiplier_2_s2),
    .S3(matrixmultiplier_2_s3), .W0(matrixmultiplier_2_w0), .W1(matrixmultiplier_2_w1),
    .W2(matrixmultiplier_2_w2), .W3(matrixmultiplier_2_w3));
  MatrixAdder matrixadder_2 (
    .B0(matrixmultiplier_2_s0), .B1(matrixmultiplier_2_s1), .B2(matrixmultiplier_2_s2),
    .B3(matrixmultiplier_2_s3), .A0(matrixmultiplier_2_w0), .A1(matrixmultiplier_2_w1),
    .A2(matrixmultiplier_2_w2), .A3(matrixmultiplier_2_w3), .S0(matrixadder_2_s0), .S1(matrixadder_2_s1),
    .S2(matrixadder_2_s2), .S3(matrixadder_2_s3));
  MatrixMultiplier matrixmultiplier_3 (
    .A3(registerbankedged_3_s3), .A2(registerbankedged_3_s2), .A1(registerbankedged_3_s1),
    .A0(registerbankedged_3_s0), .P(MM_PASSTHROUGH), .B3(registerbankedged_11_s3),
    .B2(registerbankedged_11_s2), .B1(registerbankedged_11_s1), .B0(registerbankedged_11_s0),
    .S0(matrixmultiplier_3_s0), .S1(matrixmultiplier_3_s1), .S2(matrixmultiplier_3_s2),
    .S3(matrixmultiplier_3_s3), .W0(matrixmultiplier_3_w0), .W1(matrixmultiplier_3_w1),
    .W2(matrixmultiplier_3_w2), .W3(matrixmultiplier_3_w3));
  MatrixAdder matrixadder_3 (
    .B0(matrixmultiplier_3_s0), .B1(matrixmultiplier_3_s1), .B2(matrixmultiplier_3_s2),
    .B3(matrixmultiplier_3_s3), .A0(matrixmultiplier_3_w0), .A1(matrixmultiplier_3_w1),
    .A2(matrixmultiplier_3_w2), .A3(matrixmultiplier_3_w3), .S0(matrixadder_3_s0), .S1(matrixadder_3_s1),
    .S2(matrixadder_3_s2), .S3(matrixadder_3_s3));
  MatrixMultiplier matrixmultiplier_4 (
    .A3(registerbankedged_4_s3), .A2(registerbankedged_4_s2), .A1(registerbankedged_4_s1),
    .A0(registerbankedged_4_s0), .P(MM_PASSTHROUGH), .B3(registerbankedged_12_s3),
    .B2(registerbankedged_12_s2), .B1(registerbankedged_12_s1), .B0(registerbankedged_12_s0),
    .S0(matrixmultiplier_4_s0), .S1(matrixmultiplier_4_s1), .S2(matrixmultiplier_4_s2),
    .S3(matrixmultiplier_4_s3), .W0(matrixmultiplier_4_w0), .W1(matrixmultiplier_4_w1),
    .W2(matrixmultiplier_4_w2), .W3(matrixmultiplier_4_w3));
  MatrixAdder matrixadder_4 (
    .B0(matrixmultiplier_4_s0), .B1(matrixmultiplier_4_s1), .B2(matrixmultiplier_4_s2),
    .B3(matrixmultiplier_4_s3), .A0(matrixmultiplier_4_w0), .A1(matrixmultiplier_4_w1),
    .A2(matrixmultiplier_4_w2), .A3(matrixmultiplier_4_w3), .S0(matrixadder_4_s0), .S1(matrixadder_4_s1),
    .S2(matrixadder_4_s2), .S3(matrixadder_4_s3));
  MatrixMultiplier matrixmultiplier_5 (
    .A3(registerbankedged_5_s3), .A2(registerbankedged_5_s2), .A1(registerbankedged_5_s1),
    .A0(registerbankedged_5_s0), .P(MM_PASSTHROUGH), .B3(registerbankedged_13_s3),
    .B2(registerbankedged_13_s2), .B1(registerbankedged_13_s1), .B0(registerbankedged_13_s0),
    .S0(matrixmultiplier_5_s0), .S1(matrixmultiplier_5_s1), .S2(matrixmultiplier_5_s2),
    .S3(matrixmultiplier_5_s3), .W0(matrixmultiplier_5_w0), .W1(matrixmultiplier_5_w1),
    .W2(matrixmultiplier_5_w2), .W3(matrixmultiplier_5_w3));
  MatrixAdder matrixadder_5 (
    .B0(matrixmultiplier_5_s0), .B1(matrixmultiplier_5_s1), .B2(matrixmultiplier_5_s2),
    .B3(matrixmultiplier_5_s3), .A0(matrixmultiplier_5_w0), .A1(matrixmultiplier_5_w1),
    .A2(matrixmultiplier_5_w2), .A3(matrixmultiplier_5_w3), .S0(matrixadder_5_s0), .S1(matrixadder_5_s1),
    .S2(matrixadder_5_s2), .S3(matrixadder_5_s3));
  MatrixMultiplier matrixmultiplier_6 (
    .A3(registerbankedged_6_s3), .A2(registerbankedged_6_s2), .A1(registerbankedged_6_s1),
    .A0(registerbankedged_6_s0), .P(MM_PASSTHROUGH), .B3(registerbankedged_14_s3),
    .B2(registerbankedged_14_s2), .B1(registerbankedged_14_s1), .B0(registerbankedged_14_s0),
    .S0(matrixmultiplier_6_s0), .S1(matrixmultiplier_6_s1), .S2(matrixmultiplier_6_s2),
    .S3(matrixmultiplier_6_s3), .W0(matrixmultiplier_6_w0), .W1(matrixmultiplier_6_w1),
    .W2(matrixmultiplier_6_w2), .W3(matrixmultiplier_6_w3));
  MatrixAdder matrixadder_6 (
    .B0(matrixmultiplier_6_s0), .B1(matrixmultiplier_6_s1), .B2(matrixmultiplier_6_s2),
    .B3(matrixmultiplier_6_s3), .A0(matrixmultiplier_6_w0), .A1(matrixmultiplier_6_w1),
    .A2(matrixmultiplier_6_w2), .A3(matrixmultiplier_6_w3), .S0(matrixadder_6_s0), .S1(matrixadder_6_s1),
    .S2(matrixadder_6_s2), .S3(matrixadder_6_s3));
  MatrixMultiplier matrixmultiplier_7 (
    .A3(registerbankedged_7_s3), .A2(registerbankedged_7_s2), .A1(registerbankedged_7_s1),
    .A0(registerbankedged_7_s0), .B3(registerbankedged_15_s3), .B2(registerbankedged_15_s2),
    .B1(registerbankedged_15_s1), .B0(registerbankedged_15_s0), .S0(matrixmultiplier_7_s0),
    .S1(matrixmultiplier_7_s1), .S2(matrixmultiplier_7_s2), .S3(matrixmultiplier_7_s3),
    .W0(matrixmultiplier_7_w0), .W1(matrixmultiplier_7_w1), .W2(matrixmultiplier_7_w2),
    .W3(matrixmultiplier_7_w3));  // open: P
  MatrixAdder matrixadder_7 (
    .B0(matrixmultiplier_7_s0), .B1(matrixmultiplier_7_s1), .B2(matrixmultiplier_7_s2),
    .B3(matrixmultiplier_7_s3), .A0(matrixmultiplier_7_w0), .A1(matrixmultiplier_7_w1),
    .A2(matrixmultiplier_7_w2), .A3(matrixmultiplier_7_w3), .S0(matrixadder_7_s0), .S1(matrixadder_7_s1),
    .S2(matrixadder_7_s2), .S3(matrixadder_7_s3));
  MatrixMultiplier matrixmultiplier_8 (
    .A3(registerbankedged_8_s3), .A2(registerbankedged_8_s2), .A1(registerbankedged_8_s1),
    .A0(registerbankedged_8_s0), .P(MM_PASSTHROUGH), .B3(registerbankedged_16_s3),
    .B2(registerbankedged_16_s2), .B1(registerbankedged_16_s1), .B0(registerbankedged_16_s0),
    .S0(matrixmultiplier_8_s0), .S1(matrixmultiplier_8_s1), .S2(matrixmultiplier_8_s2),
    .S3(matrixmultiplier_8_s3), .W0(matrixmultiplier_8_w0), .W1(matrixmultiplier_8_w1),
    .W2(matrixmultiplier_8_w2), .W3(matrixmultiplier_8_w3));
  MatrixAdder matrixadder_8 (
    .B0(matrixmultiplier_8_s0), .B1(matrixmultiplier_8_s1), .B2(matrixmultiplier_8_s2),
    .B3(matrixmultiplier_8_s3), .A0(matrixmultiplier_8_w0), .A1(matrixmultiplier_8_w1),
    .A2(matrixmultiplier_8_w2), .A3(matrixmultiplier_8_w3), .S0(matrixadder_8_s0), .S1(matrixadder_8_s1),
    .S2(matrixadder_8_s2), .S3(matrixadder_8_s3));
  // Probe on ram_2_dout
  // Probe on {controlunit_1_control_a, EN_27_28_A, EN_17_18_A, EN_25_26_A, EN_15_16_A, EN_23_24_A, EN_13_14_A, EN_21_22_A, EN_11_12_A}
  MatrixAdder matrixadder_9 (
    .B0(matrixadder_1_s0), .B1(matrixadder_1_s1), .B2(matrixadder_1_s2), .B3(matrixadder_1_s3),
    .A0(matrixadder_2_s0), .A1(matrixadder_2_s1), .A2(matrixadder_2_s2), .A3(matrixadder_2_s3),
    .S0(matrixadder_9_s0), .S1(matrixadder_9_s1), .S2(matrixadder_9_s2), .S3(matrixadder_9_s3));
  MatrixAdder matrixadder_10 (
    .B0(matrixadder_3_s0), .B1(matrixadder_3_s1), .B2(matrixadder_3_s2), .B3(matrixadder_3_s3),
    .A0(matrixadder_4_s0), .A1(matrixadder_4_s1), .A2(matrixadder_4_s2), .A3(matrixadder_4_s3),
    .S0(matrixadder_10_s0), .S1(matrixadder_10_s1), .S2(matrixadder_10_s2), .S3(matrixadder_10_s3));
  MatrixAdder matrixadder_11 (
    .B0(matrixadder_5_s0), .B1(matrixadder_5_s1), .B2(matrixadder_5_s2), .B3(matrixadder_5_s3),
    .A0(matrixadder_6_s0), .A1(matrixadder_6_s1), .A2(matrixadder_6_s2), .A3(matrixadder_6_s3),
    .S0(matrixadder_11_s0), .S1(matrixadder_11_s1), .S2(matrixadder_11_s2), .S3(matrixadder_11_s3));
  MatrixAdder matrixadder_12 (
    .B0(matrixadder_7_s0), .B1(matrixadder_7_s1), .B2(matrixadder_7_s2), .B3(matrixadder_7_s3),
    .A0(matrixadder_8_s0), .A1(matrixadder_8_s1), .A2(matrixadder_8_s2), .A3(matrixadder_8_s3),
    .S0(matrixadder_12_s0), .S1(matrixadder_12_s1), .S2(matrixadder_12_s2), .S3(matrixadder_12_s3));
  MatrixAdder matrixadder_13 (
    .B0(matrixadder_9_s0), .B1(matrixadder_9_s1), .B2(matrixadder_9_s2), .B3(matrixadder_9_s3),
    .A0(matrixadder_10_s0), .A1(matrixadder_10_s1), .A2(matrixadder_10_s2), .A3(matrixadder_10_s3),
    .S0(matrixadder_13_s0), .S1(matrixadder_13_s1), .S2(matrixadder_13_s2), .S3(matrixadder_13_s3));
  MatrixAdder matrixadder_14 (
    .B0(matrixadder_11_s0), .B1(matrixadder_11_s1), .B2(matrixadder_11_s2), .B3(matrixadder_11_s3),
    .A0(matrixadder_12_s0), .A1(matrixadder_12_s1), .A2(matrixadder_12_s2), .A3(matrixadder_12_s3),
    .S0(matrixadder_14_s0), .S1(matrixadder_14_s1), .S2(matrixadder_14_s2), .S3(matrixadder_14_s3));
  ControlUnit controlunit_1 (
    .ROM_INPUT(rom_1_data), .OP(OP_GLOBAL), .FLAG(subcirc_instructionsplitter_1_flag),
    .AddressA(subcirc_instructionsplitter_1_addressa), .AddressB(subcirc_instructionsplitter_1_addressb),
    .STEP_COUNT(STEP_COUNT), .CLK(CLOCK_GLOBAL),
    .Control_A({controlunit_1_control_a, EN_27_28_A, EN_17_18_A, EN_25_26_A, EN_15_16_A, EN_23_24_A, EN_13_14_A, EN_21_22_A, EN_11_12_A}),
    .Control_B({controlunit_1_control_b, EN_81_82_B, EN_71_72_B, EN_61_62_B, EN_51_52_B, EN_41_42_B, EN_31_32_B, EN_21_22_B, EN_11_12_B}),
    .PINS({controlunit_1_pins, IRAM_OE, DRAM_OE, DRAM_WE, RESET_IRAM_COUNTER, ENABLE_IRAM_COUNTER, RESET_ROM_STEP, ORAM_WE, ACCUMULATOR_CLEAR, MM_PASSTHROUGH, INPUT_REG_CLEAR}));
  SUBCIRC_InstructionSplitter subcirc_instructionsplitter_1 (
    .I(ram_2_dout), .AddressB(subcirc_instructionsplitter_1_addressb),
    .AddressA(subcirc_instructionsplitter_1_addressa), .OP(OP_GLOBAL),
    .Flag(subcirc_instructionsplitter_1_flag));
  MatrixAdder matrixadder_15 (
    .B0(matrixadder_13_s0), .B1(matrixadder_13_s1), .B2(matrixadder_13_s2), .B3(matrixadder_13_s3),
    .A0(matrixadder_14_s0), .A1(matrixadder_14_s1), .A2(matrixadder_14_s2), .A3(matrixadder_14_s3),
    .S0(matrixadder_15_s0), .S1(matrixadder_15_s1), .S2(matrixadder_15_s2), .S3(matrixadder_15_s3));
  // Probe on OP_GLOBAL
  Register u_AddressA (
    .D(subcirc_instructionsplitter_1_addressa), .en(I_BlockLoad), .Q(AddressA), .clk(CLOCK_GLOBAL));  // open: clr
  Register #(.width(4)) OuterDimA (
    .D(subcirc_instructionsplitter_1_addressa[3:0]), .en(I_DIM), .Q(DIMN_A_GLOBAL), .clk(CLOCK_GLOBAL));  // open: clr
  Register #(.width(4)) DIM (
    .D(subcirc_instructionsplitter_1_flag), .en(I_DIM), .Q(DIMK_GLOBAL), .clk(CLOCK_GLOBAL));  // open: clr
  Register #(.width(4)) OuterDimB (
    .D(subcirc_instructionsplitter_1_addressb[3:0]), .en(I_DIM), .Q(DIMN_B_GLOBAL), .clk(CLOCK_GLOBAL));  // open: clr
  Register u_AddressB (
    .D(subcirc_instructionsplitter_1_addressb), .en(I_BlockLoad), .Q(AddressB), .clk(CLOCK_GLOBAL));  // open: clr
  RAM #(.addrWidth(16), .dataWidth(64)) ram_3 (
    .addr(undriven), .we(ORAM_WE), .clk(CLOCK_GLOBAL), .din(matrixadder_15_s0), .dout(ram_3_dout));  // open: oe
  RAM #(.addrWidth(16), .dataWidth(64)) ram_4 (
    .addr(undriven), .we(ORAM_WE), .clk(CLOCK_GLOBAL), .din(matrixadder_15_s1), .dout(ram_4_dout));  // open: oe
  RAM #(.addrWidth(16), .dataWidth(64)) ram_5 (
    .addr(undriven), .we(ORAM_WE), .clk(CLOCK_GLOBAL), .din(matrixadder_15_s2), .dout(ram_5_dout));  // open: oe
  RAM #(.addrWidth(16), .dataWidth(64)) ram_6 (
    .addr(undriven), .we(ORAM_WE), .clk(CLOCK_GLOBAL), .din(matrixadder_15_s3), .dout(ram_6_dout));  // open: oe
  not not_1 (not_1_out, OP_GLOBAL[0]);
  not not_2 (not_2_out, OP_GLOBAL[2]);
  not not_3 (not_3_out, OP_GLOBAL[3]);
  not not_4 (not_4_out, OP_GLOBAL[2]);
  not not_5 (not_5_out, OP_GLOBAL[3]);
  not not_6 (not_6_out, OP_GLOBAL[0]);
  not not_7 (not_7_out, OP_GLOBAL[1]);
  not not_8 (not_8_out, OP_GLOBAL[3]);
  and and_1 (I_BlockLoad, not_1_out, OP_GLOBAL[1], not_2_out, not_3_out);
  and and_2 (I_Execute, OP_GLOBAL[0], OP_GLOBAL[1], not_4_out, not_5_out);
  and and_3 (I_BlockStore, not_6_out, not_7_out, OP_GLOBAL[2], not_8_out);
  not not_9 (not_9_out, OP_GLOBAL[1]);
  not not_10 (not_10_out, OP_GLOBAL[3]);
  not not_11 (not_11_out, OP_GLOBAL[0]);
  not not_12 (not_12_out, OP_GLOBAL[3]);
  not not_13 (not_13_out, OP_GLOBAL[0]);
  and and_4 (I_BlockMove, OP_GLOBAL[0], not_9_out, OP_GLOBAL[2], not_10_out);
  and and_5 (I_MatrixAdd, not_11_out, OP_GLOBAL[1], OP_GLOBAL[2], not_12_out);
  and and_6 (I_Loop, not_13_out, OP_GLOBAL[1], OP_GLOBAL[2], OP_GLOBAL[3]);
  not not_14 (not_14_out, OP_GLOBAL[0]);
  not not_15 (not_15_out, OP_GLOBAL[1]);
  not not_16 (not_16_out, OP_GLOBAL[2]);
  not not_17 (not_17_out, OP_GLOBAL[1]);
  not not_18 (not_18_out, OP_GLOBAL[2]);
  not not_19 (not_19_out, OP_GLOBAL[3]);
  and and_7 (I_Halt, not_14_out, not_15_out, not_16_out, OP_GLOBAL[3]);
  and and_8 (I_DIM, OP_GLOBAL[0], not_17_out, not_18_out, not_19_out);

  // Notes on the sheet:
  //   Halted Status
  //   Internal System uses 16 Bit Addresses, 
  //   Make first 8 MSB (0000 0000) + Address to get desired results
  //   Preview
  //   Clock Counter
  //   ROM Address
  //   8 - Bit step counter (OP+STEP_COUNT = 12 Bits) (count up to 2^12 Cycles)
  //   RAM Bank A
  //   RAM Bank B
  //   Input Bus
  //   ROM Step Counter
  //   Final Output RAM
  //   A11 A12 A21 A22
  //   A11 A12 A21 A22
  //   Register Bank A
  //   Triggered 1/2 Clock Cycle
  //   |
  //   |
  //   |
  //   |
  //   |
  //   |
  //   |
  //   |
  //   |
  //   |
  //   |
  //   |
  //   |
  //   |
  //   Register Bank B
  //   B11 B12 B21 B22
  //   Control Unit
  //   OP + Step Counter = 12 Bit
  //   contents of rom_1 (hex, n*v repeats v):
  //   4500000000 21000000000 23000000000 3000000000
  //   Instruction RAM / C
  //   Micro Code ROM
  //   (i) Should not be controlled since ENABLE_IRAM_COUNTER can be set to 0 which will hold IRAM instruction
  //   AW+BY+CX+DZ
  //   Calculate 16x16 Multiplication
  //   1x 16x2 Row and 1x 16x2 Colmun (8 2x2) => 1 2x2
  //   AW+BY+CX+DZ
  //   (i) Should have 8 Terms, but since 1 Term is a 2x2 we get 8/2 Terms
  //   Unified Output Bus
  //   A11 A12 A21 A22
  //   DIM Instruction
  //   Block Load Instruction
  //   Execute Instruction
  //   Block Store Instruction
  //   Unified Memory
  //   Block Move Instruction
  //   Matrix Add Instruction
  //   Loop Instruction
  //   Halt Instruction
  //   DIM Instruction
endmodule

module SUBCIRC_MakeEven (
  input  [3:0] I,
  output [3:0] O
);

  wire [3:0] adder_1_out;

  Adder #(.width(4)) adder_1 (.a(I), .b(4'b0001), .out(adder_1_out));  // open: cin, cout
  Multiplexer #(.width(4)) multiplexer_1 (.in0(I), .in1(adder_1_out), .out(O), .sel(I[0]));
endmodule

module SUBCIRC_DataRAMBSequencer (
  input  [15:0] SHIFT,
  input  CLK,
  input  [15:0] N,
  input  [15:0] K,
  output [15:0] R0,
  output [15:0] R1
);

  wire comparator_1_eq, comparator_1_gt, comparator_2_eq;
  wire [15:0] adder_1_out, adder_2_out, adder_3_out, adder_4_out, multiplier_1_out, multiplier_2_out,
       register_1_q, subcirc_halfcyclecounter_1_a, subtractor_1_out;

  Register #(.trigger("falling"), .width(16)) register_1 (
    .D(adder_1_out), .en(comparator_1_eq), .Q(register_1_q), .clk(CLK), .clr(comparator_2_eq));
  Subtractor #(.width(16)) subtractor_1 (.a(K), .b(16'h1), .out(subtractor_1_out));  // open: bin, bout
  Multiplier #(.width(16)) multiplier_1 (.a(16'h2), .b(K), .out(multiplier_1_out));  // open: cin, cout
  Adder #(.width(16)) adder_1 (.a(16'h1), .b(register_1_q), .out(adder_1_out));  // open: cin, cout
  Multiplier #(.width(16)) multiplier_2 (
    .a(register_1_q), .b(multiplier_1_out), .out(multiplier_2_out));  // open: cin, cout
  SUBCIRC_HalfCycleCounter subcirc_halfcyclecounter_1 (
    .CLK(CLK), .Clear(comparator_1_gt), .A(subcirc_halfcyclecounter_1_a));  // open: SHIFT
  // Probe on adder_2_out
  Adder #(.width(16)) adder_2 (
    .a(multiplier_2_out), .b(subcirc_halfcyclecounter_1_a), .out(adder_2_out));  // open: cin, cout
  Comparator #(.width(16)) comparator_1 (
    .a(subcirc_halfcyclecounter_1_a), .b(subtractor_1_out), .gt(comparator_1_gt), .eq(comparator_1_eq));  // open: lt
  Adder #(.width(16)) adder_3 (.a(register_1_q), .b(16'h2), .out(adder_3_out));  // open: cin, cout
  Comparator #(.width(16)) comparator_2 (.a(adder_3_out), .b(N), .eq(comparator_2_eq));  // open: gt, lt
  Adder #(.width(16)) adder_4 (.a(adder_2_out), .b(K), .out(adder_4_out));  // open: cin, cout
  // Probe on adder_4_out
  // Probe on N
  // Probe on K
  // Probe on subtractor_1_out
  Adder #(.width(16)) adder_5 (.a(SHIFT), .b(adder_2_out), .out(R0));  // open: cin, cout
  Adder #(.width(16)) adder_6 (.a(SHIFT), .b(adder_4_out), .out(R1));  // open: cin, cout

  // Notes on the sheet:
  //   After K increment multiplier input
  //   K-1
  //   2K
  //   Shifting using RAMController not possible
  //   Async, so it clears right after it becomes 6
  //   X
  //   X+K
endmodule
